// Logisim project 4BitCPU.circ as structural Verilog: 59 circuits, main circuit main
module main (
  input  A_3,
  input  A_2,
  input  A_1,
  input  A_0,
  input  B_3,
  input  B_2,
  input  B_1,
  input  B_0,
  input  WE,
  input  S2,
  input  S1,
  input  S0,
  output OVF,
  output N,
  output C,
  output Z,
  output O_3,
  output O_2,
  output O_1,
  output O_0,
  output out_21,
  output out_22,
  output out_23,
  output out_24
);

  wire Adder_out, and_1_out, and_2_out, and_3_out, and_4_out, and_5_out, and_6_out, and_7_out, and_8_out,
       and_9_out, and_10_out, and_11_out, and_12_out, and_13_out, and_14_out, and_15_out, and_16_out,
       and_17_out, and_18_out, and_19_out, and_20_out, and_21_out, and_22_out, and_23_out, and_24_out,
       and_25_out, and_26_out, and_27_out, and_28_out, and_29_out, and_30_out, and_31_out, and_32_out,
       and_33_out, and_34_out, and_35_out, and_36_out, and_37_out, and_38_out, and_39_out, and_40_out,
       and_41_out, and_42_out, and_43_out, and_44_out, and_45_out, and_46_out, and_47_out, and_48_out,
       and_49_out, and_50_out, and_51_out, and_52_out, and_53_out, and_54_out, and_55_out, and_56_out,
       and_57_out, and_58_out, and_59_out, and_60_out, and_62_out, and_63_out, and_64_out, and_65_out,
       and_66_out, and_67_out, and_68_out, and_69_out, ANDOP_out, clock_1_out, MUX2x1_out, nand_1_out,
       nand_2_out, nand_3_out, nand_4_out, nand_5_out, nand_6_out, nand_7_out, nand_8_out, nand_9_out,
       nand_10_out, nand_11_out, nand_12_out, nand_13_out, nand_14_out, nand_15_out, nand_16_out,
       nand_17_out, nand_18_out, nand_19_out, nand_20_out, nand_21_out, nand_22_out, nand_23_out,
       nand_24_out, nand_26_out, nand_28_out, nand_30_out, nand_32_out, not_1_out, not_2_out, not_3_out,
       not_4_out, not_5_out, not_6_out, not_7_out, not_8_out, not_9_out, not_10_out, not_11_out, not_12_out,
       not_13_out, not_14_out, not_15_out, not_16_out, not_17_out, not_18_out, not_19_out, not_20_out,
       not_21_out, not_22_out, not_24_out, not_25_out, not_26_out, not_27_out, not_28_out, not_29_out,
       not_30_out, not_31_out, not_32_out, not_33_out, not_34_out, not_35_out, not_36_out, not_37_out,
       not_38_out, not_39_out, not_40_out, not_41_out, not_42_out, not_43_out, not_44_out, not_45_out,
       not_46_out, not_47_out, or_1_out, or_2_out, or_3_out, or_4_out, or_5_out, or_6_out, or_7_out,
       or_8_out, or_9_out, or_10_out, or_11_out, or_12_out, or_13_out, or_14_out, or_15_out, or_19_out,
       or_20_out, or_21_out, or_22_out, or_23_out, or_24_out, OROP_out, Subtractor_out, xor_1_out, xor_2_out,
       xor_3_out, xor_4_out, xor_5_out, xor_6_out, xor_7_out, xor_8_out, xor_9_out, xor_10_out, xor_11_out,
       xor_12_out, xor_13_out, xor_14_out, xor_15_out, xor_16_out, xor_17_out, xor_18_out, xor_19_out,
       XOROP_out;

  not not_1 (not_1_out, A_0);
  not not_2 (not_2_out, A_1);
  not not_3 (not_3_out, A_2);
  not not_4 (not_4_out, A_3);
  xor Adder (Adder_out, A_0, B_0);
  xor xor_1 (xor_1_out, A_1, B_1);
  xor xor_2 (xor_2_out, A_2, B_2);
  xor xor_3 (xor_3_out, A_3, B_3);
  and and_1 (and_1_out, not_1_out, B_0);
  and and_2 (and_2_out, not_1_out, 1'b0);
  and and_3 (and_3_out, B_0, 1'b0);
  xor xor_4 (xor_4_out, A_1, B_1);
  and and_4 (and_4_out, not_2_out, B_1);
  and and_5 (and_5_out, not_2_out, or_8_out);
  and and_6 (and_6_out, B_1, or_8_out);
  xor xor_5 (xor_5_out, A_2, B_2);
  and and_7 (and_7_out, not_3_out, B_2);
  and and_8 (and_8_out, not_3_out, or_9_out);
  and and_9 (and_9_out, B_2, or_9_out);
  xor xor_6 (xor_6_out, A_3, B_3);
  and and_10 (and_10_out, not_4_out, B_3);
  and and_11 (and_11_out, not_4_out, or_10_out);
  and and_12 (and_12_out, B_3, or_10_out);
  xor Subtractor (Subtractor_out, A_0, B_0);
  or or_1 (or_1_out, and_1_out, and_2_out);
  or or_2 (or_2_out, and_4_out, and_5_out);
  or or_3 (or_3_out, and_7_out, and_8_out);
  or or_4 (or_4_out, and_10_out, and_11_out);
  and ANDOP (ANDOP_out, A_0, B_0);
  and and_13 (and_13_out, A_1, B_1);
  and and_14 (and_14_out, A_2, B_2);
  and and_15 (and_15_out, A_3, B_3);
  or OROP (OROP_out, A_0, B_0);
  or or_5 (or_5_out, A_1, B_1);
  or or_6 (or_6_out, A_2, B_2);
  or or_7 (or_7_out, A_3, B_3);
  xor XOROP (XOROP_out, A_0, B_0);
  xor xor_7 (xor_7_out, A_1, B_1);
  xor xor_8 (xor_8_out, A_2, B_2);
  xor xor_9 (xor_9_out, A_3, B_3);
  not not_5 (not_5_out, A_0);
  not not_6 (not_6_out, A_1);
  not not_7 (not_7_out, A_2);
  not not_8 (not_8_out, A_3);
  xor xor_10 (xor_10_out, 1'b0, Adder_out);
  and and_16 (and_16_out, 1'b0, Adder_out);
  and and_17 (and_17_out, A_0, B_0);
  xor xor_11 (xor_11_out, or_12_out, xor_1_out);
  and and_18 (and_18_out, or_12_out, xor_1_out);
  and and_19 (and_19_out, A_1, B_1);
  xor xor_12 (xor_12_out, or_13_out, xor_2_out);
  and and_20 (and_20_out, or_13_out, xor_2_out);
  and and_21 (and_21_out, A_2, B_2);
  xor xor_13 (xor_13_out, or_14_out, xor_3_out);
  and and_22 (and_22_out, or_14_out, xor_3_out);
  and and_23 (and_23_out, A_3, B_3);
  or or_8 (or_8_out, or_1_out, and_3_out);
  xor xor_14 (xor_14_out, xor_4_out, or_8_out);
  or or_9 (or_9_out, or_2_out, and_6_out);
  xor xor_15 (xor_15_out, xor_5_out, or_9_out);
  or or_10 (or_10_out, or_3_out, and_9_out);
  xor xor_16 (xor_16_out, xor_6_out, or_10_out);
  or or_11 (or_11_out, or_4_out, and_12_out);
  xor xor_17 (xor_17_out, Subtractor_out, 1'b0);
  or or_12 (or_12_out, and_16_out, and_17_out);
  or or_13 (or_13_out, and_18_out, and_19_out);
  or or_14 (or_14_out, and_20_out, and_21_out);
  or or_15 (or_15_out, and_22_out, and_23_out);
  xor xor_18 (xor_18_out, or_14_out, or_15_out);
  xor xor_19 (xor_19_out, or_10_out, or_11_out);
  not not_9 (not_9_out, S2);
  not not_10 (not_10_out, S2);
  not not_11 (not_11_out, S2);
  not not_12 (not_12_out, S2);
  not not_13 (not_13_out, S1);
  not not_14 (not_14_out, S1);
  not not_15 (not_15_out, S1);
  not not_16 (not_16_out, S1);
  not not_17 (not_17_out, S0);
  not not_18 (not_18_out, S0);
  not not_19 (not_19_out, S0);
  not not_20 (not_20_out, S0);
  and and_24 (and_24_out, xor_10_out, not_17_out, not_13_out, not_9_out);
  and and_25 (and_25_out, xor_17_out, S0, not_13_out, not_9_out);
  and and_26 (and_26_out, ANDOP_out, not_17_out, S1, not_9_out);
  and and_27 (and_27_out, OROP_out, S0, S1, not_9_out);
  and and_28 (and_28_out, XOROP_out, not_17_out, not_13_out, S2);
  and and_29 (and_29_out, not_5_out, S0, not_13_out, S2);
  and and_30 (and_30_out, xor_10_out, not_17_out, S1, S2);
  and and_31 (and_31_out, xor_17_out, S0, S1, S2);
  and and_32 (and_32_out, xor_11_out, not_18_out, not_14_out, not_10_out);
  and and_33 (and_33_out, xor_14_out, S0, not_14_out, not_10_out);
  and and_34 (and_34_out, and_13_out, not_18_out, S1, not_10_out);
  and and_35 (and_35_out, or_5_out, S0, S1, not_10_out);
  and and_36 (and_36_out, xor_7_out, not_18_out, not_14_out, S2);
  and and_37 (and_37_out, not_6_out, S0, not_14_out, S2);
  and and_38 (and_38_out, xor_11_out, not_18_out, S1, S2);
  and and_39 (and_39_out, xor_14_out, S0, S1, S2);
  and and_40 (and_40_out, xor_12_out, not_19_out, not_15_out, not_11_out);
  and and_41 (and_41_out, xor_15_out, S0, not_15_out, not_11_out);
  and and_42 (and_42_out, and_14_out, not_19_out, S1, not_11_out);
  and and_43 (and_43_out, or_6_out, S0, S1, not_11_out);
  and and_44 (and_44_out, xor_8_out, not_19_out, not_15_out, S2);
  and and_45 (and_45_out, not_7_out, S0, not_15_out, S2);
  and and_46 (and_46_out, xor_12_out, not_19_out, S1, S2);
  and and_47 (and_47_out, xor_15_out, S0, S1, S2);
  and and_48 (and_48_out, xor_13_out, not_20_out, not_16_out, not_12_out);
  and and_49 (and_49_out, xor_16_out, S0, not_16_out, not_12_out);
  and and_50 (and_50_out, and_15_out, not_20_out, S1, not_12_out);
  and and_51 (and_51_out, or_7_out, S0, S1, not_12_out);
  and and_52 (and_52_out, xor_9_out, not_20_out, not_16_out, S2);
  and and_53 (and_53_out, not_8_out, S0, not_16_out, S2);
  and and_54 (and_54_out, xor_13_out, not_20_out, S1, S2);
  and and_55 (and_55_out, xor_16_out, S0, S1, S2);
  and and_56 (and_56_out, not_13_out, not_9_out);
  or MUX8x1 (O_0, and_24_out, and_25_out, and_26_out, and_27_out, and_28_out, and_29_out, and_30_out, and_31_out);
  or or_16 (O_1, and_32_out, and_33_out, and_34_out, and_35_out, and_36_out, and_37_out, and_38_out, and_39_out);
  or or_17 (O_2, and_40_out, and_41_out, and_42_out, and_43_out, and_44_out, and_45_out, and_46_out, and_47_out);
  or or_18 (N, and_48_out, and_49_out, and_50_out, and_51_out, and_52_out, and_53_out, and_54_out, and_55_out);
  not not_21 (not_21_out, S0);
  not not_22 (not_22_out, S0);
  or or_19 (or_19_out, O_0, O_1, O_2, N);
  not not_23 (Z, or_19_out);
  and and_57 (and_57_out, not_21_out, xor_18_out);
  and and_58 (and_58_out, S0, xor_19_out);
  and and_59 (and_59_out, not_22_out, or_15_out);
  and and_60 (and_60_out, S0, or_11_out);
  or MUX2x1 (MUX2x1_out, and_57_out, and_58_out);
  or or_20 (or_20_out, and_59_out, and_60_out);
  and VALIDOPCODE (OVF, MUX2x1_out, and_56_out);
  and and_61 (C, or_20_out, and_56_out);
  Clock clock_1 (.out(clock_1_out));
  not not_24 (not_24_out, WE);
  not not_25 (not_25_out, WE);
  not not_26 (not_26_out, WE);
  not not_27 (not_27_out, WE);
  and and_62 (and_62_out, not_24_out, out_21);
  and and_63 (and_63_out, WE, O_0);
  and and_64 (and_64_out, not_25_out, out_22);
  and and_65 (and_65_out, WE, O_1);
  and and_66 (and_66_out, not_26_out, out_23);
  and and_67 (and_67_out, WE, O_2);
  and and_68 (and_68_out, not_27_out, out_24);
  and and_69 (and_69_out, WE, N);
  not not_28 (not_28_out, clock_1_out);
  or or_21 (or_21_out, and_62_out, and_63_out);
  not not_29 (not_29_out, clock_1_out);
  or or_22 (or_22_out, and_64_out, and_65_out);
  not not_30 (not_30_out, clock_1_out);
  or or_23 (or_23_out, and_66_out, and_67_out);
  not not_31 (not_31_out, clock_1_out);
  or or_24 (or_24_out, and_68_out, and_69_out);
  not not_32 (not_32_out, not_28_out);
  not not_33 (not_33_out, not_29_out);
  not not_34 (not_34_out, not_30_out);
  not not_35 (not_35_out, not_31_out);
  not not_36 (not_36_out, or_21_out);
  not not_37 (not_37_out, or_22_out);
  not not_38 (not_38_out, or_23_out);
  not not_39 (not_39_out, or_24_out);
  nand nand_1 (nand_1_out, or_21_out, not_32_out);
  nand nand_2 (nand_2_out, not_32_out, not_36_out);
  nand nand_3 (nand_3_out, or_22_out, not_33_out);
  nand nand_4 (nand_4_out, not_33_out, not_37_out);
  nand nand_5 (nand_5_out, or_23_out, not_34_out);
  nand nand_6 (nand_6_out, not_34_out, not_38_out);
  nand nand_7 (nand_7_out, or_24_out, not_35_out);
  nand nand_8 (nand_8_out, not_35_out, not_39_out);
  nand nand_9 (nand_9_out, nand_1_out, nand_10_out);
  nand nand_10 (nand_10_out, nand_9_out, nand_2_out);
  nand nand_11 (nand_11_out, nand_3_out, nand_12_out);
  nand nand_12 (nand_12_out, nand_11_out, nand_4_out);
  nand nand_13 (nand_13_out, nand_5_out, nand_14_out);
  nand nand_14 (nand_14_out, nand_13_out, nand_6_out);
  nand nand_15 (nand_15_out, nand_7_out, nand_16_out);
  nand nand_16 (nand_16_out, nand_15_out, nand_8_out);
  not not_40 (not_40_out, not_32_out);
  not not_41 (not_41_out, not_33_out);
  not not_42 (not_42_out, not_34_out);
  not not_43 (not_43_out, not_35_out);
  not not_44 (not_44_out, nand_9_out);
  not not_45 (not_45_out, nand_11_out);
  not not_46 (not_46_out, nand_13_out);
  not not_47 (not_47_out, nand_15_out);
  nand nand_17 (nand_17_out, nand_9_out, not_40_out);
  nand nand_18 (nand_18_out, not_40_out, not_44_out);
  nand nand_19 (nand_19_out, nand_11_out, not_41_out);
  nand nand_20 (nand_20_out, not_41_out, not_45_out);
  nand nand_21 (nand_21_out, nand_13_out, not_42_out);
  nand nand_22 (nand_22_out, not_42_out, not_46_out);
  nand nand_23 (nand_23_out, nand_15_out, not_43_out);
  nand nand_24 (nand_24_out, not_43_out, not_47_out);
  nand nand_25 (out_21, nand_17_out, nand_26_out);
  nand nand_26 (nand_26_out, out_21, nand_18_out);
  nand nand_27 (out_22, nand_19_out, nand_28_out);
  nand nand_28 (nand_28_out, out_22, nand_20_out);
  nand nand_29 (out_23, nand_21_out, nand_30_out);
  nand nand_30 (nand_30_out, out_23, nand_22_out);
  nand nand_31 (out_24, nand_23_out, nand_32_out);
  nand nand_32 (nand_32_out, out_24, nand_24_out);

  assign O_3 = N;
endmodule

module Blocks (
  input  in_1,
  input  in_2,
  input  in_3,
  input  WE,
  input  in_5,
  input  in_6,
  input  in_7,
  input  in_8,
  input  in_9,
  input  in_10,
  input  in_11,
  input  in_12,
  input  in_13,
  input  in_14,
  input  in_15,
  input  in_16,
  input  in_17,
  input  in_18,
  input  in_19,
  input  in_20,
  input  in_21,
  input  in_22,
  input  D,
  input  in_24,
  input  HARD_RESET,
  input  in_26,
  input  in_27,
  input  in_28,
  input  in_29,
  input  in_30,
  input  in_31,
  input  in_32,
  input  in_33,
  input  in_34,
  input  in_35,
  input  in_36,
  input  in_37,
  input  in_38,
  input  in_39,
  input  in_40,
  input  in_41,
  input  in_42,
  input  in_43,
  input  in_44,
  input  in_45,
  input  in_46,
  input  in_47,
  input  in_48,
  input  in_49,
  input  in_50,
  input  in_51,
  input  in_52,
  input  in_53,
  input  in_54,
  input  in_55,
  input  in_56,
  input  in_57,
  input  in_58,
  input  in_59,
  input  in_60,
  input  in_61,
  input  in_62,
  input  in_63,
  input  in_64,
  input  in_65,
  input  in_66,
  input  in_67,
  input  in_68,
  input  in_69,
  input  in_70,
  input  in_71,
  input  in_72,
  input  D7,
  input  D6,
  input  D5,
  input  D4,
  input  D3,
  input  D2,
  input  D1,
  input  D0,
  input  S2,
  input  S1,
  input  S0,
  input  in_84,
  input  in_85,
  input  in_86,
  input  in_87,
  input  in_88,
  output out_89,
  output out_90,
  output out_91,
  output out_92,
  output out_93,
  output out_94,
  output out_95,
  output out_96,
  output out_97,
  output out_98,
  output out_99,
  output out_100,
  output out_101,
  output out_102,
  output out_103,
  output out_104,
  output out_105,
  output out_106,
  output out_107,
  output out_108,
  output out_109,
  output out_110,
  output out_111,
  output out_112,
  output DEC_O15,
  output DEC_O14,
  output DEC_O13,
  output DEC_O12,
  output DEC_O11,
  output DEC_O10,
  output DEC_O9,
  output DEC_O8,
  output DEC_O7,
  output DEC_O6,
  output DEC_O5,
  output DEC_O4,
  output DEC_O3,
  output DEC_O2,
  output DEC_O1,
  output DEC_O0,
  output out_129,
  output out_130,
  output out_131,
  output out_132,
  output out_133,
  output out_134,
  output out_135,
  output out_136,
  output out_137,
  output out_138,
  output out_139,
  output out_140,
  output out_141,
  output out_142,
  output out_143,
  output out_144,
  output out_145,
  output out_146,
  output out_147,
  output out_148,
  output out_149
);

  wire Adder_out, and_4_out, and_5_out, and_6_out, and_7_out, and_8_out, and_9_out, and_10_out, and_11_out,
       and_12_out, and_13_out, and_14_out, and_15_out, and_16_out, and_17_out, and_18_out, and_19_out,
       and_20_out, and_21_out, and_22_out, and_23_out, and_24_out, and_25_out, and_26_out, and_27_out,
       and_28_out, and_29_out, and_30_out, and_31_out, and_32_out, and_33_out, and_34_out, and_35_out,
       and_36_out, and_37_out, and_38_out, and_39_out, and_40_out, and_41_out, and_42_out, and_43_out,
       and_44_out, and_45_out, and_61_out, and_62_out, clock_1_out, clock_2_out, nand_1_out, nand_2_out,
       nand_3_out, nand_5_out, nand_6_out, nand_8_out, nand_9_out, nand_10_out, nand_11_out, nand_12_out,
       nand_13_out, nand_14_out, nand_15_out, nand_16_out, nand_17_out, nand_18_out, nand_19_out,
       nand_20_out, nand_21_out, nand_22_out, nand_23_out, nand_24_out, nand_25_out, nand_26_out,
       nand_27_out, nand_28_out, nand_29_out, nand_30_out, nand_31_out, nand_32_out, nand_33_out,
       nand_34_out, nand_35_out, nand_36_out, nand_37_out, nand_38_out, nand_39_out, nand_41_out,
       nand_43_out, nand_45_out, nand_46_out, nand_47_out, nand_48_out, nand_49_out, nand_50_out,
       nand_51_out, nand_53_out, not_5_out, not_6_out, not_7_out, not_8_out, not_9_out, not_10_out,
       not_11_out, not_12_out, not_13_out, not_14_out, not_15_out, not_16_out, not_17_out, not_18_out,
       not_19_out, not_20_out, not_21_out, not_22_out, not_23_out, not_24_out, not_25_out, not_26_out,
       not_27_out, not_28_out, not_29_out, not_30_out, not_31_out, not_32_out, not_33_out, not_34_out,
       not_35_out, not_36_out, not_37_out, not_38_out, not_39_out, not_40_out, not_41_out, not_42_out,
       not_43_out, not_44_out, not_45_out, not_46_out, not_47_out, not_48_out, not_49_out, not_50_out,
       not_51_out, not_52_out, not_53_out, not_54_out, not_55_out, not_56_out, not_57_out, not_58_out,
       or_1_out, or_2_out, or_3_out, or_8_out, or_9_out, or_10_out, or_11_out, or_12_out, or_13_out,
       or_15_out, or_16_out, or_17_out, or_18_out, or_19_out, or_20_out, or_21_out, or_22_out,
       Subtractor_out, xor_1_out, xor_2_out, xor_3_out, xor_11_out, xor_12_out, xor_13_out;

  and ANDOP (out_133, in_47, in_56);
  and and_1 (out_132, in_46, in_55);
  and and_2 (out_131, in_45, in_54);
  and and_3 (out_130, in_44, in_53);
  xor Adder (Adder_out, in_13, in_21);
  xor xor_1 (xor_1_out, in_12, in_20);
  xor xor_2 (xor_2_out, in_11, in_19);
  xor xor_3 (xor_3_out, in_10, in_18);
  xor xor_4 (out_99, in_5, Adder_out);
  and and_4 (and_4_out, in_5, Adder_out);
  and and_5 (and_5_out, in_13, in_21);
  xor xor_5 (out_98, or_1_out, xor_1_out);
  and and_6 (and_6_out, or_1_out, xor_1_out);
  and and_7 (and_7_out, in_12, in_20);
  xor xor_6 (out_97, or_2_out, xor_2_out);
  and and_8 (and_8_out, or_2_out, xor_2_out);
  and and_9 (and_9_out, in_11, in_19);
  xor xor_7 (out_96, or_3_out, xor_3_out);
  and and_10 (and_10_out, or_3_out, xor_3_out);
  and and_11 (and_11_out, in_10, in_18);
  or or_1 (or_1_out, and_4_out, and_5_out);
  or or_2 (or_2_out, and_6_out, and_7_out);
  or or_3 (or_3_out, and_8_out, and_9_out);
  or or_4 (out_95, and_10_out, and_11_out);
  or OROP (out_137, in_51, in_60);
  or or_5 (out_136, in_50, in_59);
  or or_6 (out_135, in_49, in_58);
  or or_7 (out_134, in_48, in_57);
  xor XOROP (out_141, in_65, in_69);
  xor xor_8 (out_140, in_64, in_68);
  xor xor_9 (out_139, in_63, in_67);
  xor xor_10 (out_138, in_62, in_66);
  not not_1 (out_147, in_87);
  not not_2 (out_146, in_86);
  not not_3 (out_145, in_85);
  not not_4 (out_144, in_84);
  not not_5 (not_5_out, in_8);
  not not_6 (not_6_out, in_7);
  not not_7 (not_7_out, in_6);
  not not_8 (not_8_out, in_9);
  xor xor_11 (xor_11_out, in_8, in_16);
  and and_12 (and_12_out, not_5_out, in_16);
  and and_13 (and_13_out, not_5_out, or_15_out);
  and and_14 (and_14_out, in_16, or_15_out);
  xor xor_12 (xor_12_out, in_7, in_15);
  and and_15 (and_15_out, not_6_out, in_15);
  and and_16 (and_16_out, not_6_out, or_12_out);
  and and_17 (and_17_out, in_15, or_12_out);
  xor xor_13 (xor_13_out, in_6, in_14);
  and and_18 (and_18_out, not_7_out, in_14);
  and and_19 (and_19_out, not_7_out, or_13_out);
  and and_20 (and_20_out, in_14, or_13_out);
  xor Subtractor (Subtractor_out, in_9, in_17);
  and and_21 (and_21_out, not_8_out, in_17);
  and and_22 (and_22_out, not_8_out, in_2);
  and and_23 (and_23_out, in_17, in_2);
  or or_8 (or_8_out, and_12_out, and_13_out);
  or or_9 (or_9_out, and_15_out, and_16_out);
  or or_10 (or_10_out, and_18_out, and_19_out);
  not not_9 (not_9_out, S2);
  or or_11 (or_11_out, and_21_out, and_22_out);
  xor xor_14 (out_92, xor_11_out, or_15_out);
  or or_12 (or_12_out, or_8_out, and_14_out);
  xor xor_15 (out_91, xor_12_out, or_12_out);
  or or_13 (or_13_out, or_9_out, and_17_out);
  xor xor_16 (out_90, xor_13_out, or_13_out);
  or or_14 (out_89, or_10_out, and_20_out);
  not not_10 (not_10_out, S1);
  xor xor_17 (out_93, Subtractor_out, in_2);
  or or_15 (or_15_out, or_11_out, and_23_out);
  not not_11 (not_11_out, S0);
  and and_24 (and_24_out, D0, not_11_out, not_10_out, not_9_out);
  and and_25 (and_25_out, D1, S0, not_10_out, not_9_out);
  and and_26 (and_26_out, D2, not_11_out, S1, not_9_out);
  and and_27 (and_27_out, D3, S0, S1, not_9_out);
  and and_28 (and_28_out, D4, not_11_out, not_10_out, S2);
  and and_29 (and_29_out, D5, S0, not_10_out, S2);
  and and_30 (and_30_out, D6, not_11_out, S1, S2);
  and and_31 (and_31_out, D7, S0, S1, S2);
  not not_12 (not_12_out, in_22);
  not not_13 (not_13_out, not_12_out);
  not not_14 (not_14_out, in_61);
  and and_32 (and_32_out, not_14_out, in_70);
  and and_33 (and_33_out, in_61, in_72);
  or MUX8x1 (out_149, and_24_out, and_25_out, and_26_out, and_27_out, and_28_out, and_29_out, and_30_out, and_31_out);
  not not_15 (not_15_out, in_3);
  nand nand_1 (nand_1_out, in_3, not_13_out);
  nand nand_2 (nand_2_out, not_13_out, not_15_out);
  or MUX2x1 (out_143, and_32_out, and_33_out);
  nand nand_3 (nand_3_out, nand_1_out, out_101);
  nand nand_4 (out_101, nand_3_out, nand_2_out);
  not not_16 (not_16_out, not_13_out);
  ALU alu_1 (
    .A_3(in_26), .A_2(in_27), .A_1(in_28), .A_0(in_29), .B_3(in_30), .B_2(in_31), .B_1(in_32), .B_0(in_33),
    .S2(in_35), .S1(in_36), .S0(in_37), .OVF(out_103), .N(out_104), .C(out_105), .Z(out_106), .O_3(out_108),
    .O_2(out_109), .O_1(out_110), .O_0(out_111));
  not not_17 (not_17_out, nand_3_out);
  nand nand_5 (nand_5_out, nand_3_out, not_16_out);
  nand nand_6 (nand_6_out, not_16_out, not_17_out);
  nand MASTERSLAVEDFF (out_94, nand_5_out, out_102);
  nand nand_7 (out_102, out_94, nand_6_out);
  not not_18 (not_18_out, WE);
  and and_34 (and_34_out, not_18_out, out_100);
  and and_35 (and_35_out, WE, D);
  or or_16 (or_16_out, and_34_out, and_35_out);
  not not_19 (not_19_out, in_1);
  Clock clock_1 (.out(clock_1_out));
  not not_20 (not_20_out, not_19_out);
  not not_21 (not_21_out, or_16_out);
  nand nand_8 (nand_8_out, or_16_out, not_20_out);
  nand nand_9 (nand_9_out, not_20_out, not_21_out);
  not not_22 (not_22_out, in_38);
  not not_23 (not_23_out, in_38);
  not not_24 (not_24_out, in_38);
  not not_25 (not_25_out, in_38);
  and and_36 (and_36_out, not_22_out, out_112);
  and and_37 (and_37_out, in_38, in_43);
  and and_38 (and_38_out, not_23_out, out_129);
  and and_39 (and_39_out, in_38, in_52);
  and and_40 (and_40_out, not_24_out, out_142);
  and and_41 (and_41_out, in_38, in_71);
  and and_42 (and_42_out, not_25_out, out_148);
  and and_43 (and_43_out, in_38, in_88);
  nand nand_10 (nand_10_out, nand_8_out, nand_11_out);
  nand nand_11 (nand_11_out, nand_10_out, nand_9_out);
  not not_26 (not_26_out, not_20_out);
  not not_27 (not_27_out, clock_1_out);
  or or_17 (or_17_out, and_36_out, and_37_out);
  not not_28 (not_28_out, clock_1_out);
  or or_18 (or_18_out, and_38_out, and_39_out);
  not not_29 (not_29_out, clock_1_out);
  or or_19 (or_19_out, and_40_out, and_41_out);
  not not_30 (not_30_out, clock_1_out);
  or or_20 (or_20_out, and_42_out, and_43_out);
  not not_31 (not_31_out, not_27_out);
  not not_32 (not_32_out, not_28_out);
  not not_33 (not_33_out, not_29_out);
  not not_34 (not_34_out, not_30_out);
  not not_35 (not_35_out, nand_10_out);
  not not_36 (not_36_out, or_17_out);
  not not_37 (not_37_out, or_18_out);
  not not_38 (not_38_out, or_19_out);
  not not_39 (not_39_out, or_20_out);
  nand nand_12 (nand_12_out, nand_10_out, not_26_out);
  nand nand_13 (nand_13_out, not_26_out, not_35_out);
  nand nand_14 (nand_14_out, or_17_out, not_31_out);
  nand nand_15 (nand_15_out, not_31_out, not_36_out);
  nand nand_16 (nand_16_out, or_18_out, not_32_out);
  nand nand_17 (nand_17_out, not_32_out, not_37_out);
  nand nand_18 (nand_18_out, or_19_out, not_33_out);
  nand nand_19 (nand_19_out, not_33_out, not_38_out);
  nand nand_20 (nand_20_out, or_20_out, not_34_out);
  nand nand_21 (nand_21_out, not_34_out, not_39_out);
  nand MSDFF_RETAINER_REG (out_100, nand_12_out, nand_22_out);
  nand nand_22 (nand_22_out, out_100, nand_13_out);
  nand nand_23 (nand_23_out, nand_14_out, nand_24_out);
  nand nand_24 (nand_24_out, nand_23_out, nand_15_out);
  nand nand_25 (nand_25_out, nand_16_out, nand_26_out);
  nand nand_26 (nand_26_out, nand_25_out, nand_17_out);
  nand nand_27 (nand_27_out, nand_18_out, nand_28_out);
  nand nand_28 (nand_28_out, nand_27_out, nand_19_out);
  nand nand_29 (nand_29_out, nand_20_out, nand_30_out);
  nand nand_30 (nand_30_out, nand_29_out, nand_21_out);
  not not_40 (not_40_out, not_31_out);
  not not_41 (not_41_out, not_32_out);
  not not_42 (not_42_out, not_33_out);
  not not_43 (not_43_out, not_34_out);
  not not_44 (not_44_out, nand_23_out);
  not not_45 (not_45_out, nand_25_out);
  not not_46 (not_46_out, nand_27_out);
  not not_47 (not_47_out, nand_29_out);
  nand nand_31 (nand_31_out, nand_23_out, not_40_out);
  nand nand_32 (nand_32_out, not_40_out, not_44_out);
  nand nand_33 (nand_33_out, nand_25_out, not_41_out);
  nand nand_34 (nand_34_out, not_41_out, not_45_out);
  nand nand_35 (nand_35_out, nand_27_out, not_42_out);
  nand nand_36 (nand_36_out, not_42_out, not_46_out);
  nand nand_37 (nand_37_out, nand_29_out, not_43_out);
  nand nand_38 (nand_38_out, not_43_out, not_47_out);
  nand REGISTER_4BIT (out_112, nand_31_out, nand_39_out);
  nand nand_39 (nand_39_out, out_112, nand_32_out);
  nand nand_40 (out_129, nand_33_out, nand_41_out);
  nand nand_41 (nand_41_out, out_129, nand_34_out);
  nand nand_42 (out_142, nand_35_out, nand_43_out);
  nand nand_43 (nand_43_out, out_142, nand_36_out);
  nand nand_44 (out_148, nand_37_out, nand_45_out);
  nand nand_45 (nand_45_out, out_148, nand_38_out);
  not not_48 (not_48_out, in_39);
  not not_49 (not_49_out, in_40);
  not not_50 (not_50_out, in_41);
  not not_51 (not_51_out, in_24);
  not not_52 (not_52_out, in_42);
  and and_44 (and_44_out, not_51_out, out_107);
  and and_45 (and_45_out, in_24, in_34);
  and DECORDER_4x16 (DEC_O0, not_52_out, not_50_out, not_49_out, not_48_out);
  and and_46 (DEC_O1, in_42, not_50_out, not_49_out, not_48_out);
  and and_47 (DEC_O2, not_52_out, in_41, not_49_out, not_48_out);
  and and_48 (DEC_O3, in_42, in_41, not_49_out, not_48_out);
  and and_49 (DEC_O4, not_52_out, not_50_out, in_40, not_48_out);
  and and_50 (DEC_O5, in_42, not_50_out, in_40, not_48_out);
  and and_51 (DEC_O6, not_52_out, in_41, in_40, not_48_out);
  and and_52 (DEC_O7, in_42, in_41, in_40, not_48_out);
  and and_53 (DEC_O8, not_52_out, not_50_out, not_49_out, in_39);
  and and_54 (DEC_O9, in_42, not_50_out, not_49_out, in_39);
  and and_55 (DEC_O10, not_52_out, in_41, not_49_out, in_39);
  and and_56 (DEC_O11, in_42, in_41, not_49_out, in_39);
  and and_57 (DEC_O12, not_52_out, not_50_out, in_40, in_39);
  and and_58 (DEC_O13, in_42, not_50_out, in_40, in_39);
  and and_59 (DEC_O14, not_52_out, in_41, in_40, in_39);
  and and_60 (DEC_O15, in_42, in_41, in_40, in_39);
  Clock clock_2 (.out(clock_2_out));
  or or_21 (or_21_out, and_44_out, and_45_out);
  not not_53 (not_53_out, HARD_RESET);
  and and_61 (and_61_out, not_53_out, or_21_out);
  and and_62 (and_62_out, HARD_RESET, 1'b0);
  not not_54 (not_54_out, clock_2_out);
  or or_22 (or_22_out, and_61_out, and_62_out);
  not not_55 (not_55_out, not_54_out);
  not not_56 (not_56_out, or_22_out);
  nand nand_46 (nand_46_out, or_22_out, not_55_out);
  nand nand_47 (nand_47_out, not_55_out, not_56_out);
  nand nand_48 (nand_48_out, nand_46_out, nand_49_out);
  nand nand_49 (nand_49_out, nand_48_out, nand_47_out);
  not not_57 (not_57_out, not_55_out);
  not not_58 (not_58_out, nand_48_out);
  nand nand_50 (nand_50_out, nand_48_out, not_57_out);
  nand nand_51 (nand_51_out, not_57_out, not_58_out);
  nand nand_52 (out_107, nand_50_out, nand_53_out);
  nand nand_53 (nand_53_out, out_107, nand_51_out);
endmodule

module ALU (
  input  A_3,
  input  A_2,
  input  A_1,
  input  A_0,
  input  B_3,
  input  B_2,
  input  B_1,
  input  B_0,
  input  S2,
  input  S1,
  input  S0,
  output OVF,
  output N,
  output C,
  output Z,
  output O_3,
  output O_2,
  output O_1,
  output O_0
);

  wire Adder_out, and_1_out, and_2_out, and_3_out, and_4_out, and_5_out, and_6_out, and_7_out, and_8_out,
       and_9_out, and_10_out, and_11_out, and_12_out, and_13_out, and_14_out, and_15_out, and_16_out,
       and_17_out, and_18_out, and_19_out, and_20_out, and_21_out, and_22_out, and_23_out, and_24_out,
       and_25_out, and_26_out, and_27_out, and_28_out, and_29_out, and_30_out, and_31_out, and_32_out,
       and_33_out, and_34_out, and_35_out, and_36_out, and_37_out, and_38_out, and_39_out, and_40_out,
       and_41_out, and_42_out, and_43_out, and_44_out, and_45_out, and_46_out, and_47_out, and_48_out,
       and_49_out, and_50_out, and_51_out, and_52_out, and_53_out, and_54_out, and_55_out, and_56_out,
       and_57_out, and_58_out, and_59_out, and_60_out, ANDOP_out, MUX2x1_out, not_1_out, not_2_out,
       not_3_out, not_4_out, not_5_out, not_6_out, not_7_out, not_8_out, not_9_out, not_10_out, not_11_out,
       not_12_out, not_13_out, not_14_out, not_15_out, not_16_out, not_17_out, not_18_out, not_19_out,
       not_20_out, not_21_out, not_22_out, or_1_out, or_2_out, or_3_out, or_4_out, or_5_out, or_6_out,
       or_7_out, or_8_out, or_9_out, or_10_out, or_11_out, or_12_out, or_13_out, or_14_out, or_15_out,
       or_19_out, or_20_out, OROP_out, Subtractor_out, xor_1_out, xor_2_out, xor_3_out, xor_4_out, xor_5_out,
       xor_6_out, xor_7_out, xor_8_out, xor_9_out, xor_10_out, xor_11_out, xor_12_out, xor_13_out,
       xor_14_out, xor_15_out, xor_16_out, xor_17_out, xor_18_out, xor_19_out, XOROP_out;

  not not_1 (not_1_out, A_0);
  not not_2 (not_2_out, A_1);
  not not_3 (not_3_out, A_2);
  not not_4 (not_4_out, A_3);
  xor Adder (Adder_out, A_0, B_0);
  xor xor_1 (xor_1_out, A_1, B_1);
  xor xor_2 (xor_2_out, A_2, B_2);
  xor xor_3 (xor_3_out, A_3, B_3);
  and and_1 (and_1_out, not_1_out, B_0);
  and and_2 (and_2_out, not_1_out, 1'b0);
  and and_3 (and_3_out, B_0, 1'b0);
  xor xor_4 (xor_4_out, A_1, B_1);
  and and_4 (and_4_out, not_2_out, B_1);
  and and_5 (and_5_out, not_2_out, or_8_out);
  and and_6 (and_6_out, B_1, or_8_out);
  xor xor_5 (xor_5_out, A_2, B_2);
  and and_7 (and_7_out, not_3_out, B_2);
  and and_8 (and_8_out, not_3_out, or_9_out);
  and and_9 (and_9_out, B_2, or_9_out);
  xor xor_6 (xor_6_out, A_3, B_3);
  and and_10 (and_10_out, not_4_out, B_3);
  and and_11 (and_11_out, not_4_out, or_10_out);
  and and_12 (and_12_out, B_3, or_10_out);
  xor Subtractor (Subtractor_out, A_0, B_0);
  or or_1 (or_1_out, and_1_out, and_2_out);
  or or_2 (or_2_out, and_4_out, and_5_out);
  or or_3 (or_3_out, and_7_out, and_8_out);
  or or_4 (or_4_out, and_10_out, and_11_out);
  and ANDOP (ANDOP_out, A_0, B_0);
  and and_13 (and_13_out, A_1, B_1);
  and and_14 (and_14_out, A_2, B_2);
  and and_15 (and_15_out, A_3, B_3);
  or OROP (OROP_out, A_0, B_0);
  or or_5 (or_5_out, A_1, B_1);
  or or_6 (or_6_out, A_2, B_2);
  or or_7 (or_7_out, A_3, B_3);
  xor XOROP (XOROP_out, A_0, B_0);
  xor xor_7 (xor_7_out, A_1, B_1);
  xor xor_8 (xor_8_out, A_2, B_2);
  xor xor_9 (xor_9_out, A_3, B_3);
  not not_5 (not_5_out, A_0);
  not not_6 (not_6_out, A_1);
  not not_7 (not_7_out, A_2);
  not not_8 (not_8_out, A_3);
  xor xor_10 (xor_10_out, 1'b0, Adder_out);
  and and_16 (and_16_out, 1'b0, Adder_out);
  and and_17 (and_17_out, A_0, B_0);
  xor xor_11 (xor_11_out, or_12_out, xor_1_out);
  and and_18 (and_18_out, or_12_out, xor_1_out);
  and and_19 (and_19_out, A_1, B_1);
  xor xor_12 (xor_12_out, or_13_out, xor_2_out);
  and and_20 (and_20_out, or_13_out, xor_2_out);
  and and_21 (and_21_out, A_2, B_2);
  xor xor_13 (xor_13_out, or_14_out, xor_3_out);
  and and_22 (and_22_out, or_14_out, xor_3_out);
  and and_23 (and_23_out, A_3, B_3);
  or or_8 (or_8_out, or_1_out, and_3_out);
  xor xor_14 (xor_14_out, xor_4_out, or_8_out);
  or or_9 (or_9_out, or_2_out, and_6_out);
  xor xor_15 (xor_15_out, xor_5_out, or_9_out);
  or or_10 (or_10_out, or_3_out, and_9_out);
  xor xor_16 (xor_16_out, xor_6_out, or_10_out);
  or or_11 (or_11_out, or_4_out, and_12_out);
  xor xor_17 (xor_17_out, Subtractor_out, 1'b0);
  or or_12 (or_12_out, and_16_out, and_17_out);
  or or_13 (or_13_out, and_18_out, and_19_out);
  or or_14 (or_14_out, and_20_out, and_21_out);
  or or_15 (or_15_out, and_22_out, and_23_out);
  xor xor_18 (xor_18_out, or_14_out, or_15_out);
  xor xor_19 (xor_19_out, or_10_out, or_11_out);
  not not_9 (not_9_out, S2);
  not not_10 (not_10_out, S2);
  not not_11 (not_11_out, S2);
  not not_12 (not_12_out, S2);
  not not_13 (not_13_out, S1);
  not not_14 (not_14_out, S1);
  not not_15 (not_15_out, S1);
  not not_16 (not_16_out, S1);
  not not_17 (not_17_out, S0);
  not not_18 (not_18_out, S0);
  not not_19 (not_19_out, S0);
  not not_20 (not_20_out, S0);
  and and_24 (and_24_out, xor_10_out, not_17_out, not_13_out, not_9_out);
  and and_25 (and_25_out, xor_17_out, S0, not_13_out, not_9_out);
  and and_26 (and_26_out, ANDOP_out, not_17_out, S1, not_9_out);
  and and_27 (and_27_out, OROP_out, S0, S1, not_9_out);
  and and_28 (and_28_out, XOROP_out, not_17_out, not_13_out, S2);
  and and_29 (and_29_out, not_5_out, S0, not_13_out, S2);
  and and_30 (and_30_out, xor_10_out, not_17_out, S1, S2);
  and and_31 (and_31_out, xor_17_out, S0, S1, S2);
  and and_32 (and_32_out, xor_11_out, not_18_out, not_14_out, not_10_out);
  and and_33 (and_33_out, xor_14_out, S0, not_14_out, not_10_out);
  and and_34 (and_34_out, and_13_out, not_18_out, S1, not_10_out);
  and and_35 (and_35_out, or_5_out, S0, S1, not_10_out);
  and and_36 (and_36_out, xor_7_out, not_18_out, not_14_out, S2);
  and and_37 (and_37_out, not_6_out, S0, not_14_out, S2);
  and and_38 (and_38_out, xor_11_out, not_18_out, S1, S2);
  and and_39 (and_39_out, xor_14_out, S0, S1, S2);
  and and_40 (and_40_out, xor_12_out, not_19_out, not_15_out, not_11_out);
  and and_41 (and_41_out, xor_15_out, S0, not_15_out, not_11_out);
  and and_42 (and_42_out, and_14_out, not_19_out, S1, not_11_out);
  and and_43 (and_43_out, or_6_out, S0, S1, not_11_out);
  and and_44 (and_44_out, xor_8_out, not_19_out, not_15_out, S2);
  and and_45 (and_45_out, not_7_out, S0, not_15_out, S2);
  and and_46 (and_46_out, xor_12_out, not_19_out, S1, S2);
  and and_47 (and_47_out, xor_15_out, S0, S1, S2);
  and and_48 (and_48_out, xor_13_out, not_20_out, not_16_out, not_12_out);
  and and_49 (and_49_out, xor_16_out, S0, not_16_out, not_12_out);
  and and_50 (and_50_out, and_15_out, not_20_out, S1, not_12_out);
  and and_51 (and_51_out, or_7_out, S0, S1, not_12_out);
  and and_52 (and_52_out, xor_9_out, not_20_out, not_16_out, S2);
  and and_53 (and_53_out, not_8_out, S0, not_16_out, S2);
  and and_54 (and_54_out, xor_13_out, not_20_out, S1, S2);
  and and_55 (and_55_out, xor_16_out, S0, S1, S2);
  and and_56 (and_56_out, not_13_out, not_9_out);
  or MUX8x1 (O_0, and_24_out, and_25_out, and_26_out, and_27_out, and_28_out, and_29_out, and_30_out, and_31_out);
  or or_16 (O_1, and_32_out, and_33_out, and_34_out, and_35_out, and_36_out, and_37_out, and_38_out, and_39_out);
  or or_17 (O_2, and_40_out, and_41_out, and_42_out, and_43_out, and_44_out, and_45_out, and_46_out, and_47_out);
  or or_18 (N, and_48_out, and_49_out, and_50_out, and_51_out, and_52_out, and_53_out, and_54_out, and_55_out);
  not not_21 (not_21_out, S0);
  not not_22 (not_22_out, S0);
  or or_19 (or_19_out, O_0, O_1, O_2, N);
  not not_23 (Z, or_19_out);
  and and_57 (and_57_out, not_21_out, xor_18_out);
  and and_58 (and_58_out, S0, xor_19_out);
  and and_59 (and_59_out, not_22_out, or_15_out);
  and and_60 (and_60_out, S0, or_11_out);
  or MUX2x1 (MUX2x1_out, and_57_out, and_58_out);
  or or_20 (or_20_out, and_59_out, and_60_out);
  and VALIDOPCODE (OVF, MUX2x1_out, and_56_out);
  and and_61 (C, or_20_out, and_56_out);

  assign O_3 = N;
endmodule

module ALU_ACC (
  input  A_3,
  input  A_2,
  input  A_1,
  input  A_0,
  input  B_3,
  input  B_2,
  input  B_1,
  input  B_0,
  input  HARD_RESET,
  input  CLK,
  input  WE,
  input  S2,
  input  S1,
  input  S0,
  output OVF,
  output N,
  output C,
  output Z,
  output O_3,
  output O_2,
  output O_1,
  output O_0,
  output ACC_D0,
  output ACC_D1,
  output ACC_D2,
  output ACC_D3
);

  wire Adder_out, and_1_out, and_2_out, and_3_out, and_4_out, and_5_out, and_6_out, and_7_out, and_8_out,
       and_9_out, and_10_out, and_11_out, and_12_out, and_13_out, and_14_out, and_15_out, and_16_out,
       and_17_out, and_18_out, and_19_out, and_20_out, and_21_out, and_22_out, and_23_out, and_24_out,
       and_25_out, and_26_out, and_27_out, and_28_out, and_29_out, and_30_out, and_31_out, and_32_out,
       and_33_out, and_34_out, and_35_out, and_36_out, and_37_out, and_38_out, and_39_out, and_40_out,
       and_41_out, and_42_out, and_43_out, and_44_out, and_45_out, and_46_out, and_47_out, and_48_out,
       and_49_out, and_50_out, and_51_out, and_52_out, and_53_out, and_54_out, and_55_out, and_56_out,
       and_57_out, and_58_out, and_59_out, and_60_out, and_62_out, and_63_out, and_64_out, and_65_out,
       and_66_out, and_67_out, and_68_out, and_69_out, and_70_out, and_71_out, and_72_out, and_73_out,
       and_74_out, and_75_out, and_76_out, and_77_out, ANDOP_out, MUX2x1_out, nand_1_out, nand_2_out,
       nand_3_out, nand_4_out, nand_5_out, nand_6_out, nand_7_out, nand_8_out, nand_9_out, nand_10_out,
       nand_11_out, nand_12_out, nand_13_out, nand_14_out, nand_15_out, nand_16_out, nand_17_out,
       nand_18_out, nand_19_out, nand_20_out, nand_21_out, nand_22_out, nand_23_out, nand_24_out,
       nand_26_out, nand_28_out, nand_30_out, nand_32_out, not_1_out, not_2_out, not_3_out, not_4_out,
       not_5_out, not_6_out, not_7_out, not_8_out, not_9_out, not_10_out, not_11_out, not_12_out, not_13_out,
       not_14_out, not_15_out, not_16_out, not_17_out, not_18_out, not_19_out, not_20_out, not_21_out,
       not_22_out, not_24_out, not_25_out, not_26_out, not_27_out, not_28_out, not_29_out, not_30_out,
       not_31_out, not_32_out, not_33_out, not_34_out, not_35_out, not_36_out, not_37_out, not_38_out,
       not_39_out, not_40_out, not_41_out, not_42_out, not_43_out, not_44_out, not_45_out, not_46_out,
       not_47_out, not_48_out, not_49_out, not_50_out, not_51_out, or_1_out, or_2_out, or_3_out, or_4_out,
       or_5_out, or_6_out, or_7_out, or_8_out, or_9_out, or_10_out, or_11_out, or_12_out, or_13_out,
       or_14_out, or_15_out, or_19_out, or_20_out, or_21_out, or_22_out, or_23_out, or_24_out, or_25_out,
       or_26_out, or_27_out, or_28_out, OROP_out, Subtractor_out, xor_1_out, xor_2_out, xor_3_out, xor_4_out,
       xor_5_out, xor_6_out, xor_7_out, xor_8_out, xor_9_out, xor_10_out, xor_11_out, xor_12_out, xor_13_out,
       xor_14_out, xor_15_out, xor_16_out, xor_17_out, xor_18_out, xor_19_out, XOROP_out;

  not not_1 (not_1_out, A_0);
  not not_2 (not_2_out, A_1);
  not not_3 (not_3_out, A_2);
  not not_4 (not_4_out, A_3);
  xor Adder (Adder_out, A_0, B_0);
  xor xor_1 (xor_1_out, A_1, B_1);
  xor xor_2 (xor_2_out, A_2, B_2);
  xor xor_3 (xor_3_out, A_3, B_3);
  and and_1 (and_1_out, not_1_out, B_0);
  and and_2 (and_2_out, not_1_out, 1'b0);
  and and_3 (and_3_out, B_0, 1'b0);
  xor xor_4 (xor_4_out, A_1, B_1);
  and and_4 (and_4_out, not_2_out, B_1);
  and and_5 (and_5_out, not_2_out, or_8_out);
  and and_6 (and_6_out, B_1, or_8_out);
  xor xor_5 (xor_5_out, A_2, B_2);
  and and_7 (and_7_out, not_3_out, B_2);
  and and_8 (and_8_out, not_3_out, or_9_out);
  and and_9 (and_9_out, B_2, or_9_out);
  xor xor_6 (xor_6_out, A_3, B_3);
  and and_10 (and_10_out, not_4_out, B_3);
  and and_11 (and_11_out, not_4_out, or_10_out);
  and and_12 (and_12_out, B_3, or_10_out);
  xor Subtractor (Subtractor_out, A_0, B_0);
  or or_1 (or_1_out, and_1_out, and_2_out);
  or or_2 (or_2_out, and_4_out, and_5_out);
  or or_3 (or_3_out, and_7_out, and_8_out);
  or or_4 (or_4_out, and_10_out, and_11_out);
  and ANDOP (ANDOP_out, A_0, B_0);
  and and_13 (and_13_out, A_1, B_1);
  and and_14 (and_14_out, A_2, B_2);
  and and_15 (and_15_out, A_3, B_3);
  or OROP (OROP_out, A_0, B_0);
  or or_5 (or_5_out, A_1, B_1);
  or or_6 (or_6_out, A_2, B_2);
  or or_7 (or_7_out, A_3, B_3);
  xor XOROP (XOROP_out, A_0, B_0);
  xor xor_7 (xor_7_out, A_1, B_1);
  xor xor_8 (xor_8_out, A_2, B_2);
  xor xor_9 (xor_9_out, A_3, B_3);
  not not_5 (not_5_out, A_0);
  not not_6 (not_6_out, A_1);
  not not_7 (not_7_out, A_2);
  not not_8 (not_8_out, A_3);
  xor xor_10 (xor_10_out, 1'b0, Adder_out);
  and and_16 (and_16_out, 1'b0, Adder_out);
  and and_17 (and_17_out, A_0, B_0);
  xor xor_11 (xor_11_out, or_12_out, xor_1_out);
  and and_18 (and_18_out, or_12_out, xor_1_out);
  and and_19 (and_19_out, A_1, B_1);
  xor xor_12 (xor_12_out, or_13_out, xor_2_out);
  and and_20 (and_20_out, or_13_out, xor_2_out);
  and and_21 (and_21_out, A_2, B_2);
  xor xor_13 (xor_13_out, or_14_out, xor_3_out);
  and and_22 (and_22_out, or_14_out, xor_3_out);
  and and_23 (and_23_out, A_3, B_3);
  or or_8 (or_8_out, or_1_out, and_3_out);
  xor xor_14 (xor_14_out, xor_4_out, or_8_out);
  or or_9 (or_9_out, or_2_out, and_6_out);
  xor xor_15 (xor_15_out, xor_5_out, or_9_out);
  or or_10 (or_10_out, or_3_out, and_9_out);
  xor xor_16 (xor_16_out, xor_6_out, or_10_out);
  or or_11 (or_11_out, or_4_out, and_12_out);
  xor xor_17 (xor_17_out, Subtractor_out, 1'b0);
  or or_12 (or_12_out, and_16_out, and_17_out);
  or or_13 (or_13_out, and_18_out, and_19_out);
  or or_14 (or_14_out, and_20_out, and_21_out);
  or or_15 (or_15_out, and_22_out, and_23_out);
  xor xor_18 (xor_18_out, or_14_out, or_15_out);
  xor xor_19 (xor_19_out, or_10_out, or_11_out);
  not not_9 (not_9_out, S2);
  not not_10 (not_10_out, S2);
  not not_11 (not_11_out, S2);
  not not_12 (not_12_out, S2);
  not not_13 (not_13_out, S1);
  not not_14 (not_14_out, S1);
  not not_15 (not_15_out, S1);
  not not_16 (not_16_out, S1);
  not not_17 (not_17_out, S0);
  not not_18 (not_18_out, S0);
  not not_19 (not_19_out, S0);
  not not_20 (not_20_out, S0);
  and and_24 (and_24_out, xor_10_out, not_17_out, not_13_out, not_9_out);
  and and_25 (and_25_out, xor_17_out, S0, not_13_out, not_9_out);
  and and_26 (and_26_out, ANDOP_out, not_17_out, S1, not_9_out);
  and and_27 (and_27_out, OROP_out, S0, S1, not_9_out);
  and and_28 (and_28_out, XOROP_out, not_17_out, not_13_out, S2);
  and and_29 (and_29_out, not_5_out, S0, not_13_out, S2);
  and and_30 (and_30_out, xor_10_out, not_17_out, S1, S2);
  and and_31 (and_31_out, xor_17_out, S0, S1, S2);
  and and_32 (and_32_out, xor_11_out, not_18_out, not_14_out, not_10_out);
  and and_33 (and_33_out, xor_14_out, S0, not_14_out, not_10_out);
  and and_34 (and_34_out, and_13_out, not_18_out, S1, not_10_out);
  and and_35 (and_35_out, or_5_out, S0, S1, not_10_out);
  and and_36 (and_36_out, xor_7_out, not_18_out, not_14_out, S2);
  and and_37 (and_37_out, not_6_out, S0, not_14_out, S2);
  and and_38 (and_38_out, xor_11_out, not_18_out, S1, S2);
  and and_39 (and_39_out, xor_14_out, S0, S1, S2);
  and and_40 (and_40_out, xor_12_out, not_19_out, not_15_out, not_11_out);
  and and_41 (and_41_out, xor_15_out, S0, not_15_out, not_11_out);
  and and_42 (and_42_out, and_14_out, not_19_out, S1, not_11_out);
  and and_43 (and_43_out, or_6_out, S0, S1, not_11_out);
  and and_44 (and_44_out, xor_8_out, not_19_out, not_15_out, S2);
  and and_45 (and_45_out, not_7_out, S0, not_15_out, S2);
  and and_46 (and_46_out, xor_12_out, not_19_out, S1, S2);
  and and_47 (and_47_out, xor_15_out, S0, S1, S2);
  and and_48 (and_48_out, xor_13_out, not_20_out, not_16_out, not_12_out);
  and and_49 (and_49_out, xor_16_out, S0, not_16_out, not_12_out);
  and and_50 (and_50_out, and_15_out, not_20_out, S1, not_12_out);
  and and_51 (and_51_out, or_7_out, S0, S1, not_12_out);
  and and_52 (and_52_out, xor_9_out, not_20_out, not_16_out, S2);
  and and_53 (and_53_out, not_8_out, S0, not_16_out, S2);
  and and_54 (and_54_out, xor_13_out, not_20_out, S1, S2);
  and and_55 (and_55_out, xor_16_out, S0, S1, S2);
  and and_56 (and_56_out, not_13_out, not_9_out);
  or MUX8x1 (O_0, and_24_out, and_25_out, and_26_out, and_27_out, and_28_out, and_29_out, and_30_out, and_31_out);
  or or_16 (O_1, and_32_out, and_33_out, and_34_out, and_35_out, and_36_out, and_37_out, and_38_out, and_39_out);
  or or_17 (O_2, and_40_out, and_41_out, and_42_out, and_43_out, and_44_out, and_45_out, and_46_out, and_47_out);
  or or_18 (N, and_48_out, and_49_out, and_50_out, and_51_out, and_52_out, and_53_out, and_54_out, and_55_out);
  not not_21 (not_21_out, S0);
  not not_22 (not_22_out, S0);
  or or_19 (or_19_out, O_0, O_1, O_2, N);
  not not_23 (Z, or_19_out);
  and and_57 (and_57_out, not_21_out, xor_18_out);
  and and_58 (and_58_out, S0, xor_19_out);
  and and_59 (and_59_out, not_22_out, or_15_out);
  and and_60 (and_60_out, S0, or_11_out);
  or MUX2x1 (MUX2x1_out, and_57_out, and_58_out);
  or or_20 (or_20_out, and_59_out, and_60_out);
  and VALIDOPCODE (OVF, MUX2x1_out, and_56_out);
  and and_61 (C, or_20_out, and_56_out);
  not not_24 (not_24_out, WE);
  not not_25 (not_25_out, WE);
  not not_26 (not_26_out, WE);
  not not_27 (not_27_out, WE);
  and and_62 (and_62_out, not_24_out, ACC_D0);
  and and_63 (and_63_out, WE, O_0);
  and and_64 (and_64_out, not_25_out, ACC_D1);
  and and_65 (and_65_out, WE, O_1);
  and and_66 (and_66_out, not_26_out, ACC_D2);
  and and_67 (and_67_out, WE, O_2);
  and and_68 (and_68_out, not_27_out, ACC_D3);
  and and_69 (and_69_out, WE, N);
  or or_21 (or_21_out, and_62_out, and_63_out);
  or or_22 (or_22_out, and_64_out, and_65_out);
  or or_23 (or_23_out, and_66_out, and_67_out);
  or or_24 (or_24_out, and_68_out, and_69_out);
  not not_28 (not_28_out, HARD_RESET);
  not not_29 (not_29_out, HARD_RESET);
  not not_30 (not_30_out, HARD_RESET);
  not not_31 (not_31_out, HARD_RESET);
  and and_70 (and_70_out, not_28_out, or_21_out);
  and and_71 (and_71_out, HARD_RESET, 1'b0);
  and and_72 (and_72_out, not_29_out, or_22_out);
  and and_73 (and_73_out, HARD_RESET, 1'b0);
  and and_74 (and_74_out, not_30_out, or_23_out);
  and and_75 (and_75_out, HARD_RESET, 1'b0);
  and and_76 (and_76_out, not_31_out, or_24_out);
  and and_77 (and_77_out, HARD_RESET, 1'b0);
  or or_25 (or_25_out, and_70_out, and_71_out);
  or or_26 (or_26_out, and_72_out, and_73_out);
  or or_27 (or_27_out, and_74_out, and_75_out);
  or or_28 (or_28_out, and_76_out, and_77_out);
  not not_32 (not_32_out, CLK);
  not not_33 (not_33_out, CLK);
  not not_34 (not_34_out, CLK);
  not not_35 (not_35_out, CLK);
  not not_36 (not_36_out, not_32_out);
  not not_37 (not_37_out, not_33_out);
  not not_38 (not_38_out, not_34_out);
  not not_39 (not_39_out, not_35_out);
  not not_40 (not_40_out, or_25_out);
  not not_41 (not_41_out, or_26_out);
  not not_42 (not_42_out, or_27_out);
  not not_43 (not_43_out, or_28_out);
  nand nand_1 (nand_1_out, or_25_out, not_36_out);
  nand nand_2 (nand_2_out, not_36_out, not_40_out);
  nand nand_3 (nand_3_out, or_26_out, not_37_out);
  nand nand_4 (nand_4_out, not_37_out, not_41_out);
  nand nand_5 (nand_5_out, or_27_out, not_38_out);
  nand nand_6 (nand_6_out, not_38_out, not_42_out);
  nand nand_7 (nand_7_out, or_28_out, not_39_out);
  nand nand_8 (nand_8_out, not_39_out, not_43_out);
  nand nand_9 (nand_9_out, nand_1_out, nand_10_out);
  nand nand_10 (nand_10_out, nand_9_out, nand_2_out);
  nand nand_11 (nand_11_out, nand_3_out, nand_12_out);
  nand nand_12 (nand_12_out, nand_11_out, nand_4_out);
  nand nand_13 (nand_13_out, nand_5_out, nand_14_out);
  nand nand_14 (nand_14_out, nand_13_out, nand_6_out);
  nand nand_15 (nand_15_out, nand_7_out, nand_16_out);
  nand nand_16 (nand_16_out, nand_15_out, nand_8_out);
  not not_44 (not_44_out, not_36_out);
  not not_45 (not_45_out, not_37_out);
  not not_46 (not_46_out, not_38_out);
  not not_47 (not_47_out, not_39_out);
  not not_48 (not_48_out, nand_9_out);
  not not_49 (not_49_out, nand_11_out);
  not not_50 (not_50_out, nand_13_out);
  not not_51 (not_51_out, nand_15_out);
  nand nand_17 (nand_17_out, nand_9_out, not_44_out);
  nand nand_18 (nand_18_out, not_44_out, not_48_out);
  nand nand_19 (nand_19_out, nand_11_out, not_45_out);
  nand nand_20 (nand_20_out, not_45_out, not_49_out);
  nand nand_21 (nand_21_out, nand_13_out, not_46_out);
  nand nand_22 (nand_22_out, not_46_out, not_50_out);
  nand nand_23 (nand_23_out, nand_15_out, not_47_out);
  nand nand_24 (nand_24_out, not_47_out, not_51_out);
  nand nand_25 (ACC_D0, nand_17_out, nand_26_out);
  nand nand_26 (nand_26_out, ACC_D0, nand_18_out);
  nand nand_27 (ACC_D1, nand_19_out, nand_28_out);
  nand nand_28 (nand_28_out, ACC_D1, nand_20_out);
  nand nand_29 (ACC_D2, nand_21_out, nand_30_out);
  nand nand_30 (nand_30_out, ACC_D2, nand_22_out);
  nand nand_31 (ACC_D3, nand_23_out, nand_32_out);
  nand nand_32 (nand_32_out, ACC_D3, nand_24_out);

  assign O_3 = N;
endmodule

module ProgCounter (
  input  HARD_RESET,
  input  CLK,
  output PCO3,
  output PCO2,
  output PCO1,
  output PCO0
);

  wire Adder_out, and_1_out, and_2_out, and_3_out, and_4_out, and_5_out, and_6_out, and_7_out, and_8_out,
       and_9_out, and_10_out, and_11_out, and_12_out, and_13_out, and_14_out, and_15_out, and_16_out,
       and_17_out, and_18_out, and_19_out, and_20_out, and_21_out, and_22_out, and_23_out, and_24_out,
       nand_1_out, nand_2_out, nand_3_out, nand_4_out, nand_5_out, nand_6_out, nand_7_out, nand_8_out,
       nand_9_out, nand_10_out, nand_11_out, nand_12_out, nand_13_out, nand_14_out, nand_15_out, nand_16_out,
       nand_17_out, nand_18_out, nand_19_out, nand_20_out, nand_21_out, nand_22_out, nand_23_out,
       nand_24_out, nand_26_out, nand_28_out, nand_30_out, nand_32_out, not_1_out, not_2_out, not_3_out,
       not_4_out, not_5_out, not_6_out, not_7_out, not_8_out, not_9_out, not_10_out, not_11_out, not_12_out,
       not_13_out, not_14_out, not_15_out, not_16_out, not_17_out, not_18_out, not_19_out, not_20_out,
       not_21_out, not_22_out, not_23_out, not_24_out, not_25_out, not_26_out, not_27_out, not_28_out,
       or_1_out, or_2_out, or_3_out, or_5_out, or_6_out, or_7_out, or_8_out, or_9_out, or_10_out, or_11_out,
       or_12_out, xor_1_out, xor_2_out, xor_3_out, xor_4_out, xor_5_out, xor_6_out, xor_7_out;

  xor Adder (Adder_out, PCO0, 1'b1);
  xor xor_1 (xor_1_out, PCO1, 1'b0);
  xor xor_2 (xor_2_out, PCO2, 1'b0);
  xor xor_3 (xor_3_out, PCO3, 1'b0);
  xor xor_4 (xor_4_out, 1'b0, Adder_out);
  and and_1 (and_1_out, 1'b0, Adder_out);
  and and_2 (and_2_out, PCO0, 1'b1);
  xor xor_5 (xor_5_out, or_1_out, xor_1_out);
  and and_3 (and_3_out, or_1_out, xor_1_out);
  and and_4 (and_4_out, PCO1, 1'b0);
  xor xor_6 (xor_6_out, or_2_out, xor_2_out);
  and and_5 (and_5_out, or_2_out, xor_2_out);
  and and_6 (and_6_out, PCO2, 1'b0);
  xor xor_7 (xor_7_out, or_3_out, xor_3_out);
  and and_7 (and_7_out, or_3_out, xor_3_out);
  and and_8 (and_8_out, PCO3, 1'b0);
  or or_1 (or_1_out, and_1_out, and_2_out);
  or or_2 (or_2_out, and_3_out, and_4_out);
  or or_3 (or_3_out, and_5_out, and_6_out);
  // OR_Gate or_4 has open pins: in0=and_7_out, in1=and_8_out, out=open
  not not_1 (not_1_out, 1'b1);
  not not_2 (not_2_out, 1'b1);
  not not_3 (not_3_out, 1'b1);
  not not_4 (not_4_out, 1'b1);
  and and_9 (and_9_out, not_1_out, PCO0);
  and and_10 (and_10_out, 1'b1, xor_4_out);
  and and_11 (and_11_out, not_2_out, PCO1);
  and and_12 (and_12_out, 1'b1, xor_5_out);
  and and_13 (and_13_out, not_3_out, PCO2);
  and and_14 (and_14_out, 1'b1, xor_6_out);
  and and_15 (and_15_out, not_4_out, PCO3);
  and and_16 (and_16_out, 1'b1, xor_7_out);
  or or_5 (or_5_out, and_9_out, and_10_out);
  or or_6 (or_6_out, and_11_out, and_12_out);
  or or_7 (or_7_out, and_13_out, and_14_out);
  or or_8 (or_8_out, and_15_out, and_16_out);
  not not_5 (not_5_out, HARD_RESET);
  not not_6 (not_6_out, HARD_RESET);
  not not_7 (not_7_out, HARD_RESET);
  not not_8 (not_8_out, HARD_RESET);
  and and_17 (and_17_out, not_5_out, or_5_out);
  and and_18 (and_18_out, HARD_RESET, 1'b0);
  and and_19 (and_19_out, not_6_out, or_6_out);
  and and_20 (and_20_out, HARD_RESET, 1'b0);
  and and_21 (and_21_out, not_7_out, or_7_out);
  and and_22 (and_22_out, HARD_RESET, 1'b0);
  and and_23 (and_23_out, not_8_out, or_8_out);
  and and_24 (and_24_out, HARD_RESET, 1'b0);
  not not_9 (not_9_out, CLK);
  or or_9 (or_9_out, and_17_out, and_18_out);
  not not_10 (not_10_out, CLK);
  or or_10 (or_10_out, and_19_out, and_20_out);
  not not_11 (not_11_out, CLK);
  or or_11 (or_11_out, and_21_out, and_22_out);
  not not_12 (not_12_out, CLK);
  or or_12 (or_12_out, and_23_out, and_24_out);
  not not_13 (not_13_out, not_9_out);
  not not_14 (not_14_out, not_10_out);
  not not_15 (not_15_out, not_11_out);
  not not_16 (not_16_out, not_12_out);
  not not_17 (not_17_out, or_9_out);
  not not_18 (not_18_out, or_10_out);
  not not_19 (not_19_out, or_11_out);
  not not_20 (not_20_out, or_12_out);
  nand nand_1 (nand_1_out, or_9_out, not_13_out);
  nand nand_2 (nand_2_out, not_13_out, not_17_out);
  nand nand_3 (nand_3_out, or_10_out, not_14_out);
  nand nand_4 (nand_4_out, not_14_out, not_18_out);
  nand nand_5 (nand_5_out, or_11_out, not_15_out);
  nand nand_6 (nand_6_out, not_15_out, not_19_out);
  nand nand_7 (nand_7_out, or_12_out, not_16_out);
  nand nand_8 (nand_8_out, not_16_out, not_20_out);
  nand nand_9 (nand_9_out, nand_1_out, nand_10_out);
  nand nand_10 (nand_10_out, nand_9_out, nand_2_out);
  nand nand_11 (nand_11_out, nand_3_out, nand_12_out);
  nand nand_12 (nand_12_out, nand_11_out, nand_4_out);
  nand nand_13 (nand_13_out, nand_5_out, nand_14_out);
  nand nand_14 (nand_14_out, nand_13_out, nand_6_out);
  nand nand_15 (nand_15_out, nand_7_out, nand_16_out);
  nand nand_16 (nand_16_out, nand_15_out, nand_8_out);
  not not_21 (not_21_out, not_13_out);
  not not_22 (not_22_out, not_14_out);
  not not_23 (not_23_out, not_15_out);
  not not_24 (not_24_out, not_16_out);
  not not_25 (not_25_out, nand_9_out);
  not not_26 (not_26_out, nand_11_out);
  not not_27 (not_27_out, nand_13_out);
  not not_28 (not_28_out, nand_15_out);
  nand nand_17 (nand_17_out, nand_9_out, not_21_out);
  nand nand_18 (nand_18_out, not_21_out, not_25_out);
  nand nand_19 (nand_19_out, nand_11_out, not_22_out);
  nand nand_20 (nand_20_out, not_22_out, not_26_out);
  nand nand_21 (nand_21_out, nand_13_out, not_23_out);
  nand nand_22 (nand_22_out, not_23_out, not_27_out);
  nand nand_23 (nand_23_out, nand_15_out, not_24_out);
  nand nand_24 (nand_24_out, not_24_out, not_28_out);
  nand nand_25 (PCO0, nand_17_out, nand_26_out);
  nand nand_26 (nand_26_out, PCO0, nand_18_out);
  nand nand_27 (PCO1, nand_19_out, nand_28_out);
  nand nand_28 (nand_28_out, PCO1, nand_20_out);
  nand nand_29 (PCO2, nand_21_out, nand_30_out);
  nand nand_30 (nand_30_out, PCO2, nand_22_out);
  nand nand_31 (PCO3, nand_23_out, nand_32_out);
  nand nand_32 (nand_32_out, PCO3, nand_24_out);
endmodule

module ROMCIRC (
  input  ROMI3,
  input  ROMI2,
  input  ROMI1,
  input  ROMI0,
  output OPC3,
  output OPC2,
  output OPC1,
  output OPC0,
  output OPRAND3,
  output OPRAND2,
  output OPRAND1,
  output OPRAND0
);

  wire and_1_out, and_2_out, and_3_out, and_4_out, and_5_out, and_6_out, and_7_out, and_8_out, and_9_out,
       and_10_out, and_11_out, and_12_out, and_13_out, and_14_out, and_15_out, and_16_out, and_17_out,
       and_18_out, and_19_out, and_20_out, and_21_out, and_22_out, and_23_out, and_24_out, and_25_out,
       and_26_out, and_27_out, and_28_out, and_29_out, and_30_out, and_31_out, and_32_out, and_33_out,
       and_34_out, and_35_out, and_36_out, and_37_out, and_38_out, and_39_out, and_40_out, and_41_out,
       and_42_out, and_43_out, and_44_out, and_45_out, and_46_out, and_47_out, and_48_out, and_49_out,
       and_50_out, and_51_out, and_52_out, and_53_out, and_54_out, and_55_out, and_56_out, and_57_out,
       and_58_out, and_59_out, and_60_out, and_61_out, and_62_out, and_63_out, and_64_out, and_65_out,
       and_66_out, and_67_out, and_68_out, and_69_out, and_70_out, and_71_out, and_72_out, and_73_out,
       and_74_out, and_75_out, and_76_out, and_77_out, and_78_out, and_79_out, and_80_out, and_81_out,
       and_82_out, and_83_out, and_84_out, and_85_out, and_86_out, and_87_out, and_88_out, and_89_out,
       and_90_out, and_91_out, and_92_out, and_93_out, and_94_out, and_95_out, and_96_out, and_97_out,
       and_98_out, and_99_out, and_100_out, and_101_out, and_102_out, and_103_out, and_104_out, and_105_out,
       and_106_out, and_107_out, and_108_out, and_109_out, and_110_out, and_111_out, and_112_out,
       and_113_out, and_114_out, and_115_out, and_116_out, and_117_out, and_118_out, and_119_out,
       and_120_out, and_121_out, and_122_out, and_123_out, and_124_out, and_125_out, and_126_out,
       and_127_out, and_128_out, and_129_out, and_130_out, and_131_out, and_132_out, and_133_out,
       and_134_out, and_135_out, and_136_out, and_137_out, and_138_out, and_139_out, and_140_out,
       and_141_out, and_142_out, and_143_out, DECORDER_4x16_out, not_1_out, not_2_out, not_3_out, not_4_out,
       or_1_out, or_3_out, or_4_out, or_6_out, or_7_out, or_8_out, or_10_out, or_11_out, or_13_out,
       or_15_out, or_16_out, or_18_out, or_19_out, or_21_out, or_22_out, or_24_out;

  not not_1 (not_1_out, ROMI3);
  not not_2 (not_2_out, ROMI2);
  not not_3 (not_3_out, ROMI1);
  not not_4 (not_4_out, ROMI0);
  and DECORDER_4x16 (DECORDER_4x16_out, not_4_out, not_3_out, not_2_out, not_1_out);
  and and_1 (and_1_out, ROMI0, not_3_out, not_2_out, not_1_out);
  and and_2 (and_2_out, not_4_out, ROMI1, not_2_out, not_1_out);
  and and_3 (and_3_out, ROMI0, ROMI1, not_2_out, not_1_out);
  and and_4 (and_4_out, not_4_out, not_3_out, ROMI2, not_1_out);
  and and_5 (and_5_out, ROMI0, not_3_out, ROMI2, not_1_out);
  and and_6 (and_6_out, not_4_out, ROMI1, ROMI2, not_1_out);
  and and_7 (and_7_out, ROMI0, ROMI1, ROMI2, not_1_out);
  and and_8 (and_8_out, not_4_out, not_3_out, not_2_out, ROMI3);
  and and_9 (and_9_out, ROMI0, not_3_out, not_2_out, ROMI3);
  and and_10 (and_10_out, not_4_out, ROMI1, not_2_out, ROMI3);
  and and_11 (and_11_out, ROMI0, ROMI1, not_2_out, ROMI3);
  and and_12 (and_12_out, not_4_out, not_3_out, ROMI2, ROMI3);
  and and_13 (and_13_out, ROMI0, not_3_out, ROMI2, ROMI3);
  and and_14 (and_14_out, not_4_out, ROMI1, ROMI2, ROMI3);
  and and_15 (and_15_out, ROMI0, ROMI1, ROMI2, ROMI3);
  or or_1 (or_1_out, and_31_out, and_30_out, and_29_out, and_28_out, and_27_out, and_26_out, and_25_out, and_24_out);
  and and_16 (and_16_out, DECORDER_4x16_out, 1'b0);
  and and_17 (and_17_out, and_1_out, 1'b0);
  and and_18 (and_18_out, and_2_out, 1'b0);
  and and_19 (and_19_out, and_3_out, 1'b0);
  and and_20 (and_20_out, and_4_out, 1'b0);
  and and_21 (and_21_out, and_5_out, 1'b0);
  and and_22 (and_22_out, and_6_out, 1'b0);
  and and_23 (and_23_out, and_7_out, 1'b0);
  and and_24 (and_24_out, and_8_out, 1'b0);
  and and_25 (and_25_out, and_9_out, 1'b0);
  and and_26 (and_26_out, and_10_out, 1'b0);
  and and_27 (and_27_out, and_11_out, 1'b0);
  and and_28 (and_28_out, and_12_out, 1'b0);
  and and_29 (and_29_out, and_13_out, 1'b0);
  and and_30 (and_30_out, and_14_out, 1'b0);
  and and_31 (and_31_out, and_15_out, 1'b0);
  or or_2 (OPC3, or_1_out, or_3_out);
  or or_3 (or_3_out, and_16_out, and_17_out, and_18_out, and_19_out, and_20_out, and_21_out, and_22_out, and_23_out);
  or or_4 (or_4_out, and_47_out, and_46_out, and_45_out, and_44_out, and_43_out, and_42_out, and_41_out, and_40_out);
  and and_32 (and_32_out, DECORDER_4x16_out, 1'b0);
  and and_33 (and_33_out, and_1_out, 1'b0);
  and and_34 (and_34_out, and_2_out, 1'b1);
  and and_35 (and_35_out, and_3_out, 1'b0);
  and and_36 (and_36_out, and_4_out, 1'b1);
  and and_37 (and_37_out, and_5_out, 1'b1);
  and and_38 (and_38_out, and_6_out, 1'b1);
  and and_39 (and_39_out, and_7_out, 1'b0);
  and and_40 (and_40_out, and_8_out, 1'b0);
  and and_41 (and_41_out, and_9_out, 1'b0);
  and and_42 (and_42_out, and_10_out, 1'b0);
  and and_43 (and_43_out, and_11_out, 1'b0);
  and and_44 (and_44_out, and_12_out, 1'b0);
  and and_45 (and_45_out, and_13_out, 1'b0);
  and and_46 (and_46_out, and_14_out, 1'b0);
  and and_47 (and_47_out, and_15_out, 1'b0);
  or or_5 (OPC2, or_4_out, or_6_out);
  or or_6 (or_6_out, and_32_out, and_33_out, and_34_out, and_35_out, and_36_out, and_37_out, and_38_out, and_39_out);
  and and_48 (and_48_out, DECORDER_4x16_out, 1'b0);
  and and_49 (and_49_out, and_1_out, 1'b0);
  and and_50 (and_50_out, and_2_out, 1'b0);
  and and_51 (and_51_out, and_3_out, 1'b0);
  and and_52 (and_52_out, and_4_out, 1'b1);
  and and_53 (and_53_out, and_5_out, 1'b1);
  and and_54 (and_54_out, and_6_out, 1'b0);
  and and_55 (and_55_out, and_7_out, 1'b0);
  and and_56 (and_56_out, and_8_out, 1'b0);
  and and_57 (and_57_out, and_9_out, 1'b0);
  and and_58 (and_58_out, and_10_out, 1'b0);
  and and_59 (and_59_out, and_11_out, 1'b0);
  and and_60 (and_60_out, and_12_out, 1'b0);
  and and_61 (and_61_out, and_13_out, 1'b0);
  and and_62 (and_62_out, and_14_out, 1'b0);
  and and_63 (and_63_out, and_15_out, 1'b0);
  or or_7 (or_7_out, and_63_out, and_62_out, and_61_out, and_60_out, and_59_out, and_58_out, and_57_out, and_56_out);
  or or_8 (or_8_out, and_48_out, and_49_out, and_50_out, and_51_out, and_52_out, and_53_out, and_54_out, and_55_out);
  or or_9 (OPC1, or_7_out, or_8_out);
  or or_10 (or_10_out, and_79_out, and_78_out, and_77_out, and_76_out, and_75_out, and_74_out, and_73_out, and_72_out);
  and and_64 (and_64_out, DECORDER_4x16_out, 1'b0);
  and and_65 (and_65_out, and_1_out, 1'b0);
  and and_66 (and_66_out, and_2_out, 1'b0);
  and and_67 (and_67_out, and_3_out, 1'b1);
  and and_68 (and_68_out, and_4_out, 1'b0);
  and and_69 (and_69_out, and_5_out, 1'b1);
  and and_70 (and_70_out, and_6_out, 1'b1);
  and and_71 (and_71_out, and_7_out, 1'b0);
  and and_72 (and_72_out, and_8_out, 1'b0);
  and and_73 (and_73_out, and_9_out, 1'b0);
  and and_74 (and_74_out, and_10_out, 1'b0);
  and and_75 (and_75_out, and_11_out, 1'b0);
  and and_76 (and_76_out, and_12_out, 1'b0);
  and and_77 (and_77_out, and_13_out, 1'b0);
  and and_78 (and_78_out, and_14_out, 1'b0);
  and and_79 (and_79_out, and_15_out, 1'b0);
  or or_11 (or_11_out, and_64_out, and_65_out, and_66_out, and_67_out, and_68_out, and_69_out, and_70_out, and_71_out);
  or or_12 (OPC0, or_10_out, or_11_out);
  or or_13 (or_13_out, and_95_out, and_94_out, and_93_out, and_92_out, and_91_out, and_90_out, and_89_out, and_88_out);
  and and_80 (and_80_out, DECORDER_4x16_out, 1'b0);
  and and_81 (and_81_out, and_1_out, 1'b0);
  and and_82 (and_82_out, and_2_out, 1'b0);
  and and_83 (and_83_out, and_3_out, 1'b0);
  and and_84 (and_84_out, and_4_out, 1'b0);
  and and_85 (and_85_out, and_5_out, 1'b0);
  and and_86 (and_86_out, and_6_out, 1'b0);
  and and_87 (and_87_out, and_7_out, 1'b0);
  and and_88 (and_88_out, and_8_out, 1'b0);
  and and_89 (and_89_out, and_9_out, 1'b0);
  and and_90 (and_90_out, and_10_out, 1'b0);
  and and_91 (and_91_out, and_11_out, 1'b0);
  and and_92 (and_92_out, and_12_out, 1'b0);
  and and_93 (and_93_out, and_13_out, 1'b0);
  and and_94 (and_94_out, and_14_out, 1'b0);
  and and_95 (and_95_out, and_15_out, 1'b0);
  or or_14 (OPRAND3, or_13_out, or_15_out);
  or or_15 (or_15_out, and_80_out, and_81_out, and_82_out, and_83_out, and_84_out, and_85_out, and_86_out, and_87_out);
  or or_16 (or_16_out, and_111_out, and_110_out, and_109_out, and_108_out, and_107_out, and_106_out, and_105_out, and_104_out);
  and and_96 (and_96_out, DECORDER_4x16_out, 1'b0);
  and and_97 (and_97_out, and_1_out, 1'b0);
  and and_98 (and_98_out, and_2_out, 1'b0);
  and and_99 (and_99_out, and_3_out, 1'b1);
  and and_100 (and_100_out, and_4_out, 1'b0);
  and and_101 (and_101_out, and_5_out, 1'b0);
  and and_102 (and_102_out, and_6_out, 1'b0);
  and and_103 (and_103_out, and_7_out, 1'b0);
  and and_104 (and_104_out, and_8_out, 1'b0);
  and and_105 (and_105_out, and_9_out, 1'b0);
  and and_106 (and_106_out, and_10_out, 1'b0);
  and and_107 (and_107_out, and_11_out, 1'b0);
  and and_108 (and_108_out, and_12_out, 1'b0);
  and and_109 (and_109_out, and_13_out, 1'b0);
  and and_110 (and_110_out, and_14_out, 1'b0);
  and and_111 (and_111_out, and_15_out, 1'b0);
  or or_17 (OPRAND2, or_16_out, or_18_out);
  or or_18 (or_18_out, and_96_out, and_97_out, and_98_out, and_99_out, and_100_out, and_101_out, and_102_out, and_103_out);
  or or_19 (or_19_out, and_127_out, and_126_out, and_125_out, and_124_out, and_123_out, and_122_out, and_121_out, and_120_out);
  and and_112 (and_112_out, DECORDER_4x16_out, 1'b1);
  and and_113 (and_113_out, and_1_out, 1'b1);
  and and_114 (and_114_out, and_2_out, 1'b0);
  and and_115 (and_115_out, and_3_out, 1'b0);
  and and_116 (and_116_out, and_4_out, 1'b0);
  and and_117 (and_117_out, and_5_out, 1'b0);
  and and_118 (and_118_out, and_6_out, 1'b0);
  and and_119 (and_119_out, and_7_out, 1'b0);
  and and_120 (and_120_out, and_8_out, 1'b0);
  and and_121 (and_121_out, and_9_out, 1'b0);
  and and_122 (and_122_out, and_10_out, 1'b0);
  and and_123 (and_123_out, and_11_out, 1'b0);
  and and_124 (and_124_out, and_12_out, 1'b0);
  and and_125 (and_125_out, and_13_out, 1'b0);
  and and_126 (and_126_out, and_14_out, 1'b0);
  and and_127 (and_127_out, and_15_out, 1'b0);
  or or_20 (OPRAND1, or_19_out, or_21_out);
  or or_21 (or_21_out, and_112_out, and_113_out, and_114_out, and_115_out, and_116_out, and_117_out, and_118_out, and_119_out);
  or or_22 (or_22_out, and_143_out, and_142_out, and_141_out, and_140_out, and_139_out, and_138_out, and_137_out, and_136_out);
  and and_128 (and_128_out, DECORDER_4x16_out, 1'b1);
  and and_129 (and_129_out, and_1_out, 1'b0);
  and and_130 (and_130_out, and_2_out, 1'b1);
  and and_131 (and_131_out, and_3_out, 1'b0);
  and and_132 (and_132_out, and_4_out, 1'b0);
  and and_133 (and_133_out, and_5_out, 1'b0);
  and and_134 (and_134_out, and_6_out, 1'b0);
  and and_135 (and_135_out, and_7_out, 1'b0);
  and and_136 (and_136_out, and_8_out, 1'b0);
  and and_137 (and_137_out, and_9_out, 1'b0);
  and and_138 (and_138_out, and_10_out, 1'b0);
  and and_139 (and_139_out, and_11_out, 1'b0);
  and and_140 (and_140_out, and_12_out, 1'b0);
  and and_141 (and_141_out, and_13_out, 1'b0);
  and and_142 (and_142_out, and_14_out, 1'b0);
  and and_143 (and_143_out, and_15_out, 1'b0);
  or or_23 (OPRAND0, or_22_out, or_24_out);
  or or_24 (or_24_out, and_128_out, and_129_out, and_130_out, and_131_out, and_132_out, and_133_out, and_134_out, and_135_out);
endmodule

module CTRLUNIT (
  input  CTRL_S2,
  input  CTRL_S1,
  input  CTRL_S0,
  input  CTRL_OPR3,
  input  CTRL_OPR2,
  input  CTRL_OPR1,
  input  CTRL_OPR0,
  output CTRL_OP2,
  output CTRL_OP1,
  output CTRL_OP0,
  output CTRL_WE,
  output CTRL_B3,
  output CTRL_B2,
  output CTRL_B1,
  output CTRL_B0
);

  wire and_1_out, and_2_out, and_3_out, and_4_out, and_5_out, and_6_out, and_7_out, B_SEL_0001_out,
       DECORDER_3x8_out, not_1_out, not_2_out, not_3_out, not_4_out, or_1_out, or_2_out, or_3_out, or_4_out,
       or_5_out;

  not not_1 (not_1_out, CTRL_S2);
  not not_2 (not_2_out, CTRL_S1);
  not not_3 (not_3_out, CTRL_S0);
  and DECORDER_3x8 (DECORDER_3x8_out, not_3_out, not_2_out, not_1_out);
  and and_1 (and_1_out, CTRL_S0, not_2_out, not_1_out);
  and and_2 (and_2_out, not_3_out, CTRL_S1, not_1_out);
  and and_3 (and_3_out, CTRL_S0, CTRL_S1, not_1_out);
  and and_4 (and_4_out, not_3_out, not_2_out, CTRL_S2);
  and and_5 (and_5_out, CTRL_S0, not_2_out, CTRL_S2);
  and and_6 (and_6_out, not_3_out, CTRL_S1, CTRL_S2);
  and and_7 (and_7_out, CTRL_S0, CTRL_S1, CTRL_S2);
  or or_1 (or_1_out, DECORDER_3x8_out, and_1_out);
  or or_2 (or_2_out, and_2_out, and_3_out);
  or or_3 (or_3_out, and_4_out, and_5_out);
  or or_4 (or_4_out, or_1_out, or_2_out);
  or or_5 (or_5_out, or_3_out, B_SEL_0001_out);
  or B_SEL_0001 (B_SEL_0001_out, and_6_out, and_7_out);
  not not_4 (not_4_out, B_SEL_0001_out);
  or or_6 (CTRL_OP0, and_1_out, and_3_out, and_5_out, and_7_out);
  or or_7 (CTRL_OP1, and_2_out, and_3_out, and_6_out, and_7_out);
  or or_8 (CTRL_OP2, and_4_out, and_5_out, and_6_out, and_7_out);
  or or_9 (CTRL_WE, or_4_out, or_5_out);
  or or_10 (CTRL_B0, B_SEL_0001_out, CTRL_OPR0);
  and and_8 (CTRL_B1, not_4_out, CTRL_OPR1);
  and and_9 (CTRL_B2, not_4_out, CTRL_OPR2);
  and and_10 (CTRL_B3, not_4_out, CTRL_OPR3);
endmodule

module CPU (
  input  in_1,
  output OVF,
  output N,
  output C,
  output Z,
  output out_6,
  output out_7,
  output out_8,
  output out_9,
  output out_10,
  output out_11,
  output out_12,
  output out_13,
  output out_14,
  output out_15,
  output out_16,
  output out_17,
  output out_18,
  output out_19,
  output out_20,
  output out_21
);

  wire alu_acc_1_c, alu_acc_1_n, alu_acc_1_ovf, alu_acc_1_z, clock_1_out, ctrlunit_ext_1_ctrl_b0,
       ctrlunit_ext_1_ctrl_b1, ctrlunit_ext_1_ctrl_b2, ctrlunit_ext_1_ctrl_b3, ctrlunit_ext_1_ctrl_op0,
       ctrlunit_ext_1_ctrl_op1, ctrlunit_ext_1_ctrl_op2, ctrlunit_ext_1_ctrl_we, ctrlunit_ext_1_jmp_sig,
       progcounter_ext_1_pco0, progcounter_ext_1_pco1, progcounter_ext_1_pco2, progcounter_ext_1_pco3;

  ProgCounter_EXT progcounter_ext_1 (
    .A3(in_1), .A2(clock_1_out), .A1(ctrlunit_ext_1_ctrl_b3), .A0(ctrlunit_ext_1_ctrl_b2),
    .PC_OPR3(ctrlunit_ext_1_ctrl_b1), .PC_OPR2(ctrlunit_ext_1_ctrl_b0), .PC_OPR1(ctrlunit_ext_1_jmp_sig),
    .PCO3(progcounter_ext_1_pco3), .PCO2(progcounter_ext_1_pco2), .PCO1(progcounter_ext_1_pco1),
    .PCO0(progcounter_ext_1_pco0));  // open: PC_OPR0, JMP_JZ, FTCH
  JN_TESTER jn_tester_1 (
    .ROMI3(progcounter_ext_1_pco3), .ROMI2(progcounter_ext_1_pco2), .ROMI1(progcounter_ext_1_pco1),
    .ROMI0(progcounter_ext_1_pco0), .OPC3(out_6), .OPC2(out_7), .OPC1(out_8), .OPC0(out_9), .OPRAND3(out_10),
    .OPRAND2(out_11), .OPRAND1(out_12), .OPRAND0(out_13));
  CTRLUNIT_EXT ctrlunit_ext_1 (
    .CTRL_S3(out_6), .CTRL_S2(out_7), .CTRL_S1(out_8), .CTRL_S0(out_9), .CTRL_OPR3(out_10),
    .CTRL_OPR2(out_11), .CTRL_OPR1(out_12), .CTRL_OPR0(out_13), .FLAG_N(N), .FLAG_Z(Z),
    .CTRL_OP2(ctrlunit_ext_1_ctrl_op2), .CTRL_OP1(ctrlunit_ext_1_ctrl_op1),
    .CTRL_OP0(ctrlunit_ext_1_ctrl_op0), .CTRL_WE(ctrlunit_ext_1_ctrl_we), .CTRL_B3(ctrlunit_ext_1_ctrl_b3),
    .CTRL_B2(ctrlunit_ext_1_ctrl_b2), .CTRL_B1(ctrlunit_ext_1_ctrl_b1), .CTRL_B0(ctrlunit_ext_1_ctrl_b0),
    .JMP_SIG(ctrlunit_ext_1_jmp_sig), .ALU_SIG(Z));  // open: FLAG_OVF, FLAG_C, CTRL_OP3, HLT_SIG, LDI_SIG, LDA_SIG, STA_SIG
  ALU_ACC alu_acc_1 (
    .A_3(out_18), .A_2(out_19), .A_1(out_20), .A_0(out_21), .B_3(ctrlunit_ext_1_ctrl_b3),
    .B_2(ctrlunit_ext_1_ctrl_b2), .B_1(ctrlunit_ext_1_ctrl_b1), .B_0(ctrlunit_ext_1_ctrl_b0),
    .HARD_RESET(in_1), .CLK(clock_1_out), .WE(ctrlunit_ext_1_ctrl_we), .S2(ctrlunit_ext_1_ctrl_op2),
    .S1(ctrlunit_ext_1_ctrl_op1), .S0(ctrlunit_ext_1_ctrl_op0), .OVF(alu_acc_1_ovf), .N(alu_acc_1_n),
    .C(alu_acc_1_c), .Z(alu_acc_1_z), .O_3(out_14), .O_2(out_15), .O_1(out_16), .O_0(out_17),
    .ACC_D0(out_21), .ACC_D1(out_20), .ACC_D2(out_19), .ACC_D3(out_18));
  Clock clock_1 (.out(clock_1_out));
  REGISTER_4BIT FLAG_REG (
    .HARD_RESET(in_1), .CLK(clock_1_out), .REG_I3(alu_acc_1_ovf), .REG_I2(alu_acc_1_n), .REG_I1(alu_acc_1_c),
    .REG_I0(alu_acc_1_z), .WE(ctrlunit_ext_1_ctrl_we), .REG_O3(OVF), .REG_O2(N), .REG_O1(C), .REG_O0(Z));
  ALU_EXT alu_ext_1 ();  // open: A_3, A_2, A_1, A_0, B_3, B_2, B_1, B_0, S2, S1, S0, OVF, N, C, Z, O_3, O_2, O_1, O_0
  REGISTER_4BIT ALU_REG ();  // open: HARD_RESET, CLK, REG_I3, REG_I2, REG_I1, REG_I0, WE, REG_O3, REG_O2, REG_O1, REG_O0
endmodule

module REGISTER_4BIT (
  input  HARD_RESET,
  input  CLK,
  input  REG_I3,
  input  REG_I2,
  input  REG_I1,
  input  REG_I0,
  input  WE,
  output REG_O3,
  output REG_O2,
  output REG_O1,
  output REG_O0
);

  wire and_1_out, and_2_out, and_3_out, and_4_out, and_5_out, and_6_out, and_7_out, and_8_out, and_9_out,
       and_10_out, and_11_out, and_12_out, and_13_out, and_14_out, and_15_out, and_16_out, nand_1_out,
       nand_2_out, nand_3_out, nand_4_out, nand_5_out, nand_6_out, nand_7_out, nand_8_out, nand_9_out,
       nand_10_out, nand_11_out, nand_12_out, nand_13_out, nand_14_out, nand_15_out, nand_16_out,
       nand_17_out, nand_18_out, nand_19_out, nand_20_out, nand_21_out, nand_22_out, nand_23_out,
       nand_24_out, nand_26_out, nand_28_out, nand_30_out, nand_32_out, not_1_out, not_2_out, not_3_out,
       not_4_out, not_5_out, not_6_out, not_7_out, not_8_out, not_9_out, not_10_out, not_11_out, not_12_out,
       not_13_out, not_14_out, not_15_out, not_16_out, not_17_out, not_18_out, not_19_out, not_20_out,
       not_21_out, not_22_out, not_23_out, not_24_out, not_25_out, not_26_out, not_27_out, not_28_out,
       or_1_out, or_2_out, or_3_out, or_4_out, or_5_out, or_6_out, or_7_out, or_8_out, or_9_out;

  or or_1 (or_1_out, HARD_RESET, CLK);
  not not_1 (not_1_out, WE);
  not not_2 (not_2_out, WE);
  not not_3 (not_3_out, WE);
  not not_4 (not_4_out, WE);
  and and_1 (and_1_out, not_1_out, REG_O0);
  and and_2 (and_2_out, WE, REG_I0);
  and and_3 (and_3_out, not_2_out, REG_O1);
  and and_4 (and_4_out, WE, REG_I1);
  and and_5 (and_5_out, not_3_out, REG_O2);
  and and_6 (and_6_out, WE, REG_I2);
  and and_7 (and_7_out, not_4_out, REG_O3);
  and and_8 (and_8_out, WE, REG_I3);
  or or_2 (or_2_out, and_1_out, and_2_out);
  or or_3 (or_3_out, and_3_out, and_4_out);
  or or_4 (or_4_out, and_5_out, and_6_out);
  or or_5 (or_5_out, and_7_out, and_8_out);
  not not_5 (not_5_out, HARD_RESET);
  not not_6 (not_6_out, HARD_RESET);
  not not_7 (not_7_out, HARD_RESET);
  not not_8 (not_8_out, HARD_RESET);
  and and_9 (and_9_out, not_5_out, or_2_out);
  and and_10 (and_10_out, HARD_RESET, 1'b0);
  and and_11 (and_11_out, not_6_out, or_3_out);
  and and_12 (and_12_out, HARD_RESET, 1'b0);
  and and_13 (and_13_out, not_7_out, or_4_out);
  and and_14 (and_14_out, HARD_RESET, 1'b0);
  and and_15 (and_15_out, not_8_out, or_5_out);
  and and_16 (and_16_out, HARD_RESET, 1'b0);
  or or_6 (or_6_out, and_9_out, and_10_out);
  or or_7 (or_7_out, and_11_out, and_12_out);
  or or_8 (or_8_out, and_13_out, and_14_out);
  or or_9 (or_9_out, and_15_out, and_16_out);
  not not_9 (not_9_out, or_1_out);
  not not_10 (not_10_out, or_1_out);
  not not_11 (not_11_out, or_1_out);
  not not_12 (not_12_out, or_1_out);
  not not_13 (not_13_out, not_9_out);
  not not_14 (not_14_out, not_10_out);
  not not_15 (not_15_out, not_11_out);
  not not_16 (not_16_out, not_12_out);
  not not_17 (not_17_out, or_6_out);
  not not_18 (not_18_out, or_7_out);
  not not_19 (not_19_out, or_8_out);
  not not_20 (not_20_out, or_9_out);
  nand nand_1 (nand_1_out, or_6_out, not_13_out);
  nand nand_2 (nand_2_out, not_13_out, not_17_out);
  nand nand_3 (nand_3_out, or_7_out, not_14_out);
  nand nand_4 (nand_4_out, not_14_out, not_18_out);
  nand nand_5 (nand_5_out, or_8_out, not_15_out);
  nand nand_6 (nand_6_out, not_15_out, not_19_out);
  nand nand_7 (nand_7_out, or_9_out, not_16_out);
  nand nand_8 (nand_8_out, not_16_out, not_20_out);
  nand nand_9 (nand_9_out, nand_1_out, nand_10_out);
  nand nand_10 (nand_10_out, nand_9_out, nand_2_out);
  nand nand_11 (nand_11_out, nand_3_out, nand_12_out);
  nand nand_12 (nand_12_out, nand_11_out, nand_4_out);
  nand nand_13 (nand_13_out, nand_5_out, nand_14_out);
  nand nand_14 (nand_14_out, nand_13_out, nand_6_out);
  nand nand_15 (nand_15_out, nand_7_out, nand_16_out);
  nand nand_16 (nand_16_out, nand_15_out, nand_8_out);
  not not_21 (not_21_out, not_13_out);
  not not_22 (not_22_out, not_14_out);
  not not_23 (not_23_out, not_15_out);
  not not_24 (not_24_out, not_16_out);
  not not_25 (not_25_out, nand_9_out);
  not not_26 (not_26_out, nand_11_out);
  not not_27 (not_27_out, nand_13_out);
  not not_28 (not_28_out, nand_15_out);
  nand nand_17 (nand_17_out, nand_9_out, not_21_out);
  nand nand_18 (nand_18_out, not_21_out, not_25_out);
  nand nand_19 (nand_19_out, nand_11_out, not_22_out);
  nand nand_20 (nand_20_out, not_22_out, not_26_out);
  nand nand_21 (nand_21_out, nand_13_out, not_23_out);
  nand nand_22 (nand_22_out, not_23_out, not_27_out);
  nand nand_23 (nand_23_out, nand_15_out, not_24_out);
  nand nand_24 (nand_24_out, not_24_out, not_28_out);
  nand nand_25 (REG_O0, nand_17_out, nand_26_out);
  nand nand_26 (nand_26_out, REG_O0, nand_18_out);
  nand nand_27 (REG_O1, nand_19_out, nand_28_out);
  nand nand_28 (nand_28_out, REG_O1, nand_20_out);
  nand nand_29 (REG_O2, nand_21_out, nand_30_out);
  nand nand_30 (nand_30_out, REG_O2, nand_22_out);
  nand nand_31 (REG_O3, nand_23_out, nand_32_out);
  nand nand_32 (nand_32_out, REG_O3, nand_24_out);
endmodule

module CTRLUNIT_EXT (
  input  CTRL_S3,
  input  CTRL_S2,
  input  CTRL_S1,
  input  CTRL_S0,
  input  CTRL_OPR3,
  input  CTRL_OPR2,
  input  CTRL_OPR1,
  input  CTRL_OPR0,
  input  FLAG_OVF,
  input  FLAG_N,
  input  FLAG_C,
  input  FLAG_Z,
  output CTRL_OP3,
  output CTRL_OP2,
  output CTRL_OP1,
  output CTRL_OP0,
  output CTRL_WE,
  output CTRL_B3,
  output CTRL_B2,
  output CTRL_B1,
  output CTRL_B0,
  output JMP_SIG,
  output HLT_SIG,
  output LDI_SIG,
  output LDA_SIG,
  output STA_SIG,
  output ALU_SIG
);

  wire ADD_out, and_1_out, and_2_out, and_3_out, and_4_out, and_5_out, and_6_out, and_7_out, and_8_out,
       and_9_out, and_10_out, and_11_out, B_SEL_0001_out, DEC_out, INC_out, JMP_out, JN_out, JZ_out, ND_out,
       NOOT_out, not_1_out, not_2_out, not_3_out, not_4_out, not_5_out, not_6_out, not_7_out, not_8_out,
       not_9_out, OOR_out, or_4_out, or_5_out, or_6_out, or_7_out, or_8_out, or_10_out, or_13_out, SUB_out,
       XOOR_out;

  not not_1 (not_1_out, CTRL_S3);
  not not_2 (not_2_out, CTRL_S2);
  not not_3 (not_3_out, CTRL_S1);
  not not_4 (not_4_out, CTRL_S0);
  and and_1 (and_1_out, not_2_out, not_1_out);
  and and_2 (and_2_out, not_2_out, not_1_out);
  and and_3 (and_3_out, not_2_out, not_1_out);
  and and_4 (and_4_out, not_2_out, not_1_out);
  and and_5 (and_5_out, CTRL_S2, not_1_out);
  and and_6 (and_6_out, CTRL_S2, not_1_out);
  and and_7 (and_7_out, CTRL_S2, not_1_out);
  and and_8 (and_8_out, CTRL_S2, not_1_out);
  and ADD (ADD_out, not_4_out, not_3_out, and_1_out);
  and SUB (SUB_out, CTRL_S0, not_3_out, and_2_out);
  and ND (ND_out, not_4_out, CTRL_S1, and_3_out);
  and OOR (OOR_out, CTRL_S0, CTRL_S1, and_4_out);
  and XOOR (XOOR_out, not_4_out, not_3_out, and_5_out);
  and NOOT (NOOT_out, CTRL_S0, not_3_out, and_6_out);
  and INC (INC_out, not_4_out, CTRL_S1, and_7_out);
  and DEC (DEC_out, CTRL_S0, CTRL_S1, and_8_out);
  and JMP (JMP_out, not_4_out, not_3_out, not_2_out, CTRL_S3);
  and JZ (JZ_out, CTRL_S0, not_3_out, not_2_out, CTRL_S3);
  and JN (JN_out, not_4_out, CTRL_S1, not_2_out, CTRL_S3);
  and HLT (HLT_SIG, CTRL_S0, CTRL_S1, not_2_out, CTRL_S3);
  and LDI (LDI_SIG, not_4_out, not_3_out, CTRL_S2, CTRL_S3);
  and LDA (LDA_SIG, CTRL_S0, not_3_out, CTRL_S2, CTRL_S3);
  and STA (STA_SIG, not_4_out, CTRL_S1, CTRL_S2, CTRL_S3);
  and and_9 (and_9_out, CTRL_S0, CTRL_S1, CTRL_S2, CTRL_S3);
  or DECORDER_3x8 (CTRL_OP0, SUB_out, OOR_out, NOOT_out, DEC_out, JZ_out, HLT_SIG, LDA_SIG, and_9_out);
  or or_1 (CTRL_OP1, ND_out, OOR_out, INC_out, DEC_out, JN_out, HLT_SIG, STA_SIG, and_9_out);
  or or_2 (CTRL_OP2, XOOR_out, NOOT_out, INC_out, DEC_out, LDI_SIG, LDA_SIG, STA_SIG, and_9_out);
  or or_3 (CTRL_OP3, JMP_out, JZ_out, JN_out, HLT_SIG, LDI_SIG, LDA_SIG, STA_SIG, and_9_out);
  or or_4 (or_4_out, ADD_out, SUB_out);
  or or_5 (or_5_out, ND_out, OOR_out);
  or or_6 (or_6_out, XOOR_out, NOOT_out);
  or or_7 (or_7_out, or_4_out, or_5_out);
  and and_10 (and_10_out, JZ_out, FLAG_Z);
  or or_8 (or_8_out, or_6_out, B_SEL_0001_out);
  and and_11 (and_11_out, JN_out, FLAG_N);
  or B_SEL_0001 (B_SEL_0001_out, INC_out, DEC_out);
  not not_5 (not_5_out, B_SEL_0001_out);
  or or_9 (ALU_SIG, or_7_out, or_8_out);
  not not_6 (not_6_out, JZ_out);
  or or_10 (or_10_out, not_6_out, not_8_out, not_7_out, not_9_out);
  not not_7 (not_7_out, JN_out);
  not not_8 (not_8_out, JMP_out);
  not not_9 (not_9_out, HLT_SIG);
  or or_11 (CTRL_B0, B_SEL_0001_out, CTRL_OPR0);
  and and_12 (CTRL_B1, not_5_out, CTRL_OPR1);
  and and_13 (CTRL_B2, not_5_out, CTRL_OPR2);
  and and_14 (CTRL_B3, not_5_out, CTRL_OPR3);
  or or_12 (JMP_SIG, JMP_out, and_10_out, and_11_out);
  or or_13 (or_13_out, LDI_SIG, ALU_SIG);
  and and_15 (CTRL_WE, or_13_out, or_10_out);
endmodule

module ADER (
  input  A_3,
  input  A_2,
  input  A_1,
  input  A_0,
  input  B_3,
  input  B_2,
  input  B_1,
  input  B_0
);

  wire Adder_out, and_1_out, and_2_out, and_3_out, and_4_out, and_5_out, and_6_out, and_7_out, and_8_out,
       or_1_out, or_2_out, or_3_out, undriven, xor_1_out, xor_2_out, xor_3_out;

  xor Adder (Adder_out, A_0, B_0);
  xor xor_1 (xor_1_out, A_1, B_1);
  xor xor_2 (xor_2_out, A_2, B_2);
  xor xor_3 (xor_3_out, A_3, B_3);
  // XOR_Gate xor_4 has open pins: in0=undriven, in1=Adder_out, out=open
  and and_1 (and_1_out, undriven, Adder_out);
  and and_2 (and_2_out, A_0, B_0);
  // XOR_Gate xor_5 has open pins: in0=or_1_out, in1=xor_1_out, out=open
  and and_3 (and_3_out, or_1_out, xor_1_out);
  and and_4 (and_4_out, A_1, B_1);
  // XOR_Gate xor_6 has open pins: in0=or_2_out, in1=xor_2_out, out=open
  and and_5 (and_5_out, or_2_out, xor_2_out);
  and and_6 (and_6_out, A_2, B_2);
  // XOR_Gate xor_7 has open pins: in0=or_3_out, in1=xor_3_out, out=open
  and and_7 (and_7_out, or_3_out, xor_3_out);
  and and_8 (and_8_out, A_3, B_3);
  or or_1 (or_1_out, and_1_out, and_2_out);
  or or_2 (or_2_out, and_3_out, and_4_out);
  or or_3 (or_3_out, and_5_out, and_6_out);
  // OR_Gate or_4 has open pins: in0=and_7_out, in1=and_8_out, out=open
endmodule

module ProgCounter_EXT (
  input  A3,
  input  A2,
  input  A1,
  input  A0,
  input  PC_OPR3,
  input  PC_OPR2,
  input  PC_OPR1,
  input  PC_OPR0,
  input  JMP_JZ,
  input  FTCH,
  output PCO3,
  output PCO2,
  output PCO1,
  output PCO0
);

  wire Adder_out, and_1_out, and_2_out, and_3_out, and_4_out, and_5_out, and_6_out, and_7_out, and_8_out,
       and_9_out, and_10_out, and_11_out, and_12_out, and_13_out, and_14_out, and_15_out, and_16_out,
       and_17_out, not_1_out, not_2_out, not_3_out, not_4_out, or_1_out, or_2_out, or_3_out, xor_1_out,
       xor_2_out, xor_3_out, xor_4_out, xor_5_out, xor_6_out, xor_7_out;

  and and_1 (and_1_out, 1'b1, FTCH);
  xor Adder (Adder_out, A0, and_1_out);
  xor xor_1 (xor_1_out, A1, 1'b0);
  xor xor_2 (xor_2_out, A2, 1'b0);
  xor xor_3 (xor_3_out, A3, 1'b0);
  xor xor_4 (xor_4_out, 1'b0, Adder_out);
  and and_2 (and_2_out, 1'b0, Adder_out);
  and and_3 (and_3_out, A0, and_1_out);
  xor xor_5 (xor_5_out, or_1_out, xor_1_out);
  and and_4 (and_4_out, or_1_out, xor_1_out);
  and and_5 (and_5_out, A1, 1'b0);
  xor xor_6 (xor_6_out, or_2_out, xor_2_out);
  and and_6 (and_6_out, or_2_out, xor_2_out);
  and and_7 (and_7_out, A2, 1'b0);
  xor xor_7 (xor_7_out, or_3_out, xor_3_out);
  and and_8 (and_8_out, or_3_out, xor_3_out);
  and and_9 (and_9_out, A3, 1'b0);
  or or_1 (or_1_out, and_2_out, and_3_out);
  or or_2 (or_2_out, and_4_out, and_5_out);
  or or_3 (or_3_out, and_6_out, and_7_out);
  // OR_Gate or_4 has open pins: in0=and_8_out, in1=and_9_out, out=open
  not not_1 (not_1_out, JMP_JZ);
  not not_2 (not_2_out, JMP_JZ);
  not not_3 (not_3_out, JMP_JZ);
  not not_4 (not_4_out, JMP_JZ);
  and and_10 (and_10_out, not_1_out, xor_4_out);
  and and_11 (and_11_out, JMP_JZ, PC_OPR0);
  and and_12 (and_12_out, not_2_out, xor_5_out);
  and and_13 (and_13_out, JMP_JZ, PC_OPR1);
  and and_14 (and_14_out, not_3_out, xor_6_out);
  and and_15 (and_15_out, JMP_JZ, PC_OPR2);
  and and_16 (and_16_out, not_4_out, xor_7_out);
  and and_17 (and_17_out, JMP_JZ, PC_OPR3);
  or MUX2x1 (PCO0, and_10_out, and_11_out);
  or or_5 (PCO1, and_12_out, and_13_out);
  or or_6 (PCO2, and_14_out, and_15_out);
  or or_7 (PCO3, and_16_out, and_17_out);
endmodule

module BLANKROM (
  input  ROMI3,
  input  ROMI2,
  input  ROMI1,
  input  ROMI0,
  output OPC3,
  output OPC2,
  output OPC1,
  output OPC0,
  output OPRAND3,
  output OPRAND2,
  output OPRAND1,
  output OPRAND0
);

  wire and_1_out, and_2_out, and_3_out, and_4_out, and_5_out, and_6_out, and_7_out, and_8_out, and_9_out,
       and_10_out, and_11_out, and_12_out, and_13_out, and_14_out, and_15_out, and_16_out, and_17_out,
       and_18_out, and_19_out, and_20_out, and_21_out, and_22_out, and_23_out, and_24_out, and_25_out,
       and_26_out, and_27_out, and_28_out, and_29_out, and_30_out, and_31_out, and_32_out, and_33_out,
       and_34_out, and_35_out, and_36_out, and_37_out, and_38_out, and_39_out, and_40_out, and_41_out,
       and_42_out, and_43_out, and_44_out, and_45_out, and_46_out, and_47_out, and_48_out, and_49_out,
       and_50_out, and_51_out, and_52_out, and_53_out, and_54_out, and_55_out, and_56_out, and_57_out,
       and_58_out, and_59_out, and_60_out, and_61_out, and_62_out, and_63_out, and_64_out, and_65_out,
       and_66_out, and_67_out, and_68_out, and_69_out, and_70_out, and_71_out, and_72_out, and_73_out,
       and_74_out, and_75_out, and_76_out, and_77_out, and_78_out, and_79_out, and_80_out, and_81_out,
       and_82_out, and_83_out, and_84_out, and_85_out, and_86_out, and_87_out, and_88_out, and_89_out,
       and_90_out, and_91_out, and_92_out, and_93_out, and_94_out, and_95_out, and_96_out, and_97_out,
       and_98_out, and_99_out, and_100_out, and_101_out, and_102_out, and_103_out, and_104_out, and_105_out,
       and_106_out, and_107_out, and_108_out, and_109_out, and_110_out, and_111_out, and_112_out,
       and_113_out, and_114_out, and_115_out, and_116_out, and_117_out, and_118_out, and_119_out,
       and_120_out, and_121_out, and_122_out, and_123_out, and_124_out, and_125_out, and_126_out,
       and_127_out, and_128_out, and_129_out, and_130_out, and_131_out, and_132_out, and_133_out,
       and_134_out, and_135_out, and_136_out, and_137_out, and_138_out, and_139_out, and_140_out,
       and_141_out, and_142_out, and_143_out, DECORDER_4x16_out, not_1_out, not_2_out, not_3_out, not_4_out,
       or_1_out, or_3_out, or_4_out, or_6_out, or_7_out, or_8_out, or_10_out, or_11_out, or_13_out,
       or_15_out, or_16_out, or_18_out, or_19_out, or_21_out, or_22_out, or_24_out;

  not not_1 (not_1_out, ROMI3);
  not not_2 (not_2_out, ROMI2);
  not not_3 (not_3_out, ROMI1);
  not not_4 (not_4_out, ROMI0);
  and DECORDER_4x16 (DECORDER_4x16_out, not_4_out, not_3_out, not_2_out, not_1_out);
  and and_1 (and_1_out, ROMI0, not_3_out, not_2_out, not_1_out);
  and and_2 (and_2_out, not_4_out, ROMI1, not_2_out, not_1_out);
  and and_3 (and_3_out, ROMI0, ROMI1, not_2_out, not_1_out);
  and and_4 (and_4_out, not_4_out, not_3_out, ROMI2, not_1_out);
  and and_5 (and_5_out, ROMI0, not_3_out, ROMI2, not_1_out);
  and and_6 (and_6_out, not_4_out, ROMI1, ROMI2, not_1_out);
  and and_7 (and_7_out, ROMI0, ROMI1, ROMI2, not_1_out);
  and and_8 (and_8_out, not_4_out, not_3_out, not_2_out, ROMI3);
  and and_9 (and_9_out, ROMI0, not_3_out, not_2_out, ROMI3);
  and and_10 (and_10_out, not_4_out, ROMI1, not_2_out, ROMI3);
  and and_11 (and_11_out, ROMI0, ROMI1, not_2_out, ROMI3);
  and and_12 (and_12_out, not_4_out, not_3_out, ROMI2, ROMI3);
  and and_13 (and_13_out, ROMI0, not_3_out, ROMI2, ROMI3);
  and and_14 (and_14_out, not_4_out, ROMI1, ROMI2, ROMI3);
  and and_15 (and_15_out, ROMI0, ROMI1, ROMI2, ROMI3);
  or or_1 (or_1_out, and_31_out, and_30_out, and_29_out, and_28_out, and_27_out, and_26_out, and_25_out, and_24_out);
  and and_16 (and_16_out, DECORDER_4x16_out, 1'b0);
  and and_17 (and_17_out, and_1_out, 1'b0);
  and and_18 (and_18_out, and_2_out, 1'b0);
  and and_19 (and_19_out, and_3_out, 1'b0);
  and and_20 (and_20_out, and_4_out, 1'b0);
  and and_21 (and_21_out, and_5_out, 1'b0);
  and and_22 (and_22_out, and_6_out, 1'b0);
  and and_23 (and_23_out, and_7_out, 1'b0);
  and and_24 (and_24_out, and_8_out, 1'b0);
  and and_25 (and_25_out, and_9_out, 1'b0);
  and and_26 (and_26_out, and_10_out, 1'b0);
  and and_27 (and_27_out, and_11_out, 1'b0);
  and and_28 (and_28_out, and_12_out, 1'b0);
  and and_29 (and_29_out, and_13_out, 1'b0);
  and and_30 (and_30_out, and_14_out, 1'b0);
  and and_31 (and_31_out, and_15_out, 1'b0);
  or or_2 (OPC3, or_1_out, or_3_out);
  or or_3 (or_3_out, and_16_out, and_17_out, and_18_out, and_19_out, and_20_out, and_21_out, and_22_out, and_23_out);
  or or_4 (or_4_out, and_47_out, and_46_out, and_45_out, and_44_out, and_43_out, and_42_out, and_41_out, and_40_out);
  and and_32 (and_32_out, DECORDER_4x16_out, 1'b0);
  and and_33 (and_33_out, and_1_out, 1'b0);
  and and_34 (and_34_out, and_2_out, 1'b0);
  and and_35 (and_35_out, and_3_out, 1'b0);
  and and_36 (and_36_out, and_4_out, 1'b0);
  and and_37 (and_37_out, and_5_out, 1'b0);
  and and_38 (and_38_out, and_6_out, 1'b0);
  and and_39 (and_39_out, and_7_out, 1'b0);
  and and_40 (and_40_out, and_8_out, 1'b0);
  and and_41 (and_41_out, and_9_out, 1'b0);
  and and_42 (and_42_out, and_10_out, 1'b0);
  and and_43 (and_43_out, and_11_out, 1'b0);
  and and_44 (and_44_out, and_12_out, 1'b0);
  and and_45 (and_45_out, and_13_out, 1'b0);
  and and_46 (and_46_out, and_14_out, 1'b0);
  and and_47 (and_47_out, and_15_out, 1'b0);
  or or_5 (OPC2, or_4_out, or_6_out);
  or or_6 (or_6_out, and_32_out, and_33_out, and_34_out, and_35_out, and_36_out, and_37_out, and_38_out, and_39_out);
  and and_48 (and_48_out, DECORDER_4x16_out, 1'b0);
  and and_49 (and_49_out, and_1_out, 1'b0);
  and and_50 (and_50_out, and_2_out, 1'b0);
  and and_51 (and_51_out, and_3_out, 1'b0);
  and and_52 (and_52_out, and_4_out, 1'b0);
  and and_53 (and_53_out, and_5_out, 1'b0);
  and and_54 (and_54_out, and_6_out, 1'b0);
  and and_55 (and_55_out, and_7_out, 1'b0);
  and and_56 (and_56_out, and_8_out, 1'b0);
  and and_57 (and_57_out, and_9_out, 1'b0);
  and and_58 (and_58_out, and_10_out, 1'b0);
  and and_59 (and_59_out, and_11_out, 1'b0);
  and and_60 (and_60_out, and_12_out, 1'b0);
  and and_61 (and_61_out, and_13_out, 1'b0);
  and and_62 (and_62_out, and_14_out, 1'b0);
  and and_63 (and_63_out, and_15_out, 1'b0);
  or or_7 (or_7_out, and_63_out, and_62_out, and_61_out, and_60_out, and_59_out, and_58_out, and_57_out, and_56_out);
  or or_8 (or_8_out, and_48_out, and_49_out, and_50_out, and_51_out, and_52_out, and_53_out, and_54_out, and_55_out);
  or or_9 (OPC1, or_7_out, or_8_out);
  or or_10 (or_10_out, and_79_out, and_78_out, and_77_out, and_76_out, and_75_out, and_74_out, and_73_out, and_72_out);
  and and_64 (and_64_out, DECORDER_4x16_out, 1'b0);
  and and_65 (and_65_out, and_1_out, 1'b0);
  and and_66 (and_66_out, and_2_out, 1'b0);
  and and_67 (and_67_out, and_3_out, 1'b0);
  and and_68 (and_68_out, and_4_out, 1'b0);
  and and_69 (and_69_out, and_5_out, 1'b0);
  and and_70 (and_70_out, and_6_out, 1'b0);
  and and_71 (and_71_out, and_7_out, 1'b0);
  and and_72 (and_72_out, and_8_out, 1'b0);
  and and_73 (and_73_out, and_9_out, 1'b0);
  and and_74 (and_74_out, and_10_out, 1'b0);
  and and_75 (and_75_out, and_11_out, 1'b0);
  and and_76 (and_76_out, and_12_out, 1'b0);
  and and_77 (and_77_out, and_13_out, 1'b0);
  and and_78 (and_78_out, and_14_out, 1'b0);
  and and_79 (and_79_out, and_15_out, 1'b0);
  or or_11 (or_11_out, and_64_out, and_65_out, and_66_out, and_67_out, and_68_out, and_69_out, and_70_out, and_71_out);
  or or_12 (OPC0, or_10_out, or_11_out);
  or or_13 (or_13_out, and_95_out, and_94_out, and_93_out, and_92_out, and_91_out, and_90_out, and_89_out, and_88_out);
  and and_80 (and_80_out, DECORDER_4x16_out, 1'b0);
  and and_81 (and_81_out, and_1_out, 1'b0);
  and and_82 (and_82_out, and_2_out, 1'b0);
  and and_83 (and_83_out, and_3_out, 1'b0);
  and and_84 (and_84_out, and_4_out, 1'b0);
  and and_85 (and_85_out, and_5_out, 1'b0);
  and and_86 (and_86_out, and_6_out, 1'b0);
  and and_87 (and_87_out, and_7_out, 1'b0);
  and and_88 (and_88_out, and_8_out, 1'b0);
  and and_89 (and_89_out, and_9_out, 1'b0);
  and and_90 (and_90_out, and_10_out, 1'b0);
  and and_91 (and_91_out, and_11_out, 1'b0);
  and and_92 (and_92_out, and_12_out, 1'b0);
  and and_93 (and_93_out, and_13_out, 1'b0);
  and and_94 (and_94_out, and_14_out, 1'b0);
  and and_95 (and_95_out, and_15_out, 1'b0);
  or or_14 (OPRAND3, or_13_out, or_15_out);
  or or_15 (or_15_out, and_80_out, and_81_out, and_82_out, and_83_out, and_84_out, and_85_out, and_86_out, and_87_out);
  or or_16 (or_16_out, and_111_out, and_110_out, and_109_out, and_108_out, and_107_out, and_106_out, and_105_out, and_104_out);
  and and_96 (and_96_out, DECORDER_4x16_out, 1'b0);
  and and_97 (and_97_out, and_1_out, 1'b0);
  and and_98 (and_98_out, and_2_out, 1'b0);
  and and_99 (and_99_out, and_3_out, 1'b0);
  and and_100 (and_100_out, and_4_out, 1'b0);
  and and_101 (and_101_out, and_5_out, 1'b0);
  and and_102 (and_102_out, and_6_out, 1'b0);
  and and_103 (and_103_out, and_7_out, 1'b0);
  and and_104 (and_104_out, and_8_out, 1'b0);
  and and_105 (and_105_out, and_9_out, 1'b0);
  and and_106 (and_106_out, and_10_out, 1'b0);
  and and_107 (and_107_out, and_11_out, 1'b0);
  and and_108 (and_108_out, and_12_out, 1'b0);
  and and_109 (and_109_out, and_13_out, 1'b0);
  and and_110 (and_110_out, and_14_out, 1'b0);
  and and_111 (and_111_out, and_15_out, 1'b0);
  or or_17 (OPRAND2, or_16_out, or_18_out);
  or or_18 (or_18_out, and_96_out, and_97_out, and_98_out, and_99_out, and_100_out, and_101_out, and_102_out, and_103_out);
  or or_19 (or_19_out, and_127_out, and_126_out, and_125_out, and_124_out, and_123_out, and_122_out, and_121_out, and_120_out);
  and and_112 (and_112_out, DECORDER_4x16_out, 1'b0);
  and and_113 (and_113_out, and_1_out, 1'b1);
  and and_114 (and_114_out, and_2_out, 1'b0);
  and and_115 (and_115_out, and_3_out, 1'b0);
  and and_116 (and_116_out, and_4_out, 1'b0);
  and and_117 (and_117_out, and_5_out, 1'b0);
  and and_118 (and_118_out, and_6_out, 1'b0);
  and and_119 (and_119_out, and_7_out, 1'b0);
  and and_120 (and_120_out, and_8_out, 1'b0);
  and and_121 (and_121_out, and_9_out, 1'b0);
  and and_122 (and_122_out, and_10_out, 1'b0);
  and and_123 (and_123_out, and_11_out, 1'b0);
  and and_124 (and_124_out, and_12_out, 1'b0);
  and and_125 (and_125_out, and_13_out, 1'b0);
  and and_126 (and_126_out, and_14_out, 1'b0);
  and and_127 (and_127_out, and_15_out, 1'b0);
  or or_20 (OPRAND1, or_19_out, or_21_out);
  or or_21 (or_21_out, and_112_out, and_113_out, and_114_out, and_115_out, and_116_out, and_117_out, and_118_out, and_119_out);
  or or_22 (or_22_out, and_143_out, and_142_out, and_141_out, and_140_out, and_139_out, and_138_out, and_137_out, and_136_out);
  and and_128 (and_128_out, DECORDER_4x16_out, 1'b0);
  and and_129 (and_129_out, and_1_out, 1'b0);
  and and_130 (and_130_out, and_2_out, 1'b0);
  and and_131 (and_131_out, and_3_out, 1'b0);
  and and_132 (and_132_out, and_4_out, 1'b0);
  and and_133 (and_133_out, and_5_out, 1'b0);
  and and_134 (and_134_out, and_6_out, 1'b0);
  and and_135 (and_135_out, and_7_out, 1'b0);
  and and_136 (and_136_out, and_8_out, 1'b0);
  and and_137 (and_137_out, and_9_out, 1'b0);
  and and_138 (and_138_out, and_10_out, 1'b0);
  and and_139 (and_139_out, and_11_out, 1'b0);
  and and_140 (and_140_out, and_12_out, 1'b0);
  and and_141 (and_141_out, and_13_out, 1'b0);
  and and_142 (and_142_out, and_14_out, 1'b0);
  and and_143 (and_143_out, and_15_out, 1'b0);
  or or_23 (OPRAND0, or_22_out, or_24_out);
  or or_24 (or_24_out, and_128_out, and_129_out, and_130_out, and_131_out, and_132_out, and_133_out, and_134_out, and_135_out);
endmodule
module BLANKROM_EXT (
  input  ROMI3,
  input  ROMI2,
  input  ROMI1,
  input  ROMI0,
  output OPC3,
  output OPC2,
  output OPC1,
  output OPC0,
  output OPRAND3,
  output OPRAND2,
  output OPRAND1,
  output OPRAND0
);

  wire and_1_out, and_2_out, and_3_out, and_4_out, and_5_out, and_6_out, and_7_out, and_8_out, and_9_out,
       and_10_out, and_11_out, and_12_out, and_13_out, and_14_out, and_15_out, and_16_out, and_17_out,
       and_18_out, and_19_out, and_20_out, and_21_out, and_22_out, and_23_out, and_24_out, and_25_out,
       and_26_out, and_27_out, and_28_out, and_29_out, and_30_out, and_31_out, and_32_out, and_33_out,
       and_34_out, and_35_out, and_36_out, and_37_out, and_38_out, and_39_out, and_40_out, and_41_out,
       and_42_out, and_43_out, and_44_out, and_45_out, and_46_out, and_47_out, and_48_out, and_49_out,
       and_50_out, and_51_out, and_52_out, and_53_out, and_54_out, and_55_out, and_56_out, and_57_out,
       and_58_out, and_59_out, and_60_out, and_61_out, and_62_out, and_63_out, and_64_out, and_65_out,
       and_66_out, and_67_out, and_68_out, and_69_out, and_70_out, and_71_out, and_72_out, and_73_out,
       and_74_out, and_75_out, and_76_out, and_77_out, and_78_out, and_79_out, and_80_out, and_81_out,
       and_82_out, and_83_out, and_84_out, and_85_out, and_86_out, and_87_out, and_88_out, and_89_out,
       and_90_out, and_91_out, and_92_out, and_93_out, and_94_out, and_95_out, and_96_out, and_97_out,
       and_98_out, and_99_out, and_100_out, and_101_out, and_102_out, and_103_out, and_104_out, and_105_out,
       and_106_out, and_107_out, and_108_out, and_109_out, and_110_out, and_111_out, and_112_out,
       and_113_out, and_114_out, and_115_out, and_116_out, and_117_out, and_118_out, and_119_out,
       and_120_out, and_121_out, and_122_out, and_123_out, and_124_out, and_125_out, and_126_out,
       and_127_out, and_128_out, and_129_out, and_130_out, and_131_out, and_132_out, and_133_out,
       and_134_out, and_135_out, and_136_out, and_137_out, and_138_out, and_139_out, and_140_out,
       and_141_out, and_142_out, and_143_out, DECORDER_4x16_out, not_1_out, not_2_out, not_3_out, not_4_out,
       or_1_out, or_3_out, or_4_out, or_6_out, or_7_out, or_8_out, or_10_out, or_12_out, or_13_out,
       or_14_out, or_16_out, or_18_out, or_19_out, or_21_out, or_22_out, or_23_out;

  not not_1 (not_1_out, ROMI3);
  not not_2 (not_2_out, ROMI2);
  not not_3 (not_3_out, ROMI1);
  not not_4 (not_4_out, ROMI0);
  and DECORDER_4x16 (DECORDER_4x16_out, not_4_out, not_3_out, not_2_out, not_1_out);
  and and_1 (and_1_out, ROMI0, not_3_out, not_2_out, not_1_out);
  and and_2 (and_2_out, not_4_out, ROMI1, not_2_out, not_1_out);
  and and_3 (and_3_out, ROMI0, ROMI1, not_2_out, not_1_out);
  and and_4 (and_4_out, not_4_out, not_3_out, ROMI2, not_1_out);
  and and_5 (and_5_out, ROMI0, not_3_out, ROMI2, not_1_out);
  and and_6 (and_6_out, not_4_out, ROMI1, ROMI2, not_1_out);
  and and_7 (and_7_out, ROMI0, ROMI1, ROMI2, not_1_out);
  and and_8 (and_8_out, not_4_out, not_3_out, not_2_out, ROMI3);
  and and_9 (and_9_out, ROMI0, not_3_out, not_2_out, ROMI3);
  and and_10 (and_10_out, not_4_out, ROMI1, not_2_out, ROMI3);
  and and_11 (and_11_out, ROMI0, ROMI1, not_2_out, ROMI3);
  and and_12 (and_12_out, not_4_out, not_3_out, ROMI2, ROMI3);
  and and_13 (and_13_out, ROMI0, not_3_out, ROMI2, ROMI3);
  and and_14 (and_14_out, not_4_out, ROMI1, ROMI2, ROMI3);
  and and_15 (and_15_out, ROMI0, ROMI1, ROMI2, ROMI3);
  or or_1 (or_1_out, and_31_out, and_30_out, and_29_out, and_28_out, and_27_out, and_26_out, and_25_out, and_24_out);
  and and_16 (and_16_out, DECORDER_4x16_out, 1'b0);
  and and_17 (and_17_out, and_1_out, 1'b0);
  and and_18 (and_18_out, and_2_out, 1'b0);
  and and_19 (and_19_out, and_3_out, 1'b0);
  and and_20 (and_20_out, and_4_out, 1'b0);
  and and_21 (and_21_out, and_5_out, 1'b0);
  and and_22 (and_22_out, and_6_out, 1'b0);
  and and_23 (and_23_out, and_7_out, 1'b0);
  and and_24 (and_24_out, and_8_out, 1'b0);
  and and_25 (and_25_out, and_9_out, 1'b0);
  and and_26 (and_26_out, and_10_out, 1'b0);
  and and_27 (and_27_out, and_11_out, 1'b0);
  and and_28 (and_28_out, and_12_out, 1'b0);
  and and_29 (and_29_out, and_13_out, 1'b0);
  and and_30 (and_30_out, and_14_out, 1'b0);
  and and_31 (and_31_out, and_15_out, 1'b0);
  or or_2 (OPC3, or_1_out, or_3_out);
  or or_3 (or_3_out, and_16_out, and_17_out, and_18_out, and_19_out, and_20_out, and_21_out, and_22_out, and_23_out);
  or or_4 (or_4_out, and_47_out, and_46_out, and_45_out, and_44_out, and_43_out, and_42_out, and_41_out, and_40_out);
  and and_32 (and_32_out, DECORDER_4x16_out, 1'b0);
  and and_33 (and_33_out, and_1_out, 1'b0);
  and and_34 (and_34_out, and_2_out, 1'b0);
  and and_35 (and_35_out, and_3_out, 1'b0);
  and and_36 (and_36_out, and_4_out, 1'b0);
  and and_37 (and_37_out, and_5_out, 1'b0);
  and and_38 (and_38_out, and_6_out, 1'b0);
  and and_39 (and_39_out, and_7_out, 1'b0);
  and and_40 (and_40_out, and_8_out, 1'b0);
  and and_41 (and_41_out, and_9_out, 1'b0);
  and and_42 (and_42_out, and_10_out, 1'b0);
  and and_43 (and_43_out, and_11_out, 1'b0);
  and and_44 (and_44_out, and_12_out, 1'b0);
  and and_45 (and_45_out, and_13_out, 1'b0);
  and and_46 (and_46_out, and_14_out, 1'b0);
  and and_47 (and_47_out, and_15_out, 1'b0);
  or or_5 (OPC2, or_4_out, or_6_out);
  or or_6 (or_6_out, and_32_out, and_33_out, and_34_out, and_35_out, and_36_out, and_37_out, and_38_out, and_39_out);
  and and_48 (and_48_out, DECORDER_4x16_out, 1'b0);
  and and_49 (and_49_out, and_1_out, 1'b0);
  and and_50 (and_50_out, and_2_out, 1'b0);
  and and_51 (and_51_out, and_3_out, 1'b0);
  and and_52 (and_52_out, and_4_out, 1'b0);
  and and_53 (and_53_out, and_5_out, 1'b0);
  and and_54 (and_54_out, and_6_out, 1'b0);
  and and_55 (and_55_out, and_7_out, 1'b0);
  and and_56 (and_56_out, and_8_out, 1'b0);
  and and_57 (and_57_out, and_9_out, 1'b0);
  and and_58 (and_58_out, and_10_out, 1'b0);
  and and_59 (and_59_out, and_11_out, 1'b0);
  and and_60 (and_60_out, and_12_out, 1'b0);
  and and_61 (and_61_out, and_13_out, 1'b0);
  and and_62 (and_62_out, and_14_out, 1'b0);
  and and_63 (and_63_out, and_15_out, 1'b0);
  or or_7 (or_7_out, and_63_out, and_62_out, and_61_out, and_60_out, and_59_out, and_58_out, and_57_out, and_56_out);
  or or_8 (or_8_out, and_48_out, and_49_out, and_50_out, and_51_out, and_52_out, and_53_out, and_54_out, and_55_out);
  or or_9 (OPC1, or_7_out, or_8_out);
  or or_10 (or_10_out, and_79_out, and_78_out, and_77_out, and_76_out, and_75_out, and_74_out, and_73_out, and_72_out);
  and and_64 (and_64_out, DECORDER_4x16_out, 1'b0);
  and and_65 (and_65_out, and_1_out, 1'b0);
  and and_66 (and_66_out, and_2_out, 1'b0);
  and and_67 (and_67_out, and_3_out, 1'b0);
  and and_68 (and_68_out, and_4_out, 1'b0);
  and and_69 (and_69_out, and_5_out, 1'b0);
  and and_70 (and_70_out, and_6_out, 1'b0);
  and and_71 (and_71_out, and_7_out, 1'b0);
  and and_72 (and_72_out, and_8_out, 1'b0);
  and and_73 (and_73_out, and_9_out, 1'b0);
  and and_74 (and_74_out, and_10_out, 1'b0);
  and and_75 (and_75_out, and_11_out, 1'b0);
  and and_76 (and_76_out, and_12_out, 1'b0);
  and and_77 (and_77_out, and_13_out, 1'b0);
  and and_78 (and_78_out, and_14_out, 1'b0);
  and and_79 (and_79_out, and_15_out, 1'b0);
  or or_11 (OPC0, or_10_out, or_12_out);
  or or_12 (or_12_out, and_64_out, and_65_out, and_66_out, and_67_out, and_68_out, and_69_out, and_70_out, and_71_out);
  or or_13 (or_13_out, and_95_out, and_94_out, and_93_out, and_92_out, and_91_out, and_90_out, and_89_out, and_88_out);
  and and_80 (and_80_out, DECORDER_4x16_out, 1'b0);
  and and_81 (and_81_out, and_1_out, 1'b0);
  and and_82 (and_82_out, and_2_out, 1'b0);
  and and_83 (and_83_out, and_3_out, 1'b0);
  and and_84 (and_84_out, and_4_out, 1'b0);
  and and_85 (and_85_out, and_5_out, 1'b0);
  and and_86 (and_86_out, and_6_out, 1'b0);
  and and_87 (and_87_out, and_7_out, 1'b0);
  and and_88 (and_88_out, and_8_out, 1'b0);
  and and_89 (and_89_out, and_9_out, 1'b0);
  and and_90 (and_90_out, and_10_out, 1'b0);
  and and_91 (and_91_out, and_11_out, 1'b0);
  and and_92 (and_92_out, and_12_out, 1'b0);
  and and_93 (and_93_out, and_13_out, 1'b0);
  and and_94 (and_94_out, and_14_out, 1'b0);
  and and_95 (and_95_out, and_15_out, 1'b0);
  or or_14 (or_14_out, and_80_out, and_81_out, and_82_out, and_83_out, and_84_out, and_85_out, and_86_out, and_87_out);
  or or_15 (OPRAND3, or_13_out, or_14_out);
  or or_16 (or_16_out, and_111_out, and_110_out, and_109_out, and_108_out, and_107_out, and_106_out, and_105_out, and_104_out);
  and and_96 (and_96_out, DECORDER_4x16_out, 1'b0);
  and and_97 (and_97_out, and_1_out, 1'b0);
  and and_98 (and_98_out, and_2_out, 1'b0);
  and and_99 (and_99_out, and_3_out, 1'b0);
  and and_100 (and_100_out, and_4_out, 1'b0);
  and and_101 (and_101_out, and_5_out, 1'b0);
  and and_102 (and_102_out, and_6_out, 1'b0);
  and and_103 (and_103_out, and_7_out, 1'b0);
  and and_104 (and_104_out, and_8_out, 1'b0);
  and and_105 (and_105_out, and_9_out, 1'b0);
  and and_106 (and_106_out, and_10_out, 1'b0);
  and and_107 (and_107_out, and_11_out, 1'b0);
  and and_108 (and_108_out, and_12_out, 1'b0);
  and and_109 (and_109_out, and_13_out, 1'b0);
  and and_110 (and_110_out, and_14_out, 1'b0);
  and and_111 (and_111_out, and_15_out, 1'b0);
  or or_17 (OPRAND2, or_16_out, or_18_out);
  or or_18 (or_18_out, and_96_out, and_97_out, and_98_out, and_99_out, and_100_out, and_101_out, and_102_out, and_103_out);
  or or_19 (or_19_out, and_127_out, and_126_out, and_125_out, and_124_out, and_123_out, and_122_out, and_121_out, and_120_out);
  and and_112 (and_112_out, DECORDER_4x16_out, 1'b0);
  and and_113 (and_113_out, and_1_out, 1'b0);
  and and_114 (and_114_out, and_2_out, 1'b0);
  and and_115 (and_115_out, and_3_out, 1'b0);
  and and_116 (and_116_out, and_4_out, 1'b0);
  and and_117 (and_117_out, and_5_out, 1'b0);
  and and_118 (and_118_out, and_6_out, 1'b0);
  and and_119 (and_119_out, and_7_out, 1'b0);
  and and_120 (and_120_out, and_8_out, 1'b0);
  and and_121 (and_121_out, and_9_out, 1'b0);
  and and_122 (and_122_out, and_10_out, 1'b0);
  and and_123 (and_123_out, and_11_out, 1'b0);
  and and_124 (and_124_out, and_12_out, 1'b0);
  and and_125 (and_125_out, and_13_out, 1'b0);
  and and_126 (and_126_out, and_14_out, 1'b0);
  and and_127 (and_127_out, and_15_out, 1'b0);
  or or_20 (OPRAND1, or_19_out, or_21_out);
  or or_21 (or_21_out, and_112_out, and_113_out, and_114_out, and_115_out, and_116_out, and_117_out, and_118_out, and_119_out);
  or or_22 (or_22_out, and_143_out, and_142_out, and_141_out, and_140_out, and_139_out, and_138_out, and_137_out, and_136_out);
  and and_128 (and_128_out, DECORDER_4x16_out, 1'b0);
  and and_129 (and_129_out, and_1_out, 1'b0);
  and and_130 (and_130_out, and_2_out, 1'b0);
  and and_131 (and_131_out, and_3_out, 1'b0);
  and and_132 (and_132_out, and_4_out, 1'b0);
  and and_133 (and_133_out, and_5_out, 1'b0);
  and and_134 (and_134_out, and_6_out, 1'b0);
  and and_135 (and_135_out, and_7_out, 1'b0);
  and and_136 (and_136_out, and_8_out, 1'b0);
  and and_137 (and_137_out, and_9_out, 1'b0);
  and and_138 (and_138_out, and_10_out, 1'b0);
  and and_139 (and_139_out, and_11_out, 1'b0);
  and and_140 (and_140_out, and_12_out, 1'b0);
  and and_141 (and_141_out, and_13_out, 1'b0);
  and and_142 (and_142_out, and_14_out, 1'b0);
  and and_143 (and_143_out, and_15_out, 1'b0);
  or or_23 (or_23_out, and_128_out, and_129_out, and_130_out, and_131_out, and_132_out, and_133_out, and_134_out, and_135_out);
  or or_24 (OPRAND0, or_22_out, or_23_out);
endmodule

module JMP_TESTER (
  input  ROMI3,
  input  ROMI2,
  input  ROMI1,
  input  ROMI0,
  output OPC3,
  output OPC2,
  output OPC1,
  output OPC0,
  output OPRAND3,
  output OPRAND2,
  output OPRAND1,
  output OPRAND0
);

  wire and_1_out, and_2_out, and_3_out, and_4_out, and_5_out, and_6_out, and_7_out, and_8_out, and_9_out,
       and_10_out, and_11_out, and_12_out, and_13_out, and_14_out, and_15_out, and_16_out, and_17_out,
       and_18_out, and_19_out, and_20_out, and_21_out, and_22_out, and_23_out, and_24_out, and_25_out,
       and_26_out, and_27_out, and_28_out, and_29_out, and_30_out, and_31_out, and_32_out, and_33_out,
       and_34_out, and_35_out, and_36_out, and_37_out, and_38_out, and_39_out, and_40_out, and_41_out,
       and_42_out, and_43_out, and_44_out, and_45_out, and_46_out, and_47_out, and_48_out, and_49_out,
       and_50_out, and_51_out, and_52_out, and_53_out, and_54_out, and_55_out, and_56_out, and_57_out,
       and_58_out, and_59_out, and_60_out, and_61_out, and_62_out, and_63_out, and_64_out, and_65_out,
       and_66_out, and_67_out, and_68_out, and_69_out, and_70_out, and_71_out, and_72_out, and_73_out,
       and_74_out, and_75_out, and_76_out, and_77_out, and_78_out, and_79_out, and_80_out, and_81_out,
       and_82_out, and_83_out, and_84_out, and_85_out, and_86_out, and_87_out, and_88_out, and_89_out,
       and_90_out, and_91_out, and_92_out, and_93_out, and_94_out, and_95_out, and_96_out, and_97_out,
       and_98_out, and_99_out, and_100_out, and_101_out, and_102_out, and_103_out, and_104_out, and_105_out,
       and_106_out, and_107_out, and_108_out, and_109_out, and_110_out, and_111_out, and_112_out,
       and_113_out, and_114_out, and_115_out, and_116_out, and_117_out, and_118_out, and_119_out,
       and_120_out, and_121_out, and_122_out, and_123_out, and_124_out, and_125_out, and_126_out,
       and_127_out, and_128_out, and_129_out, and_130_out, and_131_out, and_132_out, and_133_out,
       and_134_out, and_135_out, and_136_out, and_137_out, and_138_out, and_139_out, and_140_out,
       and_141_out, and_142_out, and_143_out, DECORDER_4x16_out, not_1_out, not_2_out, not_3_out, not_4_out,
       or_1_out, or_3_out, or_4_out, or_6_out, or_7_out, or_8_out, or_10_out, or_12_out, or_13_out,
       or_14_out, or_16_out, or_18_out, or_19_out, or_21_out, or_22_out, or_23_out;

  not not_1 (not_1_out, ROMI3);
  not not_2 (not_2_out, ROMI2);
  not not_3 (not_3_out, ROMI1);
  not not_4 (not_4_out, ROMI0);
  and DECORDER_4x16 (DECORDER_4x16_out, not_4_out, not_3_out, not_2_out, not_1_out);
  and and_1 (and_1_out, ROMI0, not_3_out, not_2_out, not_1_out);
  and and_2 (and_2_out, not_4_out, ROMI1, not_2_out, not_1_out);
  and and_3 (and_3_out, ROMI0, ROMI1, not_2_out, not_1_out);
  and and_4 (and_4_out, not_4_out, not_3_out, ROMI2, not_1_out);
  and and_5 (and_5_out, ROMI0, not_3_out, ROMI2, not_1_out);
  and and_6 (and_6_out, not_4_out, ROMI1, ROMI2, not_1_out);
  and and_7 (and_7_out, ROMI0, ROMI1, ROMI2, not_1_out);
  and and_8 (and_8_out, not_4_out, not_3_out, not_2_out, ROMI3);
  and and_9 (and_9_out, ROMI0, not_3_out, not_2_out, ROMI3);
  and and_10 (and_10_out, not_4_out, ROMI1, not_2_out, ROMI3);
  and and_11 (and_11_out, ROMI0, ROMI1, not_2_out, ROMI3);
  and and_12 (and_12_out, not_4_out, not_3_out, ROMI2, ROMI3);
  and and_13 (and_13_out, ROMI0, not_3_out, ROMI2, ROMI3);
  and and_14 (and_14_out, not_4_out, ROMI1, ROMI2, ROMI3);
  and and_15 (and_15_out, ROMI0, ROMI1, ROMI2, ROMI3);
  or or_1 (or_1_out, and_31_out, and_30_out, and_29_out, and_28_out, and_27_out, and_26_out, and_25_out, and_24_out);
  and and_16 (and_16_out, DECORDER_4x16_out, 1'b0);
  and and_17 (and_17_out, and_1_out, 1'b1);
  and and_18 (and_18_out, and_2_out, 1'b0);
  and and_19 (and_19_out, and_3_out, 1'b0);
  and and_20 (and_20_out, and_4_out, 1'b0);
  and and_21 (and_21_out, and_5_out, 1'b0);
  and and_22 (and_22_out, and_6_out, 1'b0);
  and and_23 (and_23_out, and_7_out, 1'b0);
  and and_24 (and_24_out, and_8_out, 1'b0);
  and and_25 (and_25_out, and_9_out, 1'b0);
  and and_26 (and_26_out, and_10_out, 1'b0);
  and and_27 (and_27_out, and_11_out, 1'b0);
  and and_28 (and_28_out, and_12_out, 1'b0);
  and and_29 (and_29_out, and_13_out, 1'b0);
  and and_30 (and_30_out, and_14_out, 1'b0);
  and and_31 (and_31_out, and_15_out, 1'b0);
  or or_2 (OPC3, or_1_out, or_3_out);
  or or_3 (or_3_out, and_16_out, and_17_out, and_18_out, and_19_out, and_20_out, and_21_out, and_22_out, and_23_out);
  or or_4 (or_4_out, and_47_out, and_46_out, and_45_out, and_44_out, and_43_out, and_42_out, and_41_out, and_40_out);
  and and_32 (and_32_out, DECORDER_4x16_out, 1'b0);
  and and_33 (and_33_out, and_1_out, 1'b0);
  and and_34 (and_34_out, and_2_out, 1'b0);
  and and_35 (and_35_out, and_3_out, 1'b0);
  and and_36 (and_36_out, and_4_out, 1'b0);
  and and_37 (and_37_out, and_5_out, 1'b0);
  and and_38 (and_38_out, and_6_out, 1'b0);
  and and_39 (and_39_out, and_7_out, 1'b0);
  and and_40 (and_40_out, and_8_out, 1'b0);
  and and_41 (and_41_out, and_9_out, 1'b0);
  and and_42 (and_42_out, and_10_out, 1'b0);
  and and_43 (and_43_out, and_11_out, 1'b0);
  and and_44 (and_44_out, and_12_out, 1'b0);
  and and_45 (and_45_out, and_13_out, 1'b0);
  and and_46 (and_46_out, and_14_out, 1'b0);
  and and_47 (and_47_out, and_15_out, 1'b0);
  or or_5 (OPC2, or_4_out, or_6_out);
  or or_6 (or_6_out, and_32_out, and_33_out, and_34_out, and_35_out, and_36_out, and_37_out, and_38_out, and_39_out);
  and and_48 (and_48_out, DECORDER_4x16_out, 1'b0);
  and and_49 (and_49_out, and_1_out, 1'b0);
  and and_50 (and_50_out, and_2_out, 1'b0);
  and and_51 (and_51_out, and_3_out, 1'b0);
  and and_52 (and_52_out, and_4_out, 1'b0);
  and and_53 (and_53_out, and_5_out, 1'b0);
  and and_54 (and_54_out, and_6_out, 1'b0);
  and and_55 (and_55_out, and_7_out, 1'b0);
  and and_56 (and_56_out, and_8_out, 1'b0);
  and and_57 (and_57_out, and_9_out, 1'b0);
  and and_58 (and_58_out, and_10_out, 1'b0);
  and and_59 (and_59_out, and_11_out, 1'b0);
  and and_60 (and_60_out, and_12_out, 1'b0);
  and and_61 (and_61_out, and_13_out, 1'b0);
  and and_62 (and_62_out, and_14_out, 1'b0);
  and and_63 (and_63_out, and_15_out, 1'b0);
  or or_7 (or_7_out, and_63_out, and_62_out, and_61_out, and_60_out, and_59_out, and_58_out, and_57_out, and_56_out);
  or or_8 (or_8_out, and_48_out, and_49_out, and_50_out, and_51_out, and_52_out, and_53_out, and_54_out, and_55_out);
  or or_9 (OPC1, or_7_out, or_8_out);
  or or_10 (or_10_out, and_79_out, and_78_out, and_77_out, and_76_out, and_75_out, and_74_out, and_73_out, and_72_out);
  and and_64 (and_64_out, DECORDER_4x16_out, 1'b0);
  and and_65 (and_65_out, and_1_out, 1'b0);
  and and_66 (and_66_out, and_2_out, 1'b0);
  and and_67 (and_67_out, and_3_out, 1'b0);
  and and_68 (and_68_out, and_4_out, 1'b0);
  and and_69 (and_69_out, and_5_out, 1'b0);
  and and_70 (and_70_out, and_6_out, 1'b0);
  and and_71 (and_71_out, and_7_out, 1'b0);
  and and_72 (and_72_out, and_8_out, 1'b0);
  and and_73 (and_73_out, and_9_out, 1'b0);
  and and_74 (and_74_out, and_10_out, 1'b0);
  and and_75 (and_75_out, and_11_out, 1'b0);
  and and_76 (and_76_out, and_12_out, 1'b0);
  and and_77 (and_77_out, and_13_out, 1'b0);
  and and_78 (and_78_out, and_14_out, 1'b0);
  and and_79 (and_79_out, and_15_out, 1'b0);
  or or_11 (OPC0, or_10_out, or_12_out);
  or or_12 (or_12_out, and_64_out, and_65_out, and_66_out, and_67_out, and_68_out, and_69_out, and_70_out, and_71_out);
  or or_13 (or_13_out, and_95_out, and_94_out, and_93_out, and_92_out, and_91_out, and_90_out, and_89_out, and_88_out);
  and and_80 (and_80_out, DECORDER_4x16_out, 1'b0);
  and and_81 (and_81_out, and_1_out, 1'b0);
  and and_82 (and_82_out, and_2_out, 1'b0);
  and and_83 (and_83_out, and_3_out, 1'b0);
  and and_84 (and_84_out, and_4_out, 1'b0);
  and and_85 (and_85_out, and_5_out, 1'b0);
  and and_86 (and_86_out, and_6_out, 1'b0);
  and and_87 (and_87_out, and_7_out, 1'b0);
  and and_88 (and_88_out, and_8_out, 1'b0);
  and and_89 (and_89_out, and_9_out, 1'b0);
  and and_90 (and_90_out, and_10_out, 1'b0);
  and and_91 (and_91_out, and_11_out, 1'b0);
  and and_92 (and_92_out, and_12_out, 1'b0);
  and and_93 (and_93_out, and_13_out, 1'b0);
  and and_94 (and_94_out, and_14_out, 1'b0);
  and and_95 (and_95_out, and_15_out, 1'b0);
  or or_14 (or_14_out, and_80_out, and_81_out, and_82_out, and_83_out, and_84_out, and_85_out, and_86_out, and_87_out);
  or or_15 (OPRAND3, or_13_out, or_14_out);
  or or_16 (or_16_out, and_111_out, and_110_out, and_109_out, and_108_out, and_107_out, and_106_out, and_105_out, and_104_out);
  and and_96 (and_96_out, DECORDER_4x16_out, 1'b0);
  and and_97 (and_97_out, and_1_out, 1'b1);
  and and_98 (and_98_out, and_2_out, 1'b0);
  and and_99 (and_99_out, and_3_out, 1'b0);
  and and_100 (and_100_out, and_4_out, 1'b0);
  and and_101 (and_101_out, and_5_out, 1'b0);
  and and_102 (and_102_out, and_6_out, 1'b0);
  and and_103 (and_103_out, and_7_out, 1'b0);
  and and_104 (and_104_out, and_8_out, 1'b0);
  and and_105 (and_105_out, and_9_out, 1'b0);
  and and_106 (and_106_out, and_10_out, 1'b0);
  and and_107 (and_107_out, and_11_out, 1'b0);
  and and_108 (and_108_out, and_12_out, 1'b0);
  and and_109 (and_109_out, and_13_out, 1'b0);
  and and_110 (and_110_out, and_14_out, 1'b0);
  and and_111 (and_111_out, and_15_out, 1'b0);
  or or_17 (OPRAND2, or_16_out, or_18_out);
  or or_18 (or_18_out, and_96_out, and_97_out, and_98_out, and_99_out, and_100_out, and_101_out, and_102_out, and_103_out);
  or or_19 (or_19_out, and_127_out, and_126_out, and_125_out, and_124_out, and_123_out, and_122_out, and_121_out, and_120_out);
  and and_112 (and_112_out, DECORDER_4x16_out, 1'b0);
  and and_113 (and_113_out, and_1_out, 1'b0);
  and and_114 (and_114_out, and_2_out, 1'b1);
  and and_115 (and_115_out, and_3_out, 1'b1);
  and and_116 (and_116_out, and_4_out, 1'b0);
  and and_117 (and_117_out, and_5_out, 1'b0);
  and and_118 (and_118_out, and_6_out, 1'b0);
  and and_119 (and_119_out, and_7_out, 1'b0);
  and and_120 (and_120_out, and_8_out, 1'b0);
  and and_121 (and_121_out, and_9_out, 1'b0);
  and and_122 (and_122_out, and_10_out, 1'b0);
  and and_123 (and_123_out, and_11_out, 1'b0);
  and and_124 (and_124_out, and_12_out, 1'b0);
  and and_125 (and_125_out, and_13_out, 1'b0);
  and and_126 (and_126_out, and_14_out, 1'b0);
  and and_127 (and_127_out, and_15_out, 1'b0);
  or or_20 (OPRAND1, or_19_out, or_21_out);
  or or_21 (or_21_out, and_112_out, and_113_out, and_114_out, and_115_out, and_116_out, and_117_out, and_118_out, and_119_out);
  or or_22 (or_22_out, and_143_out, and_142_out, and_141_out, and_140_out, and_139_out, and_138_out, and_137_out, and_136_out);
  and and_128 (and_128_out, DECORDER_4x16_out, 1'b1);
  and and_129 (and_129_out, and_1_out, 1'b0);
  and and_130 (and_130_out, and_2_out, 1'b0);
  and and_131 (and_131_out, and_3_out, 1'b0);
  and and_132 (and_132_out, and_4_out, 1'b1);
  and and_133 (and_133_out, and_5_out, 1'b0);
  and and_134 (and_134_out, and_6_out, 1'b0);
  and and_135 (and_135_out, and_7_out, 1'b0);
  and and_136 (and_136_out, and_8_out, 1'b0);
  and and_137 (and_137_out, and_9_out, 1'b0);
  and and_138 (and_138_out, and_10_out, 1'b0);
  and and_139 (and_139_out, and_11_out, 1'b0);
  and and_140 (and_140_out, and_12_out, 1'b0);
  and and_141 (and_141_out, and_13_out, 1'b0);
  and and_142 (and_142_out, and_14_out, 1'b0);
  and and_143 (and_143_out, and_15_out, 1'b0);
  or or_23 (or_23_out, and_128_out, and_129_out, and_130_out, and_131_out, and_132_out, and_133_out, and_134_out, and_135_out);
  or or_24 (OPRAND0, or_22_out, or_23_out);
endmodule

module JZ_TESTER (
  input  ROMI3,
  input  ROMI2,
  input  ROMI1,
  input  ROMI0,
  output OPC3,
  output OPC2,
  output OPC1,
  output OPC0,
  output OPRAND3,
  output OPRAND2,
  output OPRAND1,
  output OPRAND0
);

  wire and_1_out, and_2_out, and_3_out, and_4_out, and_5_out, and_6_out, and_7_out, and_8_out, and_9_out,
       and_10_out, and_11_out, and_12_out, and_13_out, and_14_out, and_15_out, and_16_out, and_17_out,
       and_18_out, and_19_out, and_20_out, and_21_out, and_22_out, and_23_out, and_24_out, and_25_out,
       and_26_out, and_27_out, and_28_out, and_29_out, and_30_out, and_31_out, and_32_out, and_33_out,
       and_34_out, and_35_out, and_36_out, and_37_out, and_38_out, and_39_out, and_40_out, and_41_out,
       and_42_out, and_43_out, and_44_out, and_45_out, and_46_out, and_47_out, and_48_out, and_49_out,
       and_50_out, and_51_out, and_52_out, and_53_out, and_54_out, and_55_out, and_56_out, and_57_out,
       and_58_out, and_59_out, and_60_out, and_61_out, and_62_out, and_63_out, and_64_out, and_65_out,
       and_66_out, and_67_out, and_68_out, and_69_out, and_70_out, and_71_out, and_72_out, and_73_out,
       and_74_out, and_75_out, and_76_out, and_77_out, and_78_out, and_79_out, and_80_out, and_81_out,
       and_82_out, and_83_out, and_84_out, and_85_out, and_86_out, and_87_out, and_88_out, and_89_out,
       and_90_out, and_91_out, and_92_out, and_93_out, and_94_out, and_95_out, and_96_out, and_97_out,
       and_98_out, and_99_out, and_100_out, and_101_out, and_102_out, and_103_out, and_104_out, and_105_out,
       and_106_out, and_107_out, and_108_out, and_109_out, and_110_out, and_111_out, and_112_out,
       and_113_out, and_114_out, and_115_out, and_116_out, and_117_out, and_118_out, and_119_out,
       and_120_out, and_121_out, and_122_out, and_123_out, and_124_out, and_125_out, and_126_out,
       and_127_out, and_128_out, and_129_out, and_130_out, and_131_out, and_132_out, and_133_out,
       and_134_out, and_135_out, and_136_out, and_137_out, and_138_out, and_139_out, and_140_out,
       and_141_out, and_142_out, and_143_out, DECORDER_4x16_out, not_1_out, not_2_out, not_3_out, not_4_out,
       or_1_out, or_3_out, or_4_out, or_6_out, or_7_out, or_8_out, or_10_out, or_12_out, or_13_out,
       or_15_out, or_16_out, or_18_out, or_19_out, or_21_out, or_22_out, or_24_out;

  not not_1 (not_1_out, ROMI3);
  not not_2 (not_2_out, ROMI2);
  not not_3 (not_3_out, ROMI1);
  not not_4 (not_4_out, ROMI0);
  and DECORDER_4x16 (DECORDER_4x16_out, not_4_out, not_3_out, not_2_out, not_1_out);
  and and_1 (and_1_out, ROMI0, not_3_out, not_2_out, not_1_out);
  and and_2 (and_2_out, not_4_out, ROMI1, not_2_out, not_1_out);
  and and_3 (and_3_out, ROMI0, ROMI1, not_2_out, not_1_out);
  and and_4 (and_4_out, not_4_out, not_3_out, ROMI2, not_1_out);
  and and_5 (and_5_out, ROMI0, not_3_out, ROMI2, not_1_out);
  and and_6 (and_6_out, not_4_out, ROMI1, ROMI2, not_1_out);
  and and_7 (and_7_out, ROMI0, ROMI1, ROMI2, not_1_out);
  and and_8 (and_8_out, not_4_out, not_3_out, not_2_out, ROMI3);
  and and_9 (and_9_out, ROMI0, not_3_out, not_2_out, ROMI3);
  and and_10 (and_10_out, not_4_out, ROMI1, not_2_out, ROMI3);
  and and_11 (and_11_out, ROMI0, ROMI1, not_2_out, ROMI3);
  and and_12 (and_12_out, not_4_out, not_3_out, ROMI2, ROMI3);
  and and_13 (and_13_out, ROMI0, not_3_out, ROMI2, ROMI3);
  and and_14 (and_14_out, not_4_out, ROMI1, ROMI2, ROMI3);
  and and_15 (and_15_out, ROMI0, ROMI1, ROMI2, ROMI3);
  or or_1 (or_1_out, and_31_out, and_30_out, and_29_out, and_28_out, and_27_out, and_26_out, and_25_out, and_24_out);
  and and_16 (and_16_out, DECORDER_4x16_out, 1'b0);
  and and_17 (and_17_out, and_1_out, 1'b0);
  and and_18 (and_18_out, and_2_out, 1'b1);
  and and_19 (and_19_out, and_3_out, 1'b0);
  and and_20 (and_20_out, and_4_out, 1'b0);
  and and_21 (and_21_out, and_5_out, 1'b0);
  and and_22 (and_22_out, and_6_out, 1'b0);
  and and_23 (and_23_out, and_7_out, 1'b0);
  and and_24 (and_24_out, and_8_out, 1'b0);
  and and_25 (and_25_out, and_9_out, 1'b0);
  and and_26 (and_26_out, and_10_out, 1'b0);
  and and_27 (and_27_out, and_11_out, 1'b0);
  and and_28 (and_28_out, and_12_out, 1'b0);
  and and_29 (and_29_out, and_13_out, 1'b0);
  and and_30 (and_30_out, and_14_out, 1'b0);
  and and_31 (and_31_out, and_15_out, 1'b0);
  or or_2 (OPC3, or_1_out, or_3_out);
  or or_3 (or_3_out, and_16_out, and_17_out, and_18_out, and_19_out, and_20_out, and_21_out, and_22_out, and_23_out);
  or or_4 (or_4_out, and_47_out, and_46_out, and_45_out, and_44_out, and_43_out, and_42_out, and_41_out, and_40_out);
  and and_32 (and_32_out, DECORDER_4x16_out, 1'b0);
  and and_33 (and_33_out, and_1_out, 1'b0);
  and and_34 (and_34_out, and_2_out, 1'b0);
  and and_35 (and_35_out, and_3_out, 1'b0);
  and and_36 (and_36_out, and_4_out, 1'b0);
  and and_37 (and_37_out, and_5_out, 1'b0);
  and and_38 (and_38_out, and_6_out, 1'b0);
  and and_39 (and_39_out, and_7_out, 1'b0);
  and and_40 (and_40_out, and_8_out, 1'b0);
  and and_41 (and_41_out, and_9_out, 1'b0);
  and and_42 (and_42_out, and_10_out, 1'b0);
  and and_43 (and_43_out, and_11_out, 1'b0);
  and and_44 (and_44_out, and_12_out, 1'b0);
  and and_45 (and_45_out, and_13_out, 1'b0);
  and and_46 (and_46_out, and_14_out, 1'b0);
  and and_47 (and_47_out, and_15_out, 1'b0);
  or or_5 (OPC2, or_4_out, or_6_out);
  or or_6 (or_6_out, and_32_out, and_33_out, and_34_out, and_35_out, and_36_out, and_37_out, and_38_out, and_39_out);
  or or_7 (or_7_out, and_63_out, and_62_out, and_61_out, and_60_out, and_59_out, and_58_out, and_57_out, and_56_out);
  and and_48 (and_48_out, DECORDER_4x16_out, 1'b0);
  and and_49 (and_49_out, and_1_out, 1'b0);
  and and_50 (and_50_out, and_2_out, 1'b0);
  and and_51 (and_51_out, and_3_out, 1'b0);
  and and_52 (and_52_out, and_4_out, 1'b0);
  and and_53 (and_53_out, and_5_out, 1'b0);
  and and_54 (and_54_out, and_6_out, 1'b0);
  and and_55 (and_55_out, and_7_out, 1'b0);
  and and_56 (and_56_out, and_8_out, 1'b0);
  and and_57 (and_57_out, and_9_out, 1'b0);
  and and_58 (and_58_out, and_10_out, 1'b0);
  and and_59 (and_59_out, and_11_out, 1'b0);
  and and_60 (and_60_out, and_12_out, 1'b0);
  and and_61 (and_61_out, and_13_out, 1'b0);
  and and_62 (and_62_out, and_14_out, 1'b0);
  and and_63 (and_63_out, and_15_out, 1'b0);
  or or_8 (or_8_out, and_48_out, and_49_out, and_50_out, and_51_out, and_52_out, and_53_out, and_54_out, and_55_out);
  or or_9 (OPC1, or_7_out, or_8_out);
  or or_10 (or_10_out, and_79_out, and_78_out, and_77_out, and_76_out, and_75_out, and_74_out, and_73_out, and_72_out);
  and and_64 (and_64_out, DECORDER_4x16_out, 1'b0);
  and and_65 (and_65_out, and_1_out, 1'b1);
  and and_66 (and_66_out, and_2_out, 1'b1);
  and and_67 (and_67_out, and_3_out, 1'b0);
  and and_68 (and_68_out, and_4_out, 1'b0);
  and and_69 (and_69_out, and_5_out, 1'b0);
  and and_70 (and_70_out, and_6_out, 1'b0);
  and and_71 (and_71_out, and_7_out, 1'b0);
  and and_72 (and_72_out, and_8_out, 1'b0);
  and and_73 (and_73_out, and_9_out, 1'b0);
  and and_74 (and_74_out, and_10_out, 1'b0);
  and and_75 (and_75_out, and_11_out, 1'b0);
  and and_76 (and_76_out, and_12_out, 1'b0);
  and and_77 (and_77_out, and_13_out, 1'b0);
  and and_78 (and_78_out, and_14_out, 1'b0);
  and and_79 (and_79_out, and_15_out, 1'b0);
  or or_11 (OPC0, or_10_out, or_12_out);
  or or_12 (or_12_out, and_64_out, and_65_out, and_66_out, and_67_out, and_68_out, and_69_out, and_70_out, and_71_out);
  or or_13 (or_13_out, and_95_out, and_94_out, and_93_out, and_92_out, and_91_out, and_90_out, and_89_out, and_88_out);
  and and_80 (and_80_out, DECORDER_4x16_out, 1'b0);
  and and_81 (and_81_out, and_1_out, 1'b0);
  and and_82 (and_82_out, and_2_out, 1'b0);
  and and_83 (and_83_out, and_3_out, 1'b0);
  and and_84 (and_84_out, and_4_out, 1'b0);
  and and_85 (and_85_out, and_5_out, 1'b0);
  and and_86 (and_86_out, and_6_out, 1'b0);
  and and_87 (and_87_out, and_7_out, 1'b0);
  and and_88 (and_88_out, and_8_out, 1'b0);
  and and_89 (and_89_out, and_9_out, 1'b0);
  and and_90 (and_90_out, and_10_out, 1'b0);
  and and_91 (and_91_out, and_11_out, 1'b0);
  and and_92 (and_92_out, and_12_out, 1'b0);
  and and_93 (and_93_out, and_13_out, 1'b0);
  and and_94 (and_94_out, and_14_out, 1'b0);
  and and_95 (and_95_out, and_15_out, 1'b0);
  or or_14 (OPRAND3, or_13_out, or_15_out);
  or or_15 (or_15_out, and_80_out, and_81_out, and_82_out, and_83_out, and_84_out, and_85_out, and_86_out, and_87_out);
  or or_16 (or_16_out, and_111_out, and_110_out, and_109_out, and_108_out, and_107_out, and_106_out, and_105_out, and_104_out);
  and and_96 (and_96_out, DECORDER_4x16_out, 1'b0);
  and and_97 (and_97_out, and_1_out, 1'b0);
  and and_98 (and_98_out, and_2_out, 1'b1);
  and and_99 (and_99_out, and_3_out, 1'b0);
  and and_100 (and_100_out, and_4_out, 1'b0);
  and and_101 (and_101_out, and_5_out, 1'b0);
  and and_102 (and_102_out, and_6_out, 1'b0);
  and and_103 (and_103_out, and_7_out, 1'b0);
  and and_104 (and_104_out, and_8_out, 1'b0);
  and and_105 (and_105_out, and_9_out, 1'b0);
  and and_106 (and_106_out, and_10_out, 1'b0);
  and and_107 (and_107_out, and_11_out, 1'b0);
  and and_108 (and_108_out, and_12_out, 1'b0);
  and and_109 (and_109_out, and_13_out, 1'b0);
  and and_110 (and_110_out, and_14_out, 1'b0);
  and and_111 (and_111_out, and_15_out, 1'b0);
  or or_17 (OPRAND2, or_16_out, or_18_out);
  or or_18 (or_18_out, and_96_out, and_97_out, and_98_out, and_99_out, and_100_out, and_101_out, and_102_out, and_103_out);
  or or_19 (or_19_out, and_127_out, and_126_out, and_125_out, and_124_out, and_123_out, and_122_out, and_121_out, and_120_out);
  and and_112 (and_112_out, DECORDER_4x16_out, 1'b0);
  and and_113 (and_113_out, and_1_out, 1'b0);
  and and_114 (and_114_out, and_2_out, 1'b0);
  and and_115 (and_115_out, and_3_out, 1'b0);
  and and_116 (and_116_out, and_4_out, 1'b1);
  and and_117 (and_117_out, and_5_out, 1'b0);
  and and_118 (and_118_out, and_6_out, 1'b0);
  and and_119 (and_119_out, and_7_out, 1'b0);
  and and_120 (and_120_out, and_8_out, 1'b0);
  and and_121 (and_121_out, and_9_out, 1'b0);
  and and_122 (and_122_out, and_10_out, 1'b0);
  and and_123 (and_123_out, and_11_out, 1'b0);
  and and_124 (and_124_out, and_12_out, 1'b0);
  and and_125 (and_125_out, and_13_out, 1'b0);
  and and_126 (and_126_out, and_14_out, 1'b0);
  and and_127 (and_127_out, and_15_out, 1'b0);
  or or_20 (OPRAND1, or_19_out, or_21_out);
  or or_21 (or_21_out, and_112_out, and_113_out, and_114_out, and_115_out, and_116_out, and_117_out, and_118_out, and_119_out);
  or or_22 (or_22_out, and_143_out, and_142_out, and_141_out, and_140_out, and_139_out, and_138_out, and_137_out, and_136_out);
  and and_128 (and_128_out, DECORDER_4x16_out, 1'b1);
  and and_129 (and_129_out, and_1_out, 1'b1);
  and and_130 (and_130_out, and_2_out, 1'b0);
  and and_131 (and_131_out, and_3_out, 1'b1);
  and and_132 (and_132_out, and_4_out, 1'b1);
  and and_133 (and_133_out, and_5_out, 1'b0);
  and and_134 (and_134_out, and_6_out, 1'b0);
  and and_135 (and_135_out, and_7_out, 1'b0);
  and and_136 (and_136_out, and_8_out, 1'b0);
  and and_137 (and_137_out, and_9_out, 1'b0);
  and and_138 (and_138_out, and_10_out, 1'b0);
  and and_139 (and_139_out, and_11_out, 1'b0);
  and and_140 (and_140_out, and_12_out, 1'b0);
  and and_141 (and_141_out, and_13_out, 1'b0);
  and and_142 (and_142_out, and_14_out, 1'b0);
  and and_143 (and_143_out, and_15_out, 1'b0);
  or or_23 (OPRAND0, or_22_out, or_24_out);
  or or_24 (or_24_out, and_128_out, and_129_out, and_130_out, and_131_out, and_132_out, and_133_out, and_134_out, and_135_out);
endmodule

module JN_TESTER (
  input  ROMI3,
  input  ROMI2,
  input  ROMI1,
  input  ROMI0,
  output OPC3,
  output OPC2,
  output OPC1,
  output OPC0,
  output OPRAND3,
  output OPRAND2,
  output OPRAND1,
  output OPRAND0
);

  wire and_1_out, and_2_out, and_3_out, and_4_out, and_5_out, and_6_out, and_7_out, and_8_out, and_9_out,
       and_10_out, and_11_out, and_12_out, and_13_out, and_14_out, and_15_out, and_16_out, and_17_out,
       and_18_out, and_19_out, and_20_out, and_21_out, and_22_out, and_23_out, and_24_out, and_25_out,
       and_26_out, and_27_out, and_28_out, and_29_out, and_30_out, and_31_out, and_32_out, and_33_out,
       and_34_out, and_35_out, and_36_out, and_37_out, and_38_out, and_39_out, and_40_out, and_41_out,
       and_42_out, and_43_out, and_44_out, and_45_out, and_46_out, and_47_out, and_48_out, and_49_out,
       and_50_out, and_51_out, and_52_out, and_53_out, and_54_out, and_55_out, and_56_out, and_57_out,
       and_58_out, and_59_out, and_60_out, and_61_out, and_62_out, and_63_out, and_64_out, and_65_out,
       and_66_out, and_67_out, and_68_out, and_69_out, and_70_out, and_71_out, and_72_out, and_73_out,
       and_74_out, and_75_out, and_76_out, and_77_out, and_78_out, and_79_out, and_80_out, and_81_out,
       and_82_out, and_83_out, and_84_out, and_85_out, and_86_out, and_87_out, and_88_out, and_89_out,
       and_90_out, and_91_out, and_92_out, and_93_out, and_94_out, and_95_out, and_96_out, and_97_out,
       and_98_out, and_99_out, and_100_out, and_101_out, and_102_out, and_103_out, and_104_out, and_105_out,
       and_106_out, and_107_out, and_108_out, and_109_out, and_110_out, and_111_out, and_112_out,
       and_113_out, and_114_out, and_115_out, and_116_out, and_117_out, and_118_out, and_119_out,
       and_120_out, and_121_out, and_122_out, and_123_out, and_124_out, and_125_out, and_126_out,
       and_127_out, and_128_out, and_129_out, and_130_out, and_131_out, and_132_out, and_133_out,
       and_134_out, and_135_out, and_136_out, and_137_out, and_138_out, and_139_out, and_140_out,
       and_141_out, and_142_out, and_143_out, DECORDER_4x16_out, not_1_out, not_2_out, not_3_out, not_4_out,
       or_1_out, or_3_out, or_4_out, or_6_out, or_7_out, or_8_out, or_10_out, or_12_out, or_13_out,
       or_15_out, or_16_out, or_18_out, or_19_out, or_21_out, or_22_out, or_24_out;

  not not_1 (not_1_out, ROMI3);
  not not_2 (not_2_out, ROMI2);
  not not_3 (not_3_out, ROMI1);
  not not_4 (not_4_out, ROMI0);
  and DECORDER_4x16 (DECORDER_4x16_out, not_4_out, not_3_out, not_2_out, not_1_out);
  and and_1 (and_1_out, ROMI0, not_3_out, not_2_out, not_1_out);
  and and_2 (and_2_out, not_4_out, ROMI1, not_2_out, not_1_out);
  and and_3 (and_3_out, ROMI0, ROMI1, not_2_out, not_1_out);
  and and_4 (and_4_out, not_4_out, not_3_out, ROMI2, not_1_out);
  and and_5 (and_5_out, ROMI0, not_3_out, ROMI2, not_1_out);
  and and_6 (and_6_out, not_4_out, ROMI1, ROMI2, not_1_out);
  and and_7 (and_7_out, ROMI0, ROMI1, ROMI2, not_1_out);
  and and_8 (and_8_out, not_4_out, not_3_out, not_2_out, ROMI3);
  and and_9 (and_9_out, ROMI0, not_3_out, not_2_out, ROMI3);
  and and_10 (and_10_out, not_4_out, ROMI1, not_2_out, ROMI3);
  and and_11 (and_11_out, ROMI0, ROMI1, not_2_out, ROMI3);
  and and_12 (and_12_out, not_4_out, not_3_out, ROMI2, ROMI3);
  and and_13 (and_13_out, ROMI0, not_3_out, ROMI2, ROMI3);
  and and_14 (and_14_out, not_4_out, ROMI1, ROMI2, ROMI3);
  and and_15 (and_15_out, ROMI0, ROMI1, ROMI2, ROMI3);
  or or_1 (or_1_out, and_31_out, and_30_out, and_29_out, and_28_out, and_27_out, and_26_out, and_25_out, and_24_out);
  and and_16 (and_16_out, DECORDER_4x16_out, 1'b0);
  and and_17 (and_17_out, and_1_out, 1'b0);
  and and_18 (and_18_out, and_2_out, 1'b1);
  and and_19 (and_19_out, and_3_out, 1'b0);
  and and_20 (and_20_out, and_4_out, 1'b0);
  and and_21 (and_21_out, and_5_out, 1'b0);
  and and_22 (and_22_out, and_6_out, 1'b0);
  and and_23 (and_23_out, and_7_out, 1'b0);
  and and_24 (and_24_out, and_8_out, 1'b0);
  and and_25 (and_25_out, and_9_out, 1'b0);
  and and_26 (and_26_out, and_10_out, 1'b0);
  and and_27 (and_27_out, and_11_out, 1'b0);
  and and_28 (and_28_out, and_12_out, 1'b0);
  and and_29 (and_29_out, and_13_out, 1'b0);
  and and_30 (and_30_out, and_14_out, 1'b0);
  and and_31 (and_31_out, and_15_out, 1'b0);
  or or_2 (OPC3, or_1_out, or_3_out);
  or or_3 (or_3_out, and_16_out, and_17_out, and_18_out, and_19_out, and_20_out, and_21_out, and_22_out, and_23_out);
  or or_4 (or_4_out, and_47_out, and_46_out, and_45_out, and_44_out, and_43_out, and_42_out, and_41_out, and_40_out);
  and and_32 (and_32_out, DECORDER_4x16_out, 1'b0);
  and and_33 (and_33_out, and_1_out, 1'b0);
  and and_34 (and_34_out, and_2_out, 1'b0);
  and and_35 (and_35_out, and_3_out, 1'b0);
  and and_36 (and_36_out, and_4_out, 1'b0);
  and and_37 (and_37_out, and_5_out, 1'b0);
  and and_38 (and_38_out, and_6_out, 1'b0);
  and and_39 (and_39_out, and_7_out, 1'b0);
  and and_40 (and_40_out, and_8_out, 1'b0);
  and and_41 (and_41_out, and_9_out, 1'b0);
  and and_42 (and_42_out, and_10_out, 1'b0);
  and and_43 (and_43_out, and_11_out, 1'b0);
  and and_44 (and_44_out, and_12_out, 1'b0);
  and and_45 (and_45_out, and_13_out, 1'b0);
  and and_46 (and_46_out, and_14_out, 1'b0);
  and and_47 (and_47_out, and_15_out, 1'b0);
  or or_5 (OPC2, or_4_out, or_6_out);
  or or_6 (or_6_out, and_32_out, and_33_out, and_34_out, and_35_out, and_36_out, and_37_out, and_38_out, and_39_out);
  or or_7 (or_7_out, and_63_out, and_62_out, and_61_out, and_60_out, and_59_out, and_58_out, and_57_out, and_56_out);
  and and_48 (and_48_out, DECORDER_4x16_out, 1'b0);
  and and_49 (and_49_out, and_1_out, 1'b0);
  and and_50 (and_50_out, and_2_out, 1'b1);
  and and_51 (and_51_out, and_3_out, 1'b0);
  and and_52 (and_52_out, and_4_out, 1'b0);
  and and_53 (and_53_out, and_5_out, 1'b0);
  and and_54 (and_54_out, and_6_out, 1'b0);
  and and_55 (and_55_out, and_7_out, 1'b0);
  and and_56 (and_56_out, and_8_out, 1'b0);
  and and_57 (and_57_out, and_9_out, 1'b0);
  and and_58 (and_58_out, and_10_out, 1'b0);
  and and_59 (and_59_out, and_11_out, 1'b0);
  and and_60 (and_60_out, and_12_out, 1'b0);
  and and_61 (and_61_out, and_13_out, 1'b0);
  and and_62 (and_62_out, and_14_out, 1'b0);
  and and_63 (and_63_out, and_15_out, 1'b0);
  or or_8 (or_8_out, and_48_out, and_49_out, and_50_out, and_51_out, and_52_out, and_53_out, and_54_out, and_55_out);
  or or_9 (OPC1, or_7_out, or_8_out);
  or or_10 (or_10_out, and_79_out, and_78_out, and_77_out, and_76_out, and_75_out, and_74_out, and_73_out, and_72_out);
  and and_64 (and_64_out, DECORDER_4x16_out, 1'b0);
  and and_65 (and_65_out, and_1_out, 1'b1);
  and and_66 (and_66_out, and_2_out, 1'b0);
  and and_67 (and_67_out, and_3_out, 1'b0);
  and and_68 (and_68_out, and_4_out, 1'b0);
  and and_69 (and_69_out, and_5_out, 1'b0);
  and and_70 (and_70_out, and_6_out, 1'b0);
  and and_71 (and_71_out, and_7_out, 1'b0);
  and and_72 (and_72_out, and_8_out, 1'b0);
  and and_73 (and_73_out, and_9_out, 1'b0);
  and and_74 (and_74_out, and_10_out, 1'b0);
  and and_75 (and_75_out, and_11_out, 1'b0);
  and and_76 (and_76_out, and_12_out, 1'b0);
  and and_77 (and_77_out, and_13_out, 1'b0);
  and and_78 (and_78_out, and_14_out, 1'b0);
  and and_79 (and_79_out, and_15_out, 1'b0);
  or or_11 (OPC0, or_10_out, or_12_out);
  or or_12 (or_12_out, and_64_out, and_65_out, and_66_out, and_67_out, and_68_out, and_69_out, and_70_out, and_71_out);
  or or_13 (or_13_out, and_95_out, and_94_out, and_93_out, and_92_out, and_91_out, and_90_out, and_89_out, and_88_out);
  and and_80 (and_80_out, DECORDER_4x16_out, 1'b0);
  and and_81 (and_81_out, and_1_out, 1'b0);
  and and_82 (and_82_out, and_2_out, 1'b0);
  and and_83 (and_83_out, and_3_out, 1'b0);
  and and_84 (and_84_out, and_4_out, 1'b0);
  and and_85 (and_85_out, and_5_out, 1'b0);
  and and_86 (and_86_out, and_6_out, 1'b0);
  and and_87 (and_87_out, and_7_out, 1'b0);
  and and_88 (and_88_out, and_8_out, 1'b0);
  and and_89 (and_89_out, and_9_out, 1'b0);
  and and_90 (and_90_out, and_10_out, 1'b0);
  and and_91 (and_91_out, and_11_out, 1'b0);
  and and_92 (and_92_out, and_12_out, 1'b0);
  and and_93 (and_93_out, and_13_out, 1'b0);
  and and_94 (and_94_out, and_14_out, 1'b0);
  and and_95 (and_95_out, and_15_out, 1'b0);
  or or_14 (OPRAND3, or_13_out, or_15_out);
  or or_15 (or_15_out, and_80_out, and_81_out, and_82_out, and_83_out, and_84_out, and_85_out, and_86_out, and_87_out);
  or or_16 (or_16_out, and_111_out, and_110_out, and_109_out, and_108_out, and_107_out, and_106_out, and_105_out, and_104_out);
  and and_96 (and_96_out, DECORDER_4x16_out, 1'b0);
  and and_97 (and_97_out, and_1_out, 1'b0);
  and and_98 (and_98_out, and_2_out, 1'b1);
  and and_99 (and_99_out, and_3_out, 1'b0);
  and and_100 (and_100_out, and_4_out, 1'b0);
  and and_101 (and_101_out, and_5_out, 1'b0);
  and and_102 (and_102_out, and_6_out, 1'b0);
  and and_103 (and_103_out, and_7_out, 1'b0);
  and and_104 (and_104_out, and_8_out, 1'b0);
  and and_105 (and_105_out, and_9_out, 1'b0);
  and and_106 (and_106_out, and_10_out, 1'b0);
  and and_107 (and_107_out, and_11_out, 1'b0);
  and and_108 (and_108_out, and_12_out, 1'b0);
  and and_109 (and_109_out, and_13_out, 1'b0);
  and and_110 (and_110_out, and_14_out, 1'b0);
  and and_111 (and_111_out, and_15_out, 1'b0);
  or or_17 (OPRAND2, or_16_out, or_18_out);
  or or_18 (or_18_out, and_96_out, and_97_out, and_98_out, and_99_out, and_100_out, and_101_out, and_102_out, and_103_out);
  or or_19 (or_19_out, and_127_out, and_126_out, and_125_out, and_124_out, and_123_out, and_122_out, and_121_out, and_120_out);
  and and_112 (and_112_out, DECORDER_4x16_out, 1'b0);
  and and_113 (and_113_out, and_1_out, 1'b0);
  and and_114 (and_114_out, and_2_out, 1'b0);
  and and_115 (and_115_out, and_3_out, 1'b0);
  and and_116 (and_116_out, and_4_out, 1'b1);
  and and_117 (and_117_out, and_5_out, 1'b0);
  and and_118 (and_118_out, and_6_out, 1'b0);
  and and_119 (and_119_out, and_7_out, 1'b0);
  and and_120 (and_120_out, and_8_out, 1'b0);
  and and_121 (and_121_out, and_9_out, 1'b0);
  and and_122 (and_122_out, and_10_out, 1'b0);
  and and_123 (and_123_out, and_11_out, 1'b0);
  and and_124 (and_124_out, and_12_out, 1'b0);
  and and_125 (and_125_out, and_13_out, 1'b0);
  and and_126 (and_126_out, and_14_out, 1'b0);
  and and_127 (and_127_out, and_15_out, 1'b0);
  or or_20 (OPRAND1, or_19_out, or_21_out);
  or or_21 (or_21_out, and_112_out, and_113_out, and_114_out, and_115_out, and_116_out, and_117_out, and_118_out, and_119_out);
  or or_22 (or_22_out, and_143_out, and_142_out, and_141_out, and_140_out, and_139_out, and_138_out, and_137_out, and_136_out);
  and and_128 (and_128_out, DECORDER_4x16_out, 1'b0);
  and and_129 (and_129_out, and_1_out, 1'b1);
  and and_130 (and_130_out, and_2_out, 1'b0);
  and and_131 (and_131_out, and_3_out, 1'b1);
  and and_132 (and_132_out, and_4_out, 1'b1);
  and and_133 (and_133_out, and_5_out, 1'b0);
  and and_134 (and_134_out, and_6_out, 1'b0);
  and and_135 (and_135_out, and_7_out, 1'b0);
  and and_136 (and_136_out, and_8_out, 1'b0);
  and and_137 (and_137_out, and_9_out, 1'b0);
  and and_138 (and_138_out, and_10_out, 1'b0);
  and and_139 (and_139_out, and_11_out, 1'b0);
  and and_140 (and_140_out, and_12_out, 1'b0);
  and and_141 (and_141_out, and_13_out, 1'b0);
  and and_142 (and_142_out, and_14_out, 1'b0);
  and and_143 (and_143_out, and_15_out, 1'b0);
  or or_23 (OPRAND0, or_22_out, or_24_out);
  or or_24 (or_24_out, and_128_out, and_129_out, and_130_out, and_131_out, and_132_out, and_133_out, and_134_out, and_135_out);
endmodule

module ALU_EXT (
  input  A_3,
  input  A_2,
  input  A_1,
  input  A_0,
  input  B_3,
  input  B_2,
  input  B_1,
  input  B_0,
  input  S2,
  input  S1,
  input  S0,
  output OVF,
  output N,
  output C,
  output Z,
  output O_3,
  output O_2,
  output O_1,
  output O_0
);

  wire Adder_out, and_1_out, and_2_out, and_3_out, and_4_out, and_5_out, and_6_out, and_7_out, and_8_out,
       and_9_out, and_10_out, and_11_out, and_12_out, and_13_out, and_14_out, and_15_out, and_16_out,
       and_17_out, and_18_out, and_19_out, and_20_out, and_21_out, and_22_out, and_23_out, and_24_out,
       and_25_out, and_26_out, and_27_out, and_28_out, and_29_out, and_30_out, and_31_out, and_32_out,
       and_33_out, and_34_out, and_35_out, and_36_out, and_37_out, and_38_out, and_39_out, and_40_out,
       and_41_out, and_42_out, and_43_out, and_44_out, and_45_out, and_46_out, and_47_out, and_48_out,
       and_49_out, and_50_out, and_51_out, and_52_out, and_53_out, and_54_out, and_55_out, and_56_out,
       and_57_out, and_58_out, and_59_out, and_60_out, ANDOP_out, MUX2x1_out, not_1_out, not_2_out,
       not_3_out, not_4_out, not_5_out, not_6_out, not_7_out, not_8_out, not_9_out, not_10_out, not_11_out,
       not_12_out, not_13_out, not_14_out, not_15_out, not_16_out, not_17_out, not_18_out, not_19_out,
       not_20_out, not_21_out, not_22_out, or_1_out, or_2_out, or_3_out, or_4_out, or_5_out, or_6_out,
       or_7_out, or_8_out, or_9_out, or_10_out, or_11_out, or_12_out, or_13_out, or_14_out, or_15_out,
       or_19_out, or_20_out, OROP_out, Subtractor_out, xor_1_out, xor_2_out, xor_3_out, xor_4_out, xor_5_out,
       xor_6_out, xor_7_out, xor_8_out, xor_9_out, xor_10_out, xor_11_out, xor_12_out, xor_13_out,
       xor_14_out, xor_15_out, xor_16_out, xor_17_out, xor_18_out, xor_19_out, XOROP_out;

  not not_1 (not_1_out, A_0);
  not not_2 (not_2_out, A_1);
  not not_3 (not_3_out, A_2);
  not not_4 (not_4_out, A_3);
  xor Adder (Adder_out, A_0, B_0);
  xor xor_1 (xor_1_out, A_1, B_1);
  xor xor_2 (xor_2_out, A_2, B_2);
  xor xor_3 (xor_3_out, A_3, B_3);
  and and_1 (and_1_out, not_1_out, B_0);
  and and_2 (and_2_out, not_1_out, 1'b0);
  and and_3 (and_3_out, B_0, 1'b0);
  xor xor_4 (xor_4_out, A_1, B_1);
  and and_4 (and_4_out, not_2_out, B_1);
  and and_5 (and_5_out, not_2_out, or_8_out);
  and and_6 (and_6_out, B_1, or_8_out);
  xor xor_5 (xor_5_out, A_2, B_2);
  and and_7 (and_7_out, not_3_out, B_2);
  and and_8 (and_8_out, not_3_out, or_9_out);
  and and_9 (and_9_out, B_2, or_9_out);
  xor xor_6 (xor_6_out, A_3, B_3);
  and and_10 (and_10_out, not_4_out, B_3);
  and and_11 (and_11_out, not_4_out, or_10_out);
  and and_12 (and_12_out, B_3, or_10_out);
  xor Subtractor (Subtractor_out, A_0, B_0);
  or or_1 (or_1_out, and_1_out, and_2_out);
  or or_2 (or_2_out, and_4_out, and_5_out);
  or or_3 (or_3_out, and_7_out, and_8_out);
  or or_4 (or_4_out, and_10_out, and_11_out);
  and ANDOP (ANDOP_out, A_0, B_0);
  and and_13 (and_13_out, A_1, B_1);
  and and_14 (and_14_out, A_2, B_2);
  and and_15 (and_15_out, A_3, B_3);
  or OROP (OROP_out, A_0, B_0);
  or or_5 (or_5_out, A_1, B_1);
  or or_6 (or_6_out, A_2, B_2);
  or or_7 (or_7_out, A_3, B_3);
  xor XOROP (XOROP_out, A_0, B_0);
  xor xor_7 (xor_7_out, A_1, B_1);
  xor xor_8 (xor_8_out, A_2, B_2);
  xor xor_9 (xor_9_out, A_3, B_3);
  not not_5 (not_5_out, A_0);
  not not_6 (not_6_out, A_1);
  not not_7 (not_7_out, A_2);
  not not_8 (not_8_out, A_3);
  xor xor_10 (xor_10_out, 1'b0, Adder_out);
  and and_16 (and_16_out, 1'b0, Adder_out);
  and and_17 (and_17_out, A_0, B_0);
  xor xor_11 (xor_11_out, or_12_out, xor_1_out);
  and and_18 (and_18_out, or_12_out, xor_1_out);
  and and_19 (and_19_out, A_1, B_1);
  xor xor_12 (xor_12_out, or_13_out, xor_2_out);
  and and_20 (and_20_out, or_13_out, xor_2_out);
  and and_21 (and_21_out, A_2, B_2);
  xor xor_13 (xor_13_out, or_14_out, xor_3_out);
  and and_22 (and_22_out, or_14_out, xor_3_out);
  and and_23 (and_23_out, A_3, B_3);
  or or_8 (or_8_out, or_1_out, and_3_out);
  xor xor_14 (xor_14_out, xor_4_out, or_8_out);
  or or_9 (or_9_out, or_2_out, and_6_out);
  xor xor_15 (xor_15_out, xor_5_out, or_9_out);
  or or_10 (or_10_out, or_3_out, and_9_out);
  xor xor_16 (xor_16_out, xor_6_out, or_10_out);
  or or_11 (or_11_out, or_4_out, and_12_out);
  xor xor_17 (xor_17_out, Subtractor_out, 1'b0);
  or or_12 (or_12_out, and_16_out, and_17_out);
  or or_13 (or_13_out, and_18_out, and_19_out);
  or or_14 (or_14_out, and_20_out, and_21_out);
  or or_15 (or_15_out, and_22_out, and_23_out);
  xor xor_18 (xor_18_out, or_14_out, or_15_out);
  xor xor_19 (xor_19_out, or_10_out, or_11_out);
  not not_9 (not_9_out, S2);
  not not_10 (not_10_out, S2);
  not not_11 (not_11_out, S2);
  not not_12 (not_12_out, S2);
  not not_13 (not_13_out, S1);
  not not_14 (not_14_out, S1);
  not not_15 (not_15_out, S1);
  not not_16 (not_16_out, S1);
  not not_17 (not_17_out, S0);
  not not_18 (not_18_out, S0);
  not not_19 (not_19_out, S0);
  not not_20 (not_20_out, S0);
  and and_24 (and_24_out, xor_10_out, not_17_out, not_13_out, not_9_out);
  and and_25 (and_25_out, xor_17_out, S0, not_13_out, not_9_out);
  and and_26 (and_26_out, ANDOP_out, not_17_out, S1, not_9_out);
  and and_27 (and_27_out, OROP_out, S0, S1, not_9_out);
  and and_28 (and_28_out, XOROP_out, not_17_out, not_13_out, S2);
  and and_29 (and_29_out, not_5_out, S0, not_13_out, S2);
  and and_30 (and_30_out, xor_10_out, not_17_out, S1, S2);
  and and_31 (and_31_out, xor_17_out, S0, S1, S2);
  and and_32 (and_32_out, xor_11_out, not_18_out, not_14_out, not_10_out);
  and and_33 (and_33_out, xor_14_out, S0, not_14_out, not_10_out);
  and and_34 (and_34_out, and_13_out, not_18_out, S1, not_10_out);
  and and_35 (and_35_out, or_5_out, S0, S1, not_10_out);
  and and_36 (and_36_out, xor_7_out, not_18_out, not_14_out, S2);
  and and_37 (and_37_out, not_6_out, S0, not_14_out, S2);
  and and_38 (and_38_out, xor_11_out, not_18_out, S1, S2);
  and and_39 (and_39_out, xor_14_out, S0, S1, S2);
  and and_40 (and_40_out, xor_12_out, not_19_out, not_15_out, not_11_out);
  and and_41 (and_41_out, xor_15_out, S0, not_15_out, not_11_out);
  and and_42 (and_42_out, and_14_out, not_19_out, S1, not_11_out);
  and and_43 (and_43_out, or_6_out, S0, S1, not_11_out);
  and and_44 (and_44_out, xor_8_out, not_19_out, not_15_out, S2);
  and and_45 (and_45_out, not_7_out, S0, not_15_out, S2);
  and and_46 (and_46_out, xor_12_out, not_19_out, S1, S2);
  and and_47 (and_47_out, xor_15_out, S0, S1, S2);
  and and_48 (and_48_out, xor_13_out, not_20_out, not_16_out, not_12_out);
  and and_49 (and_49_out, xor_16_out, S0, not_16_out, not_12_out);
  and and_50 (and_50_out, and_15_out, not_20_out, S1, not_12_out);
  and and_51 (and_51_out, or_7_out, S0, S1, not_12_out);
  and and_52 (and_52_out, xor_9_out, not_20_out, not_16_out, S2);
  and and_53 (and_53_out, not_8_out, S0, not_16_out, S2);
  and and_54 (and_54_out, xor_13_out, not_20_out, S1, S2);
  and and_55 (and_55_out, xor_16_out, S0, S1, S2);
  and and_56 (and_56_out, not_13_out, not_9_out);
  or MUX8x1 (O_0, and_24_out, and_25_out, and_26_out, and_27_out, and_28_out, and_29_out, and_30_out, and_31_out);
  or or_16 (O_1, and_32_out, and_33_out, and_34_out, and_35_out, and_36_out, and_37_out, and_38_out, and_39_out);
  or or_17 (O_2, and_40_out, and_41_out, and_42_out, and_43_out, and_44_out, and_45_out, and_46_out, and_47_out);
  or or_18 (N, and_48_out, and_49_out, and_50_out, and_51_out, and_52_out, and_53_out, and_54_out, and_55_out);
  not not_21 (not_21_out, S0);
  not not_22 (not_22_out, S0);
  or or_19 (or_19_out, O_0, O_1, O_2, N);
  not not_23 (Z, or_19_out);
  and and_57 (and_57_out, not_21_out, xor_18_out);
  and and_58 (and_58_out, S0, xor_19_out);
  and and_59 (and_59_out, not_22_out, or_15_out);
  and and_60 (and_60_out, S0, or_11_out);
  or MUX2x1 (MUX2x1_out, and_57_out, and_58_out);
  or or_20 (or_20_out, and_59_out, and_60_out);
  and VALIDOPCODE (OVF, MUX2x1_out, and_56_out);
  and and_61 (C, or_20_out, and_56_out);

  assign O_3 = N;
endmodule

module CPU_v1 (
  input  in_1,
  output OVF,
  output N,
  output C,
  output Z,
  output out_6,
  output out_7,
  output out_8,
  output out_9,
  output out_10,
  output out_11,
  output out_12,
  output out_13,
  output out_14,
  output out_15,
  output out_16,
  output out_17
);

  wire ACC_INPUT_0_o, ACC_INPUT_1_o, ACC_INPUT_2_o, ACC_INPUT_3_o, alu_ext_1_c, alu_ext_1_n, alu_ext_1_o_0,
       alu_ext_1_o_1, alu_ext_1_o_2, alu_ext_1_o_3, alu_ext_1_ovf, alu_ext_1_z, and_1_out, clock_1_out,
       ctrlunit_ext_1_ctrl_b0, ctrlunit_ext_1_ctrl_b1, ctrlunit_ext_1_ctrl_b2, ctrlunit_ext_1_ctrl_b3,
       ctrlunit_ext_1_ctrl_op0, ctrlunit_ext_1_ctrl_op1, ctrlunit_ext_1_ctrl_op2, ctrlunit_ext_1_ctrl_we,
       ctrlunit_ext_1_hlt_sig, ctrlunit_ext_1_jmp_sig, ctrlunit_ext_1_ldi_sig, ldi_tester_1_opc0,
       ldi_tester_1_opc1, ldi_tester_1_opc2, ldi_tester_1_opc3, ldi_tester_1_oprand0, ldi_tester_1_oprand1,
       ldi_tester_1_oprand2, ldi_tester_1_oprand3, not_1_out, not_2_out, PC_REG_reg_o0, PC_REG_reg_o1,
       PC_REG_reg_o2, PC_REG_reg_o3, progcounter_ext_1_pco0, progcounter_ext_1_pco1, progcounter_ext_1_pco2,
       progcounter_ext_1_pco3;

  ProgCounter_EXT progcounter_ext_1 (
    .A3(PC_REG_reg_o3), .A2(PC_REG_reg_o2), .A1(PC_REG_reg_o1), .A0(PC_REG_reg_o0),
    .PC_OPR3(ctrlunit_ext_1_ctrl_b3), .PC_OPR2(ctrlunit_ext_1_ctrl_b2), .PC_OPR1(ctrlunit_ext_1_ctrl_b1),
    .PC_OPR0(ctrlunit_ext_1_ctrl_b0), .JMP_JZ(ctrlunit_ext_1_jmp_sig), .PCO3(progcounter_ext_1_pco3),
    .PCO2(progcounter_ext_1_pco2), .PCO1(progcounter_ext_1_pco1), .PCO0(progcounter_ext_1_pco0));  // open: FTCH
  REGISTER_4BIT PC_REG (
    .HARD_RESET(in_1), .CLK(clock_1_out), .REG_I3(progcounter_ext_1_pco3), .REG_I2(progcounter_ext_1_pco2),
    .REG_I1(progcounter_ext_1_pco1), .REG_I0(progcounter_ext_1_pco0), .WE(not_2_out), .REG_O3(PC_REG_reg_o3),
    .REG_O2(PC_REG_reg_o2), .REG_O1(PC_REG_reg_o1), .REG_O0(PC_REG_reg_o0));
  LDI_TESTER ldi_tester_1 (
    .ROMI3(PC_REG_reg_o3), .ROMI2(PC_REG_reg_o2), .ROMI1(PC_REG_reg_o1), .ROMI0(PC_REG_reg_o0),
    .OPC3(ldi_tester_1_opc3), .OPC2(ldi_tester_1_opc2), .OPC1(ldi_tester_1_opc1), .OPC0(ldi_tester_1_opc0),
    .OPRAND3(ldi_tester_1_oprand3), .OPRAND2(ldi_tester_1_oprand2), .OPRAND1(ldi_tester_1_oprand1),
    .OPRAND0(ldi_tester_1_oprand0));
  REGISTER_4BIT INSTRUCTION_REG_OPC (
    .HARD_RESET(in_1), .CLK(clock_1_out), .REG_I3(ldi_tester_1_opc3), .REG_I2(ldi_tester_1_opc2),
    .REG_I1(ldi_tester_1_opc1), .REG_I0(ldi_tester_1_opc0), .WE(not_2_out), .REG_O3(out_10), .REG_O2(out_11),
    .REG_O1(out_12), .REG_O0(out_13));
  REGISTER_4BIT INSTRUCTION_REG_OPR (
    .HARD_RESET(in_1), .CLK(clock_1_out), .REG_I3(ldi_tester_1_oprand3), .REG_I2(ldi_tester_1_oprand2),
    .REG_I1(ldi_tester_1_oprand1), .REG_I0(ldi_tester_1_oprand0), .WE(not_2_out), .REG_O3(out_14),
    .REG_O2(out_15), .REG_O1(out_16), .REG_O0(out_17));
  CTRLUNIT_EXT ctrlunit_ext_1 (
    .CTRL_S3(out_10), .CTRL_S2(out_11), .CTRL_S1(out_12), .CTRL_S0(out_13), .CTRL_OPR3(out_14),
    .CTRL_OPR2(out_15), .CTRL_OPR1(out_16), .CTRL_OPR0(out_17), .FLAG_N(N), .FLAG_Z(Z),
    .CTRL_OP2(ctrlunit_ext_1_ctrl_op2), .CTRL_OP1(ctrlunit_ext_1_ctrl_op1),
    .CTRL_OP0(ctrlunit_ext_1_ctrl_op0), .CTRL_WE(ctrlunit_ext_1_ctrl_we), .CTRL_B3(ctrlunit_ext_1_ctrl_b3),
    .CTRL_B2(ctrlunit_ext_1_ctrl_b2), .CTRL_B1(ctrlunit_ext_1_ctrl_b1), .CTRL_B0(ctrlunit_ext_1_ctrl_b0),
    .JMP_SIG(ctrlunit_ext_1_jmp_sig), .HLT_SIG(ctrlunit_ext_1_hlt_sig), .LDI_SIG(ctrlunit_ext_1_ldi_sig),
    .ALU_SIG(Z));  // open: FLAG_OVF, FLAG_C, CTRL_OP3, LDA_SIG, STA_SIG
  and and_1 (and_1_out, ctrlunit_ext_1_ctrl_we, not_1_out);
  not not_1 (not_1_out, ctrlunit_ext_1_jmp_sig);
  ALU_EXT alu_ext_1 (
    .A_3(out_6), .A_2(out_7), .A_1(out_8), .A_0(out_9), .B_3(ctrlunit_ext_1_ctrl_b3),
    .B_2(ctrlunit_ext_1_ctrl_b2), .B_1(ctrlunit_ext_1_ctrl_b1), .B_0(ctrlunit_ext_1_ctrl_b0),
    .S2(ctrlunit_ext_1_ctrl_op2), .S1(ctrlunit_ext_1_ctrl_op1), .S0(ctrlunit_ext_1_ctrl_op0),
    .OVF(alu_ext_1_ovf), .N(alu_ext_1_n), .C(alu_ext_1_c), .Z(alu_ext_1_z), .O_3(alu_ext_1_o_3),
    .O_2(alu_ext_1_o_2), .O_1(alu_ext_1_o_1), .O_0(alu_ext_1_o_0));
  not not_2 (not_2_out, ctrlunit_ext_1_hlt_sig);
  MUX_2x1 ACC_INPUT_0 (.S0(ctrlunit_ext_1_ldi_sig), .I0(alu_ext_1_o_0), .I1(ctrlunit_ext_1_ctrl_b0), .O(ACC_INPUT_0_o));
  MUX_2x1 ACC_INPUT_1 (.S0(ctrlunit_ext_1_ldi_sig), .I0(alu_ext_1_o_1), .I1(ctrlunit_ext_1_ctrl_b1), .O(ACC_INPUT_1_o));
  MUX_2x1 ACC_INPUT_2 (.S0(ctrlunit_ext_1_ldi_sig), .I0(alu_ext_1_o_2), .I1(ctrlunit_ext_1_ctrl_b2), .O(ACC_INPUT_2_o));
  MUX_2x1 ACC_INPUT_3 (.S0(ctrlunit_ext_1_ldi_sig), .I0(alu_ext_1_o_3), .I1(ctrlunit_ext_1_ctrl_b3), .O(ACC_INPUT_3_o));
  Clock clock_1 (.out(clock_1_out));
  REGISTER_4BIT ACCUMULATOR_REG (
    .HARD_RESET(in_1), .CLK(clock_1_out), .REG_I3(ACC_INPUT_3_o), .REG_I2(ACC_INPUT_2_o),
    .REG_I1(ACC_INPUT_1_o), .REG_I0(ACC_INPUT_0_o), .WE(and_1_out), .REG_O3(out_6), .REG_O2(out_7),
    .REG_O1(out_8), .REG_O0(out_9));
  REGISTER_4BIT FLAG_REG (
    .HARD_RESET(in_1), .CLK(clock_1_out), .REG_I3(alu_ext_1_ovf), .REG_I2(alu_ext_1_n), .REG_I1(alu_ext_1_c),
    .REG_I0(alu_ext_1_z), .WE(and_1_out), .REG_O3(OVF), .REG_O2(N), .REG_O1(C), .REG_O0(Z));
endmodule

module HLT_TESTER (
  input  ROMI3,
  input  ROMI2,
  input  ROMI1,
  input  ROMI0,
  output OPC3,
  output OPC2,
  output OPC1,
  output OPC0,
  output OPRAND3,
  output OPRAND2,
  output OPRAND1,
  output OPRAND0
);

  wire and_1_out, and_2_out, and_3_out, and_4_out, and_5_out, and_6_out, and_7_out, and_8_out, and_9_out,
       and_10_out, and_11_out, and_12_out, and_13_out, and_14_out, and_15_out, and_16_out, and_17_out,
       and_18_out, and_19_out, and_20_out, and_21_out, and_22_out, and_23_out, and_24_out, and_25_out,
       and_26_out, and_27_out, and_28_out, and_29_out, and_30_out, and_31_out, and_32_out, and_33_out,
       and_34_out, and_35_out, and_36_out, and_37_out, and_38_out, and_39_out, and_40_out, and_41_out,
       and_42_out, and_43_out, and_44_out, and_45_out, and_46_out, and_47_out, and_48_out, and_49_out,
       and_50_out, and_51_out, and_52_out, and_53_out, and_54_out, and_55_out, and_56_out, and_57_out,
       and_58_out, and_59_out, and_60_out, and_61_out, and_62_out, and_63_out, and_64_out, and_65_out,
       and_66_out, and_67_out, and_68_out, and_69_out, and_70_out, and_71_out, and_72_out, and_73_out,
       and_74_out, and_75_out, and_76_out, and_77_out, and_78_out, and_79_out, and_80_out, and_81_out,
       and_82_out, and_83_out, and_84_out, and_85_out, and_86_out, and_87_out, and_88_out, and_89_out,
       and_90_out, and_91_out, and_92_out, and_93_out, and_94_out, and_95_out, and_96_out, and_97_out,
       and_98_out, and_99_out, and_100_out, and_101_out, and_102_out, and_103_out, and_104_out, and_105_out,
       and_106_out, and_107_out, and_108_out, and_109_out, and_110_out, and_111_out, and_112_out,
       and_113_out, and_114_out, and_115_out, and_116_out, and_117_out, and_118_out, and_119_out,
       and_120_out, and_121_out, and_122_out, and_123_out, and_124_out, and_125_out, and_126_out,
       and_127_out, and_128_out, and_129_out, and_130_out, and_131_out, and_132_out, and_133_out,
       and_134_out, and_135_out, and_136_out, and_137_out, and_138_out, and_139_out, and_140_out,
       and_141_out, and_142_out, and_143_out, DECORDER_4x16_out, not_1_out, not_2_out, not_3_out, not_4_out,
       or_1_out, or_3_out, or_4_out, or_6_out, or_7_out, or_8_out, or_10_out, or_12_out, or_13_out,
       or_15_out, or_16_out, or_18_out, or_19_out, or_21_out, or_22_out, or_24_out;

  not not_1 (not_1_out, ROMI3);
  not not_2 (not_2_out, ROMI2);
  not not_3 (not_3_out, ROMI1);
  not not_4 (not_4_out, ROMI0);
  and DECORDER_4x16 (DECORDER_4x16_out, not_4_out, not_3_out, not_2_out, not_1_out);
  and and_1 (and_1_out, ROMI0, not_3_out, not_2_out, not_1_out);
  and and_2 (and_2_out, not_4_out, ROMI1, not_2_out, not_1_out);
  and and_3 (and_3_out, ROMI0, ROMI1, not_2_out, not_1_out);
  and and_4 (and_4_out, not_4_out, not_3_out, ROMI2, not_1_out);
  and and_5 (and_5_out, ROMI0, not_3_out, ROMI2, not_1_out);
  and and_6 (and_6_out, not_4_out, ROMI1, ROMI2, not_1_out);
  and and_7 (and_7_out, ROMI0, ROMI1, ROMI2, not_1_out);
  and and_8 (and_8_out, not_4_out, not_3_out, not_2_out, ROMI3);
  and and_9 (and_9_out, ROMI0, not_3_out, not_2_out, ROMI3);
  and and_10 (and_10_out, not_4_out, ROMI1, not_2_out, ROMI3);
  and and_11 (and_11_out, ROMI0, ROMI1, not_2_out, ROMI3);
  and and_12 (and_12_out, not_4_out, not_3_out, ROMI2, ROMI3);
  and and_13 (and_13_out, ROMI0, not_3_out, ROMI2, ROMI3);
  and and_14 (and_14_out, not_4_out, ROMI1, ROMI2, ROMI3);
  and and_15 (and_15_out, ROMI0, ROMI1, ROMI2, ROMI3);
  or or_1 (or_1_out, and_31_out, and_30_out, and_29_out, and_28_out, and_27_out, and_26_out, and_25_out, and_24_out);
  and and_16 (and_16_out, DECORDER_4x16_out, 1'b0);
  and and_17 (and_17_out, and_1_out, 1'b0);
  and and_18 (and_18_out, and_2_out, 1'b1);
  and and_19 (and_19_out, and_3_out, 1'b0);
  and and_20 (and_20_out, and_4_out, 1'b0);
  and and_21 (and_21_out, and_5_out, 1'b0);
  and and_22 (and_22_out, and_6_out, 1'b0);
  and and_23 (and_23_out, and_7_out, 1'b0);
  and and_24 (and_24_out, and_8_out, 1'b0);
  and and_25 (and_25_out, and_9_out, 1'b0);
  and and_26 (and_26_out, and_10_out, 1'b0);
  and and_27 (and_27_out, and_11_out, 1'b0);
  and and_28 (and_28_out, and_12_out, 1'b0);
  and and_29 (and_29_out, and_13_out, 1'b0);
  and and_30 (and_30_out, and_14_out, 1'b0);
  and and_31 (and_31_out, and_15_out, 1'b0);
  or or_2 (OPC3, or_1_out, or_3_out);
  or or_3 (or_3_out, and_16_out, and_17_out, and_18_out, and_19_out, and_20_out, and_21_out, and_22_out, and_23_out);
  or or_4 (or_4_out, and_47_out, and_46_out, and_45_out, and_44_out, and_43_out, and_42_out, and_41_out, and_40_out);
  and and_32 (and_32_out, DECORDER_4x16_out, 1'b0);
  and and_33 (and_33_out, and_1_out, 1'b0);
  and and_34 (and_34_out, and_2_out, 1'b0);
  and and_35 (and_35_out, and_3_out, 1'b0);
  and and_36 (and_36_out, and_4_out, 1'b0);
  and and_37 (and_37_out, and_5_out, 1'b0);
  and and_38 (and_38_out, and_6_out, 1'b0);
  and and_39 (and_39_out, and_7_out, 1'b0);
  and and_40 (and_40_out, and_8_out, 1'b0);
  and and_41 (and_41_out, and_9_out, 1'b0);
  and and_42 (and_42_out, and_10_out, 1'b0);
  and and_43 (and_43_out, and_11_out, 1'b0);
  and and_44 (and_44_out, and_12_out, 1'b0);
  and and_45 (and_45_out, and_13_out, 1'b0);
  and and_46 (and_46_out, and_14_out, 1'b0);
  and and_47 (and_47_out, and_15_out, 1'b0);
  or or_5 (OPC2, or_4_out, or_6_out);
  or or_6 (or_6_out, and_32_out, and_33_out, and_34_out, and_35_out, and_36_out, and_37_out, and_38_out, and_39_out);
  or or_7 (or_7_out, and_63_out, and_62_out, and_61_out, and_60_out, and_59_out, and_58_out, and_57_out, and_56_out);
  and and_48 (and_48_out, DECORDER_4x16_out, 1'b0);
  and and_49 (and_49_out, and_1_out, 1'b0);
  and and_50 (and_50_out, and_2_out, 1'b1);
  and and_51 (and_51_out, and_3_out, 1'b0);
  and and_52 (and_52_out, and_4_out, 1'b0);
  and and_53 (and_53_out, and_5_out, 1'b0);
  and and_54 (and_54_out, and_6_out, 1'b0);
  and and_55 (and_55_out, and_7_out, 1'b0);
  and and_56 (and_56_out, and_8_out, 1'b0);
  and and_57 (and_57_out, and_9_out, 1'b0);
  and and_58 (and_58_out, and_10_out, 1'b0);
  and and_59 (and_59_out, and_11_out, 1'b0);
  and and_60 (and_60_out, and_12_out, 1'b0);
  and and_61 (and_61_out, and_13_out, 1'b0);
  and and_62 (and_62_out, and_14_out, 1'b0);
  and and_63 (and_63_out, and_15_out, 1'b0);
  or or_8 (or_8_out, and_48_out, and_49_out, and_50_out, and_51_out, and_52_out, and_53_out, and_54_out, and_55_out);
  or or_9 (OPC1, or_7_out, or_8_out);
  or or_10 (or_10_out, and_79_out, and_78_out, and_77_out, and_76_out, and_75_out, and_74_out, and_73_out, and_72_out);
  and and_64 (and_64_out, DECORDER_4x16_out, 1'b0);
  and and_65 (and_65_out, and_1_out, 1'b1);
  and and_66 (and_66_out, and_2_out, 1'b1);
  and and_67 (and_67_out, and_3_out, 1'b0);
  and and_68 (and_68_out, and_4_out, 1'b0);
  and and_69 (and_69_out, and_5_out, 1'b0);
  and and_70 (and_70_out, and_6_out, 1'b0);
  and and_71 (and_71_out, and_7_out, 1'b0);
  and and_72 (and_72_out, and_8_out, 1'b0);
  and and_73 (and_73_out, and_9_out, 1'b0);
  and and_74 (and_74_out, and_10_out, 1'b0);
  and and_75 (and_75_out, and_11_out, 1'b0);
  and and_76 (and_76_out, and_12_out, 1'b0);
  and and_77 (and_77_out, and_13_out, 1'b0);
  and and_78 (and_78_out, and_14_out, 1'b0);
  and and_79 (and_79_out, and_15_out, 1'b0);
  or or_11 (OPC0, or_10_out, or_12_out);
  or or_12 (or_12_out, and_64_out, and_65_out, and_66_out, and_67_out, and_68_out, and_69_out, and_70_out, and_71_out);
  or or_13 (or_13_out, and_95_out, and_94_out, and_93_out, and_92_out, and_91_out, and_90_out, and_89_out, and_88_out);
  and and_80 (and_80_out, DECORDER_4x16_out, 1'b0);
  and and_81 (and_81_out, and_1_out, 1'b0);
  and and_82 (and_82_out, and_2_out, 1'b0);
  and and_83 (and_83_out, and_3_out, 1'b0);
  and and_84 (and_84_out, and_4_out, 1'b0);
  and and_85 (and_85_out, and_5_out, 1'b0);
  and and_86 (and_86_out, and_6_out, 1'b0);
  and and_87 (and_87_out, and_7_out, 1'b0);
  and and_88 (and_88_out, and_8_out, 1'b0);
  and and_89 (and_89_out, and_9_out, 1'b0);
  and and_90 (and_90_out, and_10_out, 1'b0);
  and and_91 (and_91_out, and_11_out, 1'b0);
  and and_92 (and_92_out, and_12_out, 1'b0);
  and and_93 (and_93_out, and_13_out, 1'b0);
  and and_94 (and_94_out, and_14_out, 1'b0);
  and and_95 (and_95_out, and_15_out, 1'b0);
  or or_14 (OPRAND3, or_13_out, or_15_out);
  or or_15 (or_15_out, and_80_out, and_81_out, and_82_out, and_83_out, and_84_out, and_85_out, and_86_out, and_87_out);
  or or_16 (or_16_out, and_111_out, and_110_out, and_109_out, and_108_out, and_107_out, and_106_out, and_105_out, and_104_out);
  and and_96 (and_96_out, DECORDER_4x16_out, 1'b0);
  and and_97 (and_97_out, and_1_out, 1'b0);
  and and_98 (and_98_out, and_2_out, 1'b0);
  and and_99 (and_99_out, and_3_out, 1'b0);
  and and_100 (and_100_out, and_4_out, 1'b0);
  and and_101 (and_101_out, and_5_out, 1'b0);
  and and_102 (and_102_out, and_6_out, 1'b0);
  and and_103 (and_103_out, and_7_out, 1'b0);
  and and_104 (and_104_out, and_8_out, 1'b0);
  and and_105 (and_105_out, and_9_out, 1'b0);
  and and_106 (and_106_out, and_10_out, 1'b0);
  and and_107 (and_107_out, and_11_out, 1'b0);
  and and_108 (and_108_out, and_12_out, 1'b0);
  and and_109 (and_109_out, and_13_out, 1'b0);
  and and_110 (and_110_out, and_14_out, 1'b0);
  and and_111 (and_111_out, and_15_out, 1'b0);
  or or_17 (OPRAND2, or_16_out, or_18_out);
  or or_18 (or_18_out, and_96_out, and_97_out, and_98_out, and_99_out, and_100_out, and_101_out, and_102_out, and_103_out);
  or or_19 (or_19_out, and_127_out, and_126_out, and_125_out, and_124_out, and_123_out, and_122_out, and_121_out, and_120_out);
  and and_112 (and_112_out, DECORDER_4x16_out, 1'b0);
  and and_113 (and_113_out, and_1_out, 1'b0);
  and and_114 (and_114_out, and_2_out, 1'b0);
  and and_115 (and_115_out, and_3_out, 1'b0);
  and and_116 (and_116_out, and_4_out, 1'b1);
  and and_117 (and_117_out, and_5_out, 1'b0);
  and and_118 (and_118_out, and_6_out, 1'b0);
  and and_119 (and_119_out, and_7_out, 1'b0);
  and and_120 (and_120_out, and_8_out, 1'b0);
  and and_121 (and_121_out, and_9_out, 1'b0);
  and and_122 (and_122_out, and_10_out, 1'b0);
  and and_123 (and_123_out, and_11_out, 1'b0);
  and and_124 (and_124_out, and_12_out, 1'b0);
  and and_125 (and_125_out, and_13_out, 1'b0);
  and and_126 (and_126_out, and_14_out, 1'b0);
  and and_127 (and_127_out, and_15_out, 1'b0);
  or or_20 (OPRAND1, or_19_out, or_21_out);
  or or_21 (or_21_out, and_112_out, and_113_out, and_114_out, and_115_out, and_116_out, and_117_out, and_118_out, and_119_out);
  or or_22 (or_22_out, and_143_out, and_142_out, and_141_out, and_140_out, and_139_out, and_138_out, and_137_out, and_136_out);
  and and_128 (and_128_out, DECORDER_4x16_out, 1'b0);
  and and_129 (and_129_out, and_1_out, 1'b1);
  and and_130 (and_130_out, and_2_out, 1'b0);
  and and_131 (and_131_out, and_3_out, 1'b1);
  and and_132 (and_132_out, and_4_out, 1'b1);
  and and_133 (and_133_out, and_5_out, 1'b0);
  and and_134 (and_134_out, and_6_out, 1'b0);
  and and_135 (and_135_out, and_7_out, 1'b0);
  and and_136 (and_136_out, and_8_out, 1'b0);
  and and_137 (and_137_out, and_9_out, 1'b0);
  and and_138 (and_138_out, and_10_out, 1'b0);
  and and_139 (and_139_out, and_11_out, 1'b0);
  and and_140 (and_140_out, and_12_out, 1'b0);
  and and_141 (and_141_out, and_13_out, 1'b0);
  and and_142 (and_142_out, and_14_out, 1'b0);
  and and_143 (and_143_out, and_15_out, 1'b0);
  or or_23 (OPRAND0, or_22_out, or_24_out);
  or or_24 (or_24_out, and_128_out, and_129_out, and_130_out, and_131_out, and_132_out, and_133_out, and_134_out, and_135_out);
endmodule

module MUX_2x1 (
  input  S0,
  input  I0,
  input  I1,
  output O
);

  wire and_1_out, and_2_out, not_1_out;

  not not_1 (not_1_out, S0);
  and and_1 (and_1_out, not_1_out, I0);
  and and_2 (and_2_out, S0, I1);
  or MUX2x1 (O, and_1_out, and_2_out);
endmodule

module LDI_TESTER (
  input  ROMI3,
  input  ROMI2,
  input  ROMI1,
  input  ROMI0,
  output OPC3,
  output OPC2,
  output OPC1,
  output OPC0,
  output OPRAND3,
  output OPRAND2,
  output OPRAND1,
  output OPRAND0
);

  wire and_1_out, and_2_out, and_3_out, and_4_out, and_5_out, and_6_out, and_7_out, and_8_out, and_9_out,
       and_10_out, and_11_out, and_12_out, and_13_out, and_14_out, and_15_out, and_16_out, and_17_out,
       and_18_out, and_19_out, and_20_out, and_21_out, and_22_out, and_23_out, and_24_out, and_25_out,
       and_26_out, and_27_out, and_28_out, and_29_out, and_30_out, and_31_out, and_32_out, and_33_out,
       and_34_out, and_35_out, and_36_out, and_37_out, and_38_out, and_39_out, and_40_out, and_41_out,
       and_42_out, and_43_out, and_44_out, and_45_out, and_46_out, and_47_out, and_48_out, and_49_out,
       and_50_out, and_51_out, and_52_out, and_53_out, and_54_out, and_55_out, and_56_out, and_57_out,
       and_58_out, and_59_out, and_60_out, and_61_out, and_62_out, and_63_out, and_64_out, and_65_out,
       and_66_out, and_67_out, and_68_out, and_69_out, and_70_out, and_71_out, and_72_out, and_73_out,
       and_74_out, and_75_out, and_76_out, and_77_out, and_78_out, and_79_out, and_80_out, and_81_out,
       and_82_out, and_83_out, and_84_out, and_85_out, and_86_out, and_87_out, and_88_out, and_89_out,
       and_90_out, and_91_out, and_92_out, and_93_out, and_94_out, and_95_out, and_96_out, and_97_out,
       and_98_out, and_99_out, and_100_out, and_101_out, and_102_out, and_103_out, and_104_out, and_105_out,
       and_106_out, and_107_out, and_108_out, and_109_out, and_110_out, and_111_out, and_112_out,
       and_113_out, and_114_out, and_115_out, and_116_out, and_117_out, and_118_out, and_119_out,
       and_120_out, and_121_out, and_122_out, and_123_out, and_124_out, and_125_out, and_126_out,
       and_127_out, and_128_out, and_129_out, and_130_out, and_131_out, and_132_out, and_133_out,
       and_134_out, and_135_out, and_136_out, and_137_out, and_138_out, and_139_out, and_140_out,
       and_141_out, and_142_out, and_143_out, DECORDER_4x16_out, not_1_out, not_2_out, not_3_out, not_4_out,
       or_1_out, or_3_out, or_4_out, or_6_out, or_7_out, or_8_out, or_10_out, or_12_out, or_13_out,
       or_14_out, or_16_out, or_18_out, or_19_out, or_21_out, or_22_out, or_23_out;

  not not_1 (not_1_out, ROMI3);
  not not_2 (not_2_out, ROMI2);
  not not_3 (not_3_out, ROMI1);
  not not_4 (not_4_out, ROMI0);
  and DECORDER_4x16 (DECORDER_4x16_out, not_4_out, not_3_out, not_2_out, not_1_out);
  and and_1 (and_1_out, ROMI0, not_3_out, not_2_out, not_1_out);
  and and_2 (and_2_out, not_4_out, ROMI1, not_2_out, not_1_out);
  and and_3 (and_3_out, ROMI0, ROMI1, not_2_out, not_1_out);
  and and_4 (and_4_out, not_4_out, not_3_out, ROMI2, not_1_out);
  and and_5 (and_5_out, ROMI0, not_3_out, ROMI2, not_1_out);
  and and_6 (and_6_out, not_4_out, ROMI1, ROMI2, not_1_out);
  and and_7 (and_7_out, ROMI0, ROMI1, ROMI2, not_1_out);
  and and_8 (and_8_out, not_4_out, not_3_out, not_2_out, ROMI3);
  and and_9 (and_9_out, ROMI0, not_3_out, not_2_out, ROMI3);
  and and_10 (and_10_out, not_4_out, ROMI1, not_2_out, ROMI3);
  and and_11 (and_11_out, ROMI0, ROMI1, not_2_out, ROMI3);
  and and_12 (and_12_out, not_4_out, not_3_out, ROMI2, ROMI3);
  and and_13 (and_13_out, ROMI0, not_3_out, ROMI2, ROMI3);
  and and_14 (and_14_out, not_4_out, ROMI1, ROMI2, ROMI3);
  and and_15 (and_15_out, ROMI0, ROMI1, ROMI2, ROMI3);
  or or_1 (or_1_out, and_31_out, and_30_out, and_29_out, and_28_out, and_27_out, and_26_out, and_25_out, and_24_out);
  and and_16 (and_16_out, DECORDER_4x16_out, 1'b1);
  and and_17 (and_17_out, and_1_out, 1'b0);
  and and_18 (and_18_out, and_2_out, 1'b0);
  and and_19 (and_19_out, and_3_out, 1'b1);
  and and_20 (and_20_out, and_4_out, 1'b0);
  and and_21 (and_21_out, and_5_out, 1'b0);
  and and_22 (and_22_out, and_6_out, 1'b0);
  and and_23 (and_23_out, and_7_out, 1'b0);
  and and_24 (and_24_out, and_8_out, 1'b0);
  and and_25 (and_25_out, and_9_out, 1'b0);
  and and_26 (and_26_out, and_10_out, 1'b0);
  and and_27 (and_27_out, and_11_out, 1'b0);
  and and_28 (and_28_out, and_12_out, 1'b0);
  and and_29 (and_29_out, and_13_out, 1'b0);
  and and_30 (and_30_out, and_14_out, 1'b0);
  and and_31 (and_31_out, and_15_out, 1'b0);
  or or_2 (OPC3, or_1_out, or_3_out);
  or or_3 (or_3_out, and_16_out, and_17_out, and_18_out, and_19_out, and_20_out, and_21_out, and_22_out, and_23_out);
  or or_4 (or_4_out, and_47_out, and_46_out, and_45_out, and_44_out, and_43_out, and_42_out, and_41_out, and_40_out);
  and and_32 (and_32_out, DECORDER_4x16_out, 1'b1);
  and and_33 (and_33_out, and_1_out, 1'b1);
  and and_34 (and_34_out, and_2_out, 1'b1);
  and and_35 (and_35_out, and_3_out, 1'b0);
  and and_36 (and_36_out, and_4_out, 1'b0);
  and and_37 (and_37_out, and_5_out, 1'b0);
  and and_38 (and_38_out, and_6_out, 1'b0);
  and and_39 (and_39_out, and_7_out, 1'b0);
  and and_40 (and_40_out, and_8_out, 1'b0);
  and and_41 (and_41_out, and_9_out, 1'b0);
  and and_42 (and_42_out, and_10_out, 1'b0);
  and and_43 (and_43_out, and_11_out, 1'b0);
  and and_44 (and_44_out, and_12_out, 1'b0);
  and and_45 (and_45_out, and_13_out, 1'b0);
  and and_46 (and_46_out, and_14_out, 1'b0);
  and and_47 (and_47_out, and_15_out, 1'b0);
  or or_5 (OPC2, or_4_out, or_6_out);
  or or_6 (or_6_out, and_32_out, and_33_out, and_34_out, and_35_out, and_36_out, and_37_out, and_38_out, and_39_out);
  and and_48 (and_48_out, DECORDER_4x16_out, 1'b0);
  and and_49 (and_49_out, and_1_out, 1'b1);
  and and_50 (and_50_out, and_2_out, 1'b1);
  and and_51 (and_51_out, and_3_out, 1'b1);
  and and_52 (and_52_out, and_4_out, 1'b0);
  and and_53 (and_53_out, and_5_out, 1'b0);
  and and_54 (and_54_out, and_6_out, 1'b0);
  and and_55 (and_55_out, and_7_out, 1'b0);
  and and_56 (and_56_out, and_8_out, 1'b0);
  and and_57 (and_57_out, and_9_out, 1'b0);
  and and_58 (and_58_out, and_10_out, 1'b0);
  and and_59 (and_59_out, and_11_out, 1'b0);
  and and_60 (and_60_out, and_12_out, 1'b0);
  and and_61 (and_61_out, and_13_out, 1'b0);
  and and_62 (and_62_out, and_14_out, 1'b0);
  and and_63 (and_63_out, and_15_out, 1'b0);
  or or_7 (or_7_out, and_63_out, and_62_out, and_61_out, and_60_out, and_59_out, and_58_out, and_57_out, and_56_out);
  or or_8 (or_8_out, and_48_out, and_49_out, and_50_out, and_51_out, and_52_out, and_53_out, and_54_out, and_55_out);
  or or_9 (OPC1, or_7_out, or_8_out);
  or or_10 (or_10_out, and_79_out, and_78_out, and_77_out, and_76_out, and_75_out, and_74_out, and_73_out, and_72_out);
  and and_64 (and_64_out, DECORDER_4x16_out, 1'b0);
  and and_65 (and_65_out, and_1_out, 1'b0);
  and and_66 (and_66_out, and_2_out, 1'b1);
  and and_67 (and_67_out, and_3_out, 1'b1);
  and and_68 (and_68_out, and_4_out, 1'b0);
  and and_69 (and_69_out, and_5_out, 1'b0);
  and and_70 (and_70_out, and_6_out, 1'b0);
  and and_71 (and_71_out, and_7_out, 1'b0);
  and and_72 (and_72_out, and_8_out, 1'b0);
  and and_73 (and_73_out, and_9_out, 1'b0);
  and and_74 (and_74_out, and_10_out, 1'b0);
  and and_75 (and_75_out, and_11_out, 1'b0);
  and and_76 (and_76_out, and_12_out, 1'b0);
  and and_77 (and_77_out, and_13_out, 1'b0);
  and and_78 (and_78_out, and_14_out, 1'b0);
  and and_79 (and_79_out, and_15_out, 1'b0);
  or or_11 (OPC0, or_10_out, or_12_out);
  or or_12 (or_12_out, and_64_out, and_65_out, and_66_out, and_67_out, and_68_out, and_69_out, and_70_out, and_71_out);
  or or_13 (or_13_out, and_95_out, and_94_out, and_93_out, and_92_out, and_91_out, and_90_out, and_89_out, and_88_out);
  and and_80 (and_80_out, DECORDER_4x16_out, 1'b0);
  and and_81 (and_81_out, and_1_out, 1'b0);
  and and_82 (and_82_out, and_2_out, 1'b0);
  and and_83 (and_83_out, and_3_out, 1'b0);
  and and_84 (and_84_out, and_4_out, 1'b0);
  and and_85 (and_85_out, and_5_out, 1'b0);
  and and_86 (and_86_out, and_6_out, 1'b0);
  and and_87 (and_87_out, and_7_out, 1'b0);
  and and_88 (and_88_out, and_8_out, 1'b0);
  and and_89 (and_89_out, and_9_out, 1'b0);
  and and_90 (and_90_out, and_10_out, 1'b0);
  and and_91 (and_91_out, and_11_out, 1'b0);
  and and_92 (and_92_out, and_12_out, 1'b0);
  and and_93 (and_93_out, and_13_out, 1'b0);
  and and_94 (and_94_out, and_14_out, 1'b0);
  and and_95 (and_95_out, and_15_out, 1'b0);
  or or_14 (or_14_out, and_80_out, and_81_out, and_82_out, and_83_out, and_84_out, and_85_out, and_86_out, and_87_out);
  or or_15 (OPRAND3, or_13_out, or_14_out);
  or or_16 (or_16_out, and_111_out, and_110_out, and_109_out, and_108_out, and_107_out, and_106_out, and_105_out, and_104_out);
  and and_96 (and_96_out, DECORDER_4x16_out, 1'b1);
  and and_97 (and_97_out, and_1_out, 1'b0);
  and and_98 (and_98_out, and_2_out, 1'b0);
  and and_99 (and_99_out, and_3_out, 1'b0);
  and and_100 (and_100_out, and_4_out, 1'b0);
  and and_101 (and_101_out, and_5_out, 1'b0);
  and and_102 (and_102_out, and_6_out, 1'b0);
  and and_103 (and_103_out, and_7_out, 1'b0);
  and and_104 (and_104_out, and_8_out, 1'b0);
  and and_105 (and_105_out, and_9_out, 1'b0);
  and and_106 (and_106_out, and_10_out, 1'b0);
  and and_107 (and_107_out, and_11_out, 1'b0);
  and and_108 (and_108_out, and_12_out, 1'b0);
  and and_109 (and_109_out, and_13_out, 1'b0);
  and and_110 (and_110_out, and_14_out, 1'b0);
  and and_111 (and_111_out, and_15_out, 1'b0);
  or or_17 (OPRAND2, or_16_out, or_18_out);
  or or_18 (or_18_out, and_96_out, and_97_out, and_98_out, and_99_out, and_100_out, and_101_out, and_102_out, and_103_out);
  or or_19 (or_19_out, and_127_out, and_126_out, and_125_out, and_124_out, and_123_out, and_122_out, and_121_out, and_120_out);
  and and_112 (and_112_out, DECORDER_4x16_out, 1'b0);
  and and_113 (and_113_out, and_1_out, 1'b0);
  and and_114 (and_114_out, and_2_out, 1'b0);
  and and_115 (and_115_out, and_3_out, 1'b0);
  and and_116 (and_116_out, and_4_out, 1'b0);
  and and_117 (and_117_out, and_5_out, 1'b0);
  and and_118 (and_118_out, and_6_out, 1'b0);
  and and_119 (and_119_out, and_7_out, 1'b0);
  and and_120 (and_120_out, and_8_out, 1'b0);
  and and_121 (and_121_out, and_9_out, 1'b0);
  and and_122 (and_122_out, and_10_out, 1'b0);
  and and_123 (and_123_out, and_11_out, 1'b0);
  and and_124 (and_124_out, and_12_out, 1'b0);
  and and_125 (and_125_out, and_13_out, 1'b0);
  and and_126 (and_126_out, and_14_out, 1'b0);
  and and_127 (and_127_out, and_15_out, 1'b0);
  or or_20 (OPRAND1, or_19_out, or_21_out);
  or or_21 (or_21_out, and_112_out, and_113_out, and_114_out, and_115_out, and_116_out, and_117_out, and_118_out, and_119_out);
  or or_22 (or_22_out, and_143_out, and_142_out, and_141_out, and_140_out, and_139_out, and_138_out, and_137_out, and_136_out);
  and and_128 (and_128_out, DECORDER_4x16_out, 1'b1);
  and and_129 (and_129_out, and_1_out, 1'b0);
  and and_130 (and_130_out, and_2_out, 1'b0);
  and and_131 (and_131_out, and_3_out, 1'b0);
  and and_132 (and_132_out, and_4_out, 1'b0);
  and and_133 (and_133_out, and_5_out, 1'b0);
  and and_134 (and_134_out, and_6_out, 1'b0);
  and and_135 (and_135_out, and_7_out, 1'b0);
  and and_136 (and_136_out, and_8_out, 1'b0);
  and and_137 (and_137_out, and_9_out, 1'b0);
  and and_138 (and_138_out, and_10_out, 1'b0);
  and and_139 (and_139_out, and_11_out, 1'b0);
  and and_140 (and_140_out, and_12_out, 1'b0);
  and and_141 (and_141_out, and_13_out, 1'b0);
  and and_142 (and_142_out, and_14_out, 1'b0);
  and and_143 (and_143_out, and_15_out, 1'b0);
  or or_23 (or_23_out, and_128_out, and_129_out, and_130_out, and_131_out, and_132_out, and_133_out, and_134_out, and_135_out);
  or or_24 (OPRAND0, or_22_out, or_23_out);
endmodule

module CPU_v2 (
  input  in_1,
  output OVF,
  output N,
  output C,
  output Z,
  output out_6,
  output out_7,
  output out_8,
  output out_9,
  output out_10,
  output out_11,
  output out_12,
  output out_13,
  output out_14,
  output out_15,
  output out_16,
  output out_17
);

  wire ACC_INPUT_0_o, ACC_INPUT_1_o, ACC_INPUT_2_o, ACC_INPUT_3_o, alu_ext_1_c, alu_ext_1_n, alu_ext_1_o_0,
       alu_ext_1_o_1, alu_ext_1_o_2, alu_ext_1_o_3, alu_ext_1_ovf, alu_ext_1_z, and_1_out, clock_1_out,
       ctrlunit_ext_1_alu_sig, ctrlunit_ext_1_ctrl_b0, ctrlunit_ext_1_ctrl_b1, ctrlunit_ext_1_ctrl_b2,
       ctrlunit_ext_1_ctrl_b3, ctrlunit_ext_1_ctrl_op0, ctrlunit_ext_1_ctrl_op1, ctrlunit_ext_1_ctrl_op2,
       ctrlunit_ext_1_ctrl_we, ctrlunit_ext_1_hlt_sig, ctrlunit_ext_1_jmp_sig, ctrlunit_ext_1_ldi_sig,
       ldi_tester_1_opc0, ldi_tester_1_opc1, ldi_tester_1_opc2, ldi_tester_1_opc3, ldi_tester_1_oprand0,
       ldi_tester_1_oprand1, ldi_tester_1_oprand2, ldi_tester_1_oprand3, not_1_out, not_2_out, PC_REG_reg_o0,
       PC_REG_reg_o1, PC_REG_reg_o2, PC_REG_reg_o3, progcounter_ext_1_pco0, progcounter_ext_1_pco1,
       progcounter_ext_1_pco2, progcounter_ext_1_pco3, STATIC_RAM_sram_o0, STATIC_RAM_sram_o1,
       STATIC_RAM_sram_o2, STATIC_RAM_sram_o3;

  ProgCounter_EXT progcounter_ext_1 (
    .A3(PC_REG_reg_o3), .A2(PC_REG_reg_o2), .A1(PC_REG_reg_o1), .A0(PC_REG_reg_o0),
    .PC_OPR3(ctrlunit_ext_1_ctrl_b3), .PC_OPR2(ctrlunit_ext_1_ctrl_b2), .PC_OPR1(ctrlunit_ext_1_ctrl_b1),
    .PC_OPR0(ctrlunit_ext_1_ctrl_b0), .JMP_JZ(ctrlunit_ext_1_jmp_sig), .PCO3(progcounter_ext_1_pco3),
    .PCO2(progcounter_ext_1_pco2), .PCO1(progcounter_ext_1_pco1), .PCO0(progcounter_ext_1_pco0));  // open: FTCH
  REGISTER_4BIT PC_REG (
    .HARD_RESET(in_1), .CLK(clock_1_out), .REG_I3(progcounter_ext_1_pco3), .REG_I2(progcounter_ext_1_pco2),
    .REG_I1(progcounter_ext_1_pco1), .REG_I0(progcounter_ext_1_pco0), .WE(not_2_out), .REG_O3(PC_REG_reg_o3),
    .REG_O2(PC_REG_reg_o2), .REG_O1(PC_REG_reg_o1), .REG_O0(PC_REG_reg_o0));
  LDI_TESTER ldi_tester_1 (
    .ROMI3(PC_REG_reg_o3), .ROMI2(PC_REG_reg_o2), .ROMI1(PC_REG_reg_o1), .ROMI0(PC_REG_reg_o0),
    .OPC3(ldi_tester_1_opc3), .OPC2(ldi_tester_1_opc2), .OPC1(ldi_tester_1_opc1), .OPC0(ldi_tester_1_opc0),
    .OPRAND3(ldi_tester_1_oprand3), .OPRAND2(ldi_tester_1_oprand2), .OPRAND1(ldi_tester_1_oprand1),
    .OPRAND0(ldi_tester_1_oprand0));
  REGISTER_4BIT INSTRUCTION_REG_OPC (
    .HARD_RESET(in_1), .CLK(clock_1_out), .REG_I3(ldi_tester_1_opc3), .REG_I2(ldi_tester_1_opc2),
    .REG_I1(ldi_tester_1_opc1), .REG_I0(ldi_tester_1_opc0), .WE(not_2_out), .REG_O3(out_10), .REG_O2(out_11),
    .REG_O1(out_12), .REG_O0(out_13));
  REGISTER_4BIT INSTRUCTION_REG_OPR (
    .HARD_RESET(in_1), .CLK(clock_1_out), .REG_I3(ldi_tester_1_oprand3), .REG_I2(ldi_tester_1_oprand2),
    .REG_I1(ldi_tester_1_oprand1), .REG_I0(ldi_tester_1_oprand0), .WE(not_2_out), .REG_O3(out_14),
    .REG_O2(out_15), .REG_O1(out_16), .REG_O0(out_17));
  CTRLUNIT_EXT ctrlunit_ext_1 (
    .CTRL_S3(out_10), .CTRL_S2(out_11), .CTRL_S1(out_12), .CTRL_S0(out_13), .CTRL_OPR3(out_14),
    .CTRL_OPR2(out_15), .CTRL_OPR1(out_16), .CTRL_OPR0(out_17), .FLAG_N(N), .FLAG_Z(Z),
    .CTRL_OP2(ctrlunit_ext_1_ctrl_op2), .CTRL_OP1(ctrlunit_ext_1_ctrl_op1),
    .CTRL_OP0(ctrlunit_ext_1_ctrl_op0), .CTRL_WE(ctrlunit_ext_1_ctrl_we), .CTRL_B3(ctrlunit_ext_1_ctrl_b3),
    .CTRL_B2(ctrlunit_ext_1_ctrl_b2), .CTRL_B1(ctrlunit_ext_1_ctrl_b1), .CTRL_B0(ctrlunit_ext_1_ctrl_b0),
    .JMP_SIG(ctrlunit_ext_1_jmp_sig), .HLT_SIG(ctrlunit_ext_1_hlt_sig), .LDI_SIG(ctrlunit_ext_1_ldi_sig),
    .ALU_SIG(ctrlunit_ext_1_alu_sig));  // open: FLAG_OVF, FLAG_C, CTRL_OP3, LDA_SIG, STA_SIG
  and and_1 (and_1_out, ctrlunit_ext_1_ctrl_we, not_1_out);
  not not_1 (not_1_out, ctrlunit_ext_1_jmp_sig);
  ALU_EXT alu_ext_1 (
    .A_3(out_6), .A_2(out_7), .A_1(out_8), .A_0(out_9), .B_3(ctrlunit_ext_1_ctrl_b3),
    .B_2(ctrlunit_ext_1_ctrl_b2), .B_1(ctrlunit_ext_1_ctrl_b1), .B_0(ctrlunit_ext_1_ctrl_b0),
    .S2(ctrlunit_ext_1_ctrl_op2), .S1(ctrlunit_ext_1_ctrl_op1), .S0(ctrlunit_ext_1_ctrl_op0),
    .OVF(alu_ext_1_ovf), .N(alu_ext_1_n), .C(alu_ext_1_c), .Z(alu_ext_1_z), .O_3(alu_ext_1_o_3),
    .O_2(alu_ext_1_o_2), .O_1(alu_ext_1_o_1), .O_0(alu_ext_1_o_0));
  not not_2 (not_2_out, ctrlunit_ext_1_hlt_sig);
  MUX_2x1 ACC_INPUT_0 (.S0(ctrlunit_ext_1_ldi_sig), .I0(alu_ext_1_o_0), .I1(ctrlunit_ext_1_ctrl_b0), .O(ACC_INPUT_0_o));
  MUX_2x1 ACC_INPUT_1 (.S0(ctrlunit_ext_1_ldi_sig), .I0(alu_ext_1_o_1), .I1(ctrlunit_ext_1_ctrl_b1), .O(ACC_INPUT_1_o));
  MUX_2x1 ACC_INPUT_2 (.S0(ctrlunit_ext_1_ldi_sig), .I0(alu_ext_1_o_2), .I1(ctrlunit_ext_1_ctrl_b2), .O(ACC_INPUT_2_o));
  MUX_2x1 ACC_INPUT_3 (.S0(ctrlunit_ext_1_ldi_sig), .I0(alu_ext_1_o_3), .I1(ctrlunit_ext_1_ctrl_b3), .O(ACC_INPUT_3_o));
  Clock clock_1 (.out(clock_1_out));
  REGISTER_4BIT ACCUMULATOR_REG (
    .HARD_RESET(in_1), .CLK(clock_1_out), .REG_I3(ACC_INPUT_3_o), .REG_I2(ACC_INPUT_2_o),
    .REG_I1(ACC_INPUT_1_o), .REG_I0(ACC_INPUT_0_o), .WE(and_1_out), .REG_O3(out_6), .REG_O2(out_7),
    .REG_O1(out_8), .REG_O0(out_9));
  REGISTER_4BIT FLAG_REG (
    .HARD_RESET(in_1), .CLK(clock_1_out), .REG_I3(alu_ext_1_ovf), .REG_I2(alu_ext_1_n), .REG_I1(alu_ext_1_c),
    .REG_I0(alu_ext_1_z), .WE(and_1_out), .REG_O3(OVF), .REG_O2(N), .REG_O1(C), .REG_O0(Z));
  SRAM STATIC_RAM (
    .HARD_RESET(in_1), .CLK(clock_1_out), .SRAM_O3(STATIC_RAM_sram_o3), .SRAM_O2(STATIC_RAM_sram_o2),
    .SRAM_O1(STATIC_RAM_sram_o1), .SRAM_O0(STATIC_RAM_sram_o0));  // open: I3, I2, I1, I0, WE, ADDR1, ADDR0
  LED led_1 (.in(STATIC_RAM_sram_o3));
  LED led_2 (.in(STATIC_RAM_sram_o2));
  LED led_3 (.in(STATIC_RAM_sram_o1));
  LED led_4 (.in(STATIC_RAM_sram_o0));
endmodule

module Register_1BIT (
  input  HARD_RESET,
  input  CLK,
  input  REG_I0,
  input  WE,
  output REG_O0
);

  wire and_1_out, and_2_out, and_3_out, and_4_out, nand_1_out, nand_2_out, nand_3_out, nand_4_out,
       nand_5_out, nand_6_out, nand_8_out, not_1_out, not_2_out, not_3_out, not_4_out, not_5_out, not_6_out,
       not_7_out, or_1_out, or_2_out, or_3_out;

  not not_1 (not_1_out, WE);
  or or_1 (or_1_out, HARD_RESET, CLK);
  and and_1 (and_1_out, not_1_out, REG_O0);
  and and_2 (and_2_out, WE, REG_I0);
  or or_2 (or_2_out, and_1_out, and_2_out);
  not not_2 (not_2_out, HARD_RESET);
  and and_3 (and_3_out, not_2_out, or_2_out);
  and and_4 (and_4_out, HARD_RESET, 1'b0);
  or or_3 (or_3_out, and_3_out, and_4_out);
  not not_3 (not_3_out, or_1_out);
  not not_4 (not_4_out, not_3_out);
  not not_5 (not_5_out, or_3_out);
  nand nand_1 (nand_1_out, or_3_out, not_4_out);
  nand nand_2 (nand_2_out, not_4_out, not_5_out);
  nand nand_3 (nand_3_out, nand_1_out, nand_4_out);
  nand nand_4 (nand_4_out, nand_3_out, nand_2_out);
  not not_6 (not_6_out, not_4_out);
  not not_7 (not_7_out, nand_3_out);
  nand nand_5 (nand_5_out, nand_3_out, not_6_out);
  nand nand_6 (nand_6_out, not_6_out, not_7_out);
  nand nand_7 (REG_O0, nand_5_out, nand_8_out);
  nand nand_8 (nand_8_out, REG_O0, nand_6_out);
endmodule

module FSM_TIMING (
  input  in_1
);

  wire clock_1_out, not_1_out, register_1bit_1_reg_o0;

  Clock clock_1 (.out(clock_1_out));
  not not_1 (not_1_out, register_1bit_1_reg_o0);
  Register_1BIT register_1bit_1 (
    .HARD_RESET(in_1), .CLK(clock_1_out), .REG_I0(not_1_out), .WE(1'b1), .REG_O0(register_1bit_1_reg_o0));
endmodule

module SRAM (
  input  HARD_RESET,
  input  CLK,
  input  I3,
  input  I2,
  input  I1,
  input  I0,
  input  WE,
  input  ADDR1,
  input  ADDR0,
  output SRAM_O3,
  output SRAM_O2,
  output SRAM_O1,
  output SRAM_O0
);

  wire and_1_out, and_2_out, and_3_out, and_4_out, and_5_out, and_6_out, and_7_out, and_8_out, not_1_out,
       not_2_out, register_4bit_1_reg_o0, register_4bit_1_reg_o1, register_4bit_1_reg_o2,
       register_4bit_1_reg_o3, register_4bit_2_reg_o0, register_4bit_2_reg_o1, register_4bit_2_reg_o2,
       register_4bit_2_reg_o3, register_4bit_3_reg_o0, register_4bit_3_reg_o1, register_4bit_3_reg_o2,
       register_4bit_3_reg_o3, register_4bit_4_reg_o0, register_4bit_4_reg_o1, register_4bit_4_reg_o2,
       register_4bit_4_reg_o3;

  not not_1 (not_1_out, ADDR1);
  not not_2 (not_2_out, ADDR0);
  and and_1 (and_1_out, not_2_out, not_1_out);
  and and_2 (and_2_out, ADDR0, not_1_out);
  and and_3 (and_3_out, not_2_out, ADDR1);
  and and_4 (and_4_out, ADDR0, ADDR1);
  and and_5 (and_5_out, and_1_out, WE);
  and and_6 (and_6_out, and_2_out, WE);
  and and_7 (and_7_out, and_3_out, WE);
  and and_8 (and_8_out, and_4_out, WE);
  REGISTER_4BIT register_4bit_1 (
    .HARD_RESET(HARD_RESET), .CLK(CLK), .REG_I3(I3), .REG_I2(I2), .REG_I1(I1), .REG_I0(I0), .WE(and_5_out),
    .REG_O3(register_4bit_1_reg_o3), .REG_O2(register_4bit_1_reg_o2), .REG_O1(register_4bit_1_reg_o1),
    .REG_O0(register_4bit_1_reg_o0));
  REGISTER_4BIT register_4bit_2 (
    .HARD_RESET(HARD_RESET), .CLK(CLK), .REG_I3(I3), .REG_I2(I2), .REG_I1(I1), .REG_I0(I0), .WE(and_6_out),
    .REG_O3(register_4bit_2_reg_o3), .REG_O2(register_4bit_2_reg_o2), .REG_O1(register_4bit_2_reg_o1),
    .REG_O0(register_4bit_2_reg_o0));
  REGISTER_4BIT register_4bit_3 (
    .HARD_RESET(HARD_RESET), .CLK(CLK), .REG_I3(I3), .REG_I2(I2), .REG_I1(I1), .REG_I0(I0), .WE(and_7_out),
    .REG_O3(register_4bit_3_reg_o3), .REG_O2(register_4bit_3_reg_o2), .REG_O1(register_4bit_3_reg_o1),
    .REG_O0(register_4bit_3_reg_o0));
  REGISTER_4BIT register_4bit_4 (
    .HARD_RESET(HARD_RESET), .CLK(CLK), .REG_I3(I3), .REG_I2(I2), .REG_I1(I1), .REG_I0(I0), .WE(and_8_out),
    .REG_O3(register_4bit_4_reg_o3), .REG_O2(register_4bit_4_reg_o2), .REG_O1(register_4bit_4_reg_o1),
    .REG_O0(register_4bit_4_reg_o0));
  assign SRAM_O3 = and_1_out ? register_4bit_1_reg_o3 : 1'bz;  // Controlled_Buffer controlled_buffer_1
  assign SRAM_O2 = and_1_out ? register_4bit_1_reg_o2 : 1'bz;  // Controlled_Buffer controlled_buffer_2
  assign SRAM_O1 = and_1_out ? register_4bit_1_reg_o1 : 1'bz;  // Controlled_Buffer controlled_buffer_3
  assign SRAM_O0 = and_1_out ? register_4bit_1_reg_o0 : 1'bz;  // Controlled_Buffer controlled_buffer_4
  assign SRAM_O3 = and_2_out ? register_4bit_2_reg_o3 : 1'bz;  // Controlled_Buffer controlled_buffer_5
  assign SRAM_O2 = and_2_out ? register_4bit_2_reg_o2 : 1'bz;  // Controlled_Buffer controlled_buffer_6
  assign SRAM_O1 = and_2_out ? register_4bit_2_reg_o1 : 1'bz;  // Controlled_Buffer controlled_buffer_7
  assign SRAM_O0 = and_2_out ? register_4bit_2_reg_o0 : 1'bz;  // Controlled_Buffer controlled_buffer_8
  assign SRAM_O3 = and_3_out ? register_4bit_3_reg_o3 : 1'bz;  // Controlled_Buffer controlled_buffer_9
  assign SRAM_O2 = and_3_out ? register_4bit_3_reg_o2 : 1'bz;  // Controlled_Buffer controlled_buffer_10
  assign SRAM_O1 = and_3_out ? register_4bit_3_reg_o1 : 1'bz;  // Controlled_Buffer controlled_buffer_11
  assign SRAM_O0 = and_3_out ? register_4bit_3_reg_o0 : 1'bz;  // Controlled_Buffer controlled_buffer_12
  assign SRAM_O3 = and_4_out ? register_4bit_4_reg_o3 : 1'bz;  // Controlled_Buffer controlled_buffer_13
  assign SRAM_O2 = and_4_out ? register_4bit_4_reg_o2 : 1'bz;  // Controlled_Buffer controlled_buffer_14
  assign SRAM_O1 = and_4_out ? register_4bit_4_reg_o1 : 1'bz;  // Controlled_Buffer controlled_buffer_15
  assign SRAM_O0 = and_4_out ? register_4bit_4_reg_o0 : 1'bz;  // Controlled_Buffer controlled_buffer_16
endmodule

module MUX_4to1 (
  input  S1,
  input  S0,
  input  I3,
  input  I2,
  input  I1,
  input  I0,
  output O
);

  wire and_1_out, and_2_out, and_3_out, and_4_out, MUX2x1_out, not_1_out, not_2_out, or_1_out;

  not not_1 (not_1_out, S1);
  not not_2 (not_2_out, S0);
  and and_1 (and_1_out, not_2_out, not_1_out, I0);
  and and_2 (and_2_out, S0, not_1_out, I1);
  and and_3 (and_3_out, not_2_out, S1, I2);
  and and_4 (and_4_out, S0, S1, I3);
  or MUX2x1 (MUX2x1_out, and_1_out, and_2_out);
  or or_1 (or_1_out, and_3_out, and_4_out);
  or or_2 (O, MUX2x1_out, or_1_out);
endmodule

module BiDrectionalTriStateBuff (
  input  EN,
  input  INP,
  output out_3
);

  wire controlled_buffer_1_out;

  assign controlled_buffer_1_out = EN ? INP : 1'bz;  // Controlled_Buffer controlled_buffer_1
  assign out_3 = EN ? controlled_buffer_1_out : 1'bz;  // Controlled_Buffer controlled_buffer_2
endmodule
module CPU_v3 (
  input  CLK,
  input  HARD_RESET,
  input  OPC3,
  input  OPC2,
  input  OPC1,
  input  OPC0,
  input  OPRAND3,
  input  OPRAND2,
  input  OPRAND1,
  input  OPRAND0,
  output OVF,
  output N,
  output C,
  output Z,
  output ACC_O3,
  output ACC_O2,
  output ACC_O1,
  output ACC_O0,
  output ISA_OPC_3,
  output ISA_OPC_2,
  output ISA_OPC_1,
  output ISA_OPC_0,
  output ISA_OPR_3,
  output ISA_OPR_2,
  output ISA_OPR_1,
  output ISA_OPR_0,
  output ROMI3,
  output ROMI2,
  output ROMI1,
  output ROMI0
);

  wire alu_ext_1_c, alu_ext_1_n, alu_ext_1_o_0, alu_ext_1_o_1, alu_ext_1_o_2, alu_ext_1_o_3, alu_ext_1_ovf,
       alu_ext_1_z, and_1_out, controlled_buffer_1_out, controlled_buffer_2_out, controlled_buffer_3_out,
       controlled_buffer_4_out, controlled_buffer_5_out, controlled_buffer_6_out, controlled_buffer_7_out,
       controlled_buffer_8_out, ctrlunit_ext_1_alu_sig, ctrlunit_ext_1_ctrl_b0, ctrlunit_ext_1_ctrl_b1,
       ctrlunit_ext_1_ctrl_b2, ctrlunit_ext_1_ctrl_b3, ctrlunit_ext_1_ctrl_op0, ctrlunit_ext_1_ctrl_op1,
       ctrlunit_ext_1_ctrl_op2, ctrlunit_ext_1_hlt_sig, ctrlunit_ext_1_jmp_sig, ctrlunit_ext_1_lda_sig,
       ctrlunit_ext_1_ldi_sig, ctrlunit_ext_1_sta_sig, MEM_ADDR_REG_reg_o0, MEM_ADDR_REG_reg_o1, not_1_out,
       not_2_out, or_1_out, or_2_out, or_3_out, progcounter_ext_1_pco0, progcounter_ext_1_pco1,
       progcounter_ext_1_pco2, progcounter_ext_1_pco3, STATIC_RAM_sram_o0, STATIC_RAM_sram_o1,
       STATIC_RAM_sram_o2, STATIC_RAM_sram_o3;

  FSM_2BIT fsm_2bit_1 (.HARD_RESET(CLK), .CLK(HARD_RESET));  // open: HTL, FETCH, DECODE, EXECUTE, WRITEBACK
  ProgCounter_EXT progcounter_ext_1 (
    .A3(ROMI3), .A2(ROMI2), .A1(ROMI1), .A0(ROMI0), .PC_OPR3(controlled_buffer_1_out),
    .PC_OPR2(controlled_buffer_2_out), .PC_OPR1(controlled_buffer_3_out), .PC_OPR0(controlled_buffer_4_out),
    .JMP_JZ(ctrlunit_ext_1_jmp_sig), .PCO3(progcounter_ext_1_pco3), .PCO2(progcounter_ext_1_pco2),
    .PCO1(progcounter_ext_1_pco1), .PCO0(progcounter_ext_1_pco0));  // open: FTCH
  REGISTER_4BIT PC_REG (
    .HARD_RESET(HARD_RESET), .CLK(CLK), .REG_I3(progcounter_ext_1_pco3), .REG_I2(progcounter_ext_1_pco2),
    .REG_I1(progcounter_ext_1_pco1), .REG_I0(progcounter_ext_1_pco0), .WE(not_2_out), .REG_O3(ROMI3),
    .REG_O2(ROMI2), .REG_O1(ROMI1), .REG_O0(ROMI0));
  REGISTER_4BIT INSTRUCTION_REG_OPC (
    .HARD_RESET(HARD_RESET), .CLK(CLK), .REG_I3(OPC3), .REG_I2(OPC2), .REG_I1(OPC1), .REG_I0(OPC0),
    .WE(not_2_out), .REG_O3(ISA_OPC_3), .REG_O2(ISA_OPC_2), .REG_O1(ISA_OPC_1), .REG_O0(ISA_OPC_0));
  REGISTER_4BIT INSTRUCTION_REG_OPR (
    .HARD_RESET(HARD_RESET), .CLK(CLK), .REG_I3(OPRAND3), .REG_I2(OPRAND2), .REG_I1(OPRAND1),
    .REG_I0(OPRAND0), .WE(not_2_out), .REG_O3(ISA_OPR_3), .REG_O2(ISA_OPR_2), .REG_O1(ISA_OPR_1),
    .REG_O0(ISA_OPR_0));
  CTRLUNIT_EXT ctrlunit_ext_1 (
    .CTRL_S3(ISA_OPC_3), .CTRL_S2(ISA_OPC_2), .CTRL_S1(ISA_OPC_1), .CTRL_S0(ISA_OPC_0),
    .CTRL_OPR3(ISA_OPR_3), .CTRL_OPR2(ISA_OPR_2), .CTRL_OPR1(ISA_OPR_1), .CTRL_OPR0(ISA_OPR_0), .FLAG_N(N),
    .FLAG_Z(Z), .CTRL_OP2(ctrlunit_ext_1_ctrl_op2), .CTRL_OP1(ctrlunit_ext_1_ctrl_op1),
    .CTRL_OP0(ctrlunit_ext_1_ctrl_op0), .CTRL_B3(ctrlunit_ext_1_ctrl_b3), .CTRL_B2(ctrlunit_ext_1_ctrl_b2),
    .CTRL_B1(ctrlunit_ext_1_ctrl_b1), .CTRL_B0(ctrlunit_ext_1_ctrl_b0), .JMP_SIG(ctrlunit_ext_1_jmp_sig),
    .HLT_SIG(ctrlunit_ext_1_hlt_sig), .LDI_SIG(ctrlunit_ext_1_ldi_sig), .LDA_SIG(ctrlunit_ext_1_lda_sig),
    .STA_SIG(ctrlunit_ext_1_sta_sig), .ALU_SIG(ctrlunit_ext_1_alu_sig));  // open: FLAG_OVF, FLAG_C, CTRL_OP3, CTRL_WE
  not not_1 (not_1_out, ctrlunit_ext_1_lda_sig);
  assign controlled_buffer_1_out = not_1_out ? ctrlunit_ext_1_ctrl_b3 : 1'bz;  // Controlled_Buffer controlled_buffer_1
  assign controlled_buffer_2_out = not_1_out ? ctrlunit_ext_1_ctrl_b2 : 1'bz;  // Controlled_Buffer controlled_buffer_2
  assign controlled_buffer_3_out = not_1_out ? ctrlunit_ext_1_ctrl_b1 : 1'bz;  // Controlled_Buffer controlled_buffer_3
  assign controlled_buffer_4_out = not_1_out ? ctrlunit_ext_1_ctrl_b0 : 1'bz;  // Controlled_Buffer controlled_buffer_4
  not not_2 (not_2_out, ctrlunit_ext_1_hlt_sig);
  or or_1 (or_1_out, ctrlunit_ext_1_ldi_sig, ctrlunit_ext_1_lda_sig);
  ALU_EXT alu_ext_1 (
    .A_3(ACC_O3), .A_2(ACC_O2), .A_1(ACC_O1), .A_0(ACC_O0), .B_3(controlled_buffer_1_out),
    .B_2(controlled_buffer_2_out), .B_1(controlled_buffer_3_out), .B_0(controlled_buffer_4_out),
    .S2(ctrlunit_ext_1_ctrl_op2), .S1(ctrlunit_ext_1_ctrl_op1), .S0(ctrlunit_ext_1_ctrl_op0),
    .OVF(alu_ext_1_ovf), .N(alu_ext_1_n), .C(alu_ext_1_c), .Z(alu_ext_1_z), .O_3(alu_ext_1_o_3),
    .O_2(alu_ext_1_o_2), .O_1(alu_ext_1_o_1), .O_0(alu_ext_1_o_0));
  assign controlled_buffer_5_out = ctrlunit_ext_1_alu_sig ? alu_ext_1_o_3 : 1'bz;  // Controlled_Buffer controlled_buffer_5
  assign controlled_buffer_6_out = ctrlunit_ext_1_alu_sig ? alu_ext_1_o_2 : 1'bz;  // Controlled_Buffer controlled_buffer_6
  assign controlled_buffer_7_out = ctrlunit_ext_1_alu_sig ? alu_ext_1_o_1 : 1'bz;  // Controlled_Buffer controlled_buffer_7
  assign controlled_buffer_8_out = ctrlunit_ext_1_alu_sig ? alu_ext_1_o_0 : 1'bz;  // Controlled_Buffer controlled_buffer_8
  assign controlled_buffer_5_out = or_1_out ? controlled_buffer_1_out : 1'bz;  // Controlled_Buffer controlled_buffer_9
  assign controlled_buffer_6_out = or_1_out ? controlled_buffer_2_out : 1'bz;  // Controlled_Buffer controlled_buffer_10
  assign controlled_buffer_7_out = or_1_out ? controlled_buffer_3_out : 1'bz;  // Controlled_Buffer controlled_buffer_11
  assign controlled_buffer_8_out = or_1_out ? controlled_buffer_4_out : 1'bz;  // Controlled_Buffer controlled_buffer_12
  or or_2 (or_2_out, or_1_out, ctrlunit_ext_1_alu_sig);
  and and_1 (and_1_out, or_2_out, not_2_out);
  REGISTER_4BIT ACCUMULATOR_REG (
    .HARD_RESET(HARD_RESET), .CLK(CLK), .REG_I3(controlled_buffer_5_out), .REG_I2(controlled_buffer_6_out),
    .REG_I1(controlled_buffer_7_out), .REG_I0(controlled_buffer_8_out), .WE(and_1_out), .REG_O3(ACC_O3),
    .REG_O2(ACC_O2), .REG_O1(ACC_O1), .REG_O0(ACC_O0));
  REGISTER_4BIT FLAG_REG (
    .HARD_RESET(HARD_RESET), .CLK(CLK), .REG_I3(alu_ext_1_ovf), .REG_I2(alu_ext_1_n), .REG_I1(alu_ext_1_c),
    .REG_I0(alu_ext_1_z), .WE(and_1_out), .REG_O3(OVF), .REG_O2(N), .REG_O1(C), .REG_O0(Z));
  or or_3 (or_3_out, ctrlunit_ext_1_lda_sig, ctrlunit_ext_1_sta_sig);
  REGISTER_4BIT MEM_ADDR_REG (
    .HARD_RESET(HARD_RESET), .CLK(CLK), .REG_I1(ctrlunit_ext_1_ctrl_b1), .REG_I0(ctrlunit_ext_1_ctrl_b0),
    .WE(or_3_out), .REG_O1(MEM_ADDR_REG_reg_o1), .REG_O0(MEM_ADDR_REG_reg_o0));  // open: REG_I3, REG_I2, REG_O3, REG_O2
  SRAM STATIC_RAM (
    .HARD_RESET(HARD_RESET), .CLK(CLK), .I3(ACC_O3), .I2(ACC_O2), .I1(ACC_O1), .I0(ACC_O0),
    .WE(ctrlunit_ext_1_sta_sig), .ADDR1(MEM_ADDR_REG_reg_o1), .ADDR0(MEM_ADDR_REG_reg_o0),
    .SRAM_O3(STATIC_RAM_sram_o3), .SRAM_O2(STATIC_RAM_sram_o2), .SRAM_O1(STATIC_RAM_sram_o1),
    .SRAM_O0(STATIC_RAM_sram_o0));
  assign controlled_buffer_1_out = ctrlunit_ext_1_lda_sig ? STATIC_RAM_sram_o3 : 1'bz;  // Controlled_Buffer controlled_buffer_13
  assign controlled_buffer_2_out = ctrlunit_ext_1_lda_sig ? STATIC_RAM_sram_o2 : 1'bz;  // Controlled_Buffer controlled_buffer_14
  assign controlled_buffer_3_out = ctrlunit_ext_1_lda_sig ? STATIC_RAM_sram_o1 : 1'bz;  // Controlled_Buffer controlled_buffer_15
  assign controlled_buffer_4_out = ctrlunit_ext_1_lda_sig ? STATIC_RAM_sram_o0 : 1'bz;  // Controlled_Buffer controlled_buffer_16
endmodule

module CPU_v4 (
  input  in_1,
  output OVF,
  output N,
  output C,
  output Z,
  output out_6,
  output out_7,
  output out_8,
  output out_9,
  output out_10,
  output out_11,
  output out_12,
  output out_13,
  output out_14,
  output out_15,
  output out_16,
  output out_17
);

  wire ACC_INPUT_0_o, ACC_INPUT_1_o, ACC_INPUT_2_o, ACC_INPUT_3_o, alu_ext_1_c, alu_ext_1_n, alu_ext_1_o_0,
       alu_ext_1_o_1, alu_ext_1_o_2, alu_ext_1_o_3, alu_ext_1_ovf, alu_ext_1_z, and_1_out, clock_1_out,
       ctrlunit_ext_1_alu_sig, ctrlunit_ext_1_ctrl_b0, ctrlunit_ext_1_ctrl_b1, ctrlunit_ext_1_ctrl_b2,
       ctrlunit_ext_1_ctrl_b3, ctrlunit_ext_1_ctrl_op0, ctrlunit_ext_1_ctrl_op1, ctrlunit_ext_1_ctrl_op2,
       ctrlunit_ext_1_ctrl_we, ctrlunit_ext_1_hlt_sig, ctrlunit_ext_1_jmp_sig, ctrlunit_ext_1_ldi_sig,
       ldi_tester_1_opc0, ldi_tester_1_opc1, ldi_tester_1_opc2, ldi_tester_1_opc3, ldi_tester_1_oprand0,
       ldi_tester_1_oprand1, ldi_tester_1_oprand2, ldi_tester_1_oprand3, not_1_out, not_2_out, PC_REG_reg_o0,
       PC_REG_reg_o1, PC_REG_reg_o2, PC_REG_reg_o3, progcounter_ext_1_pco0, progcounter_ext_1_pco1,
       progcounter_ext_1_pco2, progcounter_ext_1_pco3, STATIC_RAM_sram_o0, STATIC_RAM_sram_o1,
       STATIC_RAM_sram_o2, STATIC_RAM_sram_o3;

  ProgCounter_EXT progcounter_ext_1 (
    .A3(PC_REG_reg_o3), .A2(PC_REG_reg_o2), .A1(PC_REG_reg_o1), .A0(PC_REG_reg_o0),
    .PC_OPR3(ctrlunit_ext_1_ctrl_b3), .PC_OPR2(ctrlunit_ext_1_ctrl_b2), .PC_OPR1(ctrlunit_ext_1_ctrl_b1),
    .PC_OPR0(ctrlunit_ext_1_ctrl_b0), .JMP_JZ(ctrlunit_ext_1_jmp_sig), .PCO3(progcounter_ext_1_pco3),
    .PCO2(progcounter_ext_1_pco2), .PCO1(progcounter_ext_1_pco1), .PCO0(progcounter_ext_1_pco0));  // open: FTCH
  REGISTER_4BIT PC_REG (
    .HARD_RESET(in_1), .CLK(clock_1_out), .REG_I3(progcounter_ext_1_pco3), .REG_I2(progcounter_ext_1_pco2),
    .REG_I1(progcounter_ext_1_pco1), .REG_I0(progcounter_ext_1_pco0), .WE(not_1_out), .REG_O3(PC_REG_reg_o3),
    .REG_O2(PC_REG_reg_o2), .REG_O1(PC_REG_reg_o1), .REG_O0(PC_REG_reg_o0));
  LDI_TESTER ldi_tester_1 (
    .ROMI3(PC_REG_reg_o3), .ROMI2(PC_REG_reg_o2), .ROMI1(PC_REG_reg_o1), .ROMI0(PC_REG_reg_o0),
    .OPC3(ldi_tester_1_opc3), .OPC2(ldi_tester_1_opc2), .OPC1(ldi_tester_1_opc1), .OPC0(ldi_tester_1_opc0),
    .OPRAND3(ldi_tester_1_oprand3), .OPRAND2(ldi_tester_1_oprand2), .OPRAND1(ldi_tester_1_oprand1),
    .OPRAND0(ldi_tester_1_oprand0));
  REGISTER_4BIT INSTRUCTION_REG_OPC (
    .HARD_RESET(in_1), .CLK(clock_1_out), .REG_I3(ldi_tester_1_opc3), .REG_I2(ldi_tester_1_opc2),
    .REG_I1(ldi_tester_1_opc1), .REG_I0(ldi_tester_1_opc0), .WE(not_1_out), .REG_O3(out_10), .REG_O2(out_11),
    .REG_O1(out_12), .REG_O0(out_13));
  REGISTER_4BIT INSTRUCTION_REG_OPR (
    .HARD_RESET(in_1), .CLK(clock_1_out), .REG_I3(ldi_tester_1_oprand3), .REG_I2(ldi_tester_1_oprand2),
    .REG_I1(ldi_tester_1_oprand1), .REG_I0(ldi_tester_1_oprand0), .WE(not_1_out), .REG_O3(out_14),
    .REG_O2(out_15), .REG_O1(out_16), .REG_O0(out_17));
  CTRLUNIT_EXT ctrlunit_ext_1 (
    .CTRL_S3(out_10), .CTRL_S2(out_11), .CTRL_S1(out_12), .CTRL_S0(out_13), .CTRL_OPR3(out_14),
    .CTRL_OPR2(out_15), .CTRL_OPR1(out_16), .CTRL_OPR0(out_17), .FLAG_N(N), .FLAG_Z(Z),
    .CTRL_OP2(ctrlunit_ext_1_ctrl_op2), .CTRL_OP1(ctrlunit_ext_1_ctrl_op1),
    .CTRL_OP0(ctrlunit_ext_1_ctrl_op0), .CTRL_WE(ctrlunit_ext_1_ctrl_we), .CTRL_B3(ctrlunit_ext_1_ctrl_b3),
    .CTRL_B2(ctrlunit_ext_1_ctrl_b2), .CTRL_B1(ctrlunit_ext_1_ctrl_b1), .CTRL_B0(ctrlunit_ext_1_ctrl_b0),
    .JMP_SIG(ctrlunit_ext_1_jmp_sig), .HLT_SIG(ctrlunit_ext_1_hlt_sig), .LDI_SIG(ctrlunit_ext_1_ldi_sig),
    .ALU_SIG(ctrlunit_ext_1_alu_sig));  // open: FLAG_OVF, FLAG_C, CTRL_OP3, LDA_SIG, STA_SIG
  not not_1 (not_1_out, ctrlunit_ext_1_hlt_sig);
  and and_1 (and_1_out, ctrlunit_ext_1_ctrl_we, not_2_out);
  not not_2 (not_2_out, ctrlunit_ext_1_jmp_sig);
  ALU_EXT alu_ext_1 (
    .A_3(out_6), .A_2(out_7), .A_1(out_8), .A_0(out_9), .B_3(ctrlunit_ext_1_ctrl_b3),
    .B_2(ctrlunit_ext_1_ctrl_b2), .B_1(ctrlunit_ext_1_ctrl_b1), .B_0(ctrlunit_ext_1_ctrl_b0),
    .S2(ctrlunit_ext_1_ctrl_op2), .S1(ctrlunit_ext_1_ctrl_op1), .S0(ctrlunit_ext_1_ctrl_op0),
    .OVF(alu_ext_1_ovf), .N(alu_ext_1_n), .C(alu_ext_1_c), .Z(alu_ext_1_z), .O_3(alu_ext_1_o_3),
    .O_2(alu_ext_1_o_2), .O_1(alu_ext_1_o_1), .O_0(alu_ext_1_o_0));
  MUX_2x1 ACC_INPUT_0 (.S0(ctrlunit_ext_1_ldi_sig), .I0(alu_ext_1_o_0), .I1(ctrlunit_ext_1_ctrl_b0), .O(ACC_INPUT_0_o));
  MUX_2x1 ACC_INPUT_1 (.S0(ctrlunit_ext_1_ldi_sig), .I0(alu_ext_1_o_1), .I1(ctrlunit_ext_1_ctrl_b1), .O(ACC_INPUT_1_o));
  MUX_2x1 ACC_INPUT_2 (.S0(ctrlunit_ext_1_ldi_sig), .I0(alu_ext_1_o_2), .I1(ctrlunit_ext_1_ctrl_b2), .O(ACC_INPUT_2_o));
  MUX_2x1 ACC_INPUT_3 (.S0(ctrlunit_ext_1_ldi_sig), .I0(alu_ext_1_o_3), .I1(ctrlunit_ext_1_ctrl_b3), .O(ACC_INPUT_3_o));
  // OR_Gate or_1 has open pins: in0=ctrlunit_ext_1_ldi_sig, in1=ctrlunit_ext_1_alu_sig, out=open
  Clock clock_1 (.out(clock_1_out));
  REGISTER_4BIT ACCUMULATOR_REG (
    .HARD_RESET(in_1), .CLK(clock_1_out), .REG_I3(ACC_INPUT_3_o), .REG_I2(ACC_INPUT_2_o),
    .REG_I1(ACC_INPUT_1_o), .REG_I0(ACC_INPUT_0_o), .WE(and_1_out), .REG_O3(out_6), .REG_O2(out_7),
    .REG_O1(out_8), .REG_O0(out_9));
  REGISTER_4BIT FLAG_REG (
    .HARD_RESET(in_1), .CLK(clock_1_out), .REG_I3(alu_ext_1_ovf), .REG_I2(alu_ext_1_n), .REG_I1(alu_ext_1_c),
    .REG_I0(alu_ext_1_z), .WE(and_1_out), .REG_O3(OVF), .REG_O2(N), .REG_O1(C), .REG_O0(Z));
  SRAM STATIC_RAM (
    .HARD_RESET(in_1), .CLK(clock_1_out), .SRAM_O3(STATIC_RAM_sram_o3), .SRAM_O2(STATIC_RAM_sram_o2),
    .SRAM_O1(STATIC_RAM_sram_o1), .SRAM_O0(STATIC_RAM_sram_o0));  // open: I3, I2, I1, I0, WE, ADDR1, ADDR0
  LED led_1 (.in(STATIC_RAM_sram_o3));
  LED led_2 (.in(STATIC_RAM_sram_o2));
  LED led_3 (.in(STATIC_RAM_sram_o1));
  LED led_4 (.in(STATIC_RAM_sram_o0));
endmodule

module PlayGround (
  input  in_1
);

  wire clock_1_out, cpu_v3_1_acc_o0, cpu_v3_1_acc_o1, cpu_v3_1_acc_o2, cpu_v3_1_acc_o3, cpu_v3_1_c,
       cpu_v3_1_isa_opc_0, cpu_v3_1_isa_opc_1, cpu_v3_1_isa_opc_2, cpu_v3_1_isa_opc_3, cpu_v3_1_isa_opr_0,
       cpu_v3_1_isa_opr_1, cpu_v3_1_isa_opr_2, cpu_v3_1_isa_opr_3, cpu_v3_1_n, cpu_v3_1_ovf, cpu_v3_1_romi0,
       cpu_v3_1_romi1, cpu_v3_1_romi2, cpu_v3_1_romi3, cpu_v3_1_z, test_prog_lda_1_opc0,
       test_prog_lda_1_opc1, test_prog_lda_1_opc2, test_prog_lda_1_opc3, test_prog_lda_1_oprand0,
       test_prog_lda_1_oprand1, test_prog_lda_1_oprand2, test_prog_lda_1_oprand3;

  Clock clock_1 (.out(clock_1_out));
  TEST_PROG_LDA test_prog_lda_1 (
    .ROMI3(cpu_v3_1_romi3), .ROMI2(cpu_v3_1_romi2), .ROMI1(cpu_v3_1_romi1), .ROMI0(cpu_v3_1_romi0),
    .OPC3(test_prog_lda_1_opc3), .OPC2(test_prog_lda_1_opc2), .OPC1(test_prog_lda_1_opc1),
    .OPC0(test_prog_lda_1_opc0), .OPRAND3(test_prog_lda_1_oprand3), .OPRAND2(test_prog_lda_1_oprand2),
    .OPRAND1(test_prog_lda_1_oprand1), .OPRAND0(test_prog_lda_1_oprand0));
  CPU_v3 cpu_v3_1 (
    .CLK(clock_1_out), .HARD_RESET(in_1), .OPC3(test_prog_lda_1_opc3), .OPC2(test_prog_lda_1_opc2),
    .OPC1(test_prog_lda_1_opc1), .OPC0(test_prog_lda_1_opc0), .OPRAND3(test_prog_lda_1_oprand3),
    .OPRAND2(test_prog_lda_1_oprand2), .OPRAND1(test_prog_lda_1_oprand1), .OPRAND0(test_prog_lda_1_oprand0),
    .OVF(cpu_v3_1_ovf), .N(cpu_v3_1_n), .C(cpu_v3_1_c), .Z(cpu_v3_1_z), .ACC_O3(cpu_v3_1_acc_o3),
    .ACC_O2(cpu_v3_1_acc_o2), .ACC_O1(cpu_v3_1_acc_o1), .ACC_O0(cpu_v3_1_acc_o0),
    .ISA_OPC_3(cpu_v3_1_isa_opc_3), .ISA_OPC_2(cpu_v3_1_isa_opc_2), .ISA_OPC_1(cpu_v3_1_isa_opc_1),
    .ISA_OPC_0(cpu_v3_1_isa_opc_0), .ISA_OPR_3(cpu_v3_1_isa_opr_3), .ISA_OPR_2(cpu_v3_1_isa_opr_2),
    .ISA_OPR_1(cpu_v3_1_isa_opr_1), .ISA_OPR_0(cpu_v3_1_isa_opr_0), .ROMI3(cpu_v3_1_romi3),
    .ROMI2(cpu_v3_1_romi2), .ROMI1(cpu_v3_1_romi1), .ROMI0(cpu_v3_1_romi0));
  LED led_1 (.in(cpu_v3_1_ovf));
  LED led_2 (.in(cpu_v3_1_n));
  LED led_3 (.in(cpu_v3_1_c));
  LED led_4 (.in(cpu_v3_1_z));
  LED led_5 (.in(cpu_v3_1_acc_o3));
  LED led_6 (.in(cpu_v3_1_acc_o2));
  LED led_7 (.in(cpu_v3_1_acc_o1));
  LED led_8 (.in(cpu_v3_1_acc_o0));
  LED led_9 (.in(cpu_v3_1_isa_opc_3));
  LED led_10 (.in(cpu_v3_1_isa_opc_2));
  LED led_11 (.in(cpu_v3_1_isa_opc_1));
  LED led_12 (.in(cpu_v3_1_isa_opc_0));
  LED led_13 (.in(cpu_v3_1_isa_opr_3));
  LED led_14 (.in(cpu_v3_1_isa_opr_2));
  LED led_15 (.in(cpu_v3_1_isa_opr_1));
  LED led_16 (.in(cpu_v3_1_isa_opr_0));
endmodule

module TEST_PROG_ADD (
  input  ROMI3,
  input  ROMI2,
  input  ROMI1,
  input  ROMI0,
  output OPC3,
  output OPC2,
  output OPC1,
  output OPC0,
  output OPRAND3,
  output OPRAND2,
  output OPRAND1,
  output OPRAND0
);

  wire and_1_out, and_2_out, and_3_out, and_4_out, and_5_out, and_6_out, and_7_out, and_8_out, and_9_out,
       and_10_out, and_11_out, and_12_out, and_13_out, and_14_out, and_15_out, and_16_out, and_17_out,
       and_18_out, and_19_out, and_20_out, and_21_out, and_22_out, and_23_out, and_24_out, and_25_out,
       and_26_out, and_27_out, and_28_out, and_29_out, and_30_out, and_31_out, and_32_out, and_33_out,
       and_34_out, and_35_out, and_36_out, and_37_out, and_38_out, and_39_out, and_40_out, and_41_out,
       and_42_out, and_43_out, and_44_out, and_45_out, and_46_out, and_47_out, and_48_out, and_49_out,
       and_50_out, and_51_out, and_52_out, and_53_out, and_54_out, and_55_out, and_56_out, and_57_out,
       and_58_out, and_59_out, and_60_out, and_61_out, and_62_out, and_63_out, and_64_out, and_65_out,
       and_66_out, and_67_out, and_68_out, and_69_out, and_70_out, and_71_out, and_72_out, and_73_out,
       and_74_out, and_75_out, and_76_out, and_77_out, and_78_out, and_79_out, and_80_out, and_81_out,
       and_82_out, and_83_out, and_84_out, and_85_out, and_86_out, and_87_out, and_88_out, and_89_out,
       and_90_out, and_91_out, and_92_out, and_93_out, and_94_out, and_95_out, and_96_out, and_97_out,
       and_98_out, and_99_out, and_100_out, and_101_out, and_102_out, and_103_out, and_104_out, and_105_out,
       and_106_out, and_107_out, and_108_out, and_109_out, and_110_out, and_111_out, and_112_out,
       and_113_out, and_114_out, and_115_out, and_116_out, and_117_out, and_118_out, and_119_out,
       and_120_out, and_121_out, and_122_out, and_123_out, and_124_out, and_125_out, and_126_out,
       and_127_out, and_128_out, and_129_out, and_130_out, and_131_out, and_132_out, and_133_out,
       and_134_out, and_135_out, and_136_out, and_137_out, and_138_out, and_139_out, and_140_out,
       and_141_out, and_142_out, and_143_out, DECORDER_4x16_out, not_1_out, not_2_out, not_3_out, not_4_out,
       or_1_out, or_3_out, or_4_out, or_6_out, or_7_out, or_8_out, or_10_out, or_12_out, or_13_out,
       or_14_out, or_16_out, or_18_out, or_19_out, or_21_out, or_22_out, or_23_out;

  not not_1 (not_1_out, ROMI3);
  not not_2 (not_2_out, ROMI2);
  not not_3 (not_3_out, ROMI1);
  not not_4 (not_4_out, ROMI0);
  and DECORDER_4x16 (DECORDER_4x16_out, not_4_out, not_3_out, not_2_out, not_1_out);
  and and_1 (and_1_out, ROMI0, not_3_out, not_2_out, not_1_out);
  and and_2 (and_2_out, not_4_out, ROMI1, not_2_out, not_1_out);
  and and_3 (and_3_out, ROMI0, ROMI1, not_2_out, not_1_out);
  and and_4 (and_4_out, not_4_out, not_3_out, ROMI2, not_1_out);
  and and_5 (and_5_out, ROMI0, not_3_out, ROMI2, not_1_out);
  and and_6 (and_6_out, not_4_out, ROMI1, ROMI2, not_1_out);
  and and_7 (and_7_out, ROMI0, ROMI1, ROMI2, not_1_out);
  and and_8 (and_8_out, not_4_out, not_3_out, not_2_out, ROMI3);
  and and_9 (and_9_out, ROMI0, not_3_out, not_2_out, ROMI3);
  and and_10 (and_10_out, not_4_out, ROMI1, not_2_out, ROMI3);
  and and_11 (and_11_out, ROMI0, ROMI1, not_2_out, ROMI3);
  and and_12 (and_12_out, not_4_out, not_3_out, ROMI2, ROMI3);
  and and_13 (and_13_out, ROMI0, not_3_out, ROMI2, ROMI3);
  and and_14 (and_14_out, not_4_out, ROMI1, ROMI2, ROMI3);
  and and_15 (and_15_out, ROMI0, ROMI1, ROMI2, ROMI3);
  or or_1 (or_1_out, and_31_out, and_30_out, and_29_out, and_28_out, and_27_out, and_26_out, and_25_out, and_24_out);
  and and_16 (and_16_out, DECORDER_4x16_out, 1'b0);
  and and_17 (and_17_out, and_1_out, 1'b0);
  and and_18 (and_18_out, and_2_out, 1'b0);
  and and_19 (and_19_out, and_3_out, 1'b0);
  and and_20 (and_20_out, and_4_out, 1'b0);
  and and_21 (and_21_out, and_5_out, 1'b0);
  and and_22 (and_22_out, and_6_out, 1'b0);
  and and_23 (and_23_out, and_7_out, 1'b0);
  and and_24 (and_24_out, and_8_out, 1'b0);
  and and_25 (and_25_out, and_9_out, 1'b0);
  and and_26 (and_26_out, and_10_out, 1'b0);
  and and_27 (and_27_out, and_11_out, 1'b0);
  and and_28 (and_28_out, and_12_out, 1'b0);
  and and_29 (and_29_out, and_13_out, 1'b0);
  and and_30 (and_30_out, and_14_out, 1'b0);
  and and_31 (and_31_out, and_15_out, 1'b0);
  or or_2 (OPC3, or_1_out, or_3_out);
  or or_3 (or_3_out, and_16_out, and_17_out, and_18_out, and_19_out, and_20_out, and_21_out, and_22_out, and_23_out);
  or or_4 (or_4_out, and_47_out, and_46_out, and_45_out, and_44_out, and_43_out, and_42_out, and_41_out, and_40_out);
  and and_32 (and_32_out, DECORDER_4x16_out, 1'b0);
  and and_33 (and_33_out, and_1_out, 1'b0);
  and and_34 (and_34_out, and_2_out, 1'b0);
  and and_35 (and_35_out, and_3_out, 1'b0);
  and and_36 (and_36_out, and_4_out, 1'b0);
  and and_37 (and_37_out, and_5_out, 1'b0);
  and and_38 (and_38_out, and_6_out, 1'b0);
  and and_39 (and_39_out, and_7_out, 1'b0);
  and and_40 (and_40_out, and_8_out, 1'b0);
  and and_41 (and_41_out, and_9_out, 1'b0);
  and and_42 (and_42_out, and_10_out, 1'b0);
  and and_43 (and_43_out, and_11_out, 1'b0);
  and and_44 (and_44_out, and_12_out, 1'b0);
  and and_45 (and_45_out, and_13_out, 1'b0);
  and and_46 (and_46_out, and_14_out, 1'b0);
  and and_47 (and_47_out, and_15_out, 1'b0);
  or or_5 (OPC2, or_4_out, or_6_out);
  or or_6 (or_6_out, and_32_out, and_33_out, and_34_out, and_35_out, and_36_out, and_37_out, and_38_out, and_39_out);
  and and_48 (and_48_out, DECORDER_4x16_out, 1'b0);
  and and_49 (and_49_out, and_1_out, 1'b0);
  and and_50 (and_50_out, and_2_out, 1'b0);
  and and_51 (and_51_out, and_3_out, 1'b0);
  and and_52 (and_52_out, and_4_out, 1'b0);
  and and_53 (and_53_out, and_5_out, 1'b0);
  and and_54 (and_54_out, and_6_out, 1'b0);
  and and_55 (and_55_out, and_7_out, 1'b0);
  and and_56 (and_56_out, and_8_out, 1'b0);
  and and_57 (and_57_out, and_9_out, 1'b0);
  and and_58 (and_58_out, and_10_out, 1'b0);
  and and_59 (and_59_out, and_11_out, 1'b0);
  and and_60 (and_60_out, and_12_out, 1'b0);
  and and_61 (and_61_out, and_13_out, 1'b0);
  and and_62 (and_62_out, and_14_out, 1'b0);
  and and_63 (and_63_out, and_15_out, 1'b0);
  or or_7 (or_7_out, and_63_out, and_62_out, and_61_out, and_60_out, and_59_out, and_58_out, and_57_out, and_56_out);
  or or_8 (or_8_out, and_48_out, and_49_out, and_50_out, and_51_out, and_52_out, and_53_out, and_54_out, and_55_out);
  or or_9 (OPC1, or_7_out, or_8_out);
  or or_10 (or_10_out, and_79_out, and_78_out, and_77_out, and_76_out, and_75_out, and_74_out, and_73_out, and_72_out);
  and and_64 (and_64_out, DECORDER_4x16_out, 1'b0);
  and and_65 (and_65_out, and_1_out, 1'b0);
  and and_66 (and_66_out, and_2_out, 1'b0);
  and and_67 (and_67_out, and_3_out, 1'b0);
  and and_68 (and_68_out, and_4_out, 1'b0);
  and and_69 (and_69_out, and_5_out, 1'b0);
  and and_70 (and_70_out, and_6_out, 1'b0);
  and and_71 (and_71_out, and_7_out, 1'b0);
  and and_72 (and_72_out, and_8_out, 1'b0);
  and and_73 (and_73_out, and_9_out, 1'b0);
  and and_74 (and_74_out, and_10_out, 1'b0);
  and and_75 (and_75_out, and_11_out, 1'b0);
  and and_76 (and_76_out, and_12_out, 1'b0);
  and and_77 (and_77_out, and_13_out, 1'b0);
  and and_78 (and_78_out, and_14_out, 1'b0);
  and and_79 (and_79_out, and_15_out, 1'b0);
  or or_11 (OPC0, or_10_out, or_12_out);
  or or_12 (or_12_out, and_64_out, and_65_out, and_66_out, and_67_out, and_68_out, and_69_out, and_70_out, and_71_out);
  or or_13 (or_13_out, and_95_out, and_94_out, and_93_out, and_92_out, and_91_out, and_90_out, and_89_out, and_88_out);
  and and_80 (and_80_out, DECORDER_4x16_out, 1'b0);
  and and_81 (and_81_out, and_1_out, 1'b0);
  and and_82 (and_82_out, and_2_out, 1'b1);
  and and_83 (and_83_out, and_3_out, 1'b0);
  and and_84 (and_84_out, and_4_out, 1'b0);
  and and_85 (and_85_out, and_5_out, 1'b0);
  and and_86 (and_86_out, and_6_out, 1'b0);
  and and_87 (and_87_out, and_7_out, 1'b0);
  and and_88 (and_88_out, and_8_out, 1'b0);
  and and_89 (and_89_out, and_9_out, 1'b0);
  and and_90 (and_90_out, and_10_out, 1'b0);
  and and_91 (and_91_out, and_11_out, 1'b0);
  and and_92 (and_92_out, and_12_out, 1'b0);
  and and_93 (and_93_out, and_13_out, 1'b0);
  and and_94 (and_94_out, and_14_out, 1'b0);
  and and_95 (and_95_out, and_15_out, 1'b0);
  or or_14 (or_14_out, and_80_out, and_81_out, and_82_out, and_83_out, and_84_out, and_85_out, and_86_out, and_87_out);
  or or_15 (OPRAND3, or_13_out, or_14_out);
  or or_16 (or_16_out, and_111_out, and_110_out, and_109_out, and_108_out, and_107_out, and_106_out, and_105_out, and_104_out);
  and and_96 (and_96_out, DECORDER_4x16_out, 1'b0);
  and and_97 (and_97_out, and_1_out, 1'b0);
  and and_98 (and_98_out, and_2_out, 1'b1);
  and and_99 (and_99_out, and_3_out, 1'b0);
  and and_100 (and_100_out, and_4_out, 1'b0);
  and and_101 (and_101_out, and_5_out, 1'b0);
  and and_102 (and_102_out, and_6_out, 1'b0);
  and and_103 (and_103_out, and_7_out, 1'b0);
  and and_104 (and_104_out, and_8_out, 1'b0);
  and and_105 (and_105_out, and_9_out, 1'b0);
  and and_106 (and_106_out, and_10_out, 1'b0);
  and and_107 (and_107_out, and_11_out, 1'b0);
  and and_108 (and_108_out, and_12_out, 1'b0);
  and and_109 (and_109_out, and_13_out, 1'b0);
  and and_110 (and_110_out, and_14_out, 1'b0);
  and and_111 (and_111_out, and_15_out, 1'b0);
  or or_17 (OPRAND2, or_16_out, or_18_out);
  or or_18 (or_18_out, and_96_out, and_97_out, and_98_out, and_99_out, and_100_out, and_101_out, and_102_out, and_103_out);
  or or_19 (or_19_out, and_127_out, and_126_out, and_125_out, and_124_out, and_123_out, and_122_out, and_121_out, and_120_out);
  and and_112 (and_112_out, DECORDER_4x16_out, 1'b1);
  and and_113 (and_113_out, and_1_out, 1'b0);
  and and_114 (and_114_out, and_2_out, 1'b1);
  and and_115 (and_115_out, and_3_out, 1'b0);
  and and_116 (and_116_out, and_4_out, 1'b0);
  and and_117 (and_117_out, and_5_out, 1'b0);
  and and_118 (and_118_out, and_6_out, 1'b0);
  and and_119 (and_119_out, and_7_out, 1'b0);
  and and_120 (and_120_out, and_8_out, 1'b0);
  and and_121 (and_121_out, and_9_out, 1'b0);
  and and_122 (and_122_out, and_10_out, 1'b0);
  and and_123 (and_123_out, and_11_out, 1'b0);
  and and_124 (and_124_out, and_12_out, 1'b0);
  and and_125 (and_125_out, and_13_out, 1'b0);
  and and_126 (and_126_out, and_14_out, 1'b0);
  and and_127 (and_127_out, and_15_out, 1'b0);
  or or_20 (OPRAND1, or_19_out, or_21_out);
  or or_21 (or_21_out, and_112_out, and_113_out, and_114_out, and_115_out, and_116_out, and_117_out, and_118_out, and_119_out);
  or or_22 (or_22_out, and_143_out, and_142_out, and_141_out, and_140_out, and_139_out, and_138_out, and_137_out, and_136_out);
  and and_128 (and_128_out, DECORDER_4x16_out, 1'b0);
  and and_129 (and_129_out, and_1_out, 1'b1);
  and and_130 (and_130_out, and_2_out, 1'b1);
  and and_131 (and_131_out, and_3_out, 1'b1);
  and and_132 (and_132_out, and_4_out, 1'b0);
  and and_133 (and_133_out, and_5_out, 1'b0);
  and and_134 (and_134_out, and_6_out, 1'b0);
  and and_135 (and_135_out, and_7_out, 1'b0);
  and and_136 (and_136_out, and_8_out, 1'b0);
  and and_137 (and_137_out, and_9_out, 1'b0);
  and and_138 (and_138_out, and_10_out, 1'b0);
  and and_139 (and_139_out, and_11_out, 1'b0);
  and and_140 (and_140_out, and_12_out, 1'b0);
  and and_141 (and_141_out, and_13_out, 1'b0);
  and and_142 (and_142_out, and_14_out, 1'b0);
  and and_143 (and_143_out, and_15_out, 1'b0);
  or or_23 (or_23_out, and_128_out, and_129_out, and_130_out, and_131_out, and_132_out, and_133_out, and_134_out, and_135_out);
  or or_24 (OPRAND0, or_22_out, or_23_out);
endmodule

module TEST_PROG_SUB (
  input  ROMI3,
  input  ROMI2,
  input  ROMI1,
  input  ROMI0,
  output OPC3,
  output OPC2,
  output OPC1,
  output OPC0,
  output OPRAND3,
  output OPRAND2,
  output OPRAND1,
  output OPRAND0
);

  wire and_1_out, and_2_out, and_3_out, and_4_out, and_5_out, and_6_out, and_7_out, and_8_out, and_9_out,
       and_10_out, and_11_out, and_12_out, and_13_out, and_14_out, and_15_out, and_16_out, and_17_out,
       and_18_out, and_19_out, and_20_out, and_21_out, and_22_out, and_23_out, and_24_out, and_25_out,
       and_26_out, and_27_out, and_28_out, and_29_out, and_30_out, and_31_out, and_32_out, and_33_out,
       and_34_out, and_35_out, and_36_out, and_37_out, and_38_out, and_39_out, and_40_out, and_41_out,
       and_42_out, and_43_out, and_44_out, and_45_out, and_46_out, and_47_out, and_48_out, and_49_out,
       and_50_out, and_51_out, and_52_out, and_53_out, and_54_out, and_55_out, and_56_out, and_57_out,
       and_58_out, and_59_out, and_60_out, and_61_out, and_62_out, and_63_out, and_64_out, and_65_out,
       and_66_out, and_67_out, and_68_out, and_69_out, and_70_out, and_71_out, and_72_out, and_73_out,
       and_74_out, and_75_out, and_76_out, and_77_out, and_78_out, and_79_out, and_80_out, and_81_out,
       and_82_out, and_83_out, and_84_out, and_85_out, and_86_out, and_87_out, and_88_out, and_89_out,
       and_90_out, and_91_out, and_92_out, and_93_out, and_94_out, and_95_out, and_96_out, and_97_out,
       and_98_out, and_99_out, and_100_out, and_101_out, and_102_out, and_103_out, and_104_out, and_105_out,
       and_106_out, and_107_out, and_108_out, and_109_out, and_110_out, and_111_out, and_112_out,
       and_113_out, and_114_out, and_115_out, and_116_out, and_117_out, and_118_out, and_119_out,
       and_120_out, and_121_out, and_122_out, and_123_out, and_124_out, and_125_out, and_126_out,
       and_127_out, and_128_out, and_129_out, and_130_out, and_131_out, and_132_out, and_133_out,
       and_134_out, and_135_out, and_136_out, and_137_out, and_138_out, and_139_out, and_140_out,
       and_141_out, and_142_out, and_143_out, DECORDER_4x16_out, not_1_out, not_2_out, not_3_out, not_4_out,
       or_1_out, or_3_out, or_4_out, or_6_out, or_7_out, or_8_out, or_10_out, or_12_out, or_13_out,
       or_14_out, or_16_out, or_18_out, or_19_out, or_21_out, or_22_out, or_23_out;

  not not_1 (not_1_out, ROMI3);
  not not_2 (not_2_out, ROMI2);
  not not_3 (not_3_out, ROMI1);
  not not_4 (not_4_out, ROMI0);
  and DECORDER_4x16 (DECORDER_4x16_out, not_4_out, not_3_out, not_2_out, not_1_out);
  and and_1 (and_1_out, ROMI0, not_3_out, not_2_out, not_1_out);
  and and_2 (and_2_out, not_4_out, ROMI1, not_2_out, not_1_out);
  and and_3 (and_3_out, ROMI0, ROMI1, not_2_out, not_1_out);
  and and_4 (and_4_out, not_4_out, not_3_out, ROMI2, not_1_out);
  and and_5 (and_5_out, ROMI0, not_3_out, ROMI2, not_1_out);
  and and_6 (and_6_out, not_4_out, ROMI1, ROMI2, not_1_out);
  and and_7 (and_7_out, ROMI0, ROMI1, ROMI2, not_1_out);
  and and_8 (and_8_out, not_4_out, not_3_out, not_2_out, ROMI3);
  and and_9 (and_9_out, ROMI0, not_3_out, not_2_out, ROMI3);
  and and_10 (and_10_out, not_4_out, ROMI1, not_2_out, ROMI3);
  and and_11 (and_11_out, ROMI0, ROMI1, not_2_out, ROMI3);
  and and_12 (and_12_out, not_4_out, not_3_out, ROMI2, ROMI3);
  and and_13 (and_13_out, ROMI0, not_3_out, ROMI2, ROMI3);
  and and_14 (and_14_out, not_4_out, ROMI1, ROMI2, ROMI3);
  and and_15 (and_15_out, ROMI0, ROMI1, ROMI2, ROMI3);
  or or_1 (or_1_out, and_31_out, and_30_out, and_29_out, and_28_out, and_27_out, and_26_out, and_25_out, and_24_out);
  and and_16 (and_16_out, DECORDER_4x16_out, 1'b1);
  and and_17 (and_17_out, and_1_out, 1'b0);
  and and_18 (and_18_out, and_2_out, 1'b0);
  and and_19 (and_19_out, and_3_out, 1'b0);
  and and_20 (and_20_out, and_4_out, 1'b0);
  and and_21 (and_21_out, and_5_out, 1'b0);
  and and_22 (and_22_out, and_6_out, 1'b0);
  and and_23 (and_23_out, and_7_out, 1'b0);
  and and_24 (and_24_out, and_8_out, 1'b0);
  and and_25 (and_25_out, and_9_out, 1'b0);
  and and_26 (and_26_out, and_10_out, 1'b0);
  and and_27 (and_27_out, and_11_out, 1'b0);
  and and_28 (and_28_out, and_12_out, 1'b0);
  and and_29 (and_29_out, and_13_out, 1'b0);
  and and_30 (and_30_out, and_14_out, 1'b0);
  and and_31 (and_31_out, and_15_out, 1'b0);
  or or_2 (OPC3, or_1_out, or_3_out);
  or or_3 (or_3_out, and_16_out, and_17_out, and_18_out, and_19_out, and_20_out, and_21_out, and_22_out, and_23_out);
  or or_4 (or_4_out, and_47_out, and_46_out, and_45_out, and_44_out, and_43_out, and_42_out, and_41_out, and_40_out);
  and and_32 (and_32_out, DECORDER_4x16_out, 1'b1);
  and and_33 (and_33_out, and_1_out, 1'b0);
  and and_34 (and_34_out, and_2_out, 1'b0);
  and and_35 (and_35_out, and_3_out, 1'b0);
  and and_36 (and_36_out, and_4_out, 1'b0);
  and and_37 (and_37_out, and_5_out, 1'b0);
  and and_38 (and_38_out, and_6_out, 1'b0);
  and and_39 (and_39_out, and_7_out, 1'b0);
  and and_40 (and_40_out, and_8_out, 1'b0);
  and and_41 (and_41_out, and_9_out, 1'b0);
  and and_42 (and_42_out, and_10_out, 1'b0);
  and and_43 (and_43_out, and_11_out, 1'b0);
  and and_44 (and_44_out, and_12_out, 1'b0);
  and and_45 (and_45_out, and_13_out, 1'b0);
  and and_46 (and_46_out, and_14_out, 1'b0);
  and and_47 (and_47_out, and_15_out, 1'b0);
  or or_5 (OPC2, or_4_out, or_6_out);
  or or_6 (or_6_out, and_32_out, and_33_out, and_34_out, and_35_out, and_36_out, and_37_out, and_38_out, and_39_out);
  and and_48 (and_48_out, DECORDER_4x16_out, 1'b0);
  and and_49 (and_49_out, and_1_out, 1'b0);
  and and_50 (and_50_out, and_2_out, 1'b0);
  and and_51 (and_51_out, and_3_out, 1'b0);
  and and_52 (and_52_out, and_4_out, 1'b0);
  and and_53 (and_53_out, and_5_out, 1'b0);
  and and_54 (and_54_out, and_6_out, 1'b0);
  and and_55 (and_55_out, and_7_out, 1'b0);
  and and_56 (and_56_out, and_8_out, 1'b0);
  and and_57 (and_57_out, and_9_out, 1'b0);
  and and_58 (and_58_out, and_10_out, 1'b0);
  and and_59 (and_59_out, and_11_out, 1'b0);
  and and_60 (and_60_out, and_12_out, 1'b0);
  and and_61 (and_61_out, and_13_out, 1'b0);
  and and_62 (and_62_out, and_14_out, 1'b0);
  and and_63 (and_63_out, and_15_out, 1'b0);
  or or_7 (or_7_out, and_63_out, and_62_out, and_61_out, and_60_out, and_59_out, and_58_out, and_57_out, and_56_out);
  or or_8 (or_8_out, and_48_out, and_49_out, and_50_out, and_51_out, and_52_out, and_53_out, and_54_out, and_55_out);
  or or_9 (OPC1, or_7_out, or_8_out);
  or or_10 (or_10_out, and_79_out, and_78_out, and_77_out, and_76_out, and_75_out, and_74_out, and_73_out, and_72_out);
  and and_64 (and_64_out, DECORDER_4x16_out, 1'b0);
  and and_65 (and_65_out, and_1_out, 1'b1);
  and and_66 (and_66_out, and_2_out, 1'b1);
  and and_67 (and_67_out, and_3_out, 1'b1);
  and and_68 (and_68_out, and_4_out, 1'b0);
  and and_69 (and_69_out, and_5_out, 1'b0);
  and and_70 (and_70_out, and_6_out, 1'b0);
  and and_71 (and_71_out, and_7_out, 1'b0);
  and and_72 (and_72_out, and_8_out, 1'b0);
  and and_73 (and_73_out, and_9_out, 1'b0);
  and and_74 (and_74_out, and_10_out, 1'b0);
  and and_75 (and_75_out, and_11_out, 1'b0);
  and and_76 (and_76_out, and_12_out, 1'b0);
  and and_77 (and_77_out, and_13_out, 1'b0);
  and and_78 (and_78_out, and_14_out, 1'b0);
  and and_79 (and_79_out, and_15_out, 1'b0);
  or or_11 (OPC0, or_10_out, or_12_out);
  or or_12 (or_12_out, and_64_out, and_65_out, and_66_out, and_67_out, and_68_out, and_69_out, and_70_out, and_71_out);
  or or_13 (or_13_out, and_95_out, and_94_out, and_93_out, and_92_out, and_91_out, and_90_out, and_89_out, and_88_out);
  and and_80 (and_80_out, DECORDER_4x16_out, 1'b0);
  and and_81 (and_81_out, and_1_out, 1'b0);
  and and_82 (and_82_out, and_2_out, 1'b0);
  and and_83 (and_83_out, and_3_out, 1'b0);
  and and_84 (and_84_out, and_4_out, 1'b0);
  and and_85 (and_85_out, and_5_out, 1'b0);
  and and_86 (and_86_out, and_6_out, 1'b0);
  and and_87 (and_87_out, and_7_out, 1'b0);
  and and_88 (and_88_out, and_8_out, 1'b0);
  and and_89 (and_89_out, and_9_out, 1'b0);
  and and_90 (and_90_out, and_10_out, 1'b0);
  and and_91 (and_91_out, and_11_out, 1'b0);
  and and_92 (and_92_out, and_12_out, 1'b0);
  and and_93 (and_93_out, and_13_out, 1'b0);
  and and_94 (and_94_out, and_14_out, 1'b0);
  and and_95 (and_95_out, and_15_out, 1'b0);
  or or_14 (or_14_out, and_80_out, and_81_out, and_82_out, and_83_out, and_84_out, and_85_out, and_86_out, and_87_out);
  or or_15 (OPRAND3, or_13_out, or_14_out);
  or or_16 (or_16_out, and_111_out, and_110_out, and_109_out, and_108_out, and_107_out, and_106_out, and_105_out, and_104_out);
  and and_96 (and_96_out, DECORDER_4x16_out, 1'b1);
  and and_97 (and_97_out, and_1_out, 1'b0);
  and and_98 (and_98_out, and_2_out, 1'b0);
  and and_99 (and_99_out, and_3_out, 1'b0);
  and and_100 (and_100_out, and_4_out, 1'b0);
  and and_101 (and_101_out, and_5_out, 1'b0);
  and and_102 (and_102_out, and_6_out, 1'b0);
  and and_103 (and_103_out, and_7_out, 1'b0);
  and and_104 (and_104_out, and_8_out, 1'b0);
  and and_105 (and_105_out, and_9_out, 1'b0);
  and and_106 (and_106_out, and_10_out, 1'b0);
  and and_107 (and_107_out, and_11_out, 1'b0);
  and and_108 (and_108_out, and_12_out, 1'b0);
  and and_109 (and_109_out, and_13_out, 1'b0);
  and and_110 (and_110_out, and_14_out, 1'b0);
  and and_111 (and_111_out, and_15_out, 1'b0);
  or or_17 (OPRAND2, or_16_out, or_18_out);
  or or_18 (or_18_out, and_96_out, and_97_out, and_98_out, and_99_out, and_100_out, and_101_out, and_102_out, and_103_out);
  or or_19 (or_19_out, and_127_out, and_126_out, and_125_out, and_124_out, and_123_out, and_122_out, and_121_out, and_120_out);
  and and_112 (and_112_out, DECORDER_4x16_out, 1'b0);
  and and_113 (and_113_out, and_1_out, 1'b1);
  and and_114 (and_114_out, and_2_out, 1'b0);
  and and_115 (and_115_out, and_3_out, 1'b0);
  and and_116 (and_116_out, and_4_out, 1'b0);
  and and_117 (and_117_out, and_5_out, 1'b0);
  and and_118 (and_118_out, and_6_out, 1'b0);
  and and_119 (and_119_out, and_7_out, 1'b0);
  and and_120 (and_120_out, and_8_out, 1'b0);
  and and_121 (and_121_out, and_9_out, 1'b0);
  and and_122 (and_122_out, and_10_out, 1'b0);
  and and_123 (and_123_out, and_11_out, 1'b0);
  and and_124 (and_124_out, and_12_out, 1'b0);
  and and_125 (and_125_out, and_13_out, 1'b0);
  and and_126 (and_126_out, and_14_out, 1'b0);
  and and_127 (and_127_out, and_15_out, 1'b0);
  or or_20 (OPRAND1, or_19_out, or_21_out);
  or or_21 (or_21_out, and_112_out, and_113_out, and_114_out, and_115_out, and_116_out, and_117_out, and_118_out, and_119_out);
  or or_22 (or_22_out, and_143_out, and_142_out, and_141_out, and_140_out, and_139_out, and_138_out, and_137_out, and_136_out);
  and and_128 (and_128_out, DECORDER_4x16_out, 1'b1);
  and and_129 (and_129_out, and_1_out, 1'b0);
  and and_130 (and_130_out, and_2_out, 1'b1);
  and and_131 (and_131_out, and_3_out, 1'b1);
  and and_132 (and_132_out, and_4_out, 1'b0);
  and and_133 (and_133_out, and_5_out, 1'b0);
  and and_134 (and_134_out, and_6_out, 1'b0);
  and and_135 (and_135_out, and_7_out, 1'b0);
  and and_136 (and_136_out, and_8_out, 1'b0);
  and and_137 (and_137_out, and_9_out, 1'b0);
  and and_138 (and_138_out, and_10_out, 1'b0);
  and and_139 (and_139_out, and_11_out, 1'b0);
  and and_140 (and_140_out, and_12_out, 1'b0);
  and and_141 (and_141_out, and_13_out, 1'b0);
  and and_142 (and_142_out, and_14_out, 1'b0);
  and and_143 (and_143_out, and_15_out, 1'b0);
  or or_23 (or_23_out, and_128_out, and_129_out, and_130_out, and_131_out, and_132_out, and_133_out, and_134_out, and_135_out);
  or or_24 (OPRAND0, or_22_out, or_23_out);
endmodule

module TEST_PROG_LDA (
  input  ROMI3,
  input  ROMI2,
  input  ROMI1,
  input  ROMI0,
  output OPC3,
  output OPC2,
  output OPC1,
  output OPC0,
  output OPRAND3,
  output OPRAND2,
  output OPRAND1,
  output OPRAND0
);

  wire and_1_out, and_2_out, and_3_out, and_4_out, and_5_out, and_6_out, and_7_out, and_8_out, and_9_out,
       and_10_out, and_11_out, and_12_out, and_13_out, and_14_out, and_15_out, and_16_out, and_17_out,
       and_18_out, and_19_out, and_20_out, and_21_out, and_22_out, and_23_out, and_24_out, and_25_out,
       and_26_out, and_27_out, and_28_out, and_29_out, and_30_out, and_31_out, and_32_out, and_33_out,
       and_34_out, and_35_out, and_36_out, and_37_out, and_38_out, and_39_out, and_40_out, and_41_out,
       and_42_out, and_43_out, and_44_out, and_45_out, and_46_out, and_47_out, and_48_out, and_49_out,
       and_50_out, and_51_out, and_52_out, and_53_out, and_54_out, and_55_out, and_56_out, and_57_out,
       and_58_out, and_59_out, and_60_out, and_61_out, and_62_out, and_63_out, and_64_out, and_65_out,
       and_66_out, and_67_out, and_68_out, and_69_out, and_70_out, and_71_out, and_72_out, and_73_out,
       and_74_out, and_75_out, and_76_out, and_77_out, and_78_out, and_79_out, and_80_out, and_81_out,
       and_82_out, and_83_out, and_84_out, and_85_out, and_86_out, and_87_out, and_88_out, and_89_out,
       and_90_out, and_91_out, and_92_out, and_93_out, and_94_out, and_95_out, and_96_out, and_97_out,
       and_98_out, and_99_out, and_100_out, and_101_out, and_102_out, and_103_out, and_104_out, and_105_out,
       and_106_out, and_107_out, and_108_out, and_109_out, and_110_out, and_111_out, and_112_out,
       and_113_out, and_114_out, and_115_out, and_116_out, and_117_out, and_118_out, and_119_out,
       and_120_out, and_121_out, and_122_out, and_123_out, and_124_out, and_125_out, and_126_out,
       and_127_out, and_128_out, and_129_out, and_130_out, and_131_out, and_132_out, and_133_out,
       and_134_out, and_135_out, and_136_out, and_137_out, and_138_out, and_139_out, and_140_out,
       and_141_out, and_142_out, and_143_out, DECORDER_4x16_out, not_1_out, not_2_out, not_3_out, not_4_out,
       or_1_out, or_3_out, or_4_out, or_6_out, or_7_out, or_8_out, or_10_out, or_12_out, or_13_out,
       or_14_out, or_16_out, or_18_out, or_19_out, or_21_out, or_22_out, or_23_out;

  not not_1 (not_1_out, ROMI3);
  not not_2 (not_2_out, ROMI2);
  not not_3 (not_3_out, ROMI1);
  not not_4 (not_4_out, ROMI0);
  and DECORDER_4x16 (DECORDER_4x16_out, not_4_out, not_3_out, not_2_out, not_1_out);
  and and_1 (and_1_out, ROMI0, not_3_out, not_2_out, not_1_out);
  and and_2 (and_2_out, not_4_out, ROMI1, not_2_out, not_1_out);
  and and_3 (and_3_out, ROMI0, ROMI1, not_2_out, not_1_out);
  and and_4 (and_4_out, not_4_out, not_3_out, ROMI2, not_1_out);
  and and_5 (and_5_out, ROMI0, not_3_out, ROMI2, not_1_out);
  and and_6 (and_6_out, not_4_out, ROMI1, ROMI2, not_1_out);
  and and_7 (and_7_out, ROMI0, ROMI1, ROMI2, not_1_out);
  and and_8 (and_8_out, not_4_out, not_3_out, not_2_out, ROMI3);
  and and_9 (and_9_out, ROMI0, not_3_out, not_2_out, ROMI3);
  and and_10 (and_10_out, not_4_out, ROMI1, not_2_out, ROMI3);
  and and_11 (and_11_out, ROMI0, ROMI1, not_2_out, ROMI3);
  and and_12 (and_12_out, not_4_out, not_3_out, ROMI2, ROMI3);
  and and_13 (and_13_out, ROMI0, not_3_out, ROMI2, ROMI3);
  and and_14 (and_14_out, not_4_out, ROMI1, ROMI2, ROMI3);
  and and_15 (and_15_out, ROMI0, ROMI1, ROMI2, ROMI3);
  or or_1 (or_1_out, and_31_out, and_30_out, and_29_out, and_28_out, and_27_out, and_26_out, and_25_out, and_24_out);
  and and_16 (and_16_out, DECORDER_4x16_out, 1'b1);
  and and_17 (and_17_out, and_1_out, 1'b1);
  and and_18 (and_18_out, and_2_out, 1'b1);
  and and_19 (and_19_out, and_3_out, 1'b1);
  and and_20 (and_20_out, and_4_out, 1'b1);
  and and_21 (and_21_out, and_5_out, 1'b1);
  and and_22 (and_22_out, and_6_out, 1'b1);
  and and_23 (and_23_out, and_7_out, 1'b0);
  and and_24 (and_24_out, and_8_out, 1'b0);
  and and_25 (and_25_out, and_9_out, 1'b0);
  and and_26 (and_26_out, and_10_out, 1'b0);
  and and_27 (and_27_out, and_11_out, 1'b0);
  and and_28 (and_28_out, and_12_out, 1'b0);
  and and_29 (and_29_out, and_13_out, 1'b0);
  and and_30 (and_30_out, and_14_out, 1'b0);
  and and_31 (and_31_out, and_15_out, 1'b0);
  or or_2 (OPC3, or_1_out, or_3_out);
  or or_3 (or_3_out, and_16_out, and_17_out, and_18_out, and_19_out, and_20_out, and_21_out, and_22_out, and_23_out);
  or or_4 (or_4_out, and_47_out, and_46_out, and_45_out, and_44_out, and_43_out, and_42_out, and_41_out, and_40_out);
  and and_32 (and_32_out, DECORDER_4x16_out, 1'b1);
  and and_33 (and_33_out, and_1_out, 1'b1);
  and and_34 (and_34_out, and_2_out, 1'b1);
  and and_35 (and_35_out, and_3_out, 1'b1);
  and and_36 (and_36_out, and_4_out, 1'b1);
  and and_37 (and_37_out, and_5_out, 1'b1);
  and and_38 (and_38_out, and_6_out, 1'b0);
  and and_39 (and_39_out, and_7_out, 1'b0);
  and and_40 (and_40_out, and_8_out, 1'b0);
  and and_41 (and_41_out, and_9_out, 1'b0);
  and and_42 (and_42_out, and_10_out, 1'b0);
  and and_43 (and_43_out, and_11_out, 1'b0);
  and and_44 (and_44_out, and_12_out, 1'b0);
  and and_45 (and_45_out, and_13_out, 1'b0);
  and and_46 (and_46_out, and_14_out, 1'b0);
  and and_47 (and_47_out, and_15_out, 1'b0);
  or or_5 (OPC2, or_4_out, or_6_out);
  or or_6 (or_6_out, and_32_out, and_33_out, and_34_out, and_35_out, and_36_out, and_37_out, and_38_out, and_39_out);
  and and_48 (and_48_out, DECORDER_4x16_out, 1'b0);
  and and_49 (and_49_out, and_1_out, 1'b1);
  and and_50 (and_50_out, and_2_out, 1'b0);
  and and_51 (and_51_out, and_3_out, 1'b0);
  and and_52 (and_52_out, and_4_out, 1'b0);
  and and_53 (and_53_out, and_5_out, 1'b0);
  and and_54 (and_54_out, and_6_out, 1'b1);
  and and_55 (and_55_out, and_7_out, 1'b0);
  and and_56 (and_56_out, and_8_out, 1'b0);
  and and_57 (and_57_out, and_9_out, 1'b0);
  and and_58 (and_58_out, and_10_out, 1'b0);
  and and_59 (and_59_out, and_11_out, 1'b0);
  and and_60 (and_60_out, and_12_out, 1'b0);
  and and_61 (and_61_out, and_13_out, 1'b0);
  and and_62 (and_62_out, and_14_out, 1'b0);
  and and_63 (and_63_out, and_15_out, 1'b0);
  or or_7 (or_7_out, and_63_out, and_62_out, and_61_out, and_60_out, and_59_out, and_58_out, and_57_out, and_56_out);
  or or_8 (or_8_out, and_48_out, and_49_out, and_50_out, and_51_out, and_52_out, and_53_out, and_54_out, and_55_out);
  or or_9 (OPC1, or_7_out, or_8_out);
  or or_10 (or_10_out, and_79_out, and_78_out, and_77_out, and_76_out, and_75_out, and_74_out, and_73_out, and_72_out);
  and and_64 (and_64_out, DECORDER_4x16_out, 1'b0);
  and and_65 (and_65_out, and_1_out, 1'b0);
  and and_66 (and_66_out, and_2_out, 1'b0);
  and and_67 (and_67_out, and_3_out, 1'b1);
  and and_68 (and_68_out, and_4_out, 1'b1);
  and and_69 (and_69_out, and_5_out, 1'b1);
  and and_70 (and_70_out, and_6_out, 1'b1);
  and and_71 (and_71_out, and_7_out, 1'b0);
  and and_72 (and_72_out, and_8_out, 1'b0);
  and and_73 (and_73_out, and_9_out, 1'b0);
  and and_74 (and_74_out, and_10_out, 1'b0);
  and and_75 (and_75_out, and_11_out, 1'b0);
  and and_76 (and_76_out, and_12_out, 1'b0);
  and and_77 (and_77_out, and_13_out, 1'b0);
  and and_78 (and_78_out, and_14_out, 1'b0);
  and and_79 (and_79_out, and_15_out, 1'b0);
  or or_11 (OPC0, or_10_out, or_12_out);
  or or_12 (or_12_out, and_64_out, and_65_out, and_66_out, and_67_out, and_68_out, and_69_out, and_70_out, and_71_out);
  or or_13 (or_13_out, and_95_out, and_94_out, and_93_out, and_92_out, and_91_out, and_90_out, and_89_out, and_88_out);
  and and_80 (and_80_out, DECORDER_4x16_out, 1'b1);
  and and_81 (and_81_out, and_1_out, 1'b0);
  and and_82 (and_82_out, and_2_out, 1'b0);
  and and_83 (and_83_out, and_3_out, 1'b0);
  and and_84 (and_84_out, and_4_out, 1'b0);
  and and_85 (and_85_out, and_5_out, 1'b0);
  and and_86 (and_86_out, and_6_out, 1'b0);
  and and_87 (and_87_out, and_7_out, 1'b0);
  and and_88 (and_88_out, and_8_out, 1'b0);
  and and_89 (and_89_out, and_9_out, 1'b0);
  and and_90 (and_90_out, and_10_out, 1'b0);
  and and_91 (and_91_out, and_11_out, 1'b0);
  and and_92 (and_92_out, and_12_out, 1'b0);
  and and_93 (and_93_out, and_13_out, 1'b0);
  and and_94 (and_94_out, and_14_out, 1'b0);
  and and_95 (and_95_out, and_15_out, 1'b0);
  or or_14 (or_14_out, and_80_out, and_81_out, and_82_out, and_83_out, and_84_out, and_85_out, and_86_out, and_87_out);
  or or_15 (OPRAND3, or_13_out, or_14_out);
  or or_16 (or_16_out, and_111_out, and_110_out, and_109_out, and_108_out, and_107_out, and_106_out, and_105_out, and_104_out);
  and and_96 (and_96_out, DECORDER_4x16_out, 1'b0);
  and and_97 (and_97_out, and_1_out, 1'b0);
  and and_98 (and_98_out, and_2_out, 1'b0);
  and and_99 (and_99_out, and_3_out, 1'b0);
  and and_100 (and_100_out, and_4_out, 1'b0);
  and and_101 (and_101_out, and_5_out, 1'b0);
  and and_102 (and_102_out, and_6_out, 1'b0);
  and and_103 (and_103_out, and_7_out, 1'b0);
  and and_104 (and_104_out, and_8_out, 1'b0);
  and and_105 (and_105_out, and_9_out, 1'b0);
  and and_106 (and_106_out, and_10_out, 1'b0);
  and and_107 (and_107_out, and_11_out, 1'b0);
  and and_108 (and_108_out, and_12_out, 1'b0);
  and and_109 (and_109_out, and_13_out, 1'b0);
  and and_110 (and_110_out, and_14_out, 1'b0);
  and and_111 (and_111_out, and_15_out, 1'b0);
  or or_17 (OPRAND2, or_16_out, or_18_out);
  or or_18 (or_18_out, and_96_out, and_97_out, and_98_out, and_99_out, and_100_out, and_101_out, and_102_out, and_103_out);
  or or_19 (or_19_out, and_127_out, and_126_out, and_125_out, and_124_out, and_123_out, and_122_out, and_121_out, and_120_out);
  and and_112 (and_112_out, DECORDER_4x16_out, 1'b1);
  and and_113 (and_113_out, and_1_out, 1'b1);
  and and_114 (and_114_out, and_2_out, 1'b0);
  and and_115 (and_115_out, and_3_out, 1'b1);
  and and_116 (and_116_out, and_4_out, 1'b0);
  and and_117 (and_117_out, and_5_out, 1'b1);
  and and_118 (and_118_out, and_6_out, 1'b0);
  and and_119 (and_119_out, and_7_out, 1'b0);
  and and_120 (and_120_out, and_8_out, 1'b0);
  and and_121 (and_121_out, and_9_out, 1'b0);
  and and_122 (and_122_out, and_10_out, 1'b0);
  and and_123 (and_123_out, and_11_out, 1'b0);
  and and_124 (and_124_out, and_12_out, 1'b0);
  and and_125 (and_125_out, and_13_out, 1'b0);
  and and_126 (and_126_out, and_14_out, 1'b0);
  and and_127 (and_127_out, and_15_out, 1'b0);
  or or_20 (OPRAND1, or_19_out, or_21_out);
  or or_21 (or_21_out, and_112_out, and_113_out, and_114_out, and_115_out, and_116_out, and_117_out, and_118_out, and_119_out);
  or or_22 (or_22_out, and_143_out, and_142_out, and_141_out, and_140_out, and_139_out, and_138_out, and_137_out, and_136_out);
  and and_128 (and_128_out, DECORDER_4x16_out, 1'b0);
  and and_129 (and_129_out, and_1_out, 1'b0);
  and and_130 (and_130_out, and_2_out, 1'b0);
  and and_131 (and_131_out, and_3_out, 1'b0);
  and and_132 (and_132_out, and_4_out, 1'b0);
  and and_133 (and_133_out, and_5_out, 1'b0);
  and and_134 (and_134_out, and_6_out, 1'b0);
  and and_135 (and_135_out, and_7_out, 1'b0);
  and and_136 (and_136_out, and_8_out, 1'b0);
  and and_137 (and_137_out, and_9_out, 1'b0);
  and and_138 (and_138_out, and_10_out, 1'b0);
  and and_139 (and_139_out, and_11_out, 1'b0);
  and and_140 (and_140_out, and_12_out, 1'b0);
  and and_141 (and_141_out, and_13_out, 1'b0);
  and and_142 (and_142_out, and_14_out, 1'b0);
  and and_143 (and_143_out, and_15_out, 1'b0);
  or or_23 (or_23_out, and_128_out, and_129_out, and_130_out, and_131_out, and_132_out, and_133_out, and_134_out, and_135_out);
  or or_24 (OPRAND0, or_22_out, or_23_out);
endmodule

module TEST_FSM (
  input  in_1,
  input  in_2,
  input  in_3,
  input  in_4,
  input  in_5,
  output FETCH,
  output DECODE,
  output EXECUTE,
  output WRITEBACK
);

  wire and_1_out, and_2_out, and_3_out, and_4_out, CLK_out, clock_1_out, not_1_out, not_2_out, not_3_out,
       not_4_out, Q0_reg_o0, Q1_reg_o0, register_1bit_1_reg_o0, xor_1_out;

  Clock clock_1 (.out(clock_1_out));
  Clock CLK (.out(CLK_out));
  and and_1 (and_1_out, clock_1_out, register_1bit_1_reg_o0);
  and and_2 (and_2_out, CLK_out, Q0_reg_o0);
  not not_1 (not_1_out, and_1_out);
  not not_2 (not_2_out, and_2_out);
  and and_3 (and_3_out, in_1, in_2);
  Register_1BIT Q0 (.HARD_RESET(in_5), .CLK(CLK_out), .REG_I0(not_2_out), .WE(1'b1), .REG_O0(Q0_reg_o0));
  Register_1BIT register_1bit_1 (
    .HARD_RESET(in_3), .CLK(clock_1_out), .REG_I0(not_1_out), .WE(in_4), .REG_O0(register_1bit_1_reg_o0));
  xor xor_1 (xor_1_out, Q0_reg_o0, Q1_reg_o0);
  and and_4 (and_4_out, and_3_out, register_1bit_1_reg_o0);
  LED led_1 (.in(and_4_out));
  Register_1BIT Q1 (.HARD_RESET(in_5), .CLK(CLK_out), .REG_I0(xor_1_out), .WE(1'b1), .REG_O0(Q1_reg_o0));
  not not_3 (not_3_out, Q1_reg_o0);
  not not_4 (not_4_out, Q0_reg_o0);
  and and_5 (FETCH, not_4_out, not_3_out);
  and and_6 (DECODE, Q0_reg_o0, not_3_out);
  and and_7 (EXECUTE, not_4_out, Q1_reg_o0);
  and and_8 (WRITEBACK, Q0_reg_o0, Q1_reg_o0);
endmodule

module FSM_2BIT (
  input  HARD_RESET,
  input  CLK,
  input  HTL,
  output FETCH,
  output DECODE,
  output EXECUTE,
  output WRITEBACK
);

  wire and_1_out, and_2_out, and_3_out, and_4_out, and_5_out, not_1_out, not_2_out, not_3_out, not_4_out,
       Q0_reg_o0, Q1_reg_o0, xor_1_out;

  not not_1 (not_1_out, HTL);
  and and_1 (and_1_out, CLK, Q0_reg_o0);
  not not_2 (not_2_out, and_1_out);
  Register_1BIT Q0 (.HARD_RESET(HARD_RESET), .CLK(CLK), .REG_I0(not_2_out), .WE(1'b1), .REG_O0(Q0_reg_o0));
  xor xor_1 (xor_1_out, Q0_reg_o0, Q1_reg_o0);
  Register_1BIT Q1 (.HARD_RESET(HARD_RESET), .CLK(CLK), .REG_I0(xor_1_out), .WE(1'b1), .REG_O0(Q1_reg_o0));
  not not_3 (not_3_out, Q1_reg_o0);
  not not_4 (not_4_out, Q0_reg_o0);
  and and_2 (and_2_out, not_4_out, not_3_out);
  and and_3 (and_3_out, Q0_reg_o0, not_3_out);
  and and_4 (and_4_out, not_4_out, Q1_reg_o0);
  and and_5 (and_5_out, Q0_reg_o0, Q1_reg_o0);
  and and_6 (FETCH, and_2_out, not_1_out);
  and and_7 (DECODE, and_3_out, not_1_out);
  and and_8 (EXECUTE, and_4_out, not_1_out);
  and and_9 (WRITEBACK, and_5_out, not_1_out);
endmodule

module cpu_v5 (
  input  CLK,
  input  HARD_RESET,
  input  OPC3,
  input  OPC2,
  input  OPC1,
  input  OPC0,
  input  OPRAND3,
  input  OPRAND2,
  input  OPRAND1,
  input  OPRAND0,
  output OVF,
  output N,
  output C,
  output Z,
  output ACC_O3,
  output ACC_O2,
  output ACC_O1,
  output ACC_O0,
  output ISA_OPC_3,
  output ISA_OPC_2,
  output ISA_OPC_1,
  output ISA_OPC_0,
  output ISA_OPR_3,
  output ISA_OPR_2,
  output ISA_OPR_1,
  output ISA_OPR_0,
  output ROMI3,
  output ROMI2,
  output ROMI1,
  output ROMI0,
  output FETCH,
  output DECODE,
  output EXECUTE,
  output WRITEBACK
);

  wire alu_ext_1_c, alu_ext_1_n, alu_ext_1_o_0, alu_ext_1_o_1, alu_ext_1_o_2, alu_ext_1_o_3, alu_ext_1_ovf,
       alu_ext_1_z, and_1_out, and_2_out, and_3_out, and_4_out, and_5_out, and_6_out, and_7_out,
       controlled_buffer_1_out, controlled_buffer_2_out, controlled_buffer_3_out, controlled_buffer_4_out,
       controlled_buffer_5_out, controlled_buffer_6_out, controlled_buffer_7_out, controlled_buffer_8_out,
       ctrlunit_ext_1_alu_sig, ctrlunit_ext_1_ctrl_b0, ctrlunit_ext_1_ctrl_b1, ctrlunit_ext_1_ctrl_b2,
       ctrlunit_ext_1_ctrl_b3, ctrlunit_ext_1_ctrl_op0, ctrlunit_ext_1_ctrl_op1, ctrlunit_ext_1_ctrl_op2,
       ctrlunit_ext_1_hlt_sig, ctrlunit_ext_1_jmp_sig, ctrlunit_ext_1_lda_sig, ctrlunit_ext_1_ldi_sig,
       ctrlunit_ext_1_sta_sig, MEM_ADDR_REG_reg_o0, MEM_ADDR_REG_reg_o1, not_1_out, not_2_out, or_1_out,
       or_2_out, or_3_out, or_4_out, PC_REG_reg_o0, PC_REG_reg_o1, PC_REG_reg_o2, PC_REG_reg_o3,
       progcounter_ext_1_pco0, progcounter_ext_1_pco1, progcounter_ext_1_pco2, progcounter_ext_1_pco3,
       STATIC_RAM_sram_o0, STATIC_RAM_sram_o1, STATIC_RAM_sram_o2, STATIC_RAM_sram_o3;

  FSM_2BIT fsm_2bit_1 (
    .HARD_RESET(HARD_RESET), .CLK(CLK), .FETCH(FETCH), .DECODE(DECODE), .EXECUTE(EXECUTE),
    .WRITEBACK(WRITEBACK));  // open: HTL
  ProgCounter_EXT progcounter_ext_1 (
    .A3(PC_REG_reg_o3), .A2(PC_REG_reg_o2), .A1(PC_REG_reg_o1), .A0(PC_REG_reg_o0),
    .PC_OPR3(controlled_buffer_1_out), .PC_OPR2(controlled_buffer_2_out), .PC_OPR1(controlled_buffer_3_out),
    .PC_OPR0(controlled_buffer_4_out), .JMP_JZ(ctrlunit_ext_1_jmp_sig), .FTCH(FETCH),
    .PCO3(progcounter_ext_1_pco3), .PCO2(progcounter_ext_1_pco2), .PCO1(progcounter_ext_1_pco1),
    .PCO0(progcounter_ext_1_pco0));
  REGISTER_4BIT PC_REG (
    .HARD_RESET(HARD_RESET), .CLK(CLK), .REG_I3(progcounter_ext_1_pco3), .REG_I2(progcounter_ext_1_pco2),
    .REG_I1(progcounter_ext_1_pco1), .REG_I0(progcounter_ext_1_pco0), .WE(not_2_out), .REG_O3(PC_REG_reg_o3),
    .REG_O2(PC_REG_reg_o2), .REG_O1(PC_REG_reg_o1), .REG_O0(PC_REG_reg_o0));
  REGISTER_4BIT register_4bit_1 (
    .HARD_RESET(HARD_RESET), .CLK(CLK), .REG_I3(PC_REG_reg_o3), .REG_I2(PC_REG_reg_o2),
    .REG_I1(PC_REG_reg_o1), .REG_I0(PC_REG_reg_o0), .WE(FETCH), .REG_O3(ROMI3), .REG_O2(ROMI2),
    .REG_O1(ROMI1), .REG_O0(ROMI0));
  and and_1 (and_1_out, not_2_out, DECODE);
  and and_2 (and_2_out, not_2_out, DECODE);
  REGISTER_4BIT INSTRUCTION_REG_OPC (
    .HARD_RESET(HARD_RESET), .CLK(CLK), .REG_I3(OPC3), .REG_I2(OPC2), .REG_I1(OPC1), .REG_I0(OPC0),
    .WE(and_1_out), .REG_O3(ISA_OPC_3), .REG_O2(ISA_OPC_2), .REG_O1(ISA_OPC_1), .REG_O0(ISA_OPC_0));
  REGISTER_4BIT INSTRUCTION_REG_OPR (
    .HARD_RESET(HARD_RESET), .CLK(CLK), .REG_I3(OPRAND3), .REG_I2(OPRAND2), .REG_I1(OPRAND1),
    .REG_I0(OPRAND0), .WE(and_2_out), .REG_O3(ISA_OPR_3), .REG_O2(ISA_OPR_2), .REG_O1(ISA_OPR_1),
    .REG_O0(ISA_OPR_0));
  CTRLUNIT_EXT ctrlunit_ext_1 (
    .CTRL_S3(ISA_OPC_3), .CTRL_S2(ISA_OPC_2), .CTRL_S1(ISA_OPC_1), .CTRL_S0(ISA_OPC_0),
    .CTRL_OPR3(ISA_OPR_3), .CTRL_OPR2(ISA_OPR_2), .CTRL_OPR1(ISA_OPR_1), .CTRL_OPR0(ISA_OPR_0), .FLAG_N(N),
    .FLAG_Z(Z), .CTRL_OP2(ctrlunit_ext_1_ctrl_op2), .CTRL_OP1(ctrlunit_ext_1_ctrl_op1),
    .CTRL_OP0(ctrlunit_ext_1_ctrl_op0), .CTRL_B3(ctrlunit_ext_1_ctrl_b3), .CTRL_B2(ctrlunit_ext_1_ctrl_b2),
    .CTRL_B1(ctrlunit_ext_1_ctrl_b1), .CTRL_B0(ctrlunit_ext_1_ctrl_b0), .JMP_SIG(ctrlunit_ext_1_jmp_sig),
    .HLT_SIG(ctrlunit_ext_1_hlt_sig), .LDI_SIG(ctrlunit_ext_1_ldi_sig), .LDA_SIG(ctrlunit_ext_1_lda_sig),
    .STA_SIG(ctrlunit_ext_1_sta_sig), .ALU_SIG(ctrlunit_ext_1_alu_sig));  // open: FLAG_OVF, FLAG_C, CTRL_OP3, CTRL_WE
  not not_1 (not_1_out, ctrlunit_ext_1_lda_sig);
  assign controlled_buffer_1_out = not_1_out ? ctrlunit_ext_1_ctrl_b3 : 1'bz;  // Controlled_Buffer controlled_buffer_1
  assign controlled_buffer_2_out = not_1_out ? ctrlunit_ext_1_ctrl_b2 : 1'bz;  // Controlled_Buffer controlled_buffer_2
  assign controlled_buffer_3_out = not_1_out ? ctrlunit_ext_1_ctrl_b1 : 1'bz;  // Controlled_Buffer controlled_buffer_3
  assign controlled_buffer_4_out = not_1_out ? ctrlunit_ext_1_ctrl_b0 : 1'bz;  // Controlled_Buffer controlled_buffer_4
  not not_2 (not_2_out, ctrlunit_ext_1_hlt_sig);
  or or_1 (or_1_out, ctrlunit_ext_1_ldi_sig, ctrlunit_ext_1_lda_sig);
  ALU_EXT alu_ext_1 (
    .A_3(ACC_O3), .A_2(ACC_O2), .A_1(ACC_O1), .A_0(ACC_O0), .B_3(controlled_buffer_1_out),
    .B_2(controlled_buffer_2_out), .B_1(controlled_buffer_3_out), .B_0(controlled_buffer_4_out),
    .S2(ctrlunit_ext_1_ctrl_op2), .S1(ctrlunit_ext_1_ctrl_op1), .S0(ctrlunit_ext_1_ctrl_op0),
    .OVF(alu_ext_1_ovf), .N(alu_ext_1_n), .C(alu_ext_1_c), .Z(alu_ext_1_z), .O_3(alu_ext_1_o_3),
    .O_2(alu_ext_1_o_2), .O_1(alu_ext_1_o_1), .O_0(alu_ext_1_o_0));
  or or_2 (or_2_out, or_1_out, ctrlunit_ext_1_sta_sig);
  assign controlled_buffer_5_out = ctrlunit_ext_1_alu_sig ? alu_ext_1_o_3 : 1'bz;  // Controlled_Buffer controlled_buffer_5
  assign controlled_buffer_6_out = ctrlunit_ext_1_alu_sig ? alu_ext_1_o_2 : 1'bz;  // Controlled_Buffer controlled_buffer_6
  assign controlled_buffer_7_out = ctrlunit_ext_1_alu_sig ? alu_ext_1_o_1 : 1'bz;  // Controlled_Buffer controlled_buffer_7
  assign controlled_buffer_8_out = ctrlunit_ext_1_alu_sig ? alu_ext_1_o_0 : 1'bz;  // Controlled_Buffer controlled_buffer_8
  assign controlled_buffer_5_out = or_2_out ? controlled_buffer_1_out : 1'bz;  // Controlled_Buffer controlled_buffer_9
  assign controlled_buffer_6_out = or_2_out ? controlled_buffer_2_out : 1'bz;  // Controlled_Buffer controlled_buffer_10
  assign controlled_buffer_7_out = or_2_out ? controlled_buffer_3_out : 1'bz;  // Controlled_Buffer controlled_buffer_11
  assign controlled_buffer_8_out = or_2_out ? controlled_buffer_4_out : 1'bz;  // Controlled_Buffer controlled_buffer_12
  or or_3 (or_3_out, or_2_out, ctrlunit_ext_1_alu_sig);
  and and_3 (and_3_out, EXECUTE, and_4_out);
  and and_4 (and_4_out, or_3_out, not_2_out);
  and and_5 (and_5_out, and_4_out, EXECUTE);
  REGISTER_4BIT ACCUMULATOR_REG (
    .HARD_RESET(HARD_RESET), .CLK(CLK), .REG_I3(controlled_buffer_5_out), .REG_I2(controlled_buffer_6_out),
    .REG_I1(controlled_buffer_7_out), .REG_I0(controlled_buffer_8_out), .WE(and_5_out), .REG_O3(ACC_O3),
    .REG_O2(ACC_O2), .REG_O1(ACC_O1), .REG_O0(ACC_O0));
  REGISTER_4BIT FLAG_REG (
    .HARD_RESET(HARD_RESET), .CLK(CLK), .REG_I3(alu_ext_1_ovf), .REG_I2(alu_ext_1_n), .REG_I1(alu_ext_1_c),
    .REG_I0(alu_ext_1_z), .WE(and_3_out), .REG_O3(OVF), .REG_O2(N), .REG_O1(C), .REG_O0(Z));
  and and_6 (and_6_out, or_4_out, or_4_out);
  or or_4 (or_4_out, ctrlunit_ext_1_lda_sig, ctrlunit_ext_1_sta_sig);
  REGISTER_4BIT MEM_ADDR_REG (
    .HARD_RESET(HARD_RESET), .CLK(CLK), .REG_I1(ctrlunit_ext_1_ctrl_b1), .REG_I0(ctrlunit_ext_1_ctrl_b0),
    .WE(and_6_out), .REG_O1(MEM_ADDR_REG_reg_o1), .REG_O0(MEM_ADDR_REG_reg_o0));  // open: REG_I3, REG_I2, REG_O3, REG_O2
  and and_7 (and_7_out, WRITEBACK, ctrlunit_ext_1_sta_sig);
  SRAM STATIC_RAM (
    .HARD_RESET(HARD_RESET), .CLK(CLK), .I3(ACC_O3), .I2(ACC_O2), .I1(ACC_O1), .I0(ACC_O0), .WE(and_7_out),
    .ADDR1(MEM_ADDR_REG_reg_o1), .ADDR0(MEM_ADDR_REG_reg_o0), .SRAM_O3(STATIC_RAM_sram_o3),
    .SRAM_O2(STATIC_RAM_sram_o2), .SRAM_O1(STATIC_RAM_sram_o1), .SRAM_O0(STATIC_RAM_sram_o0));
  assign controlled_buffer_1_out = ctrlunit_ext_1_lda_sig ? STATIC_RAM_sram_o3 : 1'bz;  // Controlled_Buffer controlled_buffer_13
  assign controlled_buffer_2_out = ctrlunit_ext_1_lda_sig ? STATIC_RAM_sram_o2 : 1'bz;  // Controlled_Buffer controlled_buffer_14
  assign controlled_buffer_3_out = ctrlunit_ext_1_lda_sig ? STATIC_RAM_sram_o1 : 1'bz;  // Controlled_Buffer controlled_buffer_15
  assign controlled_buffer_4_out = ctrlunit_ext_1_lda_sig ? STATIC_RAM_sram_o0 : 1'bz;  // Controlled_Buffer controlled_buffer_16
endmodule

module PlayGroun_v2 (
  input  in_1
);

  wire clock_1_out, cpu_v5_1_acc_o0, cpu_v5_1_acc_o1, cpu_v5_1_acc_o2, cpu_v5_1_acc_o3, cpu_v5_1_c,
       cpu_v5_1_decode, cpu_v5_1_execute, cpu_v5_1_fetch, cpu_v5_1_isa_opc_0, cpu_v5_1_isa_opc_1,
       cpu_v5_1_isa_opc_2, cpu_v5_1_isa_opc_3, cpu_v5_1_isa_opr_0, cpu_v5_1_isa_opr_1, cpu_v5_1_isa_opr_2,
       cpu_v5_1_isa_opr_3, cpu_v5_1_n, cpu_v5_1_ovf, cpu_v5_1_romi0, cpu_v5_1_romi1, cpu_v5_1_romi2,
       cpu_v5_1_romi3, cpu_v5_1_writeback, cpu_v5_1_z, test_prog_lda_1_opc0, test_prog_lda_1_opc1,
       test_prog_lda_1_opc2, test_prog_lda_1_opc3, test_prog_lda_1_oprand0, test_prog_lda_1_oprand1,
       test_prog_lda_1_oprand2, test_prog_lda_1_oprand3;

  Clock clock_1 (.out(clock_1_out));
  LED led_1 (.in(test_prog_lda_1_opc3));
  LED led_2 (.in(test_prog_lda_1_opc2));
  TEST_PROG_LDA test_prog_lda_1 (
    .ROMI3(cpu_v5_1_romi3), .ROMI2(cpu_v5_1_romi2), .ROMI1(cpu_v5_1_romi1), .ROMI0(cpu_v5_1_romi0),
    .OPC3(test_prog_lda_1_opc3), .OPC2(test_prog_lda_1_opc2), .OPC1(test_prog_lda_1_opc1),
    .OPC0(test_prog_lda_1_opc0), .OPRAND3(test_prog_lda_1_oprand3), .OPRAND2(test_prog_lda_1_oprand2),
    .OPRAND1(test_prog_lda_1_oprand1), .OPRAND0(test_prog_lda_1_oprand0));
  LED led_3 (.in(test_prog_lda_1_opc1));
  LED led_4 (.in(test_prog_lda_1_opc0));
  LED led_5 (.in(test_prog_lda_1_oprand3));
  LED led_6 (.in(test_prog_lda_1_oprand2));
  LED led_7 (.in(test_prog_lda_1_oprand1));
  LED led_8 (.in(test_prog_lda_1_oprand0));
  cpu_v5 cpu_v5_1 (
    .CLK(clock_1_out), .HARD_RESET(in_1), .OPC3(test_prog_lda_1_opc3), .OPC2(test_prog_lda_1_opc2),
    .OPC1(test_prog_lda_1_opc1), .OPC0(test_prog_lda_1_opc0), .OPRAND3(test_prog_lda_1_oprand3),
    .OPRAND2(test_prog_lda_1_oprand2), .OPRAND1(test_prog_lda_1_oprand1), .OPRAND0(test_prog_lda_1_oprand0),
    .OVF(cpu_v5_1_ovf), .N(cpu_v5_1_n), .C(cpu_v5_1_c), .Z(cpu_v5_1_z), .ACC_O3(cpu_v5_1_acc_o3),
    .ACC_O2(cpu_v5_1_acc_o2), .ACC_O1(cpu_v5_1_acc_o1), .ACC_O0(cpu_v5_1_acc_o0),
    .ISA_OPC_3(cpu_v5_1_isa_opc_3), .ISA_OPC_2(cpu_v5_1_isa_opc_2), .ISA_OPC_1(cpu_v5_1_isa_opc_1),
    .ISA_OPC_0(cpu_v5_1_isa_opc_0), .ISA_OPR_3(cpu_v5_1_isa_opr_3), .ISA_OPR_2(cpu_v5_1_isa_opr_2),
    .ISA_OPR_1(cpu_v5_1_isa_opr_1), .ISA_OPR_0(cpu_v5_1_isa_opr_0), .ROMI3(cpu_v5_1_romi3),
    .ROMI2(cpu_v5_1_romi2), .ROMI1(cpu_v5_1_romi1), .ROMI0(cpu_v5_1_romi0), .FETCH(cpu_v5_1_fetch),
    .DECODE(cpu_v5_1_decode), .EXECUTE(cpu_v5_1_execute), .WRITEBACK(cpu_v5_1_writeback));
  LED led_9 (.in(cpu_v5_1_ovf));
  LED led_10 (.in(cpu_v5_1_n));
  LED led_11 (.in(cpu_v5_1_c));
  LED led_12 (.in(cpu_v5_1_z));
  LED led_13 (.in(cpu_v5_1_acc_o3));
  LED led_14 (.in(cpu_v5_1_acc_o2));
  LED led_15 (.in(cpu_v5_1_acc_o1));
  LED led_16 (.in(cpu_v5_1_acc_o0));
  LED led_17 (.in(cpu_v5_1_fetch));
  LED led_18 (.in(cpu_v5_1_decode));
  LED led_19 (.in(cpu_v5_1_execute));
  LED led_20 (.in(cpu_v5_1_writeback));
  LED led_21 (.in(cpu_v5_1_isa_opc_3));
  LED led_22 (.in(cpu_v5_1_isa_opc_2));
  LED led_23 (.in(cpu_v5_1_isa_opc_1));
  LED led_24 (.in(cpu_v5_1_isa_opc_0));
  LED led_25 (.in(cpu_v5_1_isa_opr_3));
  LED led_26 (.in(cpu_v5_1_isa_opr_2));
  LED led_27 (.in(cpu_v5_1_isa_opr_1));
  LED led_28 (.in(cpu_v5_1_isa_opr_0));
endmodule

module test (
  input  CLK,
  input  HARD_RESET,
  output OVF,
  output N,
  output C,
  output Z,
  output ACC_O3,
  output ACC_O2,
  output ACC_O1,
  output ACC_O0,
  output ISA_OPC_3,
  output ISA_OPC_2,
  output ISA_OPC_1,
  output ISA_OPC_0,
  output ISA_OPR_3,
  output ISA_OPR_2,
  output ISA_OPR_1,
  output ISA_OPR_0
);

  wire alu_ext_1_c, alu_ext_1_n, alu_ext_1_o_0, alu_ext_1_o_1, alu_ext_1_o_2, alu_ext_1_o_3, alu_ext_1_ovf,
       alu_ext_1_z, and_1_out, and_2_out, and_3_out, and_4_out, and_5_out, and_6_out, and_7_out,
       controlled_buffer_1_out, controlled_buffer_2_out, controlled_buffer_3_out, controlled_buffer_4_out,
       controlled_buffer_5_out, controlled_buffer_6_out, controlled_buffer_7_out, controlled_buffer_8_out,
       ctrlunit_ext_1_alu_sig, ctrlunit_ext_1_ctrl_b0, ctrlunit_ext_1_ctrl_b1, ctrlunit_ext_1_ctrl_b2,
       ctrlunit_ext_1_ctrl_b3, ctrlunit_ext_1_ctrl_op0, ctrlunit_ext_1_ctrl_op1, ctrlunit_ext_1_ctrl_op2,
       ctrlunit_ext_1_hlt_sig, ctrlunit_ext_1_jmp_sig, ctrlunit_ext_1_lda_sig, ctrlunit_ext_1_ldi_sig,
       ctrlunit_ext_1_sta_sig, fsm_2bit_1_decode, fsm_2bit_1_execute, fsm_2bit_1_fetch, fsm_2bit_1_writeback,
       MEM_ADDR_REG_reg_o0, MEM_ADDR_REG_reg_o1, not_1_out, not_2_out, or_1_out, or_2_out, or_3_out,
       or_4_out, PC_REG_reg_o0, PC_REG_reg_o1, PC_REG_reg_o2, PC_REG_reg_o3, progcounter_ext_1_pco0,
       progcounter_ext_1_pco1, progcounter_ext_1_pco2, progcounter_ext_1_pco3, register_4bit_1_reg_o0,
       register_4bit_1_reg_o1, register_4bit_1_reg_o2, register_4bit_1_reg_o3, STATIC_RAM_sram_o0,
       STATIC_RAM_sram_o1, STATIC_RAM_sram_o2, STATIC_RAM_sram_o3, test_prog_lda_1_opc0,
       test_prog_lda_1_opc1, test_prog_lda_1_opc2, test_prog_lda_1_opc3, test_prog_lda_1_oprand0,
       test_prog_lda_1_oprand1, test_prog_lda_1_oprand2, test_prog_lda_1_oprand3;

  FSM_2BIT fsm_2bit_1 (
    .HARD_RESET(HARD_RESET), .CLK(CLK), .FETCH(fsm_2bit_1_fetch), .DECODE(fsm_2bit_1_decode),
    .EXECUTE(fsm_2bit_1_execute), .WRITEBACK(fsm_2bit_1_writeback));  // open: HTL
  ProgCounter_EXT progcounter_ext_1 (
    .A3(PC_REG_reg_o3), .A2(PC_REG_reg_o2), .A1(PC_REG_reg_o1), .A0(PC_REG_reg_o0),
    .PC_OPR3(controlled_buffer_1_out), .PC_OPR2(controlled_buffer_2_out), .PC_OPR1(controlled_buffer_3_out),
    .PC_OPR0(controlled_buffer_4_out), .JMP_JZ(ctrlunit_ext_1_jmp_sig), .FTCH(fsm_2bit_1_fetch),
    .PCO3(progcounter_ext_1_pco3), .PCO2(progcounter_ext_1_pco2), .PCO1(progcounter_ext_1_pco1),
    .PCO0(progcounter_ext_1_pco0));
  REGISTER_4BIT PC_REG (
    .HARD_RESET(HARD_RESET), .CLK(CLK), .REG_I3(progcounter_ext_1_pco3), .REG_I2(progcounter_ext_1_pco2),
    .REG_I1(progcounter_ext_1_pco1), .REG_I0(progcounter_ext_1_pco0), .WE(not_2_out), .REG_O3(PC_REG_reg_o3),
    .REG_O2(PC_REG_reg_o2), .REG_O1(PC_REG_reg_o1), .REG_O0(PC_REG_reg_o0));
  REGISTER_4BIT register_4bit_1 (
    .HARD_RESET(HARD_RESET), .CLK(CLK), .REG_I3(PC_REG_reg_o3), .REG_I2(PC_REG_reg_o2),
    .REG_I1(PC_REG_reg_o1), .REG_I0(PC_REG_reg_o0), .WE(fsm_2bit_1_fetch), .REG_O3(register_4bit_1_reg_o3),
    .REG_O2(register_4bit_1_reg_o2), .REG_O1(register_4bit_1_reg_o1), .REG_O0(register_4bit_1_reg_o0));
  and and_1 (and_1_out, not_2_out, fsm_2bit_1_decode);
  TEST_PROG_LDA test_prog_lda_1 (
    .ROMI3(register_4bit_1_reg_o3), .ROMI2(register_4bit_1_reg_o2), .ROMI1(register_4bit_1_reg_o1),
    .ROMI0(register_4bit_1_reg_o0), .OPC3(test_prog_lda_1_opc3), .OPC2(test_prog_lda_1_opc2),
    .OPC1(test_prog_lda_1_opc1), .OPC0(test_prog_lda_1_opc0), .OPRAND3(test_prog_lda_1_oprand3),
    .OPRAND2(test_prog_lda_1_oprand2), .OPRAND1(test_prog_lda_1_oprand1), .OPRAND0(test_prog_lda_1_oprand0));
  and and_2 (and_2_out, not_2_out, fsm_2bit_1_decode);
  REGISTER_4BIT INSTRUCTION_REG_OPC (
    .HARD_RESET(HARD_RESET), .CLK(CLK), .REG_I3(test_prog_lda_1_opc3), .REG_I2(test_prog_lda_1_opc2),
    .REG_I1(test_prog_lda_1_opc1), .REG_I0(test_prog_lda_1_opc0), .WE(and_1_out), .REG_O3(ISA_OPC_3),
    .REG_O2(ISA_OPC_2), .REG_O1(ISA_OPC_1), .REG_O0(ISA_OPC_0));
  REGISTER_4BIT INSTRUCTION_REG_OPR (
    .HARD_RESET(HARD_RESET), .CLK(CLK), .REG_I3(test_prog_lda_1_oprand3), .REG_I2(test_prog_lda_1_oprand2),
    .REG_I1(test_prog_lda_1_oprand1), .REG_I0(test_prog_lda_1_oprand0), .WE(and_2_out), .REG_O3(ISA_OPR_3),
    .REG_O2(ISA_OPR_2), .REG_O1(ISA_OPR_1), .REG_O0(ISA_OPR_0));
  CTRLUNIT_EXT ctrlunit_ext_1 (
    .CTRL_S3(ISA_OPC_3), .CTRL_S2(ISA_OPC_2), .CTRL_S1(ISA_OPC_1), .CTRL_S0(ISA_OPC_0),
    .CTRL_OPR3(ISA_OPR_3), .CTRL_OPR2(ISA_OPR_2), .CTRL_OPR1(ISA_OPR_1), .CTRL_OPR0(ISA_OPR_0), .FLAG_N(N),
    .FLAG_Z(Z), .CTRL_OP2(ctrlunit_ext_1_ctrl_op2), .CTRL_OP1(ctrlunit_ext_1_ctrl_op1),
    .CTRL_OP0(ctrlunit_ext_1_ctrl_op0), .CTRL_B3(ctrlunit_ext_1_ctrl_b3), .CTRL_B2(ctrlunit_ext_1_ctrl_b2),
    .CTRL_B1(ctrlunit_ext_1_ctrl_b1), .CTRL_B0(ctrlunit_ext_1_ctrl_b0), .JMP_SIG(ctrlunit_ext_1_jmp_sig),
    .HLT_SIG(ctrlunit_ext_1_hlt_sig), .LDI_SIG(ctrlunit_ext_1_ldi_sig), .LDA_SIG(ctrlunit_ext_1_lda_sig),
    .STA_SIG(ctrlunit_ext_1_sta_sig), .ALU_SIG(ctrlunit_ext_1_alu_sig));  // open: FLAG_OVF, FLAG_C, CTRL_OP3, CTRL_WE
  not not_1 (not_1_out, ctrlunit_ext_1_lda_sig);
  assign controlled_buffer_1_out = not_1_out ? ctrlunit_ext_1_ctrl_b3 : 1'bz;  // Controlled_Buffer controlled_buffer_1
  assign controlled_buffer_2_out = not_1_out ? ctrlunit_ext_1_ctrl_b2 : 1'bz;  // Controlled_Buffer controlled_buffer_2
  assign controlled_buffer_3_out = not_1_out ? ctrlunit_ext_1_ctrl_b1 : 1'bz;  // Controlled_Buffer controlled_buffer_3
  assign controlled_buffer_4_out = not_1_out ? ctrlunit_ext_1_ctrl_b0 : 1'bz;  // Controlled_Buffer controlled_buffer_4
  not not_2 (not_2_out, ctrlunit_ext_1_hlt_sig);
  or or_1 (or_1_out, ctrlunit_ext_1_ldi_sig, ctrlunit_ext_1_lda_sig);
  ALU_EXT alu_ext_1 (
    .A_3(ACC_O3), .A_2(ACC_O2), .A_1(ACC_O1), .A_0(ACC_O0), .B_3(controlled_buffer_1_out),
    .B_2(controlled_buffer_2_out), .B_1(controlled_buffer_3_out), .B_0(controlled_buffer_4_out),
    .S2(ctrlunit_ext_1_ctrl_op2), .S1(ctrlunit_ext_1_ctrl_op1), .S0(ctrlunit_ext_1_ctrl_op0),
    .OVF(alu_ext_1_ovf), .N(alu_ext_1_n), .C(alu_ext_1_c), .Z(alu_ext_1_z), .O_3(alu_ext_1_o_3),
    .O_2(alu_ext_1_o_2), .O_1(alu_ext_1_o_1), .O_0(alu_ext_1_o_0));
  or or_2 (or_2_out, or_1_out, ctrlunit_ext_1_sta_sig);
  assign controlled_buffer_5_out = ctrlunit_ext_1_alu_sig ? alu_ext_1_o_3 : 1'bz;  // Controlled_Buffer controlled_buffer_5
  assign controlled_buffer_6_out = ctrlunit_ext_1_alu_sig ? alu_ext_1_o_2 : 1'bz;  // Controlled_Buffer controlled_buffer_6
  assign controlled_buffer_7_out = ctrlunit_ext_1_alu_sig ? alu_ext_1_o_1 : 1'bz;  // Controlled_Buffer controlled_buffer_7
  assign controlled_buffer_8_out = ctrlunit_ext_1_alu_sig ? alu_ext_1_o_0 : 1'bz;  // Controlled_Buffer controlled_buffer_8
  assign controlled_buffer_5_out = or_2_out ? controlled_buffer_1_out : 1'bz;  // Controlled_Buffer controlled_buffer_9
  assign controlled_buffer_6_out = or_2_out ? controlled_buffer_2_out : 1'bz;  // Controlled_Buffer controlled_buffer_10
  assign controlled_buffer_7_out = or_2_out ? controlled_buffer_3_out : 1'bz;  // Controlled_Buffer controlled_buffer_11
  assign controlled_buffer_8_out = or_2_out ? controlled_buffer_4_out : 1'bz;  // Controlled_Buffer controlled_buffer_12
  or or_3 (or_3_out, or_2_out, ctrlunit_ext_1_alu_sig);
  and and_3 (and_3_out, fsm_2bit_1_execute, and_4_out);
  and and_4 (and_4_out, or_3_out, not_2_out);
  and and_5 (and_5_out, and_4_out, fsm_2bit_1_execute);
  REGISTER_4BIT ACCUMULATOR_REG (
    .HARD_RESET(HARD_RESET), .CLK(CLK), .REG_I3(controlled_buffer_5_out), .REG_I2(controlled_buffer_6_out),
    .REG_I1(controlled_buffer_7_out), .REG_I0(controlled_buffer_8_out), .WE(and_5_out), .REG_O3(ACC_O3),
    .REG_O2(ACC_O2), .REG_O1(ACC_O1), .REG_O0(ACC_O0));
  REGISTER_4BIT FLAG_REG (
    .HARD_RESET(HARD_RESET), .CLK(CLK), .REG_I3(alu_ext_1_ovf), .REG_I2(alu_ext_1_n), .REG_I1(alu_ext_1_c),
    .REG_I0(alu_ext_1_z), .WE(and_3_out), .REG_O3(OVF), .REG_O2(N), .REG_O1(C), .REG_O0(Z));
  and and_6 (and_6_out, or_4_out, fsm_2bit_1_writeback);
  or or_4 (or_4_out, ctrlunit_ext_1_lda_sig, ctrlunit_ext_1_sta_sig);
  REGISTER_4BIT MEM_ADDR_REG (
    .HARD_RESET(HARD_RESET), .CLK(CLK), .REG_I1(ctrlunit_ext_1_ctrl_b1), .REG_I0(ctrlunit_ext_1_ctrl_b0),
    .WE(and_6_out), .REG_O1(MEM_ADDR_REG_reg_o1), .REG_O0(MEM_ADDR_REG_reg_o0));  // open: REG_I3, REG_I2, REG_O3, REG_O2
  and and_7 (and_7_out, fsm_2bit_1_writeback, ctrlunit_ext_1_sta_sig);
  SRAM STATIC_RAM (
    .HARD_RESET(HARD_RESET), .CLK(CLK), .I3(ACC_O3), .I2(ACC_O2), .I1(ACC_O1), .I0(ACC_O0), .WE(and_7_out),
    .ADDR1(MEM_ADDR_REG_reg_o1), .ADDR0(MEM_ADDR_REG_reg_o0), .SRAM_O3(STATIC_RAM_sram_o3),
    .SRAM_O2(STATIC_RAM_sram_o2), .SRAM_O1(STATIC_RAM_sram_o1), .SRAM_O0(STATIC_RAM_sram_o0));
  assign controlled_buffer_1_out = ctrlunit_ext_1_lda_sig ? STATIC_RAM_sram_o3 : 1'bz;  // Controlled_Buffer controlled_buffer_13
  assign controlled_buffer_2_out = ctrlunit_ext_1_lda_sig ? STATIC_RAM_sram_o2 : 1'bz;  // Controlled_Buffer controlled_buffer_14
  assign controlled_buffer_3_out = ctrlunit_ext_1_lda_sig ? STATIC_RAM_sram_o1 : 1'bz;  // Controlled_Buffer controlled_buffer_15
  assign controlled_buffer_4_out = ctrlunit_ext_1_lda_sig ? STATIC_RAM_sram_o0 : 1'bz;  // Controlled_Buffer controlled_buffer_16
endmodule

module cpu_v6 (
  input  RESET
);

  wire alu_ext_v2_1_c, alu_ext_v2_1_n, alu_ext_v2_1_o_0, alu_ext_v2_1_o_1, alu_ext_v2_1_o_2,
       alu_ext_v2_1_o_3, alu_ext_v2_1_ovf, alu_ext_v2_1_z, and_1_out, and_2_out, and_3_out, and_4_out,
       and_5_out, and_6_out, and_7_out, clock_1_out, CONTROL_UNIT_alu_sig, CONTROL_UNIT_ctrl_b0,
       CONTROL_UNIT_ctrl_b1, CONTROL_UNIT_ctrl_b2, CONTROL_UNIT_ctrl_b3, CONTROL_UNIT_ctrl_op0,
       CONTROL_UNIT_ctrl_op1, CONTROL_UNIT_ctrl_op2, CONTROL_UNIT_ctrl_op3, CONTROL_UNIT_hlt_sig,
       CONTROL_UNIT_lda_sig, CONTROL_UNIT_ldi_sig, CONTROL_UNIT_sta_sig, controlled_buffer_1_out,
       controlled_buffer_2_out, controlled_buffer_3_out, controlled_buffer_4_out, controlled_buffer_5_out,
       controlled_buffer_6_out, controlled_buffer_7_out, controlled_buffer_8_out, CURRENT_COUNTER_reg_o0,
       CURRENT_COUNTER_reg_o1, CURRENT_COUNTER_reg_o2, CURRENT_COUNTER_reg_o3, FLAGS_reg_o0, FLAGS_reg_o1,
       FLAGS_reg_o2, FLAGS_reg_o3, FSM_decode, FSM_execute, FSM_fetch, FSM_writeback, MEM_REG_reg_o0,
       MEM_REG_reg_o1, MEM_REG_reg_o2, MEM_REG_reg_o3, NEXT_COUNTER_reg_o0, NEXT_COUNTER_reg_o1,
       NEXT_COUNTER_reg_o2, NEXT_COUNTER_reg_o3, not_1_out, not_2_out, not_3_out, not_4_out, not_5_out,
       not_6_out, not_7_out, OPCODE_reg_o0, OPCODE_reg_o1, OPCODE_reg_o2, OPCODE_reg_o3, OPERAND_reg_o0,
       OPERAND_reg_o1, OPERAND_reg_o2, OPERAND_reg_o3, or_1_out, or_2_out, or_3_out, or_4_out,
       PROGRAM_COUNTER_pco0, PROGRAM_COUNTER_pco1, PROGRAM_COUNTER_pco2, PROGRAM_COUNTER_pco3, RESULT_reg_o0,
       RESULT_reg_o1, RESULT_reg_o2, RESULT_reg_o3, ROM_opc0, ROM_opc1, ROM_opc2, ROM_opc3, ROM_oprand0,
       ROM_oprand1, ROM_oprand2, ROM_oprand3, sram_1_sram_o0, sram_1_sram_o1, sram_1_sram_o2, sram_1_sram_o3;

  Clock clock_1 (.out(clock_1_out));
  FSM_2BIT FSM (
    .HARD_RESET(RESET), .CLK(clock_1_out), .FETCH(FSM_fetch), .DECODE(FSM_decode), .EXECUTE(FSM_execute),
    .WRITEBACK(FSM_writeback));  // open: HTL
  ProgCounter_EXT PROGRAM_COUNTER (
    .A3(CURRENT_COUNTER_reg_o3), .A2(CURRENT_COUNTER_reg_o2), .A1(CURRENT_COUNTER_reg_o1),
    .A0(CURRENT_COUNTER_reg_o0), .FTCH(FSM_fetch), .PCO3(PROGRAM_COUNTER_pco3), .PCO2(PROGRAM_COUNTER_pco2),
    .PCO1(PROGRAM_COUNTER_pco1), .PCO0(PROGRAM_COUNTER_pco0));  // open: PC_OPR3, PC_OPR2, PC_OPR1, PC_OPR0, JMP_JZ
  and and_1 (and_1_out, not_1_out, FSM_fetch);
  not not_1 (not_1_out, CONTROL_UNIT_hlt_sig);
  REGISTER_4BIT NEXT_COUNTER (
    .HARD_RESET(RESET), .CLK(clock_1_out), .REG_I3(PROGRAM_COUNTER_pco3), .REG_I2(PROGRAM_COUNTER_pco2),
    .REG_I1(PROGRAM_COUNTER_pco1), .REG_I0(PROGRAM_COUNTER_pco0), .WE(and_1_out),
    .REG_O3(NEXT_COUNTER_reg_o3), .REG_O2(NEXT_COUNTER_reg_o2), .REG_O1(NEXT_COUNTER_reg_o1),
    .REG_O0(NEXT_COUNTER_reg_o0));
  not not_2 (not_2_out, and_2_out);
  and and_2 (and_2_out, not_3_out, FSM_fetch);
  not not_3 (not_3_out, CONTROL_UNIT_hlt_sig);
  REGISTER_4BIT CURRENT_COUNTER (
    .HARD_RESET(RESET), .CLK(clock_1_out), .REG_I3(NEXT_COUNTER_reg_o3), .REG_I2(NEXT_COUNTER_reg_o2),
    .REG_I1(NEXT_COUNTER_reg_o1), .REG_I0(NEXT_COUNTER_reg_o0), .WE(not_2_out),
    .REG_O3(CURRENT_COUNTER_reg_o3), .REG_O2(CURRENT_COUNTER_reg_o2), .REG_O1(CURRENT_COUNTER_reg_o1),
    .REG_O0(CURRENT_COUNTER_reg_o0));
  TEST_PROG_LDA ROM (
    .ROMI3(CURRENT_COUNTER_reg_o3), .ROMI2(CURRENT_COUNTER_reg_o2), .ROMI1(CURRENT_COUNTER_reg_o1),
    .ROMI0(CURRENT_COUNTER_reg_o0), .OPC3(ROM_opc3), .OPC2(ROM_opc2), .OPC1(ROM_opc1), .OPC0(ROM_opc0),
    .OPRAND3(ROM_oprand3), .OPRAND2(ROM_oprand2), .OPRAND1(ROM_oprand1), .OPRAND0(ROM_oprand0));
  and and_3 (and_3_out, not_4_out, FSM_decode);
  not not_4 (not_4_out, CONTROL_UNIT_hlt_sig);
  REGISTER_4BIT OPCODE (
    .HARD_RESET(RESET), .CLK(clock_1_out), .REG_I3(ROM_opc3), .REG_I2(ROM_opc2), .REG_I1(ROM_opc1),
    .REG_I0(ROM_opc0), .WE(and_3_out), .REG_O3(OPCODE_reg_o3), .REG_O2(OPCODE_reg_o2),
    .REG_O1(OPCODE_reg_o1), .REG_O0(OPCODE_reg_o0));
  REGISTER_4BIT OPERAND (
    .HARD_RESET(RESET), .CLK(clock_1_out), .REG_I3(ROM_oprand3), .REG_I2(ROM_oprand2), .REG_I1(ROM_oprand1),
    .REG_I0(ROM_oprand0), .WE(and_3_out), .REG_O3(OPERAND_reg_o3), .REG_O2(OPERAND_reg_o2),
    .REG_O1(OPERAND_reg_o1), .REG_O0(OPERAND_reg_o0));
  LED led_1 (.in(OPCODE_reg_o3));
  LED led_2 (.in(OPCODE_reg_o2));
  LED led_3 (.in(OPCODE_reg_o1));
  LED led_4 (.in(OPCODE_reg_o0));
  LED led_5 (.in(OPERAND_reg_o3));
  LED led_6 (.in(OPERAND_reg_o2));
  LED led_7 (.in(OPERAND_reg_o1));
  LED led_8 (.in(OPERAND_reg_o0));
  CTRLUNIT_EXT CONTROL_UNIT (
    .CTRL_S3(OPCODE_reg_o3), .CTRL_S2(OPCODE_reg_o2), .CTRL_S1(OPCODE_reg_o1), .CTRL_S0(OPCODE_reg_o0),
    .CTRL_OPR3(OPERAND_reg_o3), .CTRL_OPR2(OPERAND_reg_o2), .CTRL_OPR1(OPERAND_reg_o1),
    .CTRL_OPR0(OPERAND_reg_o0), .FLAG_OVF(FLAGS_reg_o3), .FLAG_N(FLAGS_reg_o2), .FLAG_C(FLAGS_reg_o1),
    .FLAG_Z(FLAGS_reg_o0), .CTRL_OP3(CONTROL_UNIT_ctrl_op3), .CTRL_OP2(CONTROL_UNIT_ctrl_op2),
    .CTRL_OP1(CONTROL_UNIT_ctrl_op1), .CTRL_OP0(CONTROL_UNIT_ctrl_op0), .CTRL_B3(CONTROL_UNIT_ctrl_b3),
    .CTRL_B2(CONTROL_UNIT_ctrl_b2), .CTRL_B1(CONTROL_UNIT_ctrl_b1), .CTRL_B0(CONTROL_UNIT_ctrl_b0),
    .HLT_SIG(CONTROL_UNIT_hlt_sig), .LDI_SIG(CONTROL_UNIT_ldi_sig), .LDA_SIG(CONTROL_UNIT_lda_sig),
    .STA_SIG(CONTROL_UNIT_sta_sig), .ALU_SIG(CONTROL_UNIT_alu_sig));  // open: CTRL_WE, JMP_SIG
  or or_1 (or_1_out, CONTROL_UNIT_sta_sig, CONTROL_UNIT_lda_sig);
  not not_5 (not_5_out, or_1_out);
  assign controlled_buffer_1_out = not_5_out ? CONTROL_UNIT_ctrl_b3 : 1'bz;  // Controlled_Buffer controlled_buffer_1
  assign controlled_buffer_2_out = not_5_out ? CONTROL_UNIT_ctrl_b2 : 1'bz;  // Controlled_Buffer controlled_buffer_2
  assign controlled_buffer_3_out = not_5_out ? CONTROL_UNIT_ctrl_b1 : 1'bz;  // Controlled_Buffer controlled_buffer_3
  assign controlled_buffer_4_out = not_5_out ? CONTROL_UNIT_ctrl_b0 : 1'bz;  // Controlled_Buffer controlled_buffer_4
  or or_2 (or_2_out, CONTROL_UNIT_lda_sig, CONTROL_UNIT_ldi_sig);
  or or_3 (or_3_out, CONTROL_UNIT_sta_sig, CONTROL_UNIT_alu_sig);
  ALU_EXT_v2 alu_ext_v2_1 (
    .A_3(RESULT_reg_o3), .A_2(RESULT_reg_o2), .A_1(RESULT_reg_o1), .A_0(RESULT_reg_o0),
    .B_3(controlled_buffer_1_out), .B_2(controlled_buffer_2_out), .B_1(controlled_buffer_3_out),
    .B_0(controlled_buffer_4_out), .S3(CONTROL_UNIT_ctrl_op3), .S2(CONTROL_UNIT_ctrl_op2),
    .S1(CONTROL_UNIT_ctrl_op1), .S0(CONTROL_UNIT_ctrl_op0), .OVF(alu_ext_v2_1_ovf), .N(alu_ext_v2_1_n),
    .C(alu_ext_v2_1_c), .Z(alu_ext_v2_1_z), .O_3(alu_ext_v2_1_o_3), .O_2(alu_ext_v2_1_o_2),
    .O_1(alu_ext_v2_1_o_1), .O_0(alu_ext_v2_1_o_0));
  not not_6 (not_6_out, CONTROL_UNIT_sta_sig);
  assign controlled_buffer_5_out = or_3_out ? alu_ext_v2_1_o_3 : 1'bz;  // Controlled_Buffer controlled_buffer_5
  assign controlled_buffer_6_out = or_3_out ? alu_ext_v2_1_o_2 : 1'bz;  // Controlled_Buffer controlled_buffer_6
  assign controlled_buffer_7_out = or_3_out ? alu_ext_v2_1_o_1 : 1'bz;  // Controlled_Buffer controlled_buffer_7
  assign controlled_buffer_8_out = or_3_out ? alu_ext_v2_1_o_0 : 1'bz;  // Controlled_Buffer controlled_buffer_8
  assign controlled_buffer_5_out = or_2_out ? controlled_buffer_1_out : 1'bz;  // Controlled_Buffer controlled_buffer_9
  assign controlled_buffer_6_out = or_2_out ? controlled_buffer_2_out : 1'bz;  // Controlled_Buffer controlled_buffer_10
  assign controlled_buffer_7_out = or_2_out ? controlled_buffer_3_out : 1'bz;  // Controlled_Buffer controlled_buffer_11
  assign controlled_buffer_8_out = or_2_out ? controlled_buffer_4_out : 1'bz;  // Controlled_Buffer controlled_buffer_12
  not not_7 (not_7_out, CONTROL_UNIT_hlt_sig);
  and and_4 (and_4_out, FSM_execute, not_6_out, not_7_out);
  REGISTER_4BIT RESULT (
    .HARD_RESET(RESET), .CLK(clock_1_out), .REG_I3(controlled_buffer_5_out),
    .REG_I2(controlled_buffer_6_out), .REG_I1(controlled_buffer_7_out), .REG_I0(controlled_buffer_8_out),
    .WE(and_4_out), .REG_O3(RESULT_reg_o3), .REG_O2(RESULT_reg_o2), .REG_O1(RESULT_reg_o1),
    .REG_O0(RESULT_reg_o0));
  REGISTER_4BIT FLAGS (
    .HARD_RESET(RESET), .CLK(clock_1_out), .REG_I3(alu_ext_v2_1_ovf), .REG_I2(alu_ext_v2_1_n),
    .REG_I1(alu_ext_v2_1_c), .REG_I0(alu_ext_v2_1_z), .WE(and_4_out), .REG_O3(FLAGS_reg_o3),
    .REG_O2(FLAGS_reg_o2), .REG_O1(FLAGS_reg_o1), .REG_O0(FLAGS_reg_o0));
  LED led_9 (.in(RESULT_reg_o3));
  LED led_10 (.in(RESULT_reg_o2));
  LED led_11 (.in(RESULT_reg_o1));
  LED led_12 (.in(RESULT_reg_o0));
  assign controlled_buffer_1_out = CONTROL_UNIT_sta_sig ? RESULT_reg_o3 : 1'bz;  // Controlled_Buffer controlled_buffer_13
  assign controlled_buffer_2_out = CONTROL_UNIT_sta_sig ? RESULT_reg_o2 : 1'bz;  // Controlled_Buffer controlled_buffer_14
  assign controlled_buffer_3_out = CONTROL_UNIT_sta_sig ? RESULT_reg_o1 : 1'bz;  // Controlled_Buffer controlled_buffer_15
  assign controlled_buffer_4_out = CONTROL_UNIT_sta_sig ? RESULT_reg_o0 : 1'bz;  // Controlled_Buffer controlled_buffer_16
  LED led_13 (.in(MEM_REG_reg_o3));
  LED led_14 (.in(MEM_REG_reg_o2));
  REGISTER_4BIT MEM_REG (
    .HARD_RESET(RESET), .CLK(clock_1_out), .REG_I1(CONTROL_UNIT_ctrl_b1), .REG_I0(CONTROL_UNIT_ctrl_b0),
    .WE(FSM_execute), .REG_O3(MEM_REG_reg_o3), .REG_O2(MEM_REG_reg_o2), .REG_O1(MEM_REG_reg_o1),
    .REG_O0(MEM_REG_reg_o0));  // open: REG_I3, REG_I2
  LED led_15 (.in(MEM_REG_reg_o1));
  LED led_16 (.in(MEM_REG_reg_o0));
  and and_5 (and_5_out, CONTROL_UNIT_sta_sig, FSM_writeback);
  and and_6 (and_6_out, CONTROL_UNIT_lda_sig, FSM_writeback);
  SRAM sram_1 (
    .HARD_RESET(RESET), .CLK(clock_1_out), .I3(controlled_buffer_1_out), .I2(controlled_buffer_2_out),
    .I1(controlled_buffer_3_out), .I0(controlled_buffer_4_out), .WE(and_5_out), .ADDR1(MEM_REG_reg_o1),
    .ADDR0(MEM_REG_reg_o0), .SRAM_O3(sram_1_sram_o3), .SRAM_O2(sram_1_sram_o2), .SRAM_O1(sram_1_sram_o1),
    .SRAM_O0(sram_1_sram_o0));
  or or_4 (or_4_out, and_6_out, and_7_out);
  and and_7 (and_7_out, CONTROL_UNIT_lda_sig, FSM_execute);
  assign controlled_buffer_4_out = or_4_out ? sram_1_sram_o0 : 1'bz;  // Controlled_Buffer controlled_buffer_17
  assign controlled_buffer_3_out = or_4_out ? sram_1_sram_o1 : 1'bz;  // Controlled_Buffer controlled_buffer_18
  assign controlled_buffer_2_out = or_4_out ? sram_1_sram_o2 : 1'bz;  // Controlled_Buffer controlled_buffer_19
  assign controlled_buffer_1_out = or_4_out ? sram_1_sram_o3 : 1'bz;  // Controlled_Buffer controlled_buffer_20
  LED DATA_BUS_3 (.in(controlled_buffer_1_out));
  LED DATA_BUS_2 (.in(controlled_buffer_2_out));
  LED DATA_BUS_1 (.in(controlled_buffer_3_out));
  LED led_17 (.in(FSM_fetch));
  LED led_18 (.in(FSM_decode));
  LED led_19 (.in(FSM_execute));
  LED DATA_BUS_0 (.in(controlled_buffer_4_out));
  LED led_20 (.in(FSM_writeback));
endmodule

module ALU_EXT_v2 (
  input  A_3,
  input  A_2,
  input  A_1,
  input  A_0,
  input  B_3,
  input  B_2,
  input  B_1,
  input  B_0,
  input  S3,
  input  S2,
  input  S1,
  input  S0,
  output OVF,
  output N,
  output C,
  output Z,
  output O_3,
  output O_2,
  output O_1,
  output O_0
);

  wire Adder_out, and_1_out, and_2_out, and_3_out, and_4_out, and_5_out, and_6_out, and_7_out, and_8_out,
       and_9_out, and_10_out, and_11_out, and_12_out, and_13_out, and_14_out, and_15_out, and_16_out,
       and_17_out, and_18_out, and_19_out, and_20_out, and_21_out, and_22_out, and_23_out, and_24_out,
       and_25_out, and_26_out, and_27_out, and_28_out, and_29_out, and_30_out, and_31_out, and_32_out,
       and_33_out, and_34_out, and_35_out, and_36_out, and_37_out, and_38_out, and_39_out, and_40_out,
       and_41_out, and_42_out, and_43_out, and_44_out, and_45_out, and_46_out, and_47_out, and_48_out,
       and_49_out, and_50_out, and_51_out, and_52_out, and_53_out, and_54_out, and_55_out, and_56_out,
       and_61_out, and_62_out, and_63_out, and_64_out, ANDOP_out, MUX2x1_out, MUX8x1_out, not_1_out,
       not_2_out, not_3_out, not_4_out, not_5_out, not_6_out, not_7_out, not_8_out, not_9_out, not_10_out,
       not_11_out, not_12_out, not_13_out, not_14_out, not_15_out, not_16_out, not_17_out, not_18_out,
       not_19_out, not_20_out, not_21_out, not_22_out, not_23_out, or_1_out, or_2_out, or_3_out, or_4_out,
       or_5_out, or_6_out, or_7_out, or_8_out, or_9_out, or_10_out, or_11_out, or_12_out, or_13_out,
       or_14_out, or_15_out, or_16_out, or_17_out, or_18_out, or_19_out, or_20_out, OROP_out, Subtractor_out,
       xor_1_out, xor_2_out, xor_3_out, xor_4_out, xor_5_out, xor_6_out, xor_7_out, xor_8_out, xor_9_out,
       xor_10_out, xor_11_out, xor_12_out, xor_13_out, xor_14_out, xor_15_out, xor_16_out, xor_17_out,
       xor_18_out, xor_19_out, XOROP_out;

  not not_1 (not_1_out, A_0);
  not not_2 (not_2_out, A_1);
  not not_3 (not_3_out, A_2);
  not not_4 (not_4_out, A_3);
  xor Adder (Adder_out, A_0, B_0);
  xor xor_1 (xor_1_out, A_1, B_1);
  xor xor_2 (xor_2_out, A_2, B_2);
  xor xor_3 (xor_3_out, A_3, B_3);
  and and_1 (and_1_out, not_1_out, B_0);
  and and_2 (and_2_out, not_1_out, 1'b0);
  and and_3 (and_3_out, B_0, 1'b0);
  xor xor_4 (xor_4_out, A_1, B_1);
  and and_4 (and_4_out, not_2_out, B_1);
  and and_5 (and_5_out, not_2_out, or_8_out);
  and and_6 (and_6_out, B_1, or_8_out);
  xor xor_5 (xor_5_out, A_2, B_2);
  and and_7 (and_7_out, not_3_out, B_2);
  and and_8 (and_8_out, not_3_out, or_9_out);
  and and_9 (and_9_out, B_2, or_9_out);
  xor xor_6 (xor_6_out, A_3, B_3);
  and and_10 (and_10_out, not_4_out, B_3);
  and and_11 (and_11_out, not_4_out, or_10_out);
  and and_12 (and_12_out, B_3, or_10_out);
  xor Subtractor (Subtractor_out, A_0, B_0);
  or or_1 (or_1_out, and_1_out, and_2_out);
  or or_2 (or_2_out, and_4_out, and_5_out);
  or or_3 (or_3_out, and_7_out, and_8_out);
  or or_4 (or_4_out, and_10_out, and_11_out);
  and ANDOP (ANDOP_out, A_0, B_0);
  and and_13 (and_13_out, A_1, B_1);
  and and_14 (and_14_out, A_2, B_2);
  and and_15 (and_15_out, A_3, B_3);
  or OROP (OROP_out, A_0, B_0);
  or or_5 (or_5_out, A_1, B_1);
  or or_6 (or_6_out, A_2, B_2);
  or or_7 (or_7_out, A_3, B_3);
  xor XOROP (XOROP_out, A_0, B_0);
  xor xor_7 (xor_7_out, A_1, B_1);
  xor xor_8 (xor_8_out, A_2, B_2);
  xor xor_9 (xor_9_out, A_3, B_3);
  not not_5 (not_5_out, A_0);
  not not_6 (not_6_out, A_1);
  not not_7 (not_7_out, A_2);
  not not_8 (not_8_out, A_3);
  xor xor_10 (xor_10_out, 1'b0, Adder_out);
  and and_16 (and_16_out, 1'b0, Adder_out);
  and and_17 (and_17_out, A_0, B_0);
  xor xor_11 (xor_11_out, or_12_out, xor_1_out);
  and and_18 (and_18_out, or_12_out, xor_1_out);
  and and_19 (and_19_out, A_1, B_1);
  xor xor_12 (xor_12_out, or_13_out, xor_2_out);
  and and_20 (and_20_out, or_13_out, xor_2_out);
  and and_21 (and_21_out, A_2, B_2);
  xor xor_13 (xor_13_out, or_14_out, xor_3_out);
  and and_22 (and_22_out, or_14_out, xor_3_out);
  and and_23 (and_23_out, A_3, B_3);
  or or_8 (or_8_out, or_1_out, and_3_out);
  xor xor_14 (xor_14_out, xor_4_out, or_8_out);
  or or_9 (or_9_out, or_2_out, and_6_out);
  xor xor_15 (xor_15_out, xor_5_out, or_9_out);
  or or_10 (or_10_out, or_3_out, and_9_out);
  xor xor_16 (xor_16_out, xor_6_out, or_10_out);
  or or_11 (or_11_out, or_4_out, and_12_out);
  xor xor_17 (xor_17_out, Subtractor_out, 1'b0);
  or or_12 (or_12_out, and_16_out, and_17_out);
  or or_13 (or_13_out, and_18_out, and_19_out);
  or or_14 (or_14_out, and_20_out, and_21_out);
  or or_15 (or_15_out, and_22_out, and_23_out);
  xor xor_18 (xor_18_out, or_14_out, or_15_out);
  xor xor_19 (xor_19_out, or_10_out, or_11_out);
  not not_9 (not_9_out, S2);
  not not_10 (not_10_out, S2);
  not not_11 (not_11_out, S2);
  not not_12 (not_12_out, S2);
  not not_13 (not_13_out, S1);
  not not_14 (not_14_out, S1);
  not not_15 (not_15_out, S1);
  not not_16 (not_16_out, S1);
  not not_17 (not_17_out, S0);
  not not_18 (not_18_out, S0);
  not not_19 (not_19_out, S0);
  not not_20 (not_20_out, S0);
  and and_24 (and_24_out, xor_10_out, not_17_out, not_13_out, not_9_out);
  and and_25 (and_25_out, xor_17_out, S0, not_13_out, not_9_out);
  and and_26 (and_26_out, ANDOP_out, not_17_out, S1, not_9_out);
  and and_27 (and_27_out, OROP_out, S0, S1, not_9_out);
  and and_28 (and_28_out, XOROP_out, not_17_out, not_13_out, S2);
  and and_29 (and_29_out, not_5_out, S0, not_13_out, S2);
  and and_30 (and_30_out, xor_10_out, not_17_out, S1, S2);
  and and_31 (and_31_out, xor_17_out, S0, S1, S2);
  and and_32 (and_32_out, xor_11_out, not_18_out, not_14_out, not_10_out);
  and and_33 (and_33_out, xor_14_out, S0, not_14_out, not_10_out);
  and and_34 (and_34_out, and_13_out, not_18_out, S1, not_10_out);
  and and_35 (and_35_out, or_5_out, S0, S1, not_10_out);
  and and_36 (and_36_out, xor_7_out, not_18_out, not_14_out, S2);
  and and_37 (and_37_out, not_6_out, S0, not_14_out, S2);
  and and_38 (and_38_out, xor_11_out, not_18_out, S1, S2);
  and and_39 (and_39_out, xor_14_out, S0, S1, S2);
  and and_40 (and_40_out, xor_12_out, not_19_out, not_15_out, not_11_out);
  and and_41 (and_41_out, xor_15_out, S0, not_15_out, not_11_out);
  and and_42 (and_42_out, and_14_out, not_19_out, S1, not_11_out);
  and and_43 (and_43_out, or_6_out, S0, S1, not_11_out);
  and and_44 (and_44_out, xor_8_out, not_19_out, not_15_out, S2);
  and and_45 (and_45_out, not_7_out, S0, not_15_out, S2);
  and and_46 (and_46_out, xor_12_out, not_19_out, S1, S2);
  and and_47 (and_47_out, xor_15_out, S0, S1, S2);
  and and_48 (and_48_out, xor_13_out, not_20_out, not_16_out, not_12_out);
  and and_49 (and_49_out, xor_16_out, S0, not_16_out, not_12_out);
  and and_50 (and_50_out, and_15_out, not_20_out, S1, not_12_out);
  and and_51 (and_51_out, or_7_out, S0, S1, not_12_out);
  and and_52 (and_52_out, xor_9_out, not_20_out, not_16_out, S2);
  and and_53 (and_53_out, not_8_out, S0, not_16_out, S2);
  and and_54 (and_54_out, xor_13_out, not_20_out, S1, S2);
  and and_55 (and_55_out, xor_16_out, S0, S1, S2);
  and and_56 (and_56_out, not_13_out, not_9_out);
  or MUX8x1 (MUX8x1_out, and_24_out, and_25_out, and_26_out, and_27_out, and_28_out, and_29_out, and_30_out, and_31_out);
  or or_16 (or_16_out, and_32_out, and_33_out, and_34_out, and_35_out, and_36_out, and_37_out, and_38_out, and_39_out);
  or or_17 (or_17_out, and_40_out, and_41_out, and_42_out, and_43_out, and_44_out, and_45_out, and_46_out, and_47_out);
  or or_18 (or_18_out, and_48_out, and_49_out, and_50_out, and_51_out, and_52_out, and_53_out, and_54_out, and_55_out);
  not not_21 (not_21_out, S3);
  and and_57 (O_0, not_21_out, MUX8x1_out);
  and and_58 (O_1, not_21_out, or_16_out);
  and and_59 (O_2, not_21_out, or_17_out);
  and and_60 (N, not_21_out, or_18_out);
  not not_22 (not_22_out, S0);
  not not_23 (not_23_out, S0);
  or or_19 (or_19_out, O_0, O_1, O_2, N);
  not not_24 (Z, or_19_out);
  and and_61 (and_61_out, not_22_out, xor_18_out);
  and and_62 (and_62_out, S0, xor_19_out);
  and and_63 (and_63_out, not_23_out, or_15_out);
  and and_64 (and_64_out, S0, or_11_out);
  or MUX2x1 (MUX2x1_out, and_61_out, and_62_out);
  or or_20 (or_20_out, and_63_out, and_64_out);
  and VALIDOPCODE (OVF, MUX2x1_out, and_56_out);
  and and_65 (C, or_20_out, and_56_out);

  assign O_3 = N;
endmodule
module cpu_v7 (
  input  in_1
);

  wire ACCU_REG_reg_o0, ACCU_REG_reg_o1, ACCU_REG_reg_o2, ACCU_REG_reg_o3, alu_ext_v2_1_c, alu_ext_v2_1_n,
       alu_ext_v2_1_o_0, alu_ext_v2_1_o_1, alu_ext_v2_1_o_2, alu_ext_v2_1_o_3, alu_ext_v2_1_ovf,
       alu_ext_v2_1_z, and_1_out, and_2_out, and_3_out, and_4_out, and_5_out, clock_1_out,
       CONTROL_UNIT_alu_sig, CONTROL_UNIT_hlt_sig, CONTROL_UNIT_lda_sig, CONTROL_UNIT_ldi_sig,
       CONTROL_UNIT_sta_sig, controlled_buffer_1_out, controlled_buffer_2_out, controlled_buffer_3_out,
       controlled_buffer_4_out, CURRENT_COUNTER_reg_o0, CURRENT_COUNTER_reg_o1, CURRENT_COUNTER_reg_o2,
       CURRENT_COUNTER_reg_o3, FLAG_REG_reg_o0, FLAG_REG_reg_o1, FLAG_REG_reg_o2, FLAG_REG_reg_o3,
       FSM_decode, FSM_execute, FSM_fetch, FSM_writeback, MEM_REG_reg_o0, MEM_REG_reg_o1, mux_2x1_1_o,
       mux_2x1_2_o, mux_2x1_3_o, mux_2x1_4_o, NEXT_COUNTER_reg_o0, NEXT_COUNTER_reg_o1, NEXT_COUNTER_reg_o2,
       NEXT_COUNTER_reg_o3, not_1_out, PROGRAM_COUNTER_pco0, PROGRAM_COUNTER_pco1, PROGRAM_COUNTER_pco2,
       PROGRAM_COUNTER_pco3, ROM_opc0, ROM_opc1, ROM_opc2, ROM_opc3, ROM_oprand0, ROM_oprand1, ROM_oprand2,
       ROM_oprand3, sram_1_sram_o0, sram_1_sram_o1, sram_1_sram_o2, sram_1_sram_o3;

  Clock clock_1 (.out(clock_1_out));
  FSM_2BIT FSM (
    .HARD_RESET(in_1), .CLK(clock_1_out), .FETCH(FSM_fetch), .DECODE(FSM_decode), .EXECUTE(FSM_execute),
    .WRITEBACK(FSM_writeback));  // open: HTL
  ProgCounter_EXT PROGRAM_COUNTER (
    .A3(CURRENT_COUNTER_reg_o3), .A2(CURRENT_COUNTER_reg_o2), .A1(CURRENT_COUNTER_reg_o1),
    .A0(CURRENT_COUNTER_reg_o0), .FTCH(FSM_fetch), .PCO3(PROGRAM_COUNTER_pco3), .PCO2(PROGRAM_COUNTER_pco2),
    .PCO1(PROGRAM_COUNTER_pco1), .PCO0(PROGRAM_COUNTER_pco0));  // open: PC_OPR3, PC_OPR2, PC_OPR1, PC_OPR0, JMP_JZ
  and and_1 (and_1_out, FSM_fetch, not_1_out);
  REGISTER_4BIT NEXT_COUNTER (
    .HARD_RESET(in_1), .CLK(clock_1_out), .REG_I3(PROGRAM_COUNTER_pco3), .REG_I2(PROGRAM_COUNTER_pco2),
    .REG_I1(PROGRAM_COUNTER_pco1), .REG_I0(PROGRAM_COUNTER_pco0), .WE(and_1_out),
    .REG_O3(NEXT_COUNTER_reg_o3), .REG_O2(NEXT_COUNTER_reg_o2), .REG_O1(NEXT_COUNTER_reg_o1),
    .REG_O0(NEXT_COUNTER_reg_o0));
  and and_2 (and_2_out, FSM_fetch, not_1_out);
  REGISTER_4BIT CURRENT_COUNTER (
    .HARD_RESET(in_1), .CLK(clock_1_out), .REG_I3(NEXT_COUNTER_reg_o3), .REG_I2(NEXT_COUNTER_reg_o2),
    .REG_I1(NEXT_COUNTER_reg_o1), .REG_I0(NEXT_COUNTER_reg_o0), .WE(and_2_out),
    .REG_O3(CURRENT_COUNTER_reg_o3), .REG_O2(CURRENT_COUNTER_reg_o2), .REG_O1(CURRENT_COUNTER_reg_o1),
    .REG_O0(CURRENT_COUNTER_reg_o0));
  TEST_PROG_LDA ROM (
    .ROMI3(CURRENT_COUNTER_reg_o3), .ROMI2(CURRENT_COUNTER_reg_o2), .ROMI1(CURRENT_COUNTER_reg_o1),
    .ROMI0(CURRENT_COUNTER_reg_o0), .OPC3(ROM_opc3), .OPC2(ROM_opc2), .OPC1(ROM_opc1), .OPC0(ROM_opc0),
    .OPRAND3(ROM_oprand3), .OPRAND2(ROM_oprand2), .OPRAND1(ROM_oprand1), .OPRAND0(ROM_oprand0));
  CTRLUNIT_EXT CONTROL_UNIT (
    .CTRL_S3(ROM_opc3), .CTRL_S2(ROM_opc2), .CTRL_S1(ROM_opc1), .CTRL_S0(ROM_opc0), .CTRL_OPR3(ROM_oprand3),
    .CTRL_OPR2(ROM_oprand2), .CTRL_OPR1(ROM_oprand1), .CTRL_OPR0(ROM_oprand0), .FLAG_OVF(FLAG_REG_reg_o3),
    .FLAG_N(FLAG_REG_reg_o2), .FLAG_C(FLAG_REG_reg_o1), .FLAG_Z(FLAG_REG_reg_o0),
    .HLT_SIG(CONTROL_UNIT_hlt_sig), .LDI_SIG(CONTROL_UNIT_ldi_sig), .LDA_SIG(CONTROL_UNIT_lda_sig),
    .STA_SIG(CONTROL_UNIT_sta_sig), .ALU_SIG(CONTROL_UNIT_alu_sig));  // open: CTRL_OP3, CTRL_OP2, CTRL_OP1, CTRL_OP0, CTRL_WE, CTRL_B3, CTRL_B2, CTRL_B1, CTRL_B0, JMP_SIG
  not not_1 (not_1_out, CONTROL_UNIT_hlt_sig);
  assign controlled_buffer_1_out = CONTROL_UNIT_alu_sig ? ROM_oprand3 : 1'bz;  // Controlled_Buffer controlled_buffer_1
  assign controlled_buffer_2_out = CONTROL_UNIT_alu_sig ? ROM_oprand2 : 1'bz;  // Controlled_Buffer controlled_buffer_2
  assign controlled_buffer_3_out = CONTROL_UNIT_alu_sig ? ROM_oprand1 : 1'bz;  // Controlled_Buffer controlled_buffer_3
  assign controlled_buffer_4_out = CONTROL_UNIT_alu_sig ? ROM_oprand0 : 1'bz;  // Controlled_Buffer controlled_buffer_4
  ALU_EXT_v2 alu_ext_v2_1 (
    .A_3(ACCU_REG_reg_o3), .A_2(ACCU_REG_reg_o2), .A_1(ACCU_REG_reg_o1), .A_0(ACCU_REG_reg_o0),
    .B_3(controlled_buffer_1_out), .B_2(controlled_buffer_2_out), .B_1(controlled_buffer_3_out),
    .B_0(controlled_buffer_4_out), .S3(ROM_opc3), .S2(ROM_opc2), .S1(ROM_opc1), .S0(ROM_opc0),
    .OVF(alu_ext_v2_1_ovf), .N(alu_ext_v2_1_n), .C(alu_ext_v2_1_c), .Z(alu_ext_v2_1_z),
    .O_3(alu_ext_v2_1_o_3), .O_2(alu_ext_v2_1_o_2), .O_1(alu_ext_v2_1_o_1), .O_0(alu_ext_v2_1_o_0));
  MUX_2x1 mux_2x1_1 (.S0(CONTROL_UNIT_ldi_sig), .I0(alu_ext_v2_1_o_3), .I1(ROM_oprand3), .O(mux_2x1_1_o));
  MUX_2x1 mux_2x1_2 (.S0(CONTROL_UNIT_ldi_sig), .I0(alu_ext_v2_1_o_2), .I1(ROM_oprand2), .O(mux_2x1_2_o));
  MUX_2x1 mux_2x1_3 (.S0(CONTROL_UNIT_ldi_sig), .I0(alu_ext_v2_1_o_1), .I1(ROM_oprand1), .O(mux_2x1_3_o));
  MUX_2x1 mux_2x1_4 (.S0(CONTROL_UNIT_ldi_sig), .I0(alu_ext_v2_1_o_0), .I1(ROM_oprand0), .O(mux_2x1_4_o));
  REGISTER_4BIT FLAG_REG (
    .HARD_RESET(in_1), .CLK(clock_1_out), .REG_I3(alu_ext_v2_1_ovf), .REG_I2(alu_ext_v2_1_n),
    .REG_I1(alu_ext_v2_1_c), .REG_I0(alu_ext_v2_1_z), .WE(and_3_out), .REG_O3(FLAG_REG_reg_o3),
    .REG_O2(FLAG_REG_reg_o2), .REG_O1(FLAG_REG_reg_o1), .REG_O0(FLAG_REG_reg_o0));
  and and_3 (and_3_out, FSM_execute, not_1_out);
  REGISTER_4BIT ACCU_REG (
    .HARD_RESET(in_1), .CLK(clock_1_out), .REG_I3(mux_2x1_1_o), .REG_I2(mux_2x1_2_o), .REG_I1(mux_2x1_3_o),
    .REG_I0(mux_2x1_4_o), .WE(and_3_out), .REG_O3(ACCU_REG_reg_o3), .REG_O2(ACCU_REG_reg_o2),
    .REG_O1(ACCU_REG_reg_o1), .REG_O0(ACCU_REG_reg_o0));
  assign controlled_buffer_1_out = CONTROL_UNIT_sta_sig ? ACCU_REG_reg_o3 : 1'bz;  // Controlled_Buffer controlled_buffer_5
  assign controlled_buffer_2_out = CONTROL_UNIT_sta_sig ? ACCU_REG_reg_o2 : 1'bz;  // Controlled_Buffer controlled_buffer_6
  assign controlled_buffer_3_out = CONTROL_UNIT_sta_sig ? ACCU_REG_reg_o1 : 1'bz;  // Controlled_Buffer controlled_buffer_7
  assign controlled_buffer_4_out = CONTROL_UNIT_sta_sig ? ACCU_REG_reg_o0 : 1'bz;  // Controlled_Buffer controlled_buffer_8
  and and_4 (and_4_out, FSM_execute, not_1_out);
  REGISTER_4BIT MEM_REG (
    .HARD_RESET(in_1), .CLK(clock_1_out), .REG_I1(ROM_oprand1), .REG_I0(ROM_oprand0), .WE(and_4_out),
    .REG_O1(MEM_REG_reg_o1), .REG_O0(MEM_REG_reg_o0));  // open: REG_I3, REG_I2, REG_O3, REG_O2
  and and_5 (and_5_out, FSM_writeback, CONTROL_UNIT_sta_sig);
  SRAM sram_1 (
    .HARD_RESET(in_1), .CLK(clock_1_out), .I3(controlled_buffer_1_out), .I2(controlled_buffer_2_out),
    .I1(controlled_buffer_3_out), .I0(controlled_buffer_4_out), .WE(and_5_out), .ADDR1(MEM_REG_reg_o1),
    .ADDR0(MEM_REG_reg_o0), .SRAM_O3(sram_1_sram_o3), .SRAM_O2(sram_1_sram_o2), .SRAM_O1(sram_1_sram_o1),
    .SRAM_O0(sram_1_sram_o0));
  assign controlled_buffer_1_out = CONTROL_UNIT_lda_sig ? sram_1_sram_o3 : 1'bz;  // Controlled_Buffer controlled_buffer_9
  assign controlled_buffer_2_out = CONTROL_UNIT_lda_sig ? sram_1_sram_o2 : 1'bz;  // Controlled_Buffer controlled_buffer_10
  assign controlled_buffer_3_out = CONTROL_UNIT_lda_sig ? sram_1_sram_o1 : 1'bz;  // Controlled_Buffer controlled_buffer_11
  assign controlled_buffer_4_out = CONTROL_UNIT_lda_sig ? sram_1_sram_o0 : 1'bz;  // Controlled_Buffer controlled_buffer_12
  LED led_1 (.in(ROM_opc3));
  LED led_2 (.in(ROM_opc2));
  LED led_3 (.in(ROM_opc1));
  LED led_4 (.in(ROM_opc0));
  LED led_5 (.in(ROM_oprand3));
  LED led_6 (.in(ROM_oprand2));
  LED led_7 (.in(ROM_oprand1));
  LED led_8 (.in(ROM_oprand0));
endmodule

module BUS_SGINGAL (
  input  FETCH,
  input  DECODE,
  input  EXECUTE,
  input  WRITEBACK,
  input  LDI,
  input  LDA,
  input  STA,
  input  HLT
);
endmodule

module cpu_v8 (
  input  in_1
);

  wire ACC_REG_reg_o0, ACC_REG_reg_o1, ACC_REG_reg_o2, ACC_REG_reg_o3, alu_ext_v2_1_c, alu_ext_v2_1_n,
       alu_ext_v2_1_o_0, alu_ext_v2_1_o_1, alu_ext_v2_1_o_2, alu_ext_v2_1_o_3, alu_ext_v2_1_ovf,
       alu_ext_v2_1_z, and_1_out, and_2_out, clock_1_out, controlled_buffer_1_out, controlled_buffer_2_out,
       controlled_buffer_3_out, controlled_buffer_4_out, controlled_buffer_9_out, controlled_buffer_10_out,
       controlled_buffer_11_out, controlled_buffer_12_out, ctrlunit_ext_1_alu_sig, ctrlunit_ext_1_hlt_sig,
       ctrlunit_ext_1_jmp_sig, ctrlunit_ext_1_lda_sig, ctrlunit_ext_1_ldi_sig, ctrlunit_ext_1_sta_sig,
       FLAG_REG_reg_o0, FLAG_REG_reg_o1, FLAG_REG_reg_o2, FLAG_REG_reg_o3, fsm_2bit_1_decode,
       fsm_2bit_1_execute, fsm_2bit_1_fetch, fsm_2bit_1_writeback, MEM_REG_reg_o0, MEM_REG_reg_o1,
       MEM_REG_reg_o2, MEM_REG_reg_o3, not_1_out, or_1_out, or_2_out, progcounter_ext_1_pco0,
       progcounter_ext_1_pco1, progcounter_ext_1_pco2, progcounter_ext_1_pco3, register_4bit_1_reg_o0,
       register_4bit_1_reg_o1, register_4bit_1_reg_o2, register_4bit_1_reg_o3, register_4bit_2_reg_o0,
       register_4bit_2_reg_o1, register_4bit_2_reg_o2, register_4bit_2_reg_o3, register_4bit_3_reg_o0,
       register_4bit_3_reg_o1, register_4bit_3_reg_o2, register_4bit_3_reg_o3, register_4bit_4_reg_o0,
       register_4bit_4_reg_o1, register_4bit_4_reg_o2, register_4bit_4_reg_o3, sram_1_sram_o0,
       sram_1_sram_o1, sram_1_sram_o2, sram_1_sram_o3, test_prog_full_1_opc0, test_prog_full_1_opc1,
       test_prog_full_1_opc2, test_prog_full_1_opc3, test_prog_full_1_oprand0, test_prog_full_1_oprand1,
       test_prog_full_1_oprand2, test_prog_full_1_oprand3, undriven;

  Clock clock_1 (.out(clock_1_out));
  FSM_2BIT fsm_2bit_1 (
    .HARD_RESET(in_1), .CLK(clock_1_out), .HTL(ctrlunit_ext_1_hlt_sig), .FETCH(fsm_2bit_1_fetch),
    .DECODE(fsm_2bit_1_decode), .EXECUTE(fsm_2bit_1_execute), .WRITEBACK(fsm_2bit_1_writeback));
  and and_1 (and_1_out, fsm_2bit_1_fetch, fsm_2bit_1_fetch);
  ProgCounter_EXT progcounter_ext_1 (
    .A3(controlled_buffer_1_out), .A2(controlled_buffer_2_out), .A1(controlled_buffer_3_out),
    .A0(controlled_buffer_4_out), .PC_OPR3(undriven), .FTCH(and_1_out), .PCO3(progcounter_ext_1_pco3),
    .PCO2(progcounter_ext_1_pco2), .PCO1(progcounter_ext_1_pco1), .PCO0(progcounter_ext_1_pco0));  // open: PC_OPR2, PC_OPR1, PC_OPR0, JMP_JZ
  not not_1 (not_1_out, ctrlunit_ext_1_jmp_sig);
  REGISTER_4BIT register_4bit_1 (
    .HARD_RESET(in_1), .CLK(clock_1_out), .REG_I3(progcounter_ext_1_pco3), .REG_I2(progcounter_ext_1_pco2),
    .REG_I1(progcounter_ext_1_pco1), .REG_I0(progcounter_ext_1_pco0), .WE(fsm_2bit_1_fetch),
    .REG_O3(register_4bit_1_reg_o3), .REG_O2(register_4bit_1_reg_o2), .REG_O1(register_4bit_1_reg_o1),
    .REG_O0(register_4bit_1_reg_o0));
  assign controlled_buffer_1_out = not_1_out ? register_4bit_1_reg_o3 : 1'bz;  // Controlled_Buffer controlled_buffer_1
  assign controlled_buffer_2_out = not_1_out ? register_4bit_1_reg_o2 : 1'bz;  // Controlled_Buffer controlled_buffer_2
  assign controlled_buffer_3_out = not_1_out ? register_4bit_1_reg_o1 : 1'bz;  // Controlled_Buffer controlled_buffer_3
  assign controlled_buffer_4_out = not_1_out ? register_4bit_1_reg_o0 : 1'bz;  // Controlled_Buffer controlled_buffer_4
  assign controlled_buffer_4_out = ctrlunit_ext_1_jmp_sig ? register_4bit_4_reg_o0 : 1'bz;  // Controlled_Buffer controlled_buffer_5
  assign controlled_buffer_3_out = ctrlunit_ext_1_jmp_sig ? register_4bit_4_reg_o1 : 1'bz;  // Controlled_Buffer controlled_buffer_6
  assign controlled_buffer_2_out = ctrlunit_ext_1_jmp_sig ? register_4bit_4_reg_o2 : 1'bz;  // Controlled_Buffer controlled_buffer_7
  assign controlled_buffer_1_out = ctrlunit_ext_1_jmp_sig ? register_4bit_4_reg_o3 : 1'bz;  // Controlled_Buffer controlled_buffer_8
  REGISTER_4BIT register_4bit_2 (
    .HARD_RESET(in_1), .CLK(clock_1_out), .REG_I3(controlled_buffer_1_out), .REG_I2(controlled_buffer_2_out),
    .REG_I1(controlled_buffer_3_out), .REG_I0(controlled_buffer_4_out), .WE(fsm_2bit_1_fetch),
    .REG_O3(register_4bit_2_reg_o3), .REG_O2(register_4bit_2_reg_o2), .REG_O1(register_4bit_2_reg_o1),
    .REG_O0(register_4bit_2_reg_o0));
  LED led_1 (.in(register_4bit_2_reg_o3));
  LED led_2 (.in(register_4bit_2_reg_o2));
  LED led_3 (.in(register_4bit_2_reg_o1));
  LED led_4 (.in(register_4bit_2_reg_o0));
  LED led_5 (.in(register_4bit_3_reg_o0));
  LED led_6 (.in(register_4bit_3_reg_o1));
  LED led_7 (.in(register_4bit_3_reg_o2));
  LED led_8 (.in(register_4bit_3_reg_o3));
  REGISTER_4BIT register_4bit_3 (
    .HARD_RESET(in_1), .CLK(clock_1_out), .REG_I3(test_prog_full_1_opc3), .REG_I2(test_prog_full_1_opc2),
    .REG_I1(test_prog_full_1_opc1), .REG_I0(test_prog_full_1_opc0), .WE(fsm_2bit_1_decode),
    .REG_O3(register_4bit_3_reg_o3), .REG_O2(register_4bit_3_reg_o2), .REG_O1(register_4bit_3_reg_o1),
    .REG_O0(register_4bit_3_reg_o0));
  TEST_PROG_FULL test_prog_full_1 (
    .ROMI3(register_4bit_2_reg_o3), .ROMI2(register_4bit_2_reg_o2), .ROMI1(register_4bit_2_reg_o1),
    .ROMI0(register_4bit_2_reg_o0), .OPC3(test_prog_full_1_opc3), .OPC2(test_prog_full_1_opc2),
    .OPC1(test_prog_full_1_opc1), .OPC0(test_prog_full_1_opc0), .OPRAND3(test_prog_full_1_oprand3),
    .OPRAND2(test_prog_full_1_oprand2), .OPRAND1(test_prog_full_1_oprand1), .OPRAND0(test_prog_full_1_oprand0));
  LED led_9 (.in(register_4bit_4_reg_o0));
  LED led_10 (.in(register_4bit_4_reg_o1));
  LED led_11 (.in(register_4bit_4_reg_o2));
  LED led_12 (.in(register_4bit_4_reg_o3));
  REGISTER_4BIT register_4bit_4 (
    .HARD_RESET(in_1), .CLK(clock_1_out), .REG_I3(test_prog_full_1_oprand3),
    .REG_I2(test_prog_full_1_oprand2), .REG_I1(test_prog_full_1_oprand1), .REG_I0(test_prog_full_1_oprand0),
    .WE(fsm_2bit_1_decode), .REG_O3(register_4bit_4_reg_o3), .REG_O2(register_4bit_4_reg_o2),
    .REG_O1(register_4bit_4_reg_o1), .REG_O0(register_4bit_4_reg_o0));
  assign controlled_buffer_9_out = ctrlunit_ext_1_ldi_sig ? register_4bit_4_reg_o0 : 1'bz;  // Controlled_Buffer controlled_buffer_9
  assign controlled_buffer_10_out = ctrlunit_ext_1_ldi_sig ? register_4bit_4_reg_o1 : 1'bz;  // Controlled_Buffer controlled_buffer_10
  assign controlled_buffer_11_out = ctrlunit_ext_1_ldi_sig ? register_4bit_4_reg_o2 : 1'bz;  // Controlled_Buffer controlled_buffer_11
  assign controlled_buffer_12_out = ctrlunit_ext_1_ldi_sig ? register_4bit_4_reg_o3 : 1'bz;  // Controlled_Buffer controlled_buffer_12
  CTRLUNIT_EXT ctrlunit_ext_1 (
    .CTRL_S3(register_4bit_3_reg_o3), .CTRL_S2(register_4bit_3_reg_o2), .CTRL_S1(register_4bit_3_reg_o1),
    .CTRL_S0(register_4bit_3_reg_o0), .CTRL_OPR3(register_4bit_4_reg_o3), .CTRL_OPR2(register_4bit_4_reg_o2),
    .CTRL_OPR1(register_4bit_4_reg_o1), .CTRL_OPR0(register_4bit_4_reg_o0), .FLAG_OVF(FLAG_REG_reg_o3),
    .FLAG_N(FLAG_REG_reg_o2), .FLAG_C(FLAG_REG_reg_o1), .FLAG_Z(FLAG_REG_reg_o0),
    .JMP_SIG(ctrlunit_ext_1_jmp_sig), .HLT_SIG(ctrlunit_ext_1_hlt_sig), .LDI_SIG(ctrlunit_ext_1_ldi_sig),
    .LDA_SIG(ctrlunit_ext_1_lda_sig), .STA_SIG(ctrlunit_ext_1_sta_sig), .ALU_SIG(ctrlunit_ext_1_alu_sig));  // open: CTRL_OP3, CTRL_OP2, CTRL_OP1, CTRL_OP0, CTRL_WE, CTRL_B3, CTRL_B2, CTRL_B1, CTRL_B0
  LED led_13 (.in(ctrlunit_ext_1_jmp_sig));
  LED led_14 (.in(ctrlunit_ext_1_hlt_sig));
  LED led_15 (.in(ctrlunit_ext_1_ldi_sig));
  LED led_16 (.in(ctrlunit_ext_1_lda_sig));
  LED led_17 (.in(ctrlunit_ext_1_sta_sig));
  LED led_18 (.in(ctrlunit_ext_1_alu_sig));
  LED led_19 (.in(FLAG_REG_reg_o2));
  LED led_20 (.in(FLAG_REG_reg_o3));
  REGISTER_4BIT FLAG_REG (
    .HARD_RESET(in_1), .CLK(clock_1_out), .REG_I3(alu_ext_v2_1_ovf), .REG_I2(alu_ext_v2_1_n),
    .REG_I1(alu_ext_v2_1_c), .REG_I0(alu_ext_v2_1_z), .WE(fsm_2bit_1_execute), .REG_O3(FLAG_REG_reg_o3),
    .REG_O2(FLAG_REG_reg_o2), .REG_O1(FLAG_REG_reg_o1), .REG_O0(FLAG_REG_reg_o0));
  ALU_EXT_v2 alu_ext_v2_1 (
    .A_3(ACC_REG_reg_o3), .A_2(ACC_REG_reg_o2), .A_1(ACC_REG_reg_o1), .A_0(ACC_REG_reg_o0),
    .B_3(register_4bit_4_reg_o3), .B_2(register_4bit_4_reg_o2), .B_1(register_4bit_4_reg_o1),
    .B_0(register_4bit_4_reg_o0), .S3(register_4bit_3_reg_o3), .S2(register_4bit_3_reg_o2),
    .S1(register_4bit_3_reg_o1), .S0(register_4bit_3_reg_o0), .OVF(alu_ext_v2_1_ovf), .N(alu_ext_v2_1_n),
    .C(alu_ext_v2_1_c), .Z(alu_ext_v2_1_z), .O_3(alu_ext_v2_1_o_3), .O_2(alu_ext_v2_1_o_2),
    .O_1(alu_ext_v2_1_o_1), .O_0(alu_ext_v2_1_o_0));
  LED led_21 (.in(MEM_REG_reg_o3));
  REGISTER_4BIT MEM_REG (
    .HARD_RESET(in_1), .CLK(clock_1_out), .REG_I3(register_4bit_4_reg_o3), .REG_I2(register_4bit_4_reg_o2),
    .REG_I1(register_4bit_4_reg_o1), .REG_I0(register_4bit_4_reg_o0), .WE(fsm_2bit_1_execute),
    .REG_O3(MEM_REG_reg_o3), .REG_O2(MEM_REG_reg_o2), .REG_O1(MEM_REG_reg_o1), .REG_O0(MEM_REG_reg_o0));
  LED led_22 (.in(FLAG_REG_reg_o0));
  LED led_23 (.in(FLAG_REG_reg_o1));
  LED led_24 (.in(MEM_REG_reg_o0));
  LED led_25 (.in(MEM_REG_reg_o1));
  LED led_26 (.in(MEM_REG_reg_o2));
  LED led_27 (.in(ACC_REG_reg_o1));
  LED led_28 (.in(ACC_REG_reg_o2));
  LED led_29 (.in(ACC_REG_reg_o3));
  REGISTER_4BIT ACC_REG (
    .HARD_RESET(in_1), .CLK(clock_1_out), .REG_I3(controlled_buffer_12_out),
    .REG_I2(controlled_buffer_11_out), .REG_I1(controlled_buffer_10_out), .REG_I0(controlled_buffer_9_out),
    .WE(or_1_out), .REG_O3(ACC_REG_reg_o3), .REG_O2(ACC_REG_reg_o2), .REG_O1(ACC_REG_reg_o1),
    .REG_O0(ACC_REG_reg_o0));
  assign controlled_buffer_12_out = ctrlunit_ext_1_alu_sig ? alu_ext_v2_1_o_3 : 1'bz;  // Controlled_Buffer controlled_buffer_13
  assign controlled_buffer_11_out = ctrlunit_ext_1_alu_sig ? alu_ext_v2_1_o_2 : 1'bz;  // Controlled_Buffer controlled_buffer_14
  assign controlled_buffer_10_out = ctrlunit_ext_1_alu_sig ? alu_ext_v2_1_o_1 : 1'bz;  // Controlled_Buffer controlled_buffer_15
  assign controlled_buffer_9_out = ctrlunit_ext_1_alu_sig ? alu_ext_v2_1_o_0 : 1'bz;  // Controlled_Buffer controlled_buffer_16
  LED led_30 (.in(ACC_REG_reg_o0));
  or or_1 (or_1_out, fsm_2bit_1_execute, ctrlunit_ext_1_lda_sig);
  assign controlled_buffer_9_out = ctrlunit_ext_1_lda_sig ? sram_1_sram_o0 : 1'bz;  // Controlled_Buffer controlled_buffer_17
  assign controlled_buffer_10_out = ctrlunit_ext_1_lda_sig ? sram_1_sram_o1 : 1'bz;  // Controlled_Buffer controlled_buffer_18
  assign controlled_buffer_11_out = ctrlunit_ext_1_lda_sig ? sram_1_sram_o2 : 1'bz;  // Controlled_Buffer controlled_buffer_19
  assign controlled_buffer_12_out = ctrlunit_ext_1_lda_sig ? sram_1_sram_o3 : 1'bz;  // Controlled_Buffer controlled_buffer_20
  assign controlled_buffer_9_out = or_2_out ? ACC_REG_reg_o0 : 1'bz;  // Controlled_Buffer controlled_buffer_21
  assign controlled_buffer_10_out = or_2_out ? ACC_REG_reg_o1 : 1'bz;  // Controlled_Buffer controlled_buffer_22
  assign controlled_buffer_11_out = or_2_out ? ACC_REG_reg_o2 : 1'bz;  // Controlled_Buffer controlled_buffer_23
  assign controlled_buffer_12_out = or_2_out ? ACC_REG_reg_o3 : 1'bz;  // Controlled_Buffer controlled_buffer_24
  or or_2 (or_2_out, ctrlunit_ext_1_sta_sig, ctrlunit_ext_1_jmp_sig);
  and and_2 (and_2_out, ctrlunit_ext_1_sta_sig, fsm_2bit_1_writeback);
  SRAM sram_1 (
    .HARD_RESET(in_1), .CLK(clock_1_out), .I3(ACC_REG_reg_o3), .I2(ACC_REG_reg_o2), .I1(ACC_REG_reg_o1),
    .I0(ACC_REG_reg_o0), .WE(and_2_out), .ADDR1(MEM_REG_reg_o1), .ADDR0(MEM_REG_reg_o0),
    .SRAM_O3(sram_1_sram_o3), .SRAM_O2(sram_1_sram_o2), .SRAM_O1(sram_1_sram_o1), .SRAM_O0(sram_1_sram_o0));
  LED led_31 (.in(sram_1_sram_o0));
  LED led_32 (.in(sram_1_sram_o1));
  LED led_33 (.in(sram_1_sram_o2));
  LED led_34 (.in(sram_1_sram_o3));
endmodule

module cput_template (
  input  in_1
);

  wire ACC_REG_reg_o0, ACC_REG_reg_o1, ACC_REG_reg_o2, ACC_REG_reg_o3, alu_ext_v2_1_c, alu_ext_v2_1_n,
       alu_ext_v2_1_o_0, alu_ext_v2_1_o_1, alu_ext_v2_1_o_2, alu_ext_v2_1_o_3, alu_ext_v2_1_ovf,
       alu_ext_v2_1_z, and_1_out, clock_1_out, ctrlunit_ext_1_alu_sig, ctrlunit_ext_1_hlt_sig,
       ctrlunit_ext_1_jmp_sig, ctrlunit_ext_1_lda_sig, ctrlunit_ext_1_ldi_sig, ctrlunit_ext_1_sta_sig,
       FLAG_REG_reg_o0, FLAG_REG_reg_o1, FLAG_REG_reg_o2, FLAG_REG_reg_o3, fsm_2bit_1_decode,
       fsm_2bit_1_execute, fsm_2bit_1_fetch, fsm_2bit_1_writeback, progcounter_ext_1_pco0,
       progcounter_ext_1_pco1, progcounter_ext_1_pco2, progcounter_ext_1_pco3, register_4bit_1_reg_o0,
       register_4bit_1_reg_o1, register_4bit_1_reg_o2, register_4bit_1_reg_o3, register_4bit_2_reg_o0,
       register_4bit_2_reg_o1, register_4bit_2_reg_o2, register_4bit_2_reg_o3, register_4bit_3_reg_o0,
       register_4bit_3_reg_o1, register_4bit_3_reg_o2, register_4bit_3_reg_o3, register_4bit_4_reg_o0,
       register_4bit_4_reg_o1, register_4bit_4_reg_o2, register_4bit_4_reg_o3, test_prog_lda_1_opc0,
       test_prog_lda_1_opc1, test_prog_lda_1_opc2, test_prog_lda_1_opc3, test_prog_lda_1_oprand0,
       test_prog_lda_1_oprand1, test_prog_lda_1_oprand2, test_prog_lda_1_oprand3, undriven, undriven_2;

  Clock clock_1 (.out(clock_1_out));
  FSM_2BIT fsm_2bit_1 (
    .HARD_RESET(in_1), .CLK(clock_1_out), .HTL(ctrlunit_ext_1_hlt_sig), .FETCH(fsm_2bit_1_fetch),
    .DECODE(fsm_2bit_1_decode), .EXECUTE(fsm_2bit_1_execute), .WRITEBACK(fsm_2bit_1_writeback));
  and and_1 (and_1_out, fsm_2bit_1_fetch, fsm_2bit_1_fetch);
  ProgCounter_EXT progcounter_ext_1 (
    .A3(register_4bit_1_reg_o3), .A2(register_4bit_1_reg_o2), .A1(register_4bit_1_reg_o1),
    .A0(register_4bit_1_reg_o0), .FTCH(and_1_out), .PCO3(progcounter_ext_1_pco3),
    .PCO2(progcounter_ext_1_pco2), .PCO1(progcounter_ext_1_pco1), .PCO0(progcounter_ext_1_pco0));  // open: PC_OPR3, PC_OPR2, PC_OPR1, PC_OPR0, JMP_JZ
  REGISTER_4BIT register_4bit_1 (
    .HARD_RESET(in_1), .CLK(clock_1_out), .REG_I3(progcounter_ext_1_pco3), .REG_I2(progcounter_ext_1_pco2),
    .REG_I1(progcounter_ext_1_pco1), .REG_I0(progcounter_ext_1_pco0), .WE(fsm_2bit_1_fetch),
    .REG_O3(register_4bit_1_reg_o3), .REG_O2(register_4bit_1_reg_o2), .REG_O1(register_4bit_1_reg_o1),
    .REG_O0(register_4bit_1_reg_o0));
  REGISTER_4BIT register_4bit_2 (
    .HARD_RESET(in_1), .CLK(clock_1_out), .REG_I3(register_4bit_1_reg_o3), .REG_I2(register_4bit_1_reg_o2),
    .REG_I1(register_4bit_1_reg_o1), .REG_I0(register_4bit_1_reg_o0), .WE(fsm_2bit_1_fetch),
    .REG_O3(register_4bit_2_reg_o3), .REG_O2(register_4bit_2_reg_o2), .REG_O1(register_4bit_2_reg_o1),
    .REG_O0(register_4bit_2_reg_o0));
  LED led_1 (.in(register_4bit_2_reg_o3));
  LED led_2 (.in(register_4bit_2_reg_o2));
  LED led_3 (.in(register_4bit_2_reg_o1));
  LED led_4 (.in(register_4bit_2_reg_o0));
  LED led_5 (.in(register_4bit_3_reg_o0));
  LED led_6 (.in(register_4bit_3_reg_o1));
  LED led_7 (.in(register_4bit_3_reg_o2));
  LED led_8 (.in(register_4bit_3_reg_o3));
  REGISTER_4BIT register_4bit_3 (
    .HARD_RESET(in_1), .CLK(clock_1_out), .REG_I3(test_prog_lda_1_opc3), .REG_I2(test_prog_lda_1_opc2),
    .REG_I1(test_prog_lda_1_opc1), .REG_I0(test_prog_lda_1_opc0), .WE(fsm_2bit_1_decode),
    .REG_O3(register_4bit_3_reg_o3), .REG_O2(register_4bit_3_reg_o2), .REG_O1(register_4bit_3_reg_o1),
    .REG_O0(register_4bit_3_reg_o0));
  TEST_PROG_LDA test_prog_lda_1 (
    .ROMI3(register_4bit_2_reg_o3), .ROMI2(register_4bit_2_reg_o2), .ROMI1(register_4bit_2_reg_o1),
    .ROMI0(register_4bit_2_reg_o0), .OPC3(test_prog_lda_1_opc3), .OPC2(test_prog_lda_1_opc2),
    .OPC1(test_prog_lda_1_opc1), .OPC0(test_prog_lda_1_opc0), .OPRAND3(test_prog_lda_1_oprand3),
    .OPRAND2(test_prog_lda_1_oprand2), .OPRAND1(test_prog_lda_1_oprand1), .OPRAND0(test_prog_lda_1_oprand0));
  LED led_9 (.in(register_4bit_4_reg_o0));
  LED led_10 (.in(register_4bit_4_reg_o1));
  LED led_11 (.in(register_4bit_4_reg_o2));
  LED led_12 (.in(register_4bit_4_reg_o3));
  REGISTER_4BIT register_4bit_4 (
    .HARD_RESET(in_1), .CLK(clock_1_out), .REG_I3(test_prog_lda_1_oprand3), .REG_I2(test_prog_lda_1_oprand2),
    .REG_I1(test_prog_lda_1_oprand1), .REG_I0(test_prog_lda_1_oprand0), .WE(fsm_2bit_1_decode),
    .REG_O3(register_4bit_4_reg_o3), .REG_O2(register_4bit_4_reg_o2), .REG_O1(register_4bit_4_reg_o1),
    .REG_O0(register_4bit_4_reg_o0));
  CTRLUNIT_EXT ctrlunit_ext_1 (
    .CTRL_S3(register_4bit_3_reg_o3), .CTRL_S2(register_4bit_3_reg_o2), .CTRL_S1(register_4bit_3_reg_o1),
    .CTRL_S0(register_4bit_3_reg_o0), .CTRL_OPR3(register_4bit_4_reg_o3), .CTRL_OPR2(register_4bit_4_reg_o2),
    .CTRL_OPR1(register_4bit_4_reg_o1), .CTRL_OPR0(register_4bit_4_reg_o0), .JMP_SIG(ctrlunit_ext_1_jmp_sig),
    .HLT_SIG(ctrlunit_ext_1_hlt_sig), .LDI_SIG(ctrlunit_ext_1_ldi_sig), .LDA_SIG(ctrlunit_ext_1_lda_sig),
    .STA_SIG(ctrlunit_ext_1_sta_sig), .ALU_SIG(ctrlunit_ext_1_alu_sig));  // open: FLAG_OVF, FLAG_N, FLAG_C, FLAG_Z, CTRL_OP3, CTRL_OP2, CTRL_OP1, CTRL_OP0, CTRL_WE, CTRL_B3, CTRL_B2, CTRL_B1, CTRL_B0
  LED led_13 (.in(ctrlunit_ext_1_jmp_sig));
  LED led_14 (.in(ctrlunit_ext_1_hlt_sig));
  LED led_15 (.in(ctrlunit_ext_1_ldi_sig));
  LED led_16 (.in(ctrlunit_ext_1_lda_sig));
  LED led_17 (.in(ctrlunit_ext_1_sta_sig));
  LED led_18 (.in(ctrlunit_ext_1_alu_sig));
  LED led_19 (.in(FLAG_REG_reg_o3));
  REGISTER_4BIT FLAG_REG (
    .HARD_RESET(undriven), .CLK(undriven_2), .REG_I3(alu_ext_v2_1_ovf), .REG_I2(alu_ext_v2_1_n),
    .REG_I1(alu_ext_v2_1_c), .REG_I0(alu_ext_v2_1_z), .REG_O3(FLAG_REG_reg_o3), .REG_O2(FLAG_REG_reg_o2),
    .REG_O1(FLAG_REG_reg_o1), .REG_O0(FLAG_REG_reg_o0));  // open: WE
  ALU_EXT_v2 alu_ext_v2_1 (
    .OVF(alu_ext_v2_1_ovf), .N(alu_ext_v2_1_n), .C(alu_ext_v2_1_c), .Z(alu_ext_v2_1_z),
    .O_3(alu_ext_v2_1_o_3), .O_2(alu_ext_v2_1_o_2), .O_1(alu_ext_v2_1_o_1), .O_0(alu_ext_v2_1_o_0));  // open: A_3, A_2, A_1, A_0, B_3, B_2, B_1, B_0, S3, S2, S1, S0
  LED led_20 (.in(FLAG_REG_reg_o0));
  LED led_21 (.in(FLAG_REG_reg_o1));
  LED led_22 (.in(FLAG_REG_reg_o2));
  LED led_23 (.in(ACC_REG_reg_o2));
  LED led_24 (.in(ACC_REG_reg_o3));
  REGISTER_4BIT ACC_REG (
    .HARD_RESET(undriven), .CLK(undriven_2), .REG_I3(alu_ext_v2_1_o_3), .REG_I2(alu_ext_v2_1_o_2),
    .REG_I1(alu_ext_v2_1_o_1), .REG_I0(alu_ext_v2_1_o_0), .REG_O3(ACC_REG_reg_o3), .REG_O2(ACC_REG_reg_o2),
    .REG_O1(ACC_REG_reg_o1), .REG_O0(ACC_REG_reg_o0));  // open: WE
  LED led_25 (.in(ACC_REG_reg_o0));
  LED led_26 (.in(ACC_REG_reg_o1));
endmodule

module cpu_v9 (
  input  RESET,
  input  CLK,
  input  OPC3,
  input  OPC2,
  input  OPC1,
  input  OPC0,
  input  OPRAND3,
  input  OPRAND2,
  input  OPRAND1,
  input  OPRAND0,
  output ISA_OPC_3,
  output ISA_OPC_2,
  output ISA_OPC_1,
  output ISA_OPC_0,
  output ISA_OPR_3,
  output ISA_OPR_2,
  output ISA_OPR_1,
  output ISA_OPR_0,
  output OVF,
  output N,
  output C,
  output Z,
  output ACC_O3,
  output ACC_O2,
  output ACC_O1,
  output ACC_O0,
  output FETCH,
  output DECODE,
  output EXECUTE,
  output WRITEBACK,
  output ROMI3,
  output ROMI2,
  output ROMI1,
  output ROMI0
);

  wire alu_ext_v2_1_c, alu_ext_v2_1_n, alu_ext_v2_1_o_0, alu_ext_v2_1_o_1, alu_ext_v2_1_o_2,
       alu_ext_v2_1_o_3, alu_ext_v2_1_ovf, alu_ext_v2_1_z, and_1_out, and_2_out, controlled_buffer_1_out,
       controlled_buffer_2_out, controlled_buffer_3_out, controlled_buffer_4_out, controlled_buffer_9_out,
       controlled_buffer_10_out, controlled_buffer_11_out, controlled_buffer_12_out, ctrlunit_ext_1_alu_sig,
       ctrlunit_ext_1_hlt_sig, ctrlunit_ext_1_jmp_sig, ctrlunit_ext_1_lda_sig, ctrlunit_ext_1_ldi_sig,
       ctrlunit_ext_1_sta_sig, MEM_REG_reg_o0, MEM_REG_reg_o1, MEM_REG_reg_o2, MEM_REG_reg_o3, not_1_out,
       or_1_out, or_2_out, progcounter_ext_1_pco0, progcounter_ext_1_pco1, progcounter_ext_1_pco2,
       progcounter_ext_1_pco3, register_4bit_1_reg_o0, register_4bit_1_reg_o1, register_4bit_1_reg_o2,
       register_4bit_1_reg_o3, sram_1_sram_o0, sram_1_sram_o1, sram_1_sram_o2, sram_1_sram_o3;

  FSM_2BIT fsm_2bit_1 (
    .HARD_RESET(RESET), .CLK(CLK), .HTL(ctrlunit_ext_1_hlt_sig), .FETCH(FETCH), .DECODE(DECODE),
    .EXECUTE(EXECUTE), .WRITEBACK(WRITEBACK));
  and and_1 (and_1_out, FETCH, FETCH);
  ProgCounter_EXT progcounter_ext_1 (
    .A3(controlled_buffer_1_out), .A2(controlled_buffer_2_out), .A1(controlled_buffer_3_out),
    .A0(controlled_buffer_4_out), .FTCH(and_1_out), .PCO3(progcounter_ext_1_pco3),
    .PCO2(progcounter_ext_1_pco2), .PCO1(progcounter_ext_1_pco1), .PCO0(progcounter_ext_1_pco0));  // open: PC_OPR3, PC_OPR2, PC_OPR1, PC_OPR0, JMP_JZ
  REGISTER_4BIT register_4bit_1 (
    .HARD_RESET(RESET), .CLK(CLK), .REG_I3(progcounter_ext_1_pco3), .REG_I2(progcounter_ext_1_pco2),
    .REG_I1(progcounter_ext_1_pco1), .REG_I0(progcounter_ext_1_pco0), .WE(FETCH),
    .REG_O3(register_4bit_1_reg_o3), .REG_O2(register_4bit_1_reg_o2), .REG_O1(register_4bit_1_reg_o1),
    .REG_O0(register_4bit_1_reg_o0));
  not not_1 (not_1_out, ctrlunit_ext_1_jmp_sig);
  assign controlled_buffer_1_out = not_1_out ? register_4bit_1_reg_o3 : 1'bz;  // Controlled_Buffer controlled_buffer_1
  assign controlled_buffer_2_out = not_1_out ? register_4bit_1_reg_o2 : 1'bz;  // Controlled_Buffer controlled_buffer_2
  assign controlled_buffer_3_out = not_1_out ? register_4bit_1_reg_o1 : 1'bz;  // Controlled_Buffer controlled_buffer_3
  assign controlled_buffer_4_out = not_1_out ? register_4bit_1_reg_o0 : 1'bz;  // Controlled_Buffer controlled_buffer_4
  assign controlled_buffer_4_out = ctrlunit_ext_1_jmp_sig ? ISA_OPR_0 : 1'bz;  // Controlled_Buffer controlled_buffer_5
  assign controlled_buffer_3_out = ctrlunit_ext_1_jmp_sig ? ISA_OPR_1 : 1'bz;  // Controlled_Buffer controlled_buffer_6
  assign controlled_buffer_2_out = ctrlunit_ext_1_jmp_sig ? ISA_OPR_2 : 1'bz;  // Controlled_Buffer controlled_buffer_7
  assign controlled_buffer_1_out = ctrlunit_ext_1_jmp_sig ? ISA_OPR_3 : 1'bz;  // Controlled_Buffer controlled_buffer_8
  REGISTER_4BIT register_4bit_2 (
    .HARD_RESET(RESET), .CLK(CLK), .REG_I3(controlled_buffer_1_out), .REG_I2(controlled_buffer_2_out),
    .REG_I1(controlled_buffer_3_out), .REG_I0(controlled_buffer_4_out), .WE(FETCH), .REG_O3(ROMI3),
    .REG_O2(ROMI2), .REG_O1(ROMI1), .REG_O0(ROMI0));
  LED led_1 (.in(ROMI3));
  LED led_2 (.in(ROMI2));
  LED led_3 (.in(ROMI1));
  LED led_4 (.in(ROMI0));
  REGISTER_4BIT register_4bit_3 (
    .HARD_RESET(RESET), .CLK(CLK), .REG_I3(OPC3), .REG_I2(OPC2), .REG_I1(OPC1), .REG_I0(OPC0), .WE(DECODE),
    .REG_O3(ISA_OPC_3), .REG_O2(ISA_OPC_2), .REG_O1(ISA_OPC_1), .REG_O0(ISA_OPC_0));
  REGISTER_4BIT register_4bit_4 (
    .HARD_RESET(RESET), .CLK(CLK), .REG_I3(OPRAND3), .REG_I2(OPRAND2), .REG_I1(OPRAND1), .REG_I0(OPRAND0),
    .WE(DECODE), .REG_O3(ISA_OPR_3), .REG_O2(ISA_OPR_2), .REG_O1(ISA_OPR_1), .REG_O0(ISA_OPR_0));
  assign controlled_buffer_9_out = ctrlunit_ext_1_ldi_sig ? ISA_OPR_0 : 1'bz;  // Controlled_Buffer controlled_buffer_9
  assign controlled_buffer_10_out = ctrlunit_ext_1_ldi_sig ? ISA_OPR_1 : 1'bz;  // Controlled_Buffer controlled_buffer_10
  assign controlled_buffer_11_out = ctrlunit_ext_1_ldi_sig ? ISA_OPR_2 : 1'bz;  // Controlled_Buffer controlled_buffer_11
  assign controlled_buffer_12_out = ctrlunit_ext_1_ldi_sig ? ISA_OPR_3 : 1'bz;  // Controlled_Buffer controlled_buffer_12
  CTRLUNIT_EXT ctrlunit_ext_1 (
    .CTRL_S3(ISA_OPC_3), .CTRL_S2(ISA_OPC_2), .CTRL_S1(ISA_OPC_1), .CTRL_S0(ISA_OPC_0),
    .CTRL_OPR3(ISA_OPR_3), .CTRL_OPR2(ISA_OPR_2), .CTRL_OPR1(ISA_OPR_1), .CTRL_OPR0(ISA_OPR_0),
    .FLAG_OVF(OVF), .FLAG_N(N), .FLAG_C(C), .FLAG_Z(Z), .JMP_SIG(ctrlunit_ext_1_jmp_sig),
    .HLT_SIG(ctrlunit_ext_1_hlt_sig), .LDI_SIG(ctrlunit_ext_1_ldi_sig), .LDA_SIG(ctrlunit_ext_1_lda_sig),
    .STA_SIG(ctrlunit_ext_1_sta_sig), .ALU_SIG(ctrlunit_ext_1_alu_sig));  // open: CTRL_OP3, CTRL_OP2, CTRL_OP1, CTRL_OP0, CTRL_WE, CTRL_B3, CTRL_B2, CTRL_B1, CTRL_B0
  LED led_5 (.in(ctrlunit_ext_1_jmp_sig));
  LED led_6 (.in(ctrlunit_ext_1_hlt_sig));
  LED led_7 (.in(ctrlunit_ext_1_ldi_sig));
  LED led_8 (.in(ctrlunit_ext_1_lda_sig));
  LED led_9 (.in(ctrlunit_ext_1_sta_sig));
  LED led_10 (.in(ctrlunit_ext_1_alu_sig));
  REGISTER_4BIT FLAG_REG (
    .HARD_RESET(RESET), .CLK(CLK), .REG_I3(alu_ext_v2_1_ovf), .REG_I2(alu_ext_v2_1_n),
    .REG_I1(alu_ext_v2_1_c), .REG_I0(alu_ext_v2_1_z), .WE(EXECUTE), .REG_O3(OVF), .REG_O2(N), .REG_O1(C),
    .REG_O0(Z));
  ALU_EXT_v2 alu_ext_v2_1 (
    .A_3(ACC_O3), .A_2(ACC_O2), .A_1(ACC_O1), .A_0(ACC_O0), .B_3(ISA_OPR_3), .B_2(ISA_OPR_2),
    .B_1(ISA_OPR_1), .B_0(ISA_OPR_0), .S3(ISA_OPC_3), .S2(ISA_OPC_2), .S1(ISA_OPC_1), .S0(ISA_OPC_0),
    .OVF(alu_ext_v2_1_ovf), .N(alu_ext_v2_1_n), .C(alu_ext_v2_1_c), .Z(alu_ext_v2_1_z),
    .O_3(alu_ext_v2_1_o_3), .O_2(alu_ext_v2_1_o_2), .O_1(alu_ext_v2_1_o_1), .O_0(alu_ext_v2_1_o_0));
  LED led_11 (.in(MEM_REG_reg_o3));
  REGISTER_4BIT MEM_REG (
    .HARD_RESET(RESET), .CLK(CLK), .REG_I3(ISA_OPR_3), .REG_I2(ISA_OPR_2), .REG_I1(ISA_OPR_1),
    .REG_I0(ISA_OPR_0), .WE(EXECUTE), .REG_O3(MEM_REG_reg_o3), .REG_O2(MEM_REG_reg_o2),
    .REG_O1(MEM_REG_reg_o1), .REG_O0(MEM_REG_reg_o0));
  LED led_12 (.in(MEM_REG_reg_o0));
  LED led_13 (.in(MEM_REG_reg_o1));
  LED led_14 (.in(MEM_REG_reg_o2));
  REGISTER_4BIT ACC_REG (
    .HARD_RESET(RESET), .CLK(CLK), .REG_I3(controlled_buffer_12_out), .REG_I2(controlled_buffer_11_out),
    .REG_I1(controlled_buffer_10_out), .REG_I0(controlled_buffer_9_out), .WE(or_1_out), .REG_O3(ACC_O3),
    .REG_O2(ACC_O2), .REG_O1(ACC_O1), .REG_O0(ACC_O0));
  assign controlled_buffer_12_out = ctrlunit_ext_1_alu_sig ? alu_ext_v2_1_o_3 : 1'bz;  // Controlled_Buffer controlled_buffer_13
  assign controlled_buffer_11_out = ctrlunit_ext_1_alu_sig ? alu_ext_v2_1_o_2 : 1'bz;  // Controlled_Buffer controlled_buffer_14
  assign controlled_buffer_10_out = ctrlunit_ext_1_alu_sig ? alu_ext_v2_1_o_1 : 1'bz;  // Controlled_Buffer controlled_buffer_15
  assign controlled_buffer_9_out = ctrlunit_ext_1_alu_sig ? alu_ext_v2_1_o_0 : 1'bz;  // Controlled_Buffer controlled_buffer_16
  or or_1 (or_1_out, EXECUTE, ctrlunit_ext_1_lda_sig);
  assign controlled_buffer_9_out = ctrlunit_ext_1_lda_sig ? sram_1_sram_o0 : 1'bz;  // Controlled_Buffer controlled_buffer_17
  assign controlled_buffer_10_out = ctrlunit_ext_1_lda_sig ? sram_1_sram_o1 : 1'bz;  // Controlled_Buffer controlled_buffer_18
  assign controlled_buffer_11_out = ctrlunit_ext_1_lda_sig ? sram_1_sram_o2 : 1'bz;  // Controlled_Buffer controlled_buffer_19
  assign controlled_buffer_12_out = ctrlunit_ext_1_lda_sig ? sram_1_sram_o3 : 1'bz;  // Controlled_Buffer controlled_buffer_20
  assign controlled_buffer_9_out = or_2_out ? ACC_O0 : 1'bz;  // Controlled_Buffer controlled_buffer_21
  assign controlled_buffer_10_out = or_2_out ? ACC_O1 : 1'bz;  // Controlled_Buffer controlled_buffer_22
  assign controlled_buffer_11_out = or_2_out ? ACC_O2 : 1'bz;  // Controlled_Buffer controlled_buffer_23
  assign controlled_buffer_12_out = or_2_out ? ACC_O3 : 1'bz;  // Controlled_Buffer controlled_buffer_24
  or or_2 (or_2_out, ctrlunit_ext_1_sta_sig, ctrlunit_ext_1_jmp_sig);
  and and_2 (and_2_out, ctrlunit_ext_1_sta_sig, WRITEBACK);
  SRAM sram_1 (
    .HARD_RESET(RESET), .CLK(CLK), .I3(ACC_O3), .I2(ACC_O2), .I1(ACC_O1), .I0(ACC_O0), .WE(and_2_out),
    .ADDR1(MEM_REG_reg_o1), .ADDR0(MEM_REG_reg_o0), .SRAM_O3(sram_1_sram_o3), .SRAM_O2(sram_1_sram_o2),
    .SRAM_O1(sram_1_sram_o1), .SRAM_O0(sram_1_sram_o0));
  LED led_15 (.in(sram_1_sram_o0));
  LED led_16 (.in(sram_1_sram_o1));
  LED led_17 (.in(sram_1_sram_o2));
  LED led_18 (.in(sram_1_sram_o3));
endmodule

module PlayGround_v3 (
  input  CLEAR,
  input  RESET,
  input  WE,
  input  ADD,
  input  SUB,
  input  AAND,
  input  OOR,
  input  XOOR,
  input  NOOT,
  input  INC,
  input  DEC,
  input  JMP,
  input  JZ,
  input  JN,
  input  HLT,
  input  LDI,
  input  LDA,
  input  STA,
  input  XXX,
  input  I0,
  input  I1,
  input  I2,
  input  I3,
  input  I4,
  input  I5,
  input  I6,
  input  I7,
  input  I8,
  input  I9,
  input  A0,
  input  A1,
  input  A2,
  input  A3,
  input  A4,
  input  A5,
  input  A6,
  input  A7,
  input  A8,
  input  A9
);

  wire assember_v2_1_opc_o0, assember_v2_1_opc_o1, assember_v2_1_opc_o2, assember_v2_1_opc_o3,
       assember_v2_1_opr_o0, assember_v2_1_opr_o1, assember_v2_1_opr_o2, assember_v2_1_opr_o3, clock_1_out,
       cpu_v9_1_acc_o0, cpu_v9_1_acc_o1, cpu_v9_1_acc_o2, cpu_v9_1_acc_o3, cpu_v9_1_c, cpu_v9_1_decode,
       cpu_v9_1_execute, cpu_v9_1_fetch, cpu_v9_1_isa_opc_0, cpu_v9_1_isa_opc_1, cpu_v9_1_isa_opc_2,
       cpu_v9_1_isa_opc_3, cpu_v9_1_isa_opr_0, cpu_v9_1_isa_opr_1, cpu_v9_1_isa_opr_2, cpu_v9_1_isa_opr_3,
       cpu_v9_1_n, cpu_v9_1_ovf, cpu_v9_1_romi0, cpu_v9_1_romi1, cpu_v9_1_romi2, cpu_v9_1_romi3,
       cpu_v9_1_writeback, cpu_v9_1_z, ENTER_out, SOTRE_MEMORY_out, STORE_STORAGE_out;

  Button SOTRE_MEMORY (.out(SOTRE_MEMORY_out));
  Button STORE_STORAGE (.out(STORE_STORAGE_out));
  Button ENTER (.out(ENTER_out));
  Clock clock_1 (.out(clock_1_out));
  ASSEMBER_V2 assember_v2_1 (
    .ADD_BIN_I3(cpu_v9_1_romi3), .ADD_BIN_I2(cpu_v9_1_romi2), .ADD_BIN_I1(cpu_v9_1_romi1),
    .ADD_BIN_I0(cpu_v9_1_romi0), .CLEAR(CLEAR), .WE(WE), .SOTRE_MEMORY(SOTRE_MEMORY_out),
    .STORE_STAGE(STORE_STORAGE_out), .ENTER(ENTER_out), .ADD(ADD), .SUB(SUB), .AAND(AAND), .OOR(OOR),
    .XOOR(XOOR), .NOOT(NOOT), .INC(INC), .DEC(DEC), .JMP(JMP), .JZ(JZ), .JN(JN), .HLT(HLT), .LDI(LDI),
    .LDA(LDA), .STA(STA), .XXX(XXX), .OPR_I0(I0), .OPR_I1(I1), .OPR_I2(I2), .OPR_I3(I3), .OPR_I4(I4),
    .OPR_I5(I5), .OPR_I6(I6), .OPR_I7(I7), .OPR_I8(I8), .OPR_I9(I9), .ADDR_I0(A0), .ADDR_I1(A1),
    .ADDR_I2(A2), .ADDR_I3(A3), .ADDR_I4(A4), .ADDR_I5(A5), .ADDR_I6(A6), .ADDR_I7(A7), .ADDR_I8(A8),
    .ADDR_I9(A9), .OPC_O3(assember_v2_1_opc_o3), .OPC_O2(assember_v2_1_opc_o2),
    .OPC_O1(assember_v2_1_opc_o1), .OPC_O0(assember_v2_1_opc_o0), .OPR_O3(assember_v2_1_opr_o3),
    .OPR_O2(assember_v2_1_opr_o2), .OPR_O1(assember_v2_1_opr_o1), .OPR_O0(assember_v2_1_opr_o0));
  cpu_v9 cpu_v9_1 (
    .RESET(RESET), .CLK(clock_1_out), .OPC3(assember_v2_1_opc_o3), .OPC2(assember_v2_1_opc_o2),
    .OPC1(assember_v2_1_opc_o1), .OPC0(assember_v2_1_opc_o0), .OPRAND3(assember_v2_1_opr_o3),
    .OPRAND2(assember_v2_1_opr_o2), .OPRAND1(assember_v2_1_opr_o1), .OPRAND0(assember_v2_1_opr_o0),
    .ISA_OPC_3(cpu_v9_1_isa_opc_3), .ISA_OPC_2(cpu_v9_1_isa_opc_2), .ISA_OPC_1(cpu_v9_1_isa_opc_1),
    .ISA_OPC_0(cpu_v9_1_isa_opc_0), .ISA_OPR_3(cpu_v9_1_isa_opr_3), .ISA_OPR_2(cpu_v9_1_isa_opr_2),
    .ISA_OPR_1(cpu_v9_1_isa_opr_1), .ISA_OPR_0(cpu_v9_1_isa_opr_0), .OVF(cpu_v9_1_ovf), .N(cpu_v9_1_n),
    .C(cpu_v9_1_c), .Z(cpu_v9_1_z), .ACC_O3(cpu_v9_1_acc_o3), .ACC_O2(cpu_v9_1_acc_o2),
    .ACC_O1(cpu_v9_1_acc_o1), .ACC_O0(cpu_v9_1_acc_o0), .FETCH(cpu_v9_1_fetch), .DECODE(cpu_v9_1_decode),
    .EXECUTE(cpu_v9_1_execute), .WRITEBACK(cpu_v9_1_writeback), .ROMI3(cpu_v9_1_romi3),
    .ROMI2(cpu_v9_1_romi2), .ROMI1(cpu_v9_1_romi1), .ROMI0(cpu_v9_1_romi0));
  LED led_1 (.in(cpu_v9_1_isa_opc_3));
  LED led_2 (.in(cpu_v9_1_isa_opc_2));
  LED FETCH (.in(cpu_v9_1_fetch));
  LED DECODE (.in(cpu_v9_1_decode));
  LED EXECUTE (.in(cpu_v9_1_execute));
  LED WRITEBACK (.in(cpu_v9_1_writeback));
  LED led_3 (.in(cpu_v9_1_isa_opc_1));
  LED led_4 (.in(cpu_v9_1_isa_opc_0));
  LED led_5 (.in(cpu_v9_1_isa_opr_3));
  LED led_6 (.in(cpu_v9_1_isa_opr_2));
  LED led_7 (.in(cpu_v9_1_isa_opr_1));
  LED led_8 (.in(cpu_v9_1_isa_opr_0));
  LED OVF (.in(cpu_v9_1_ovf));
  LED N (.in(cpu_v9_1_n));
  LED C (.in(cpu_v9_1_c));
  LED Z (.in(cpu_v9_1_z));
  LED O3 (.in(cpu_v9_1_acc_o3));
  LED O2 (.in(cpu_v9_1_acc_o2));
  LED O1 (.in(cpu_v9_1_acc_o1));
  LED O0 (.in(cpu_v9_1_acc_o0));
endmodule

module TEST_PROG_FULL (
  input  ROMI3,
  input  ROMI2,
  input  ROMI1,
  input  ROMI0,
  output OPC3,
  output OPC2,
  output OPC1,
  output OPC0,
  output OPRAND3,
  output OPRAND2,
  output OPRAND1,
  output OPRAND0
);

  wire and_1_out, and_2_out, and_3_out, and_4_out, and_5_out, and_6_out, and_7_out, and_8_out, and_9_out,
       and_10_out, and_11_out, and_12_out, and_13_out, and_14_out, and_15_out, and_16_out, and_17_out,
       and_18_out, and_19_out, and_20_out, and_21_out, and_22_out, and_23_out, and_24_out, and_25_out,
       and_26_out, and_27_out, and_28_out, and_29_out, and_30_out, and_31_out, and_32_out, and_33_out,
       and_34_out, and_35_out, and_36_out, and_37_out, and_38_out, and_39_out, and_40_out, and_41_out,
       and_42_out, and_43_out, and_44_out, and_45_out, and_46_out, and_47_out, and_48_out, and_49_out,
       and_50_out, and_51_out, and_52_out, and_53_out, and_54_out, and_55_out, and_56_out, and_57_out,
       and_58_out, and_59_out, and_60_out, and_61_out, and_62_out, and_63_out, and_64_out, and_65_out,
       and_66_out, and_67_out, and_68_out, and_69_out, and_70_out, and_71_out, and_72_out, and_73_out,
       and_74_out, and_75_out, and_76_out, and_77_out, and_78_out, and_79_out, and_80_out, and_81_out,
       and_82_out, and_83_out, and_84_out, and_85_out, and_86_out, and_87_out, and_88_out, and_89_out,
       and_90_out, and_91_out, and_92_out, and_93_out, and_94_out, and_95_out, and_96_out, and_97_out,
       and_98_out, and_99_out, and_100_out, and_101_out, and_102_out, and_103_out, and_104_out, and_105_out,
       and_106_out, and_107_out, and_108_out, and_109_out, and_110_out, and_111_out, and_112_out,
       and_113_out, and_114_out, and_115_out, and_116_out, and_117_out, and_118_out, and_119_out,
       and_120_out, and_121_out, and_122_out, and_123_out, and_124_out, and_125_out, and_126_out,
       and_127_out, and_128_out, and_129_out, and_130_out, and_131_out, and_132_out, and_133_out,
       and_134_out, and_135_out, and_136_out, and_137_out, and_138_out, and_139_out, and_140_out,
       and_141_out, and_142_out, and_143_out, DECORDER_4x16_out, not_1_out, not_2_out, not_3_out, not_4_out,
       or_1_out, or_3_out, or_4_out, or_6_out, or_7_out, or_8_out, or_10_out, or_12_out, or_13_out,
       or_14_out, or_16_out, or_18_out, or_19_out, or_21_out, or_22_out, or_23_out;

  not not_1 (not_1_out, ROMI3);
  not not_2 (not_2_out, ROMI2);
  not not_3 (not_3_out, ROMI1);
  not not_4 (not_4_out, ROMI0);
  and DECORDER_4x16 (DECORDER_4x16_out, not_4_out, not_3_out, not_2_out, not_1_out);
  and and_1 (and_1_out, ROMI0, not_3_out, not_2_out, not_1_out);
  and and_2 (and_2_out, not_4_out, ROMI1, not_2_out, not_1_out);
  and and_3 (and_3_out, ROMI0, ROMI1, not_2_out, not_1_out);
  and and_4 (and_4_out, not_4_out, not_3_out, ROMI2, not_1_out);
  and and_5 (and_5_out, ROMI0, not_3_out, ROMI2, not_1_out);
  and and_6 (and_6_out, not_4_out, ROMI1, ROMI2, not_1_out);
  and and_7 (and_7_out, ROMI0, ROMI1, ROMI2, not_1_out);
  and and_8 (and_8_out, not_4_out, not_3_out, not_2_out, ROMI3);
  and and_9 (and_9_out, ROMI0, not_3_out, not_2_out, ROMI3);
  and and_10 (and_10_out, not_4_out, ROMI1, not_2_out, ROMI3);
  and and_11 (and_11_out, ROMI0, ROMI1, not_2_out, ROMI3);
  and and_12 (and_12_out, not_4_out, not_3_out, ROMI2, ROMI3);
  and and_13 (and_13_out, ROMI0, not_3_out, ROMI2, ROMI3);
  and and_14 (and_14_out, not_4_out, ROMI1, ROMI2, ROMI3);
  and and_15 (and_15_out, ROMI0, ROMI1, ROMI2, ROMI3);
  or or_1 (or_1_out, and_31_out, and_30_out, and_29_out, and_28_out, and_27_out, and_26_out, and_25_out, and_24_out);
  and and_16 (and_16_out, DECORDER_4x16_out, 1'b1);
  and and_17 (and_17_out, and_1_out, 1'b1);
  and and_18 (and_18_out, and_2_out, 1'b1);
  and and_19 (and_19_out, and_3_out, 1'b0);
  and and_20 (and_20_out, and_4_out, 1'b1);
  and and_21 (and_21_out, and_5_out, 1'b1);
  and and_22 (and_22_out, and_6_out, 1'b0);
  and and_23 (and_23_out, and_7_out, 1'b1);
  and and_24 (and_24_out, and_8_out, 1'b1);
  and and_25 (and_25_out, and_9_out, 1'b0);
  and and_26 (and_26_out, and_10_out, 1'b1);
  and and_27 (and_27_out, and_11_out, 1'b1);
  and and_28 (and_28_out, and_12_out, 1'b0);
  and and_29 (and_29_out, and_13_out, 1'b0);
  and and_30 (and_30_out, and_14_out, 1'b0);
  and and_31 (and_31_out, and_15_out, 1'b1);
  or or_2 (OPC3, or_1_out, or_3_out);
  or or_3 (or_3_out, and_16_out, and_17_out, and_18_out, and_19_out, and_20_out, and_21_out, and_22_out, and_23_out);
  or or_4 (or_4_out, and_47_out, and_46_out, and_45_out, and_44_out, and_43_out, and_42_out, and_41_out, and_40_out);
  and and_32 (and_32_out, DECORDER_4x16_out, 1'b1);
  and and_33 (and_33_out, and_1_out, 1'b1);
  and and_34 (and_34_out, and_2_out, 1'b1);
  and and_35 (and_35_out, and_3_out, 1'b0);
  and and_36 (and_36_out, and_4_out, 1'b1);
  and and_37 (and_37_out, and_5_out, 1'b1);
  and and_38 (and_38_out, and_6_out, 1'b0);
  and and_39 (and_39_out, and_7_out, 1'b1);
  and and_40 (and_40_out, and_8_out, 1'b1);
  and and_41 (and_41_out, and_9_out, 1'b0);
  and and_42 (and_42_out, and_10_out, 1'b1);
  and and_43 (and_43_out, and_11_out, 1'b1);
  and and_44 (and_44_out, and_12_out, 1'b1);
  and and_45 (and_45_out, and_13_out, 1'b1);
  and and_46 (and_46_out, and_14_out, 1'b1);
  and and_47 (and_47_out, and_15_out, 1'b0);
  or or_5 (OPC2, or_4_out, or_6_out);
  or or_6 (or_6_out, and_32_out, and_33_out, and_34_out, and_35_out, and_36_out, and_37_out, and_38_out, and_39_out);
  and and_48 (and_48_out, DECORDER_4x16_out, 1'b0);
  and and_49 (and_49_out, and_1_out, 1'b1);
  and and_50 (and_50_out, and_2_out, 1'b0);
  and and_51 (and_51_out, and_3_out, 1'b0);
  and and_52 (and_52_out, and_4_out, 1'b1);
  and and_53 (and_53_out, and_5_out, 1'b0);
  and and_54 (and_54_out, and_6_out, 1'b0);
  and and_55 (and_55_out, and_7_out, 1'b1);
  and and_56 (and_56_out, and_8_out, 1'b0);
  and and_57 (and_57_out, and_9_out, 1'b1);
  and and_58 (and_58_out, and_10_out, 1'b1);
  and and_59 (and_59_out, and_11_out, 1'b0);
  and and_60 (and_60_out, and_12_out, 1'b0);
  and and_61 (and_61_out, and_13_out, 1'b1);
  and and_62 (and_62_out, and_14_out, 1'b1);
  and and_63 (and_63_out, and_15_out, 1'b0);
  or or_7 (or_7_out, and_63_out, and_62_out, and_61_out, and_60_out, and_59_out, and_58_out, and_57_out, and_56_out);
  or or_8 (or_8_out, and_48_out, and_49_out, and_50_out, and_51_out, and_52_out, and_53_out, and_54_out, and_55_out);
  or or_9 (OPC1, or_7_out, or_8_out);
  or or_10 (or_10_out, and_79_out, and_78_out, and_77_out, and_76_out, and_75_out, and_74_out, and_73_out, and_72_out);
  and and_64 (and_64_out, DECORDER_4x16_out, 1'b0);
  and and_65 (and_65_out, and_1_out, 1'b0);
  and and_66 (and_66_out, and_2_out, 1'b1);
  and and_67 (and_67_out, and_3_out, 1'b0);
  and and_68 (and_68_out, and_4_out, 1'b0);
  and and_69 (and_69_out, and_5_out, 1'b1);
  and and_70 (and_70_out, and_6_out, 1'b1);
  and and_71 (and_71_out, and_7_out, 1'b0);
  and and_72 (and_72_out, and_8_out, 1'b1);
  and and_73 (and_73_out, and_9_out, 1'b0);
  and and_74 (and_74_out, and_10_out, 1'b0);
  and and_75 (and_75_out, and_11_out, 1'b1);
  and and_76 (and_76_out, and_12_out, 1'b0);
  and and_77 (and_77_out, and_13_out, 1'b0);
  and and_78 (and_78_out, and_14_out, 1'b1);
  and and_79 (and_79_out, and_15_out, 1'b0);
  or or_11 (OPC0, or_10_out, or_12_out);
  or or_12 (or_12_out, and_64_out, and_65_out, and_66_out, and_67_out, and_68_out, and_69_out, and_70_out, and_71_out);
  or or_13 (or_13_out, and_95_out, and_94_out, and_93_out, and_92_out, and_91_out, and_90_out, and_89_out, and_88_out);
  and and_80 (and_80_out, DECORDER_4x16_out, 1'b0);
  and and_81 (and_81_out, and_1_out, 1'b0);
  and and_82 (and_82_out, and_2_out, 1'b0);
  and and_83 (and_83_out, and_3_out, 1'b0);
  and and_84 (and_84_out, and_4_out, 1'b0);
  and and_85 (and_85_out, and_5_out, 1'b0);
  and and_86 (and_86_out, and_6_out, 1'b0);
  and and_87 (and_87_out, and_7_out, 1'b0);
  and and_88 (and_88_out, and_8_out, 1'b0);
  and and_89 (and_89_out, and_9_out, 1'b1);
  and and_90 (and_90_out, and_10_out, 1'b0);
  and and_91 (and_91_out, and_11_out, 1'b0);
  and and_92 (and_92_out, and_12_out, 1'b1);
  and and_93 (and_93_out, and_13_out, 1'b0);
  and and_94 (and_94_out, and_14_out, 1'b0);
  and and_95 (and_95_out, and_15_out, 1'b0);
  or or_14 (or_14_out, and_80_out, and_81_out, and_82_out, and_83_out, and_84_out, and_85_out, and_86_out, and_87_out);
  or or_15 (OPRAND3, or_13_out, or_14_out);
  or or_16 (or_16_out, and_111_out, and_110_out, and_109_out, and_108_out, and_107_out, and_106_out, and_105_out, and_104_out);
  and and_96 (and_96_out, DECORDER_4x16_out, 1'b1);
  and and_97 (and_97_out, and_1_out, 1'b0);
  and and_98 (and_98_out, and_2_out, 1'b0);
  and and_99 (and_99_out, and_3_out, 1'b0);
  and and_100 (and_100_out, and_4_out, 1'b0);
  and and_101 (and_101_out, and_5_out, 1'b0);
  and and_102 (and_102_out, and_6_out, 1'b0);
  and and_103 (and_103_out, and_7_out, 1'b0);
  and and_104 (and_104_out, and_8_out, 1'b0);
  and and_105 (and_105_out, and_9_out, 1'b1);
  and and_106 (and_106_out, and_10_out, 1'b0);
  and and_107 (and_107_out, and_11_out, 1'b0);
  and and_108 (and_108_out, and_12_out, 1'b0);
  and and_109 (and_109_out, and_13_out, 1'b0);
  and and_110 (and_110_out, and_14_out, 1'b0);
  and and_111 (and_111_out, and_15_out, 1'b0);
  or or_17 (OPRAND2, or_16_out, or_18_out);
  or or_18 (or_18_out, and_96_out, and_97_out, and_98_out, and_99_out, and_100_out, and_101_out, and_102_out, and_103_out);
  or or_19 (or_19_out, and_127_out, and_126_out, and_125_out, and_124_out, and_123_out, and_122_out, and_121_out, and_120_out);
  and and_112 (and_112_out, DECORDER_4x16_out, 1'b0);
  and and_113 (and_113_out, and_1_out, 1'b0);
  and and_114 (and_114_out, and_2_out, 1'b0);
  and and_115 (and_115_out, and_3_out, 1'b1);
  and and_116 (and_116_out, and_4_out, 1'b0);
  and and_117 (and_117_out, and_5_out, 1'b0);
  and and_118 (and_118_out, and_6_out, 1'b0);
  and and_119 (and_119_out, and_7_out, 1'b1);
  and and_120 (and_120_out, and_8_out, 1'b0);
  and and_121 (and_121_out, and_9_out, 1'b1);
  and and_122 (and_122_out, and_10_out, 1'b1);
  and and_123 (and_123_out, and_11_out, 1'b0);
  and and_124 (and_124_out, and_12_out, 1'b1);
  and and_125 (and_125_out, and_13_out, 1'b0);
  and and_126 (and_126_out, and_14_out, 1'b0);
  and and_127 (and_127_out, and_15_out, 1'b1);
  or or_20 (OPRAND1, or_19_out, or_21_out);
  or or_21 (or_21_out, and_112_out, and_113_out, and_114_out, and_115_out, and_116_out, and_117_out, and_118_out, and_119_out);
  or or_22 (or_22_out, and_143_out, and_142_out, and_141_out, and_140_out, and_139_out, and_138_out, and_137_out, and_136_out);
  and and_128 (and_128_out, DECORDER_4x16_out, 1'b1);
  and and_129 (and_129_out, and_1_out, 1'b0);
  and and_130 (and_130_out, and_2_out, 1'b0);
  and and_131 (and_131_out, and_3_out, 1'b1);
  and and_132 (and_132_out, and_4_out, 1'b1);
  and and_133 (and_133_out, and_5_out, 1'b0);
  and and_134 (and_134_out, and_6_out, 1'b1);
  and and_135 (and_135_out, and_7_out, 1'b0);
  and and_136 (and_136_out, and_8_out, 1'b0);
  and and_137 (and_137_out, and_9_out, 1'b1);
  and and_138 (and_138_out, and_10_out, 1'b1);
  and and_139 (and_139_out, and_11_out, 1'b0);
  and and_140 (and_140_out, and_12_out, 1'b0);
  and and_141 (and_141_out, and_13_out, 1'b0);
  and and_142 (and_142_out, and_14_out, 1'b0);
  and and_143 (and_143_out, and_15_out, 1'b0);
  or or_23 (or_23_out, and_128_out, and_129_out, and_130_out, and_131_out, and_132_out, and_133_out, and_134_out, and_135_out);
  or or_24 (OPRAND0, or_22_out, or_23_out);
endmodule

module ASSEMBLER_OPCODE (
  input  HARD_RESET,
  input  STORE,
  input  ADD,
  input  SUB,
  input  AAND,
  input  OOR,
  input  XOOR,
  input  NOOT,
  input  INC,
  input  DEC,
  input  JMP,
  input  JZ,
  input  JN,
  input  HLT,
  input  LDI,
  input  LDA,
  input  STA,
  input  XXX,
  output OPC3,
  output OPC2,
  output OPC1,
  output OPC0,
  output FUTURE_USE_CLK
);

  wire and_1_out, and_2_out, and_3_out, and_4_out, and_5_out, and_6_out, and_7_out, and_8_out, and_9_out,
       and_10_out, and_11_out, and_12_out, and_13_out, and_14_out, and_15_out, and_16_out, and_17_out,
       and_18_out, and_19_out, and_20_out, and_21_out, and_22_out, and_23_out, and_24_out, and_25_out,
       and_26_out, and_27_out, and_28_out, and_29_out, and_30_out, and_31_out, and_32_out, and_33_out,
       and_34_out, and_35_out, and_36_out, and_37_out, and_38_out, and_39_out, and_40_out, and_41_out,
       and_42_out, and_43_out, and_44_out, and_45_out, and_46_out, and_47_out, and_48_out, and_49_out,
       and_50_out, and_51_out, and_52_out, and_53_out, and_54_out, and_55_out, and_56_out, and_57_out,
       and_58_out, and_59_out, and_60_out, and_61_out, and_62_out, and_63_out, and_64_out, and_65_out,
       and_66_out, and_67_out, and_68_out, and_69_out, and_70_out, and_71_out, and_72_out, and_73_out,
       and_74_out, and_75_out, and_76_out, and_77_out, and_78_out, and_79_out, and_80_out, and_81_out,
       and_82_out, and_83_out, and_84_out, and_85_out, and_86_out, and_87_out, and_88_out, and_89_out,
       and_90_out, and_91_out, and_92_out, and_93_out, not_1_out, not_2_out, not_3_out, not_4_out, not_5_out,
       not_6_out, not_7_out, not_8_out, not_9_out, not_10_out, not_11_out, not_12_out, not_13_out,
       not_14_out, not_15_out, not_16_out, not_17_out, or_1_out, or_2_out, or_3_out, or_4_out, or_5_out,
       or_6_out, or_7_out, or_8_out, or_9_out, or_10_out, or_11_out, or_12_out, or_13_out, or_14_out,
       or_15_out, or_16_out, or_17_out, or_18_out, or_19_out, or_20_out, or_21_out, or_22_out, or_23_out,
       or_24_out, or_25_out, or_26_out, or_27_out;

  not not_1 (not_1_out, ADD);
  not not_2 (not_2_out, SUB);
  not not_3 (not_3_out, AAND);
  not not_4 (not_4_out, OOR);
  not not_5 (not_5_out, XOOR);
  not not_6 (not_6_out, NOOT);
  not not_7 (not_7_out, INC);
  not not_8 (not_8_out, DEC);
  not not_9 (not_9_out, JMP);
  not not_10 (not_10_out, JZ);
  not not_11 (not_11_out, JN);
  not not_12 (not_12_out, HLT);
  not not_13 (not_13_out, LDI);
  not not_14 (not_14_out, LDA);
  not not_15 (not_15_out, STA);
  not not_16 (not_16_out, XXX);
  and and_1 (and_1_out, SUB, not_1_out);
  and and_2 (and_2_out, not_1_out, not_2_out);
  and and_3 (and_3_out, and_2_out, not_3_out);
  and and_4 (and_4_out, and_3_out, not_4_out);
  and and_5 (and_5_out, XOOR, and_4_out);
  and and_6 (and_6_out, and_4_out, not_5_out);
  and and_7 (and_7_out, AAND, and_2_out);
  and and_8 (and_8_out, OOR, and_3_out);
  and and_9 (and_9_out, NOOT, and_6_out);
  and and_10 (and_10_out, and_6_out, not_6_out);
  and and_11 (and_11_out, INC, and_10_out);
  and and_12 (and_12_out, and_10_out, not_7_out);
  and and_13 (and_13_out, DEC, and_12_out);
  and and_14 (and_14_out, and_12_out, not_8_out);
  and and_15 (and_15_out, and_14_out, not_9_out);
  and and_16 (and_16_out, JMP, and_14_out);
  and and_17 (and_17_out, JZ, and_15_out);
  and and_18 (and_18_out, and_15_out, not_10_out);
  and and_19 (and_19_out, JN, and_18_out);
  and and_20 (and_20_out, and_18_out, not_11_out);
  and and_21 (and_21_out, and_20_out, not_12_out);
  and and_22 (and_22_out, HLT, and_20_out);
  and and_23 (and_23_out, LDI, and_21_out);
  and and_24 (and_24_out, and_21_out, not_13_out);
  and and_25 (and_25_out, LDA, and_24_out);
  and and_26 (and_26_out, and_24_out, not_14_out);
  and and_27 (and_27_out, STA, and_26_out);
  and and_28 (and_28_out, and_26_out, not_15_out);
  and and_29 (and_29_out, XXX, and_28_out);
  or or_1 (or_1_out, and_7_out, or_2_out);
  or or_2 (or_2_out, and_1_out, ADD);
  or or_3 (or_3_out, and_5_out, or_4_out);
  or or_4 (or_4_out, and_8_out, or_1_out);
  assign FUTURE_USE_CLK = ADD ? 1'b1 : 1'bz;  // Controlled_Buffer controlled_buffer_1
  assign FUTURE_USE_CLK = and_1_out ? 1'b1 : 1'bz;  // Controlled_Buffer controlled_buffer_2
  assign FUTURE_USE_CLK = and_7_out ? 1'b1 : 1'bz;  // Controlled_Buffer controlled_buffer_3
  assign FUTURE_USE_CLK = and_8_out ? 1'b1 : 1'bz;  // Controlled_Buffer controlled_buffer_4
  assign FUTURE_USE_CLK = and_5_out ? 1'b1 : 1'bz;  // Controlled_Buffer controlled_buffer_5
  assign FUTURE_USE_CLK = and_9_out ? 1'b1 : 1'bz;  // Controlled_Buffer controlled_buffer_6
  assign FUTURE_USE_CLK = and_11_out ? 1'b1 : 1'bz;  // Controlled_Buffer controlled_buffer_7
  assign FUTURE_USE_CLK = and_13_out ? 1'b1 : 1'bz;  // Controlled_Buffer controlled_buffer_8
  assign FUTURE_USE_CLK = and_16_out ? 1'b1 : 1'bz;  // Controlled_Buffer controlled_buffer_9
  assign FUTURE_USE_CLK = and_17_out ? 1'b1 : 1'bz;  // Controlled_Buffer controlled_buffer_10
  assign FUTURE_USE_CLK = and_19_out ? 1'b1 : 1'bz;  // Controlled_Buffer controlled_buffer_11
  assign FUTURE_USE_CLK = and_22_out ? 1'b1 : 1'bz;  // Controlled_Buffer controlled_buffer_12
  assign FUTURE_USE_CLK = and_23_out ? 1'b1 : 1'bz;  // Controlled_Buffer controlled_buffer_13
  assign FUTURE_USE_CLK = and_25_out ? 1'b1 : 1'bz;  // Controlled_Buffer controlled_buffer_14
  assign FUTURE_USE_CLK = and_27_out ? 1'b1 : 1'bz;  // Controlled_Buffer controlled_buffer_15
  assign FUTURE_USE_CLK = and_29_out ? 1'b1 : 1'bz;  // Controlled_Buffer controlled_buffer_16
  or or_5 (or_5_out, and_11_out, or_6_out);
  or or_6 (or_6_out, and_9_out, or_3_out);
  or or_7 (or_7_out, and_16_out, or_8_out);
  or or_8 (or_8_out, and_13_out, or_5_out);
  or or_9 (or_9_out, and_19_out, or_10_out);
  or or_10 (or_10_out, and_17_out, or_7_out);
  or or_11 (or_11_out, and_45_out, and_44_out, and_43_out, and_42_out, and_41_out, and_40_out, and_39_out, and_38_out);
  or or_12 (or_12_out, and_23_out, or_13_out);
  or or_13 (or_13_out, and_22_out, or_9_out);
  and and_30 (and_30_out, ADD, 1'b0);
  and and_31 (and_31_out, and_1_out, 1'b0);
  and and_32 (and_32_out, and_7_out, 1'b0);
  and and_33 (and_33_out, and_8_out, 1'b0);
  and and_34 (and_34_out, and_5_out, 1'b0);
  and and_35 (and_35_out, and_9_out, 1'b0);
  and and_36 (and_36_out, and_11_out, 1'b0);
  and and_37 (and_37_out, and_13_out, 1'b0);
  and and_38 (and_38_out, and_16_out, 1'b1);
  and and_39 (and_39_out, and_17_out, 1'b1);
  and and_40 (and_40_out, and_19_out, 1'b1);
  and and_41 (and_41_out, and_22_out, 1'b1);
  and and_42 (and_42_out, and_23_out, 1'b1);
  and and_43 (and_43_out, and_25_out, 1'b1);
  and and_44 (and_44_out, and_27_out, 1'b1);
  and and_45 (and_45_out, and_29_out, 1'b1);
  or or_14 (or_14_out, or_11_out, or_17_out);
  or or_15 (or_15_out, and_27_out, or_16_out);
  or or_16 (or_16_out, and_25_out, or_12_out);
  or or_17 (or_17_out, and_30_out, and_31_out, and_32_out, and_33_out, and_34_out, and_35_out, and_36_out, and_37_out);
  or or_18 (or_18_out, and_29_out, or_15_out);
  or or_19 (or_19_out, and_61_out, and_60_out, and_59_out, and_58_out, and_57_out, and_56_out, and_55_out, and_54_out);
  and and_46 (and_46_out, ADD, 1'b0);
  and and_47 (and_47_out, and_1_out, 1'b0);
  and and_48 (and_48_out, and_7_out, 1'b0);
  and and_49 (and_49_out, and_8_out, 1'b0);
  and and_50 (and_50_out, and_5_out, 1'b1);
  and and_51 (and_51_out, and_9_out, 1'b1);
  and and_52 (and_52_out, and_11_out, 1'b1);
  and and_53 (and_53_out, and_13_out, 1'b1);
  and and_54 (and_54_out, and_16_out, 1'b0);
  and and_55 (and_55_out, and_17_out, 1'b0);
  and and_56 (and_56_out, and_19_out, 1'b0);
  and and_57 (and_57_out, and_22_out, 1'b0);
  and and_58 (and_58_out, and_23_out, 1'b1);
  and and_59 (and_59_out, and_25_out, 1'b1);
  and and_60 (and_60_out, and_27_out, 1'b1);
  and and_61 (and_61_out, and_29_out, 1'b1);
  or or_20 (or_20_out, or_19_out, or_21_out);
  not not_17 (not_17_out, or_18_out);
  or or_21 (or_21_out, and_46_out, and_47_out, and_48_out, and_49_out, and_50_out, and_51_out, and_52_out, and_53_out);
  assign FUTURE_USE_CLK = not_17_out ? 1'b0 : 1'bz;  // Controlled_Buffer controlled_buffer_17
  and and_62 (and_62_out, ADD, 1'b0);
  and and_63 (and_63_out, and_1_out, 1'b0);
  and and_64 (and_64_out, and_7_out, 1'b1);
  and and_65 (and_65_out, and_8_out, 1'b1);
  and and_66 (and_66_out, and_5_out, 1'b0);
  and and_67 (and_67_out, and_9_out, 1'b0);
  and and_68 (and_68_out, and_11_out, 1'b1);
  and and_69 (and_69_out, and_13_out, 1'b1);
  and and_70 (and_70_out, and_16_out, 1'b0);
  and and_71 (and_71_out, and_17_out, 1'b0);
  and and_72 (and_72_out, and_19_out, 1'b1);
  and and_73 (and_73_out, and_22_out, 1'b1);
  and and_74 (and_74_out, and_23_out, 1'b0);
  and and_75 (and_75_out, and_25_out, 1'b0);
  and and_76 (and_76_out, and_27_out, 1'b1);
  and and_77 (and_77_out, and_29_out, 1'b1);
  or or_22 (or_22_out, and_77_out, and_76_out, and_75_out, and_74_out, and_73_out, and_72_out, and_71_out, and_70_out);
  or or_23 (or_23_out, and_62_out, and_63_out, and_64_out, and_65_out, and_66_out, and_67_out, and_68_out, and_69_out);
  or or_24 (or_24_out, or_22_out, or_23_out);
  or or_25 (or_25_out, and_93_out, and_92_out, and_91_out, and_90_out, and_89_out, and_88_out, and_87_out, and_86_out);
  and and_78 (and_78_out, ADD, 1'b0);
  and and_79 (and_79_out, and_1_out, 1'b1);
  and and_80 (and_80_out, and_7_out, 1'b0);
  and and_81 (and_81_out, and_8_out, 1'b1);
  and and_82 (and_82_out, and_5_out, 1'b0);
  and and_83 (and_83_out, and_9_out, 1'b1);
  and and_84 (and_84_out, and_11_out, 1'b0);
  and and_85 (and_85_out, and_13_out, 1'b1);
  and and_86 (and_86_out, and_16_out, 1'b0);
  and and_87 (and_87_out, and_17_out, 1'b1);
  and and_88 (and_88_out, and_19_out, 1'b0);
  and and_89 (and_89_out, and_22_out, 1'b1);
  and and_90 (and_90_out, and_23_out, 1'b0);
  and and_91 (and_91_out, and_25_out, 1'b1);
  and and_92 (and_92_out, and_27_out, 1'b0);
  and and_93 (and_93_out, and_29_out, 1'b1);
  or or_26 (or_26_out, and_78_out, and_79_out, and_80_out, and_81_out, and_82_out, and_83_out, and_84_out, and_85_out);
  or or_27 (or_27_out, or_25_out, or_26_out);
  REGISTER_4BIT register_4bit_1 (
    .HARD_RESET(HARD_RESET), .CLK(STORE), .REG_I3(or_14_out), .REG_I2(or_20_out), .REG_I1(or_24_out),
    .REG_I0(or_27_out), .WE(1'b1), .REG_O3(OPC3), .REG_O2(OPC2), .REG_O1(OPC1), .REG_O0(OPC0));
endmodule

module ASSEMBLER_OPERAND (
  input  HARD_RESET,
  input  STORE,
  input  I0,
  input  I1,
  input  I2,
  input  I3,
  input  I4,
  input  I5,
  input  I6,
  input  I7,
  input  I8,
  input  I9,
  output OPC3,
  output OPC2,
  output OPC1,
  output OPC0,
  output FUTURE_USE_CLK
);

  wire and_1_out, and_2_out, and_3_out, and_4_out, and_5_out, and_6_out, and_7_out, and_8_out, and_9_out,
       and_10_out, and_11_out, and_12_out, and_13_out, and_14_out, and_15_out, and_16_out, and_17_out,
       and_18_out, and_19_out, and_20_out, and_21_out, and_22_out, and_23_out, and_24_out, and_25_out,
       and_26_out, and_27_out, and_28_out, and_29_out, and_30_out, and_31_out, and_32_out, and_33_out,
       and_34_out, and_35_out, and_36_out, and_37_out, and_38_out, and_39_out, and_40_out, and_41_out,
       and_42_out, and_43_out, and_44_out, and_45_out, and_46_out, and_47_out, and_48_out, and_49_out,
       and_50_out, and_51_out, and_52_out, and_53_out, not_1_out, not_2_out, not_3_out, not_4_out, not_5_out,
       not_6_out, not_7_out, not_8_out, not_9_out, not_10_out, not_11_out, or_1_out, or_2_out, or_3_out,
       or_4_out, or_5_out, or_6_out, or_7_out, or_8_out, or_9_out, or_10_out, or_11_out, or_12_out,
       or_13_out, or_14_out, or_15_out, or_16_out, or_17_out;

  not not_1 (not_1_out, I0);
  not not_2 (not_2_out, I1);
  not not_3 (not_3_out, I2);
  not not_4 (not_4_out, I3);
  not not_5 (not_5_out, I4);
  not not_6 (not_6_out, I5);
  not not_7 (not_7_out, I6);
  not not_8 (not_8_out, I7);
  not not_9 (not_9_out, I8);
  not not_10 (not_10_out, I9);
  and and_1 (and_1_out, I1, not_1_out);
  and and_2 (and_2_out, not_1_out, not_2_out);
  and and_3 (and_3_out, and_2_out, not_3_out);
  and and_4 (and_4_out, and_3_out, not_4_out);
  and and_5 (and_5_out, I4, and_4_out);
  and and_6 (and_6_out, and_4_out, not_5_out);
  and and_7 (and_7_out, I2, and_2_out);
  and and_8 (and_8_out, I3, and_3_out);
  and and_9 (and_9_out, I5, and_6_out);
  and and_10 (and_10_out, and_6_out, not_6_out);
  and and_11 (and_11_out, I6, and_10_out);
  and and_12 (and_12_out, and_10_out, not_7_out);
  and and_13 (and_13_out, I7, and_12_out);
  and and_14 (and_14_out, and_12_out, not_8_out);
  and and_15 (and_15_out, and_14_out, not_9_out);
  and and_16 (and_16_out, I8, and_14_out);
  and and_17 (and_17_out, I9, and_15_out);
  or or_1 (or_1_out, and_7_out, or_2_out);
  or or_2 (or_2_out, and_1_out, I0);
  or or_3 (or_3_out, and_5_out, or_4_out);
  or or_4 (or_4_out, and_8_out, or_1_out);
  assign FUTURE_USE_CLK = I0 ? 1'b1 : 1'bz;  // Controlled_Buffer controlled_buffer_1
  assign FUTURE_USE_CLK = and_1_out ? 1'b1 : 1'bz;  // Controlled_Buffer controlled_buffer_2
  assign FUTURE_USE_CLK = and_7_out ? 1'b1 : 1'bz;  // Controlled_Buffer controlled_buffer_3
  assign FUTURE_USE_CLK = and_8_out ? 1'b1 : 1'bz;  // Controlled_Buffer controlled_buffer_4
  assign FUTURE_USE_CLK = and_5_out ? 1'b1 : 1'bz;  // Controlled_Buffer controlled_buffer_5
  assign FUTURE_USE_CLK = and_9_out ? 1'b1 : 1'bz;  // Controlled_Buffer controlled_buffer_6
  assign FUTURE_USE_CLK = and_11_out ? 1'b1 : 1'bz;  // Controlled_Buffer controlled_buffer_7
  assign FUTURE_USE_CLK = and_13_out ? 1'b1 : 1'bz;  // Controlled_Buffer controlled_buffer_8
  assign FUTURE_USE_CLK = and_16_out ? 1'b1 : 1'bz;  // Controlled_Buffer controlled_buffer_9
  assign FUTURE_USE_CLK = and_17_out ? 1'b1 : 1'bz;  // Controlled_Buffer controlled_buffer_10
  or or_5 (or_5_out, and_11_out, or_6_out);
  or or_6 (or_6_out, and_9_out, or_3_out);
  or or_7 (or_7_out, and_16_out, or_8_out);
  or or_8 (or_8_out, and_13_out, or_5_out);
  or or_9 (or_9_out, and_17_out, or_7_out);
  and and_18 (and_18_out, I0, 1'b0);
  and and_19 (and_19_out, and_1_out, 1'b0);
  and and_20 (and_20_out, and_7_out, 1'b0);
  and and_21 (and_21_out, and_8_out, 1'b0);
  and and_22 (and_22_out, and_5_out, 1'b0);
  and and_23 (and_23_out, and_9_out, 1'b0);
  and and_24 (and_24_out, and_11_out, 1'b0);
  and and_25 (and_25_out, and_13_out, 1'b0);
  and and_26 (and_26_out, and_16_out, 1'b1);
  or or_10 (or_10_out, and_26_out, or_11_out);
  or or_11 (or_11_out, and_18_out, and_19_out, and_20_out, and_21_out, and_22_out, and_23_out, and_24_out, and_25_out);
  and and_27 (and_27_out, I0, 1'b0);
  and and_28 (and_28_out, and_1_out, 1'b0);
  and and_29 (and_29_out, and_7_out, 1'b0);
  and and_30 (and_30_out, and_8_out, 1'b0);
  and and_31 (and_31_out, and_5_out, 1'b1);
  and and_32 (and_32_out, and_9_out, 1'b1);
  and and_33 (and_33_out, and_11_out, 1'b1);
  and and_34 (and_34_out, and_13_out, 1'b1);
  and and_35 (and_35_out, and_16_out, 1'b0);
  or or_12 (or_12_out, and_35_out, or_13_out);
  not not_11 (not_11_out, or_9_out);
  or or_13 (or_13_out, and_27_out, and_28_out, and_29_out, and_30_out, and_31_out, and_32_out, and_33_out, and_34_out);
  assign FUTURE_USE_CLK = not_11_out ? 1'b0 : 1'bz;  // Controlled_Buffer controlled_buffer_11
  and and_36 (and_36_out, I0, 1'b0);
  and and_37 (and_37_out, and_1_out, 1'b0);
  and and_38 (and_38_out, and_7_out, 1'b1);
  and and_39 (and_39_out, and_8_out, 1'b1);
  and and_40 (and_40_out, and_5_out, 1'b0);
  and and_41 (and_41_out, and_9_out, 1'b0);
  and and_42 (and_42_out, and_11_out, 1'b1);
  and and_43 (and_43_out, and_13_out, 1'b1);
  and and_44 (and_44_out, and_16_out, 1'b0);
  or or_14 (or_14_out, and_44_out, or_15_out);
  or or_15 (or_15_out, and_36_out, and_37_out, and_38_out, and_39_out, and_40_out, and_41_out, and_42_out, and_43_out);
  and and_45 (and_45_out, I0, 1'b0);
  and and_46 (and_46_out, and_1_out, 1'b1);
  and and_47 (and_47_out, and_7_out, 1'b0);
  and and_48 (and_48_out, and_8_out, 1'b1);
  and and_49 (and_49_out, and_5_out, 1'b0);
  and and_50 (and_50_out, and_9_out, 1'b1);
  and and_51 (and_51_out, and_11_out, 1'b0);
  and and_52 (and_52_out, and_13_out, 1'b1);
  and and_53 (and_53_out, and_16_out, 1'b0);
  or or_16 (or_16_out, and_53_out, or_17_out);
  or or_17 (or_17_out, and_45_out, and_46_out, and_47_out, and_48_out, and_49_out, and_50_out, and_51_out, and_52_out);
  REGISTER_4BIT register_4bit_1 (
    .HARD_RESET(HARD_RESET), .CLK(STORE), .REG_I3(or_10_out), .REG_I2(or_12_out), .REG_I1(or_14_out),
    .REG_I0(or_16_out), .WE(1'b1), .REG_O3(OPC3), .REG_O2(OPC2), .REG_O1(OPC1), .REG_O0(OPC0));
endmodule

module ASSEMBLER (
  input  in_1,
  input  in_2,
  input  in_3,
  input  in_4,
  input  in_5,
  input  in_6,
  input  in_7,
  input  in_8,
  input  in_9,
  input  in_10,
  input  in_11,
  input  in_12,
  input  in_13,
  input  in_14,
  input  in_15,
  input  in_16,
  input  in_17,
  input  in_18,
  input  in_19,
  input  in_20,
  input  in_21,
  input  in_22,
  input  in_23,
  input  in_24,
  input  in_25,
  input  in_26,
  input  in_27,
  input  in_28,
  input  in_29,
  input  in_30,
  input  in_31,
  input  in_32,
  input  in_33,
  input  in_34,
  input  in_35,
  input  in_36
);

  wire CLEAR_out, ENTER_0_out, OPCODE_opc0, OPCODE_opc1, OPCODE_opc2, OPCODE_opc3, OPERAND_opc0,
       OPERAND_opc1, OPERAND_opc2, OPERAND_opc3, register_4bit_1_reg_o0, register_4bit_1_reg_o1,
       register_4bit_1_reg_o2, register_4bit_1_reg_o3, register_4bit_2_reg_o0, register_4bit_2_reg_o1,
       register_4bit_2_reg_o2, register_4bit_2_reg_o3, register_4bit_3_reg_o0, register_4bit_3_reg_o1,
       register_4bit_3_reg_o2, register_4bit_3_reg_o3, ROM_ADDR_opc0, ROM_ADDR_opc1, ROM_ADDR_opc2,
       ROM_ADDR_opc3, STORE_out;

  LED OPC3 (.in(register_4bit_1_reg_o3));
  LED OPC2 (.in(register_4bit_1_reg_o2));
  LED OPC1 (.in(register_4bit_1_reg_o1));
  LED OPC0 (.in(register_4bit_1_reg_o0));
  REGISTER_4BIT register_4bit_1 (
    .HARD_RESET(CLEAR_out), .CLK(STORE_out), .REG_I3(OPCODE_opc3), .REG_I2(OPCODE_opc2),
    .REG_I1(OPCODE_opc1), .REG_I0(OPCODE_opc0), .WE(1'b1), .REG_O3(register_4bit_1_reg_o3),
    .REG_O2(register_4bit_1_reg_o2), .REG_O1(register_4bit_1_reg_o1), .REG_O0(register_4bit_1_reg_o0));
  ASSEMBLER_OPCODE_V2 OPCODE (
    .HARD_RESET(CLEAR_out), .STORE(ENTER_0_out), .ADD(in_1), .SUB(in_2), .AAND(in_3), .OOR(in_4),
    .XOOR(in_5), .NOOT(in_6), .INC(in_7), .DEC(in_8), .JMP(in_9), .JZ(in_10), .JN(in_11), .HLT(in_12),
    .LDI(in_13), .LDA(in_14), .STA(in_15), .XXX(in_16), .OPC3(OPCODE_opc3), .OPC2(OPCODE_opc2),
    .OPC1(OPCODE_opc1), .OPC0(OPCODE_opc0));
  LED OPR3 (.in(register_4bit_2_reg_o3));
  LED OPR2 (.in(register_4bit_2_reg_o2));
  LED OPR1 (.in(register_4bit_2_reg_o1));
  LED OPR0 (.in(register_4bit_2_reg_o0));
  REGISTER_4BIT register_4bit_2 (
    .HARD_RESET(CLEAR_out), .CLK(STORE_out), .REG_I3(OPERAND_opc3), .REG_I2(OPERAND_opc2),
    .REG_I1(OPERAND_opc1), .REG_I0(OPERAND_opc0), .WE(1'b1), .REG_O3(register_4bit_2_reg_o3),
    .REG_O2(register_4bit_2_reg_o2), .REG_O1(register_4bit_2_reg_o1), .REG_O0(register_4bit_2_reg_o0));
  ASSSEMBLER_OPERAND_V2 OPERAND (
    .HARD_RESET(CLEAR_out), .STORE(ENTER_0_out), .I0(in_17), .I1(in_18), .I2(in_19), .I3(in_20), .I4(in_21),
    .I5(in_22), .I6(in_23), .I7(in_24), .I8(in_25), .I9(in_26), .OPC3(OPERAND_opc3), .OPC2(OPERAND_opc2),
    .OPC1(OPERAND_opc1), .OPC0(OPERAND_opc0));
  LED ADDR3 (.in(register_4bit_3_reg_o3));
  LED ADDR2 (.in(register_4bit_3_reg_o2));
  LED ADDR1 (.in(register_4bit_3_reg_o1));
  LED ADDR0 (.in(register_4bit_3_reg_o0));
  REGISTER_4BIT register_4bit_3 (
    .HARD_RESET(CLEAR_out), .CLK(STORE_out), .REG_I3(ROM_ADDR_opc3), .REG_I2(ROM_ADDR_opc2),
    .REG_I1(ROM_ADDR_opc1), .REG_I0(ROM_ADDR_opc0), .WE(1'b1), .REG_O3(register_4bit_3_reg_o3),
    .REG_O2(register_4bit_3_reg_o2), .REG_O1(register_4bit_3_reg_o1), .REG_O0(register_4bit_3_reg_o0));
  ASSSEMBLER_OPERAND_V2 ROM_ADDR (
    .HARD_RESET(CLEAR_out), .STORE(ENTER_0_out), .I0(in_27), .I1(in_28), .I2(in_29), .I3(in_30), .I4(in_31),
    .I5(in_32), .I6(in_33), .I7(in_34), .I8(in_35), .I9(in_36), .OPC3(ROM_ADDR_opc3), .OPC2(ROM_ADDR_opc2),
    .OPC1(ROM_ADDR_opc1), .OPC0(ROM_ADDR_opc0));
  Button STORE (.out(STORE_out));
  Button CLEAR (.out(CLEAR_out));
  Button ENTER_0 (.out(ENTER_0_out));
endmodule

module ASSEMBLER_OPCODE_V2 (
  input  HARD_RESET,
  input  STORE,
  input  ADD,
  input  SUB,
  input  AAND,
  input  OOR,
  input  XOOR,
  input  NOOT,
  input  INC,
  input  DEC,
  input  JMP,
  input  JZ,
  input  JN,
  input  HLT,
  input  LDI,
  input  LDA,
  input  STA,
  input  XXX,
  output OPC3,
  output OPC2,
  output OPC1,
  output OPC0
);

  wire and_1_out, and_2_out, and_3_out, and_4_out, and_5_out, and_6_out, and_7_out, and_8_out, and_9_out,
       and_10_out, and_11_out, and_12_out, and_13_out, and_14_out, and_15_out, and_16_out, and_17_out,
       and_18_out, and_19_out, and_20_out, and_21_out, and_22_out, and_23_out, and_24_out, and_25_out,
       and_26_out, and_27_out, and_28_out, and_29_out, and_30_out, and_31_out, and_32_out, and_33_out,
       and_34_out, and_35_out, and_36_out, and_37_out, and_38_out, and_39_out, and_40_out, and_41_out,
       and_42_out, and_43_out, and_44_out, and_45_out, and_46_out, and_47_out, and_48_out, and_49_out,
       and_50_out, and_51_out, and_52_out, and_53_out, and_54_out, and_55_out, and_56_out, and_57_out,
       and_58_out, and_59_out, and_60_out, and_61_out, and_62_out, and_63_out, and_64_out, and_65_out,
       and_66_out, and_67_out, and_68_out, and_69_out, and_70_out, and_71_out, and_72_out, and_73_out,
       and_74_out, and_75_out, and_76_out, and_77_out, and_78_out, and_79_out, and_80_out, and_81_out,
       and_82_out, and_83_out, and_84_out, and_85_out, and_86_out, and_87_out, and_88_out, and_89_out,
       and_90_out, and_91_out, and_92_out, and_93_out, controlled_buffer_1_out, not_1_out, not_2_out,
       not_3_out, not_4_out, not_5_out, not_6_out, not_7_out, not_8_out, not_9_out, not_10_out, not_11_out,
       not_12_out, not_13_out, not_14_out, not_15_out, not_16_out, not_17_out, or_1_out, or_2_out, or_3_out,
       or_4_out, or_5_out, or_6_out, or_7_out, or_8_out, or_9_out, or_10_out, or_11_out, or_12_out,
       or_13_out, or_14_out, or_15_out, or_16_out, or_17_out, or_18_out, or_19_out, or_20_out, or_21_out,
       or_22_out, or_23_out, or_24_out, or_25_out, or_26_out, or_27_out;

  not not_1 (not_1_out, ADD);
  not not_2 (not_2_out, SUB);
  not not_3 (not_3_out, AAND);
  not not_4 (not_4_out, OOR);
  not not_5 (not_5_out, XOOR);
  not not_6 (not_6_out, NOOT);
  not not_7 (not_7_out, INC);
  not not_8 (not_8_out, DEC);
  not not_9 (not_9_out, JMP);
  not not_10 (not_10_out, JZ);
  not not_11 (not_11_out, JN);
  not not_12 (not_12_out, HLT);
  not not_13 (not_13_out, LDI);
  not not_14 (not_14_out, LDA);
  not not_15 (not_15_out, STA);
  not not_16 (not_16_out, XXX);
  and and_1 (and_1_out, SUB, not_1_out);
  and and_2 (and_2_out, not_1_out, not_2_out);
  and and_3 (and_3_out, and_2_out, not_3_out);
  and and_4 (and_4_out, and_3_out, not_4_out);
  and and_5 (and_5_out, XOOR, and_4_out);
  and and_6 (and_6_out, and_4_out, not_5_out);
  and and_7 (and_7_out, AAND, and_2_out);
  and and_8 (and_8_out, OOR, and_3_out);
  and and_9 (and_9_out, NOOT, and_6_out);
  and and_10 (and_10_out, and_6_out, not_6_out);
  and and_11 (and_11_out, INC, and_10_out);
  and and_12 (and_12_out, and_10_out, not_7_out);
  and and_13 (and_13_out, DEC, and_12_out);
  and and_14 (and_14_out, and_12_out, not_8_out);
  and and_15 (and_15_out, and_14_out, not_9_out);
  and and_16 (and_16_out, JMP, and_14_out);
  and and_17 (and_17_out, JZ, and_15_out);
  and and_18 (and_18_out, and_15_out, not_10_out);
  and and_19 (and_19_out, JN, and_18_out);
  and and_20 (and_20_out, and_18_out, not_11_out);
  and and_21 (and_21_out, and_20_out, not_12_out);
  and and_22 (and_22_out, HLT, and_20_out);
  and and_23 (and_23_out, LDI, and_21_out);
  and and_24 (and_24_out, and_21_out, not_13_out);
  and and_25 (and_25_out, LDA, and_24_out);
  and and_26 (and_26_out, and_24_out, not_14_out);
  and and_27 (and_27_out, STA, and_26_out);
  and and_28 (and_28_out, and_26_out, not_15_out);
  and and_29 (and_29_out, XXX, and_28_out);
  or or_1 (or_1_out, and_1_out, ADD);
  or or_2 (or_2_out, and_8_out, or_3_out);
  or or_3 (or_3_out, and_7_out, or_1_out);
  assign controlled_buffer_1_out = ADD ? 1'b1 : 1'bz;  // Controlled_Buffer controlled_buffer_1
  assign controlled_buffer_1_out = and_1_out ? 1'b1 : 1'bz;  // Controlled_Buffer controlled_buffer_2
  assign controlled_buffer_1_out = and_7_out ? 1'b1 : 1'bz;  // Controlled_Buffer controlled_buffer_3
  assign controlled_buffer_1_out = and_8_out ? 1'b1 : 1'bz;  // Controlled_Buffer controlled_buffer_4
  assign controlled_buffer_1_out = and_5_out ? 1'b1 : 1'bz;  // Controlled_Buffer controlled_buffer_5
  assign controlled_buffer_1_out = and_9_out ? 1'b1 : 1'bz;  // Controlled_Buffer controlled_buffer_6
  assign controlled_buffer_1_out = and_11_out ? 1'b1 : 1'bz;  // Controlled_Buffer controlled_buffer_7
  assign controlled_buffer_1_out = and_13_out ? 1'b1 : 1'bz;  // Controlled_Buffer controlled_buffer_8
  assign controlled_buffer_1_out = and_16_out ? 1'b1 : 1'bz;  // Controlled_Buffer controlled_buffer_9
  assign controlled_buffer_1_out = and_17_out ? 1'b1 : 1'bz;  // Controlled_Buffer controlled_buffer_10
  assign controlled_buffer_1_out = and_19_out ? 1'b1 : 1'bz;  // Controlled_Buffer controlled_buffer_11
  assign controlled_buffer_1_out = and_22_out ? 1'b1 : 1'bz;  // Controlled_Buffer controlled_buffer_12
  assign controlled_buffer_1_out = and_23_out ? 1'b1 : 1'bz;  // Controlled_Buffer controlled_buffer_13
  assign controlled_buffer_1_out = and_25_out ? 1'b1 : 1'bz;  // Controlled_Buffer controlled_buffer_14
  assign controlled_buffer_1_out = and_27_out ? 1'b1 : 1'bz;  // Controlled_Buffer controlled_buffer_15
  assign controlled_buffer_1_out = and_29_out ? 1'b1 : 1'bz;  // Controlled_Buffer controlled_buffer_16
  or or_4 (or_4_out, and_9_out, or_5_out);
  or or_5 (or_5_out, and_5_out, or_2_out);
  or or_6 (or_6_out, and_13_out, or_7_out);
  or or_7 (or_7_out, and_11_out, or_4_out);
  or or_8 (or_8_out, and_17_out, or_9_out);
  or or_9 (or_9_out, and_16_out, or_6_out);
  or or_10 (or_10_out, and_22_out, or_11_out);
  or or_11 (or_11_out, and_19_out, or_8_out);
  or or_12 (or_12_out, and_45_out, and_44_out, and_43_out, and_42_out, and_41_out, and_40_out, and_39_out, and_38_out);
  or or_13 (or_13_out, and_25_out, or_14_out);
  or or_14 (or_14_out, and_23_out, or_10_out);
  and and_30 (and_30_out, ADD, 1'b0);
  and and_31 (and_31_out, and_1_out, 1'b0);
  and and_32 (and_32_out, and_7_out, 1'b0);
  and and_33 (and_33_out, and_8_out, 1'b0);
  and and_34 (and_34_out, and_5_out, 1'b0);
  and and_35 (and_35_out, and_9_out, 1'b0);
  and and_36 (and_36_out, and_11_out, 1'b0);
  and and_37 (and_37_out, and_13_out, 1'b0);
  and and_38 (and_38_out, and_16_out, 1'b1);
  and and_39 (and_39_out, and_17_out, 1'b1);
  and and_40 (and_40_out, and_19_out, 1'b1);
  and and_41 (and_41_out, and_22_out, 1'b1);
  and and_42 (and_42_out, and_23_out, 1'b1);
  and and_43 (and_43_out, and_25_out, 1'b1);
  and and_44 (and_44_out, and_27_out, 1'b1);
  and and_45 (and_45_out, and_29_out, 1'b1);
  or or_15 (or_15_out, or_12_out, or_18_out);
  or or_16 (or_16_out, and_29_out, or_17_out);
  or or_17 (or_17_out, and_27_out, or_13_out);
  or or_18 (or_18_out, and_30_out, and_31_out, and_32_out, and_33_out, and_34_out, and_35_out, and_36_out, and_37_out);
  and and_46 (and_46_out, ADD, 1'b0);
  and and_47 (and_47_out, and_1_out, 1'b0);
  and and_48 (and_48_out, and_7_out, 1'b0);
  and and_49 (and_49_out, and_8_out, 1'b0);
  and and_50 (and_50_out, and_5_out, 1'b1);
  and and_51 (and_51_out, and_9_out, 1'b1);
  and and_52 (and_52_out, and_11_out, 1'b1);
  and and_53 (and_53_out, and_13_out, 1'b1);
  and and_54 (and_54_out, and_16_out, 1'b0);
  and and_55 (and_55_out, and_17_out, 1'b0);
  and and_56 (and_56_out, and_19_out, 1'b0);
  and and_57 (and_57_out, and_22_out, 1'b0);
  and and_58 (and_58_out, and_23_out, 1'b1);
  and and_59 (and_59_out, and_25_out, 1'b1);
  and and_60 (and_60_out, and_27_out, 1'b1);
  and and_61 (and_61_out, and_29_out, 1'b1);
  or or_19 (or_19_out, and_61_out, and_60_out, and_59_out, and_58_out, and_57_out, and_56_out, and_55_out, and_54_out);
  not not_17 (not_17_out, or_16_out);
  or or_20 (or_20_out, and_46_out, and_47_out, and_48_out, and_49_out, and_50_out, and_51_out, and_52_out, and_53_out);
  or or_21 (or_21_out, or_19_out, or_20_out);
  assign controlled_buffer_1_out = not_17_out ? 1'b0 : 1'bz;  // Controlled_Buffer controlled_buffer_17
  or or_22 (or_22_out, and_77_out, and_76_out, and_75_out, and_74_out, and_73_out, and_72_out, and_71_out, and_70_out);
  and and_62 (and_62_out, ADD, 1'b0);
  and and_63 (and_63_out, and_1_out, 1'b0);
  and and_64 (and_64_out, and_7_out, 1'b1);
  and and_65 (and_65_out, and_8_out, 1'b1);
  and and_66 (and_66_out, and_5_out, 1'b0);
  and and_67 (and_67_out, and_9_out, 1'b0);
  and and_68 (and_68_out, and_11_out, 1'b1);
  and and_69 (and_69_out, and_13_out, 1'b1);
  and and_70 (and_70_out, and_16_out, 1'b0);
  and and_71 (and_71_out, and_17_out, 1'b0);
  and and_72 (and_72_out, and_19_out, 1'b1);
  and and_73 (and_73_out, and_22_out, 1'b1);
  and and_74 (and_74_out, and_23_out, 1'b0);
  and and_75 (and_75_out, and_25_out, 1'b0);
  and and_76 (and_76_out, and_27_out, 1'b1);
  and and_77 (and_77_out, and_29_out, 1'b1);
  or or_23 (or_23_out, or_22_out, or_24_out);
  or or_24 (or_24_out, and_62_out, and_63_out, and_64_out, and_65_out, and_66_out, and_67_out, and_68_out, and_69_out);
  or or_25 (or_25_out, and_93_out, and_92_out, and_91_out, and_90_out, and_89_out, and_88_out, and_87_out, and_86_out);
  and and_78 (and_78_out, ADD, 1'b0);
  and and_79 (and_79_out, and_1_out, 1'b1);
  and and_80 (and_80_out, and_7_out, 1'b0);
  and and_81 (and_81_out, and_8_out, 1'b1);
  and and_82 (and_82_out, and_5_out, 1'b0);
  and and_83 (and_83_out, and_9_out, 1'b1);
  and and_84 (and_84_out, and_11_out, 1'b0);
  and and_85 (and_85_out, and_13_out, 1'b1);
  and and_86 (and_86_out, and_16_out, 1'b0);
  and and_87 (and_87_out, and_17_out, 1'b1);
  and and_88 (and_88_out, and_19_out, 1'b0);
  and and_89 (and_89_out, and_22_out, 1'b1);
  and and_90 (and_90_out, and_23_out, 1'b0);
  and and_91 (and_91_out, and_25_out, 1'b1);
  and and_92 (and_92_out, and_27_out, 1'b0);
  and and_93 (and_93_out, and_29_out, 1'b1);
  or or_26 (or_26_out, or_25_out, or_27_out);
  or or_27 (or_27_out, and_78_out, and_79_out, and_80_out, and_81_out, and_82_out, and_83_out, and_84_out, and_85_out);
  REGISTER_4BIT register_4bit_1 (
    .HARD_RESET(HARD_RESET), .CLK(STORE), .REG_I3(or_15_out), .REG_I2(or_21_out), .REG_I1(or_23_out),
    .REG_I0(or_26_out), .WE(1'b1), .REG_O3(OPC3), .REG_O2(OPC2), .REG_O1(OPC1), .REG_O0(OPC0));
endmodule

module D_LATCH_4BIT (
  input  ENABLE,
  input  D3,
  input  D2,
  input  D1,
  input  D0,
  output Q3,
  output Q2,
  output Q1,
  output Q0
);

  wire nand_1_out, nand_2_out, nand_3_out, nand_4_out, nand_5_out, nand_6_out, nand_7_out, nand_8_out,
       nand_10_out, nand_12_out, nand_14_out, nand_16_out, not_1_out, not_2_out, not_3_out, not_4_out;

  not not_1 (not_1_out, D0);
  not not_2 (not_2_out, D1);
  not not_3 (not_3_out, D2);
  not not_4 (not_4_out, D3);
  nand nand_1 (nand_1_out, D0, ENABLE);
  nand nand_2 (nand_2_out, ENABLE, not_1_out);
  nand nand_3 (nand_3_out, D1, ENABLE);
  nand nand_4 (nand_4_out, ENABLE, not_2_out);
  nand nand_5 (nand_5_out, D2, ENABLE);
  nand nand_6 (nand_6_out, ENABLE, not_3_out);
  nand nand_7 (nand_7_out, D3, ENABLE);
  nand nand_8 (nand_8_out, ENABLE, not_4_out);
  nand nand_9 (Q0, nand_1_out, nand_10_out);
  nand nand_10 (nand_10_out, Q0, nand_2_out);
  nand nand_11 (Q1, nand_3_out, nand_12_out);
  nand nand_12 (nand_12_out, Q1, nand_4_out);
  nand nand_13 (Q2, nand_5_out, nand_14_out);
  nand nand_14 (nand_14_out, Q2, nand_6_out);
  nand nand_15 (Q3, nand_7_out, nand_16_out);
  nand nand_16 (nand_16_out, Q3, nand_8_out);
endmodule

module D_LATCH_1BIT (
  input  ENABLE,
  input  D0,
  output Q0
);

  wire nand_1_out, nand_2_out, nand_4_out, not_1_out;

  not not_1 (not_1_out, D0);
  nand nand_1 (nand_1_out, D0, ENABLE);
  nand nand_2 (nand_2_out, ENABLE, not_1_out);
  nand nand_3 (Q0, nand_1_out, nand_4_out);
  nand nand_4 (nand_4_out, Q0, nand_2_out);
endmodule

module SR_LATCH (
  input  SET,
  input  RESET,
  output Q
);

  wire nor_1_out;

  nor nor_1 (nor_1_out, SET, Q);
  nor nor_2 (Q, nor_1_out, RESET);
endmodule

module ASSSEMBLER_OPERAND_V2 (
  input  HARD_RESET,
  input  STORE,
  input  I0,
  input  I1,
  input  I2,
  input  I3,
  input  I4,
  input  I5,
  input  I6,
  input  I7,
  input  I8,
  input  I9,
  output OPC3,
  output OPC2,
  output OPC1,
  output OPC0
);

  wire and_1_out, and_2_out, and_3_out, and_4_out, and_5_out, and_6_out, and_7_out, and_8_out, and_9_out,
       and_10_out, and_11_out, and_12_out, and_13_out, and_14_out, and_15_out, and_16_out, and_17_out,
       and_18_out, and_19_out, and_20_out, and_21_out, and_22_out, and_23_out, and_24_out, and_25_out,
       and_26_out, and_27_out, and_28_out, and_29_out, and_30_out, and_31_out, and_32_out, and_33_out,
       and_34_out, and_35_out, and_36_out, and_37_out, and_38_out, and_39_out, and_40_out, and_41_out,
       and_42_out, and_43_out, and_44_out, and_45_out, and_46_out, and_47_out, and_48_out, and_49_out,
       and_50_out, and_51_out, and_52_out, and_53_out, controlled_buffer_1_out, not_1_out, not_2_out,
       not_3_out, not_4_out, not_5_out, not_6_out, not_7_out, not_8_out, not_9_out, not_10_out, not_11_out,
       or_1_out, or_2_out, or_3_out, or_4_out, or_5_out, or_6_out, or_7_out, or_8_out, or_9_out, or_10_out,
       or_11_out, or_12_out, or_13_out, or_14_out, or_15_out, or_16_out, or_17_out;

  not not_1 (not_1_out, I0);
  not not_2 (not_2_out, I1);
  not not_3 (not_3_out, I2);
  not not_4 (not_4_out, I3);
  not not_5 (not_5_out, I4);
  not not_6 (not_6_out, I5);
  not not_7 (not_7_out, I6);
  not not_8 (not_8_out, I7);
  not not_9 (not_9_out, I8);
  not not_10 (not_10_out, I9);
  and and_1 (and_1_out, I1, not_1_out);
  and and_2 (and_2_out, not_1_out, not_2_out);
  and and_3 (and_3_out, and_2_out, not_3_out);
  and and_4 (and_4_out, and_3_out, not_4_out);
  and and_5 (and_5_out, I4, and_4_out);
  and and_6 (and_6_out, and_4_out, not_5_out);
  and and_7 (and_7_out, I2, and_2_out);
  and and_8 (and_8_out, I3, and_3_out);
  and and_9 (and_9_out, I5, and_6_out);
  and and_10 (and_10_out, and_6_out, not_6_out);
  and and_11 (and_11_out, I6, and_10_out);
  and and_12 (and_12_out, and_10_out, not_7_out);
  and and_13 (and_13_out, I7, and_12_out);
  and and_14 (and_14_out, and_12_out, not_8_out);
  and and_15 (and_15_out, and_14_out, not_9_out);
  and and_16 (and_16_out, I8, and_14_out);
  and and_17 (and_17_out, I9, and_15_out);
  or or_1 (or_1_out, and_7_out, or_2_out);
  or or_2 (or_2_out, and_1_out, I0);
  or or_3 (or_3_out, and_5_out, or_4_out);
  or or_4 (or_4_out, and_8_out, or_1_out);
  assign controlled_buffer_1_out = I0 ? 1'b1 : 1'bz;  // Controlled_Buffer controlled_buffer_1
  assign controlled_buffer_1_out = and_1_out ? 1'b1 : 1'bz;  // Controlled_Buffer controlled_buffer_2
  assign controlled_buffer_1_out = and_7_out ? 1'b1 : 1'bz;  // Controlled_Buffer controlled_buffer_3
  assign controlled_buffer_1_out = and_8_out ? 1'b1 : 1'bz;  // Controlled_Buffer controlled_buffer_4
  assign controlled_buffer_1_out = and_5_out ? 1'b1 : 1'bz;  // Controlled_Buffer controlled_buffer_5
  assign controlled_buffer_1_out = and_9_out ? 1'b1 : 1'bz;  // Controlled_Buffer controlled_buffer_6
  assign controlled_buffer_1_out = and_11_out ? 1'b1 : 1'bz;  // Controlled_Buffer controlled_buffer_7
  assign controlled_buffer_1_out = and_13_out ? 1'b1 : 1'bz;  // Controlled_Buffer controlled_buffer_8
  assign controlled_buffer_1_out = and_16_out ? 1'b1 : 1'bz;  // Controlled_Buffer controlled_buffer_9
  assign controlled_buffer_1_out = and_17_out ? 1'b1 : 1'bz;  // Controlled_Buffer controlled_buffer_10
  or or_5 (or_5_out, and_11_out, or_6_out);
  or or_6 (or_6_out, and_9_out, or_3_out);
  or or_7 (or_7_out, and_16_out, or_8_out);
  or or_8 (or_8_out, and_13_out, or_5_out);
  or or_9 (or_9_out, and_17_out, or_7_out);
  and and_18 (and_18_out, I0, 1'b0);
  and and_19 (and_19_out, and_1_out, 1'b0);
  and and_20 (and_20_out, and_7_out, 1'b0);
  and and_21 (and_21_out, and_8_out, 1'b0);
  and and_22 (and_22_out, and_5_out, 1'b0);
  and and_23 (and_23_out, and_9_out, 1'b0);
  and and_24 (and_24_out, and_11_out, 1'b0);
  and and_25 (and_25_out, and_13_out, 1'b0);
  and and_26 (and_26_out, and_16_out, 1'b1);
  or or_10 (or_10_out, and_26_out, or_11_out);
  or or_11 (or_11_out, and_18_out, and_19_out, and_20_out, and_21_out, and_22_out, and_23_out, and_24_out, and_25_out);
  and and_27 (and_27_out, I0, 1'b0);
  and and_28 (and_28_out, and_1_out, 1'b0);
  and and_29 (and_29_out, and_7_out, 1'b0);
  and and_30 (and_30_out, and_8_out, 1'b0);
  and and_31 (and_31_out, and_5_out, 1'b1);
  and and_32 (and_32_out, and_9_out, 1'b1);
  and and_33 (and_33_out, and_11_out, 1'b1);
  and and_34 (and_34_out, and_13_out, 1'b1);
  and and_35 (and_35_out, and_16_out, 1'b0);
  or or_12 (or_12_out, and_35_out, or_13_out);
  not not_11 (not_11_out, or_9_out);
  or or_13 (or_13_out, and_27_out, and_28_out, and_29_out, and_30_out, and_31_out, and_32_out, and_33_out, and_34_out);
  assign controlled_buffer_1_out = not_11_out ? 1'b0 : 1'bz;  // Controlled_Buffer controlled_buffer_11
  and and_36 (and_36_out, I0, 1'b0);
  and and_37 (and_37_out, and_1_out, 1'b0);
  and and_38 (and_38_out, and_7_out, 1'b1);
  and and_39 (and_39_out, and_8_out, 1'b1);
  and and_40 (and_40_out, and_5_out, 1'b0);
  and and_41 (and_41_out, and_9_out, 1'b0);
  and and_42 (and_42_out, and_11_out, 1'b1);
  and and_43 (and_43_out, and_13_out, 1'b1);
  and and_44 (and_44_out, and_16_out, 1'b0);
  or or_14 (or_14_out, and_44_out, or_15_out);
  or or_15 (or_15_out, and_36_out, and_37_out, and_38_out, and_39_out, and_40_out, and_41_out, and_42_out, and_43_out);
  and and_45 (and_45_out, I0, 1'b0);
  and and_46 (and_46_out, and_1_out, 1'b1);
  and and_47 (and_47_out, and_7_out, 1'b0);
  and and_48 (and_48_out, and_8_out, 1'b1);
  and and_49 (and_49_out, and_5_out, 1'b0);
  and and_50 (and_50_out, and_9_out, 1'b1);
  and and_51 (and_51_out, and_11_out, 1'b0);
  and and_52 (and_52_out, and_13_out, 1'b1);
  and and_53 (and_53_out, and_16_out, 1'b0);
  or or_16 (or_16_out, and_53_out, or_17_out);
  or or_17 (or_17_out, and_45_out, and_46_out, and_47_out, and_48_out, and_49_out, and_50_out, and_51_out, and_52_out);
  REGISTER_4BIT register_4bit_1 (
    .HARD_RESET(HARD_RESET), .CLK(STORE), .REG_I3(or_10_out), .REG_I2(or_12_out), .REG_I1(or_14_out),
    .REG_I0(or_16_out), .WE(1'b1), .REG_O3(OPC3), .REG_O2(OPC2), .REG_O1(OPC1), .REG_O0(OPC0));
endmodule
module EEPROM (
  input  HARD_RESET,
  input  CLK,
  input  I3,
  input  I2,
  input  I1,
  input  I0,
  input  WE,
  input  ROMI3,
  input  ROMI2,
  input  ROMI1,
  input  ROMI0,
  output O3,
  output O2,
  output O1,
  output O0
);

  wire and_1_out, and_2_out, and_3_out, and_4_out, and_5_out, and_6_out, and_7_out, and_8_out, and_9_out,
       and_10_out, and_11_out, and_12_out, and_13_out, and_14_out, and_15_out, and_16_out, and_17_out,
       and_18_out, and_19_out, and_20_out, and_21_out, and_22_out, and_23_out, and_24_out, and_25_out,
       and_26_out, and_27_out, and_28_out, and_29_out, and_30_out, and_31_out, DECORDER_4x16_out, not_1_out,
       not_2_out, not_3_out, not_4_out, register_4bit_1_reg_o0, register_4bit_1_reg_o1,
       register_4bit_1_reg_o2, register_4bit_1_reg_o3, register_4bit_2_reg_o0, register_4bit_2_reg_o1,
       register_4bit_2_reg_o2, register_4bit_2_reg_o3, register_4bit_3_reg_o0, register_4bit_3_reg_o1,
       register_4bit_3_reg_o2, register_4bit_3_reg_o3, register_4bit_4_reg_o0, register_4bit_4_reg_o1,
       register_4bit_4_reg_o2, register_4bit_4_reg_o3, register_4bit_5_reg_o0, register_4bit_5_reg_o1,
       register_4bit_5_reg_o2, register_4bit_5_reg_o3, register_4bit_6_reg_o0, register_4bit_6_reg_o1,
       register_4bit_6_reg_o2, register_4bit_6_reg_o3, register_4bit_7_reg_o0, register_4bit_7_reg_o1,
       register_4bit_7_reg_o2, register_4bit_7_reg_o3, register_4bit_8_reg_o0, register_4bit_8_reg_o1,
       register_4bit_8_reg_o2, register_4bit_8_reg_o3, register_4bit_9_reg_o0, register_4bit_9_reg_o1,
       register_4bit_9_reg_o2, register_4bit_9_reg_o3, register_4bit_10_reg_o0, register_4bit_10_reg_o1,
       register_4bit_10_reg_o2, register_4bit_10_reg_o3, register_4bit_11_reg_o0, register_4bit_11_reg_o1,
       register_4bit_11_reg_o2, register_4bit_11_reg_o3, register_4bit_12_reg_o0, register_4bit_12_reg_o1,
       register_4bit_12_reg_o2, register_4bit_12_reg_o3, register_4bit_13_reg_o0, register_4bit_13_reg_o1,
       register_4bit_13_reg_o2, register_4bit_13_reg_o3, register_4bit_14_reg_o0, register_4bit_14_reg_o1,
       register_4bit_14_reg_o2, register_4bit_14_reg_o3, register_4bit_15_reg_o0, register_4bit_15_reg_o1,
       register_4bit_15_reg_o2, register_4bit_15_reg_o3, register_4bit_16_reg_o0, register_4bit_16_reg_o1,
       register_4bit_16_reg_o2, register_4bit_16_reg_o3;

  not not_1 (not_1_out, ROMI3);
  not not_2 (not_2_out, ROMI2);
  not not_3 (not_3_out, ROMI1);
  not not_4 (not_4_out, ROMI0);
  and DECORDER_4x16 (DECORDER_4x16_out, not_4_out, not_3_out, not_2_out, not_1_out);
  and and_1 (and_1_out, ROMI0, not_3_out, not_2_out, not_1_out);
  and and_2 (and_2_out, not_4_out, ROMI1, not_2_out, not_1_out);
  and and_3 (and_3_out, ROMI0, ROMI1, not_2_out, not_1_out);
  and and_4 (and_4_out, not_4_out, not_3_out, ROMI2, not_1_out);
  and and_5 (and_5_out, ROMI0, not_3_out, ROMI2, not_1_out);
  and and_6 (and_6_out, not_4_out, ROMI1, ROMI2, not_1_out);
  and and_7 (and_7_out, ROMI0, ROMI1, ROMI2, not_1_out);
  and and_8 (and_8_out, not_4_out, not_3_out, not_2_out, ROMI3);
  and and_9 (and_9_out, ROMI0, not_3_out, not_2_out, ROMI3);
  and and_10 (and_10_out, not_4_out, ROMI1, not_2_out, ROMI3);
  and and_11 (and_11_out, ROMI0, ROMI1, not_2_out, ROMI3);
  and and_12 (and_12_out, not_4_out, not_3_out, ROMI2, ROMI3);
  and and_13 (and_13_out, ROMI0, not_3_out, ROMI2, ROMI3);
  and and_14 (and_14_out, not_4_out, ROMI1, ROMI2, ROMI3);
  and and_15 (and_15_out, ROMI0, ROMI1, ROMI2, ROMI3);
  and and_16 (and_16_out, DECORDER_4x16_out, WE);
  and and_17 (and_17_out, and_1_out, WE);
  and and_18 (and_18_out, and_2_out, WE);
  and and_19 (and_19_out, and_3_out, WE);
  and and_20 (and_20_out, and_4_out, WE);
  and and_21 (and_21_out, and_5_out, WE);
  and and_22 (and_22_out, and_6_out, WE);
  and and_23 (and_23_out, and_7_out, WE);
  and and_24 (and_24_out, and_8_out, WE);
  and and_25 (and_25_out, and_9_out, WE);
  and and_26 (and_26_out, and_10_out, WE);
  and and_27 (and_27_out, and_11_out, WE);
  and and_28 (and_28_out, and_12_out, WE);
  and and_29 (and_29_out, and_13_out, WE);
  and and_30 (and_30_out, and_14_out, WE);
  and and_31 (and_31_out, and_15_out, WE);
  REGISTER_4BIT register_4bit_1 (
    .HARD_RESET(HARD_RESET), .CLK(CLK), .REG_I3(I3), .REG_I2(I2), .REG_I1(I1), .REG_I0(I0), .WE(and_16_out),
    .REG_O3(register_4bit_1_reg_o3), .REG_O2(register_4bit_1_reg_o2), .REG_O1(register_4bit_1_reg_o1),
    .REG_O0(register_4bit_1_reg_o0));
  REGISTER_4BIT register_4bit_2 (
    .HARD_RESET(HARD_RESET), .CLK(CLK), .REG_I3(I3), .REG_I2(I2), .REG_I1(I1), .REG_I0(I0), .WE(and_17_out),
    .REG_O3(register_4bit_2_reg_o3), .REG_O2(register_4bit_2_reg_o2), .REG_O1(register_4bit_2_reg_o1),
    .REG_O0(register_4bit_2_reg_o0));
  REGISTER_4BIT register_4bit_3 (
    .HARD_RESET(HARD_RESET), .CLK(CLK), .REG_I3(I3), .REG_I2(I2), .REG_I1(I1), .REG_I0(I0), .WE(and_18_out),
    .REG_O3(register_4bit_3_reg_o3), .REG_O2(register_4bit_3_reg_o2), .REG_O1(register_4bit_3_reg_o1),
    .REG_O0(register_4bit_3_reg_o0));
  REGISTER_4BIT register_4bit_4 (
    .HARD_RESET(HARD_RESET), .CLK(CLK), .REG_I3(I3), .REG_I2(I2), .REG_I1(I1), .REG_I0(I0), .WE(and_19_out),
    .REG_O3(register_4bit_4_reg_o3), .REG_O2(register_4bit_4_reg_o2), .REG_O1(register_4bit_4_reg_o1),
    .REG_O0(register_4bit_4_reg_o0));
  REGISTER_4BIT register_4bit_5 (
    .HARD_RESET(HARD_RESET), .CLK(CLK), .REG_I3(I3), .REG_I2(I2), .REG_I1(I1), .REG_I0(I0), .WE(and_20_out),
    .REG_O3(register_4bit_5_reg_o3), .REG_O2(register_4bit_5_reg_o2), .REG_O1(register_4bit_5_reg_o1),
    .REG_O0(register_4bit_5_reg_o0));
  REGISTER_4BIT register_4bit_6 (
    .HARD_RESET(HARD_RESET), .CLK(CLK), .REG_I3(I3), .REG_I2(I2), .REG_I1(I1), .REG_I0(I0), .WE(and_21_out),
    .REG_O3(register_4bit_6_reg_o3), .REG_O2(register_4bit_6_reg_o2), .REG_O1(register_4bit_6_reg_o1),
    .REG_O0(register_4bit_6_reg_o0));
  REGISTER_4BIT register_4bit_7 (
    .HARD_RESET(HARD_RESET), .CLK(CLK), .REG_I3(I3), .REG_I2(I2), .REG_I1(I1), .REG_I0(I0), .WE(and_22_out),
    .REG_O3(register_4bit_7_reg_o3), .REG_O2(register_4bit_7_reg_o2), .REG_O1(register_4bit_7_reg_o1),
    .REG_O0(register_4bit_7_reg_o0));
  REGISTER_4BIT register_4bit_8 (
    .HARD_RESET(HARD_RESET), .CLK(CLK), .REG_I3(I3), .REG_I2(I2), .REG_I1(I1), .REG_I0(I0), .WE(and_23_out),
    .REG_O3(register_4bit_8_reg_o3), .REG_O2(register_4bit_8_reg_o2), .REG_O1(register_4bit_8_reg_o1),
    .REG_O0(register_4bit_8_reg_o0));
  REGISTER_4BIT register_4bit_9 (
    .HARD_RESET(HARD_RESET), .CLK(CLK), .REG_I3(I3), .REG_I2(I2), .REG_I1(I1), .REG_I0(I0), .WE(and_24_out),
    .REG_O3(register_4bit_9_reg_o3), .REG_O2(register_4bit_9_reg_o2), .REG_O1(register_4bit_9_reg_o1),
    .REG_O0(register_4bit_9_reg_o0));
  REGISTER_4BIT register_4bit_10 (
    .HARD_RESET(HARD_RESET), .CLK(CLK), .REG_I3(I3), .REG_I2(I2), .REG_I1(I1), .REG_I0(I0), .WE(and_25_out),
    .REG_O3(register_4bit_10_reg_o3), .REG_O2(register_4bit_10_reg_o2), .REG_O1(register_4bit_10_reg_o1),
    .REG_O0(register_4bit_10_reg_o0));
  REGISTER_4BIT register_4bit_11 (
    .HARD_RESET(HARD_RESET), .CLK(CLK), .REG_I3(I3), .REG_I2(I2), .REG_I1(I1), .REG_I0(I0), .WE(and_26_out),
    .REG_O3(register_4bit_11_reg_o3), .REG_O2(register_4bit_11_reg_o2), .REG_O1(register_4bit_11_reg_o1),
    .REG_O0(register_4bit_11_reg_o0));
  REGISTER_4BIT register_4bit_12 (
    .HARD_RESET(HARD_RESET), .CLK(CLK), .REG_I3(I3), .REG_I2(I2), .REG_I1(I1), .REG_I0(I0), .WE(and_27_out),
    .REG_O3(register_4bit_12_reg_o3), .REG_O2(register_4bit_12_reg_o2), .REG_O1(register_4bit_12_reg_o1),
    .REG_O0(register_4bit_12_reg_o0));
  REGISTER_4BIT register_4bit_13 (
    .HARD_RESET(HARD_RESET), .CLK(CLK), .REG_I3(I3), .REG_I2(I2), .REG_I1(I2), .REG_I0(I0), .WE(and_28_out),
    .REG_O3(register_4bit_13_reg_o3), .REG_O2(register_4bit_13_reg_o2), .REG_O1(register_4bit_13_reg_o1),
    .REG_O0(register_4bit_13_reg_o0));
  REGISTER_4BIT register_4bit_14 (
    .HARD_RESET(HARD_RESET), .CLK(CLK), .REG_I3(I3), .REG_I2(I2), .REG_I1(I1), .REG_I0(I0), .WE(and_29_out),
    .REG_O3(register_4bit_14_reg_o3), .REG_O2(register_4bit_14_reg_o2), .REG_O1(register_4bit_14_reg_o1),
    .REG_O0(register_4bit_14_reg_o0));
  REGISTER_4BIT register_4bit_15 (
    .HARD_RESET(HARD_RESET), .CLK(CLK), .REG_I3(I3), .REG_I2(I2), .REG_I1(I1), .REG_I0(I0), .WE(and_30_out),
    .REG_O3(register_4bit_15_reg_o3), .REG_O2(register_4bit_15_reg_o2), .REG_O1(register_4bit_15_reg_o1),
    .REG_O0(register_4bit_15_reg_o0));
  REGISTER_4BIT register_4bit_16 (
    .HARD_RESET(HARD_RESET), .CLK(CLK), .REG_I3(I3), .REG_I2(I2), .REG_I1(I1), .REG_I0(I0), .WE(and_31_out),
    .REG_O3(register_4bit_16_reg_o3), .REG_O2(register_4bit_16_reg_o2), .REG_O1(register_4bit_16_reg_o1),
    .REG_O0(register_4bit_16_reg_o0));
  assign O3 = DECORDER_4x16_out ? register_4bit_1_reg_o3 : 1'bz;  // Controlled_Buffer controlled_buffer_1
  assign O2 = DECORDER_4x16_out ? register_4bit_1_reg_o2 : 1'bz;  // Controlled_Buffer controlled_buffer_2
  assign O1 = DECORDER_4x16_out ? register_4bit_1_reg_o1 : 1'bz;  // Controlled_Buffer controlled_buffer_3
  assign O0 = DECORDER_4x16_out ? register_4bit_1_reg_o0 : 1'bz;  // Controlled_Buffer controlled_buffer_4
  assign O3 = and_1_out ? register_4bit_2_reg_o3 : 1'bz;  // Controlled_Buffer controlled_buffer_5
  assign O2 = and_1_out ? register_4bit_2_reg_o2 : 1'bz;  // Controlled_Buffer controlled_buffer_6
  assign O1 = and_1_out ? register_4bit_2_reg_o1 : 1'bz;  // Controlled_Buffer controlled_buffer_7
  assign O0 = and_1_out ? register_4bit_2_reg_o0 : 1'bz;  // Controlled_Buffer controlled_buffer_8
  assign O3 = and_2_out ? register_4bit_3_reg_o3 : 1'bz;  // Controlled_Buffer controlled_buffer_9
  assign O2 = and_2_out ? register_4bit_3_reg_o2 : 1'bz;  // Controlled_Buffer controlled_buffer_10
  assign O1 = and_2_out ? register_4bit_3_reg_o1 : 1'bz;  // Controlled_Buffer controlled_buffer_11
  assign O0 = and_2_out ? register_4bit_3_reg_o0 : 1'bz;  // Controlled_Buffer controlled_buffer_12
  assign O3 = and_3_out ? register_4bit_4_reg_o3 : 1'bz;  // Controlled_Buffer controlled_buffer_13
  assign O2 = and_3_out ? register_4bit_4_reg_o2 : 1'bz;  // Controlled_Buffer controlled_buffer_14
  assign O1 = and_3_out ? register_4bit_4_reg_o1 : 1'bz;  // Controlled_Buffer controlled_buffer_15
  assign O0 = and_3_out ? register_4bit_4_reg_o0 : 1'bz;  // Controlled_Buffer controlled_buffer_16
  assign O3 = and_4_out ? register_4bit_5_reg_o3 : 1'bz;  // Controlled_Buffer controlled_buffer_17
  assign O2 = and_4_out ? register_4bit_5_reg_o2 : 1'bz;  // Controlled_Buffer controlled_buffer_18
  assign O1 = and_4_out ? register_4bit_5_reg_o1 : 1'bz;  // Controlled_Buffer controlled_buffer_19
  assign O0 = and_4_out ? register_4bit_5_reg_o0 : 1'bz;  // Controlled_Buffer controlled_buffer_20
  assign O3 = and_5_out ? register_4bit_6_reg_o3 : 1'bz;  // Controlled_Buffer controlled_buffer_21
  assign O2 = and_5_out ? register_4bit_6_reg_o2 : 1'bz;  // Controlled_Buffer controlled_buffer_22
  assign O1 = and_5_out ? register_4bit_6_reg_o1 : 1'bz;  // Controlled_Buffer controlled_buffer_23
  assign O0 = and_5_out ? register_4bit_6_reg_o0 : 1'bz;  // Controlled_Buffer controlled_buffer_24
  assign O3 = and_6_out ? register_4bit_7_reg_o3 : 1'bz;  // Controlled_Buffer controlled_buffer_25
  assign O2 = and_6_out ? register_4bit_7_reg_o2 : 1'bz;  // Controlled_Buffer controlled_buffer_26
  assign O1 = and_6_out ? register_4bit_7_reg_o1 : 1'bz;  // Controlled_Buffer controlled_buffer_27
  assign O0 = and_6_out ? register_4bit_7_reg_o0 : 1'bz;  // Controlled_Buffer controlled_buffer_28
  assign O3 = and_7_out ? register_4bit_8_reg_o3 : 1'bz;  // Controlled_Buffer controlled_buffer_29
  assign O2 = and_7_out ? register_4bit_8_reg_o2 : 1'bz;  // Controlled_Buffer controlled_buffer_30
  assign O1 = and_7_out ? register_4bit_8_reg_o1 : 1'bz;  // Controlled_Buffer controlled_buffer_31
  assign O0 = and_7_out ? register_4bit_8_reg_o0 : 1'bz;  // Controlled_Buffer controlled_buffer_32
  assign O3 = and_8_out ? register_4bit_9_reg_o3 : 1'bz;  // Controlled_Buffer controlled_buffer_33
  assign O2 = and_8_out ? register_4bit_9_reg_o2 : 1'bz;  // Controlled_Buffer controlled_buffer_34
  assign O1 = and_8_out ? register_4bit_9_reg_o1 : 1'bz;  // Controlled_Buffer controlled_buffer_35
  assign O0 = and_8_out ? register_4bit_9_reg_o0 : 1'bz;  // Controlled_Buffer controlled_buffer_36
  assign O3 = and_9_out ? register_4bit_10_reg_o3 : 1'bz;  // Controlled_Buffer controlled_buffer_37
  assign O2 = and_9_out ? register_4bit_10_reg_o2 : 1'bz;  // Controlled_Buffer controlled_buffer_38
  assign O1 = and_9_out ? register_4bit_10_reg_o1 : 1'bz;  // Controlled_Buffer controlled_buffer_39
  assign O0 = and_9_out ? register_4bit_10_reg_o0 : 1'bz;  // Controlled_Buffer controlled_buffer_40
  assign O3 = and_10_out ? register_4bit_11_reg_o3 : 1'bz;  // Controlled_Buffer controlled_buffer_41
  assign O2 = and_10_out ? register_4bit_11_reg_o2 : 1'bz;  // Controlled_Buffer controlled_buffer_42
  assign O1 = and_10_out ? register_4bit_11_reg_o1 : 1'bz;  // Controlled_Buffer controlled_buffer_43
  assign O0 = and_10_out ? register_4bit_11_reg_o0 : 1'bz;  // Controlled_Buffer controlled_buffer_44
  assign O3 = and_11_out ? register_4bit_12_reg_o3 : 1'bz;  // Controlled_Buffer controlled_buffer_45
  assign O2 = and_11_out ? register_4bit_12_reg_o2 : 1'bz;  // Controlled_Buffer controlled_buffer_46
  assign O1 = and_11_out ? register_4bit_12_reg_o1 : 1'bz;  // Controlled_Buffer controlled_buffer_47
  assign O0 = and_11_out ? register_4bit_12_reg_o0 : 1'bz;  // Controlled_Buffer controlled_buffer_48
  assign O3 = and_12_out ? register_4bit_13_reg_o3 : 1'bz;  // Controlled_Buffer controlled_buffer_49
  assign O2 = and_12_out ? register_4bit_13_reg_o2 : 1'bz;  // Controlled_Buffer controlled_buffer_50
  assign O1 = and_12_out ? register_4bit_13_reg_o1 : 1'bz;  // Controlled_Buffer controlled_buffer_51
  assign O0 = and_12_out ? register_4bit_13_reg_o0 : 1'bz;  // Controlled_Buffer controlled_buffer_52
  assign O3 = and_13_out ? register_4bit_14_reg_o3 : 1'bz;  // Controlled_Buffer controlled_buffer_53
  assign O2 = and_13_out ? register_4bit_14_reg_o2 : 1'bz;  // Controlled_Buffer controlled_buffer_54
  assign O1 = and_13_out ? register_4bit_14_reg_o1 : 1'bz;  // Controlled_Buffer controlled_buffer_55
  assign O0 = and_13_out ? register_4bit_14_reg_o0 : 1'bz;  // Controlled_Buffer controlled_buffer_56
  assign O3 = and_14_out ? register_4bit_15_reg_o3 : 1'bz;  // Controlled_Buffer controlled_buffer_57
  assign O2 = and_14_out ? register_4bit_15_reg_o2 : 1'bz;  // Controlled_Buffer controlled_buffer_58
  assign O1 = and_14_out ? register_4bit_15_reg_o1 : 1'bz;  // Controlled_Buffer controlled_buffer_59
  assign O0 = and_14_out ? register_4bit_15_reg_o0 : 1'bz;  // Controlled_Buffer controlled_buffer_60
  assign O3 = and_15_out ? register_4bit_16_reg_o3 : 1'bz;  // Controlled_Buffer controlled_buffer_61
  assign O2 = and_15_out ? register_4bit_16_reg_o2 : 1'bz;  // Controlled_Buffer controlled_buffer_62
  assign O1 = and_15_out ? register_4bit_16_reg_o1 : 1'bz;  // Controlled_Buffer controlled_buffer_63
  assign O0 = and_15_out ? register_4bit_16_reg_o0 : 1'bz;  // Controlled_Buffer controlled_buffer_64
endmodule

module ASSEMBER_V2 (
  input  ADD_BIN_I3,
  input  ADD_BIN_I2,
  input  ADD_BIN_I1,
  input  ADD_BIN_I0,
  input  CLEAR,
  input  WE,
  input  SOTRE_MEMORY,
  input  STORE_STAGE,
  input  ENTER,
  input  ADD,
  input  SUB,
  input  AAND,
  input  OOR,
  input  XOOR,
  input  NOOT,
  input  INC,
  input  DEC,
  input  JMP,
  input  JZ,
  input  JN,
  input  HLT,
  input  LDI,
  input  LDA,
  input  STA,
  input  XXX,
  input  OPR_I0,
  input  OPR_I1,
  input  OPR_I2,
  input  OPR_I3,
  input  OPR_I4,
  input  OPR_I5,
  input  OPR_I6,
  input  OPR_I7,
  input  OPR_I8,
  input  OPR_I9,
  input  ADDR_I0,
  input  ADDR_I1,
  input  ADDR_I2,
  input  ADDR_I3,
  input  ADDR_I4,
  input  ADDR_I5,
  input  ADDR_I6,
  input  ADDR_I7,
  input  ADDR_I8,
  input  ADDR_I9,
  output OPC_O3,
  output OPC_O2,
  output OPC_O1,
  output OPC_O0,
  output OPR_O3,
  output OPR_O2,
  output OPR_O1,
  output OPR_O0
);

  wire controlled_buffer_1_out, controlled_buffer_2_out, controlled_buffer_3_out, controlled_buffer_4_out,
       not_1_out, OPCODE_opc0, OPCODE_opc1, OPCODE_opc2, OPCODE_opc3, OPERAND_opc0, OPERAND_opc1,
       OPERAND_opc2, OPERAND_opc3, register_4bit_1_reg_o0, register_4bit_1_reg_o1, register_4bit_1_reg_o2,
       register_4bit_1_reg_o3, register_4bit_2_reg_o0, register_4bit_2_reg_o1, register_4bit_2_reg_o2,
       register_4bit_2_reg_o3, register_4bit_3_reg_o0, register_4bit_3_reg_o1, register_4bit_3_reg_o2,
       register_4bit_3_reg_o3, ROM_ADDR_opc0, ROM_ADDR_opc1, ROM_ADDR_opc2, ROM_ADDR_opc3;

  EEPROM eeprom_1 (
    .HARD_RESET(CLEAR), .CLK(SOTRE_MEMORY), .I3(register_4bit_1_reg_o3), .I2(register_4bit_1_reg_o2),
    .I1(register_4bit_1_reg_o1), .I0(register_4bit_1_reg_o0), .WE(WE), .ROMI3(controlled_buffer_1_out),
    .ROMI2(controlled_buffer_2_out), .ROMI1(controlled_buffer_3_out), .ROMI0(controlled_buffer_4_out),
    .O3(OPC_O3), .O2(OPC_O2), .O1(OPC_O1), .O0(OPC_O0));
  REGISTER_4BIT register_4bit_1 (
    .HARD_RESET(CLEAR), .CLK(STORE_STAGE), .REG_I3(OPCODE_opc3), .REG_I2(OPCODE_opc2), .REG_I1(OPCODE_opc1),
    .REG_I0(OPCODE_opc0), .WE(1'b1), .REG_O3(register_4bit_1_reg_o3), .REG_O2(register_4bit_1_reg_o2),
    .REG_O1(register_4bit_1_reg_o1), .REG_O0(register_4bit_1_reg_o0));
  ASSEMBLER_OPCODE_V2 OPCODE (
    .HARD_RESET(CLEAR), .STORE(ENTER), .ADD(ADD), .SUB(SUB), .AAND(AAND), .OOR(OOR), .XOOR(XOOR),
    .NOOT(NOOT), .INC(INC), .DEC(DEC), .JMP(JMP), .JZ(JZ), .JN(JN), .HLT(HLT), .LDI(LDI), .LDA(LDA),
    .STA(STA), .XXX(XXX), .OPC3(OPCODE_opc3), .OPC2(OPCODE_opc2), .OPC1(OPCODE_opc1), .OPC0(OPCODE_opc0));
  EEPROM eeprom_2 (
    .HARD_RESET(CLEAR), .CLK(SOTRE_MEMORY), .I3(register_4bit_2_reg_o3), .I2(register_4bit_2_reg_o2),
    .I1(register_4bit_2_reg_o1), .I0(register_4bit_2_reg_o0), .WE(WE), .ROMI3(controlled_buffer_1_out),
    .ROMI2(controlled_buffer_2_out), .ROMI1(controlled_buffer_3_out), .ROMI0(controlled_buffer_4_out),
    .O3(OPR_O3), .O2(OPR_O2), .O1(OPR_O1), .O0(OPR_O0));
  REGISTER_4BIT register_4bit_2 (
    .HARD_RESET(CLEAR), .CLK(STORE_STAGE), .REG_I3(OPERAND_opc3), .REG_I2(OPERAND_opc2),
    .REG_I1(OPERAND_opc1), .REG_I0(OPERAND_opc0), .WE(1'b1), .REG_O3(register_4bit_2_reg_o3),
    .REG_O2(register_4bit_2_reg_o2), .REG_O1(register_4bit_2_reg_o1), .REG_O0(register_4bit_2_reg_o0));
  ASSSEMBLER_OPERAND_V2 OPERAND (
    .HARD_RESET(CLEAR), .STORE(ENTER), .I0(OPR_I0), .I1(OPR_I1), .I2(OPR_I2), .I3(OPR_I3), .I4(OPR_I4),
    .I5(OPR_I5), .I6(OPR_I6), .I7(OPR_I7), .I8(OPR_I8), .I9(OPR_I9), .OPC3(OPERAND_opc3),
    .OPC2(OPERAND_opc2), .OPC1(OPERAND_opc1), .OPC0(OPERAND_opc0));
  LED led_1 (.in(controlled_buffer_1_out));
  LED led_2 (.in(controlled_buffer_2_out));
  LED led_3 (.in(controlled_buffer_3_out));
  assign controlled_buffer_1_out = WE ? register_4bit_3_reg_o3 : 1'bz;  // Controlled_Buffer controlled_buffer_1
  assign controlled_buffer_2_out = WE ? register_4bit_3_reg_o2 : 1'bz;  // Controlled_Buffer controlled_buffer_2
  assign controlled_buffer_3_out = WE ? register_4bit_3_reg_o1 : 1'bz;  // Controlled_Buffer controlled_buffer_3
  REGISTER_4BIT register_4bit_3 (
    .HARD_RESET(CLEAR), .CLK(STORE_STAGE), .REG_I3(ROM_ADDR_opc3), .REG_I2(ROM_ADDR_opc2),
    .REG_I1(ROM_ADDR_opc1), .REG_I0(ROM_ADDR_opc0), .WE(1'b1), .REG_O3(register_4bit_3_reg_o3),
    .REG_O2(register_4bit_3_reg_o2), .REG_O1(register_4bit_3_reg_o1), .REG_O0(register_4bit_3_reg_o0));
  ASSSEMBLER_OPERAND_V2 ROM_ADDR (
    .HARD_RESET(CLEAR), .STORE(ENTER), .I0(ADDR_I0), .I1(ADDR_I1), .I2(ADDR_I2), .I3(ADDR_I3), .I4(ADDR_I4),
    .I5(ADDR_I5), .I6(ADDR_I6), .I7(ADDR_I7), .I8(ADDR_I8), .I9(ADDR_I9), .OPC3(ROM_ADDR_opc3),
    .OPC2(ROM_ADDR_opc2), .OPC1(ROM_ADDR_opc1), .OPC0(ROM_ADDR_opc0));
  LED led_4 (.in(controlled_buffer_4_out));
  assign controlled_buffer_4_out = WE ? register_4bit_3_reg_o0 : 1'bz;  // Controlled_Buffer controlled_buffer_4
  not not_1 (not_1_out, WE);
  assign controlled_buffer_4_out = not_1_out ? ADD_BIN_I0 : 1'bz;  // Controlled_Buffer controlled_buffer_5
  assign controlled_buffer_3_out = not_1_out ? ADD_BIN_I1 : 1'bz;  // Controlled_Buffer controlled_buffer_6
  assign controlled_buffer_2_out = not_1_out ? ADD_BIN_I2 : 1'bz;  // Controlled_Buffer controlled_buffer_7
  assign controlled_buffer_1_out = not_1_out ? ADD_BIN_I3 : 1'bz;  // Controlled_Buffer controlled_buffer_8
endmodule

module FINAL_4BIT_CPUT (
  input  CLEAR,
  input  RESET,
  input  WE,
  input  ADD,
  input  SUB,
  input  AAND,
  input  OOR,
  input  XOOR,
  input  NOOT,
  input  INC,
  input  DEC,
  input  JMP,
  input  JZ,
  input  JN,
  input  HLT,
  input  LDI,
  input  LDA,
  input  STA,
  input  XXX,
  input  I0,
  input  I1,
  input  I2,
  input  I3,
  input  I4,
  input  I5,
  input  I6,
  input  I7,
  input  I8,
  input  I9,
  input  A0,
  input  A1,
  input  A2,
  input  A3,
  input  A4,
  input  A5,
  input  A6,
  input  A7,
  input  A8,
  input  A9
);

  wire assember_v2_1_opc_o0, assember_v2_1_opc_o1, assember_v2_1_opc_o2, assember_v2_1_opc_o3,
       assember_v2_1_opr_o0, assember_v2_1_opr_o1, assember_v2_1_opr_o2, assember_v2_1_opr_o3, clock_1_out,
       cpu_v9_1_acc_o0, cpu_v9_1_acc_o1, cpu_v9_1_acc_o2, cpu_v9_1_acc_o3, cpu_v9_1_c, cpu_v9_1_decode,
       cpu_v9_1_execute, cpu_v9_1_fetch, cpu_v9_1_isa_opc_0, cpu_v9_1_isa_opc_1, cpu_v9_1_isa_opc_2,
       cpu_v9_1_isa_opc_3, cpu_v9_1_isa_opr_0, cpu_v9_1_isa_opr_1, cpu_v9_1_isa_opr_2, cpu_v9_1_isa_opr_3,
       cpu_v9_1_n, cpu_v9_1_ovf, cpu_v9_1_romi0, cpu_v9_1_romi1, cpu_v9_1_romi2, cpu_v9_1_romi3,
       cpu_v9_1_writeback, cpu_v9_1_z, ENTER_out, SOTRE_MEMORY_out, STORE_STORAGE_out;

  Button SOTRE_MEMORY (.out(SOTRE_MEMORY_out));
  Button STORE_STORAGE (.out(STORE_STORAGE_out));
  Button ENTER (.out(ENTER_out));
  Clock clock_1 (.out(clock_1_out));
  ASSEMBER_V2 assember_v2_1 (
    .ADD_BIN_I3(cpu_v9_1_romi3), .ADD_BIN_I2(cpu_v9_1_romi2), .ADD_BIN_I1(cpu_v9_1_romi1),
    .ADD_BIN_I0(cpu_v9_1_romi0), .CLEAR(CLEAR), .WE(WE), .SOTRE_MEMORY(SOTRE_MEMORY_out),
    .STORE_STAGE(STORE_STORAGE_out), .ENTER(ENTER_out), .ADD(ADD), .SUB(SUB), .AAND(AAND), .OOR(OOR),
    .XOOR(XOOR), .NOOT(NOOT), .INC(INC), .DEC(DEC), .JMP(JMP), .JZ(JZ), .JN(JN), .HLT(HLT), .LDI(LDI),
    .LDA(LDA), .STA(STA), .XXX(XXX), .OPR_I0(I0), .OPR_I1(I1), .OPR_I2(I2), .OPR_I3(I3), .OPR_I4(I4),
    .OPR_I5(I5), .OPR_I6(I6), .OPR_I7(I7), .OPR_I8(I8), .OPR_I9(I9), .ADDR_I0(A0), .ADDR_I1(A1),
    .ADDR_I2(A2), .ADDR_I3(A3), .ADDR_I4(A4), .ADDR_I5(A5), .ADDR_I6(A6), .ADDR_I7(A7), .ADDR_I8(A8),
    .ADDR_I9(A9), .OPC_O3(assember_v2_1_opc_o3), .OPC_O2(assember_v2_1_opc_o2),
    .OPC_O1(assember_v2_1_opc_o1), .OPC_O0(assember_v2_1_opc_o0), .OPR_O3(assember_v2_1_opr_o3),
    .OPR_O2(assember_v2_1_opr_o2), .OPR_O1(assember_v2_1_opr_o1), .OPR_O0(assember_v2_1_opr_o0));
  cpu_v9 cpu_v9_1 (
    .RESET(RESET), .CLK(clock_1_out), .OPC3(assember_v2_1_opc_o3), .OPC2(assember_v2_1_opc_o2),
    .OPC1(assember_v2_1_opc_o1), .OPC0(assember_v2_1_opc_o0), .OPRAND3(assember_v2_1_opr_o3),
    .OPRAND2(assember_v2_1_opr_o2), .OPRAND1(assember_v2_1_opr_o1), .OPRAND0(assember_v2_1_opr_o0),
    .ISA_OPC_3(cpu_v9_1_isa_opc_3), .ISA_OPC_2(cpu_v9_1_isa_opc_2), .ISA_OPC_1(cpu_v9_1_isa_opc_1),
    .ISA_OPC_0(cpu_v9_1_isa_opc_0), .ISA_OPR_3(cpu_v9_1_isa_opr_3), .ISA_OPR_2(cpu_v9_1_isa_opr_2),
    .ISA_OPR_1(cpu_v9_1_isa_opr_1), .ISA_OPR_0(cpu_v9_1_isa_opr_0), .OVF(cpu_v9_1_ovf), .N(cpu_v9_1_n),
    .C(cpu_v9_1_c), .Z(cpu_v9_1_z), .ACC_O3(cpu_v9_1_acc_o3), .ACC_O2(cpu_v9_1_acc_o2),
    .ACC_O1(cpu_v9_1_acc_o1), .ACC_O0(cpu_v9_1_acc_o0), .FETCH(cpu_v9_1_fetch), .DECODE(cpu_v9_1_decode),
    .EXECUTE(cpu_v9_1_execute), .WRITEBACK(cpu_v9_1_writeback), .ROMI3(cpu_v9_1_romi3),
    .ROMI2(cpu_v9_1_romi2), .ROMI1(cpu_v9_1_romi1), .ROMI0(cpu_v9_1_romi0));
  LED led_1 (.in(cpu_v9_1_isa_opc_3));
  LED led_2 (.in(cpu_v9_1_isa_opc_2));
  LED FETCH (.in(cpu_v9_1_fetch));
  LED DECODE (.in(cpu_v9_1_decode));
  LED EXECUTE (.in(cpu_v9_1_execute));
  LED WRITEBACK (.in(cpu_v9_1_writeback));
  LED led_3 (.in(cpu_v9_1_isa_opc_1));
  LED led_4 (.in(cpu_v9_1_isa_opc_0));
  LED led_5 (.in(cpu_v9_1_isa_opr_3));
  LED led_6 (.in(cpu_v9_1_isa_opr_2));
  LED led_7 (.in(cpu_v9_1_isa_opr_1));
  LED led_8 (.in(cpu_v9_1_isa_opr_0));
  LED OVF (.in(cpu_v9_1_ovf));
  LED N (.in(cpu_v9_1_n));
  LED C (.in(cpu_v9_1_c));
  LED Z (.in(cpu_v9_1_z));
  LED O3 (.in(cpu_v9_1_acc_o3));
  LED O2 (.in(cpu_v9_1_acc_o2));
  LED O1 (.in(cpu_v9_1_acc_o1));
  LED O0 (.in(cpu_v9_1_acc_o0));
endmodule
